// Logisim project 32bit_fp_display.circ as structural Verilog: 5 circuits, main circuit 32bit_decoder_10div
module _32bit_decoder_10div (
  input  [15:0] in,
  output [15:0] out,
  output [3:0] num_out
);

  wire [15:4] divider_1_rem;

  Divider #(.width(16)) divider_1 (.a(in), .b(16'ha), .out(out), .rem({divider_1_rem, num_out}));  // open: upper

  // Notes on the sheet:
  //   num_out: pull=down
  //   out: pull=down
  //   in: pull=down
endmodule

module _32bit_decoder_10mul (
  input  [15:0] in,
  output [15:0] out,
  output [3:0] num_out
);

  wire [15:4] multiplier_1_cout;

  Multiplier #(.width(16)) multiplier_1 (
    .a(in), .b(16'ha), .out(out), .cout({multiplier_1_cout, num_out}));  // open: cin
  Pull_Resistor pull_resistor_1 (.node(num_out));
endmodule

module _32bit_decoder (
  input  [31:0] in,
  output sign,
  output [3:0] _4,
  output [3:0] _1,
  output [3:0] _3,
  output [3:0] _2,
  output [3:0] _2_2,
  output [3:0] _3_2,
  output [3:0] _1_2,
  output [3:0] _4_2,
  output [3:0] _0,
  output [3:0] _5,
  output dot,
  output [3:0] _6,
  output [3:0] _7,
  output [3:0] _8,
  output [3:0] _9,
  output [3:0] _10,
  output [3:0] _11,
  output [3:0] _12,
  output [3:0] _13,
  output [3:0] _14,
  output [3:0] _15,
  output [3:0] _16
);

  wire [15:0] n32bit_decoder_10div_1_out, n32bit_decoder_10div_2_out, n32bit_decoder_10div_3_out,
       n32bit_decoder_10div_4_out, n32bit_decoder_10div_5_out, n32bit_decoder_10mul_1_out,
       n32bit_decoder_10mul_2_out, n32bit_decoder_10mul_3_out, n32bit_decoder_10mul_4_out,
       n32bit_decoder_10mul_5_out, n32bit_decoder_10mul_6_out, n32bit_decoder_10mul_7_out,
       n32bit_decoder_10mul_8_out, n32bit_decoder_10mul_9_out, n32bit_decoder_10mul_10_out,
       n32bit_decoder_10mul_11_out, n32bit_decoder_10mul_12_out, n32bit_decoder_10mul_13_out,
       n32bit_decoder_10mul_14_out, n32bit_decoder_10mul_15_out;
  wire [31:0] multiplexer_1_out, subtractor_1_out;

  _32bit_decoder_10div u_32bit_decoder_10div_1 (
    .in(n32bit_decoder_10div_2_out), .out(n32bit_decoder_10div_1_out), .num_out(_4));
  _32bit_decoder_10div u_32bit_decoder_10div_2 (
    .in(n32bit_decoder_10div_4_out), .out(n32bit_decoder_10div_2_out), .num_out(_3));
  Pull_Resistor pull_resistor_1 (.node(sign));
  BitSelector #(.width(32)) bitselector_1 (.in(in), .out(sign), .sel({5{1'b1}}));
  Pull_Resistor pull_resistor_2 (.node(in));
  _32bit_decoder_10div u_32bit_decoder_10div_3 (
    .in(n32bit_decoder_10div_5_out), .out(n32bit_decoder_10div_3_out), .num_out(_1_2));
  _32bit_decoder_10div u_32bit_decoder_10div_4 (
    .in(n32bit_decoder_10div_3_out), .out(n32bit_decoder_10div_4_out), .num_out(_2_2));
  Multiplexer #(.width(32)) multiplexer_1 (
    .in0(in), .in1(subtractor_1_out), .out(multiplexer_1_out), .sel(sign));  // open: en
  Subtractor #(.width(32)) subtractor_1 (.a({32{1'b0}}), .b(in), .out(subtractor_1_out));  // open: bin, bout
  _32bit_decoder_10mul u_32bit_decoder_10mul_1 (
    .in(multiplexer_1_out[15:0]), .out(n32bit_decoder_10mul_1_out), .num_out(_1));
  _32bit_decoder_10div u_32bit_decoder_10div_5 (
    .in(multiplexer_1_out[31:16]), .out(n32bit_decoder_10div_5_out), .num_out(_0));
  _32bit_decoder_10mul u_32bit_decoder_10mul_2 (
    .in(n32bit_decoder_10mul_3_out), .out(n32bit_decoder_10mul_2_out), .num_out(_3_2));
  _32bit_decoder_10mul u_32bit_decoder_10mul_3 (
    .in(n32bit_decoder_10mul_1_out), .out(n32bit_decoder_10mul_3_out), .num_out(_2));
  _32bit_decoder_10mul u_32bit_decoder_10mul_4 (
    .in(n32bit_decoder_10mul_2_out), .out(n32bit_decoder_10mul_4_out), .num_out(_4_2));
  _32bit_decoder_10mul u_32bit_decoder_10mul_5 (
    .in(n32bit_decoder_10mul_4_out), .out(n32bit_decoder_10mul_5_out), .num_out(_5));
  _32bit_decoder_10mul u_32bit_decoder_10mul_6 (
    .in(n32bit_decoder_10mul_7_out), .out(n32bit_decoder_10mul_6_out), .num_out(_7));
  _32bit_decoder_10mul u_32bit_decoder_10mul_7 (
    .in(n32bit_decoder_10mul_5_out), .out(n32bit_decoder_10mul_7_out), .num_out(_6));
  _32bit_decoder_10mul u_32bit_decoder_10mul_8 (
    .in(n32bit_decoder_10mul_6_out), .out(n32bit_decoder_10mul_8_out), .num_out(_8));
  _32bit_decoder_10mul u_32bit_decoder_10mul_9 (
    .in(n32bit_decoder_10mul_8_out), .out(n32bit_decoder_10mul_9_out), .num_out(_9));
  _32bit_decoder_10mul u_32bit_decoder_10mul_10 (
    .in(n32bit_decoder_10mul_11_out), .out(n32bit_decoder_10mul_10_out), .num_out(_11));
  _32bit_decoder_10mul u_32bit_decoder_10mul_11 (
    .in(n32bit_decoder_10mul_9_out), .out(n32bit_decoder_10mul_11_out), .num_out(_10));
  _32bit_decoder_10mul u_32bit_decoder_10mul_12 (
    .in(n32bit_decoder_10mul_13_out), .out(n32bit_decoder_10mul_12_out), .num_out(_13));
  _32bit_decoder_10mul u_32bit_decoder_10mul_13 (
    .in(n32bit_decoder_10mul_10_out), .out(n32bit_decoder_10mul_13_out), .num_out(_12));
  _32bit_decoder_10mul u_32bit_decoder_10mul_14 (
    .in(n32bit_decoder_10mul_12_out), .out(n32bit_decoder_10mul_14_out), .num_out(_14));
  _32bit_decoder_10mul u_32bit_decoder_10mul_15 (
    .in(n32bit_decoder_10mul_14_out), .out(n32bit_decoder_10mul_15_out), .num_out(_15));
  _32bit_decoder_10mul u_32bit_decoder_10mul_16 (.in(n32bit_decoder_10mul_15_out), .num_out(_16));  // open: out

  assign dot = 1'b1;

  // Other names for the same wires on the sheet: tunnel = sign

  // Notes on the sheet:
  //   _3_2: pull=down
  //   in: pull=down
  //   _4_2: pull=down
  //   _8: pull=down
  //   _15: pull=down
  //   _10: pull=down
  //   _3: pull=down
  //   _13: pull=down
  //   _2_2: pull=down
  //   _11: pull=down
  //   _7: pull=down
  //   _12: pull=down
  //   _1: pull=down
  //   _16: pull=down
  //   _14: pull=down
  //   _9: pull=down
  //   _6: pull=down
  //   _1_2: pull=down
  //   _4: pull=down
  //   _2: pull=down
  //   _0: pull=down
  //   _5: pull=down
endmodule

module _32bit_decoder_short (
  input  [31:0] in,
  output sign,
  output [3:0] _4,
  output [3:0] _1,
  output [3:0] _3,
  output [3:0] _2,
  output [3:0] _2_2,
  output [3:0] _3_2,
  output [3:0] _1_2,
  output [3:0] _4_2,
  output [3:0] _0,
  output [3:0] _5,
  output dot
);

  wire [15:0] n32bit_decoder_10div_2_out, n32bit_decoder_10div_3_out, n32bit_decoder_10div_4_out,
       n32bit_decoder_10div_5_out, n32bit_decoder_10mul_1_out, n32bit_decoder_10mul_2_out,
       n32bit_decoder_10mul_3_out, n32bit_decoder_10mul_4_out;
  wire [31:0] multiplexer_1_out, subtractor_1_out;

  _32bit_decoder_10div u_32bit_decoder_10div_1 (.in(n32bit_decoder_10div_2_out), .num_out(_4));  // open: out
  _32bit_decoder_10div u_32bit_decoder_10div_2 (
    .in(n32bit_decoder_10div_3_out), .out(n32bit_decoder_10div_2_out), .num_out(_3));
  Pull_Resistor pull_resistor_1 (.node(sign));
  BitSelector #(.width(32)) bitselector_1 (.in(in), .out(sign), .sel({5{1'b1}}));
  Pull_Resistor pull_resistor_2 (.node(in));
  _32bit_decoder_10div u_32bit_decoder_10div_3 (
    .in(n32bit_decoder_10div_4_out), .out(n32bit_decoder_10div_3_out), .num_out(_2_2));
  _32bit_decoder_10div u_32bit_decoder_10div_4 (
    .in(n32bit_decoder_10div_5_out), .out(n32bit_decoder_10div_4_out), .num_out(_1_2));
  Multiplexer #(.width(32)) multiplexer_1 (
    .in0(in), .in1(subtractor_1_out), .out(multiplexer_1_out), .sel(sign));  // open: en
  Subtractor #(.width(32)) subtractor_1 (.a({32{1'b0}}), .b(in), .out(subtractor_1_out));  // open: bin, bout
  _32bit_decoder_10mul u_32bit_decoder_10mul_1 (
    .in(multiplexer_1_out[15:0]), .out(n32bit_decoder_10mul_1_out), .num_out(_1));
  _32bit_decoder_10div u_32bit_decoder_10div_5 (
    .in(multiplexer_1_out[31:16]), .out(n32bit_decoder_10div_5_out), .num_out(_0));
  _32bit_decoder_10mul u_32bit_decoder_10mul_2 (
    .in(n32bit_decoder_10mul_1_out), .out(n32bit_decoder_10mul_2_out), .num_out(_2));
  _32bit_decoder_10mul u_32bit_decoder_10mul_3 (
    .in(n32bit_decoder_10mul_2_out), .out(n32bit_decoder_10mul_3_out), .num_out(_3_2));
  _32bit_decoder_10mul u_32bit_decoder_10mul_4 (
    .in(n32bit_decoder_10mul_3_out), .out(n32bit_decoder_10mul_4_out), .num_out(_4_2));
  _32bit_decoder_10mul u_32bit_decoder_10mul_5 (.in(n32bit_decoder_10mul_4_out), .num_out(_5));  // open: out

  assign dot = 1'b1;

  // Other names for the same wires on the sheet: tunnel = sign

  // Notes on the sheet:
  //   _3: pull=down
  //   _4_2: pull=down
  //   _4: pull=down
  //   in: pull=down
  //   _1_2: pull=down
  //   _2: pull=down
  //   _3_2: pull=down
  //   _1: pull=down
  //   _2_2: pull=down
  //   _0: pull=down
  //   _5: pull=down
endmodule

module _32_bit_decoder_3digits_x3 (
  input  sub10,
  input  sub10_2,
  input  sub10_3,
  input  add10,
  input  add10_2,
  input  add10_3,
  input  sub1,
  input  sub1_2,
  input  sub1_3,
  input  add1,
  input  add1_2,
  input  add1_3,
  output [3:0] _2,
  output [3:0] _2_2,
  output [3:0] _2_3,
  output [3:0] _1,
  output [3:0] _1_2,
  output [3:0] _1_3,
  output [3:0] _0,
  output [3:0] _0_2,
  output [3:0] _0_3,
  output [3:0] sign,
  output [3:0] sign_2,
  output [3:0] sign_3,
  output [31:0] out_1,
  output [31:0] out_1_2,
  output [31:0] out_1_3,
  output out_28
);

  wire buffer_3_out, buffer_8_out, buffer_14_out, rising_edge_pulse_1_out, rising_edge_pulse_2_out,
       rising_edge_pulse_3_out;
  wire [15:0] n32bit_decoder_10div_1_out, n32bit_decoder_10div_3_out, n32bit_decoder_10div_5_out,
       n32bit_decoder_10div_6_out, n32bit_decoder_10div_8_out, n32bit_decoder_10div_9_out;
  wire [31:0] adder_1_out, adder_2_out, adder_3_out, adder_4_out, adder_5_out, adder_6_out,
       controlled_buffer_1_out, controlled_buffer_5_out, controlled_buffer_9_out, multiplexer_1_out,
       multiplexer_2_out, multiplexer_3_out, negator_1_out, negator_2_out, negator_3_out, subtractor_1_out,
       subtractor_2_out, subtractor_3_out, subtractor_4_out, subtractor_5_out, subtractor_6_out;

  Register #(.width(32)) register_1 (
    .D(controlled_buffer_1_out), .Q(out_1_3), .clk(rising_edge_pulse_1_out));  // open: en, clr
  rising_edge_pulse rising_edge_pulse_1 (.signal(buffer_3_out), .out(rising_edge_pulse_1_out));
  _32bit_decoder_10div u_32bit_decoder_10div_1 (
    .in(n32bit_decoder_10div_3_out), .out(n32bit_decoder_10div_1_out), .num_out(_1_3));
  _32bit_decoder_10div u_32bit_decoder_10div_2 (.in(n32bit_decoder_10div_1_out), .num_out(_2_3));  // open: out
  Multiplexer #(.width(32), .enable("false")) multiplexer_1 (
    .in0(out_1_3), .in1(negator_1_out), .out(multiplexer_1_out), .sel(out_1_3[31]));
  Negator #(.width(32)) negator_1 (.in(out_1_3), .out(negator_1_out));
  Adder #(.width(32)) adder_1 (.a(out_1_3), .b(32'h10000), .out(adder_1_out));  // open: cin, cout
  Adder #(.width(32)) adder_2 (.a(out_1_3), .b(32'ha0000), .out(adder_2_out));  // open: cin, cout
  Subtractor #(.width(32)) subtractor_1 (.a(out_1_3), .b(32'h10000), .out(subtractor_1_out));  // open: bin, bout
  Subtractor #(.width(32)) subtractor_2 (.a(out_1_3), .b(32'ha0000), .out(subtractor_2_out));  // open: bin, bout
  _32bit_decoder_10div u_32bit_decoder_10div_3 (
    .in(multiplexer_1_out[31:16]), .out(n32bit_decoder_10div_3_out), .num_out(_0_3));
  buf buffer_1 (sign_3[3], out_1_3[31]);
  buf buffer_2 (out_28, buffer_3_out);
  buf buffer_3 (buffer_3_out, sub1);
  buf buffer_4 (buffer_3_out, sub10);
  buf buffer_5 (buffer_3_out, add1);
  buf buffer_6 (buffer_3_out, add10);
  assign controlled_buffer_1_out = add1 ? adder_1_out : 32'bz;  // Controlled_Buffer controlled_buffer_1
  assign controlled_buffer_1_out = sub1 ? adder_2_out : 32'bz;  // Controlled_Buffer controlled_buffer_2
  assign controlled_buffer_1_out = add10 ? subtractor_1_out : 32'bz;  // Controlled_Buffer controlled_buffer_3
  assign controlled_buffer_1_out = sub10 ? subtractor_2_out : 32'bz;  // Controlled_Buffer controlled_buffer_4
  Pull_Resistor pull_resistor_1 (.node(out_28));
  Pull_Resistor pull_resistor_2 (.node(buffer_3_out));
  rising_edge_pulse rising_edge_pulse_2 (.signal(buffer_8_out), .out(rising_edge_pulse_2_out));
  Register #(.width(32)) register_2 (
    .D(controlled_buffer_5_out), .Q(out_1), .clk(rising_edge_pulse_2_out));  // open: en, clr
  _32bit_decoder_10div u_32bit_decoder_10div_4 (.in(n32bit_decoder_10div_5_out), .num_out(_2));  // open: out
  Negator #(.width(32)) negator_2 (.in(out_1), .out(negator_2_out));
  _32bit_decoder_10div u_32bit_decoder_10div_5 (
    .in(n32bit_decoder_10div_6_out), .out(n32bit_decoder_10div_5_out), .num_out(_1));
  _32bit_decoder_10div u_32bit_decoder_10div_6 (
    .in(multiplexer_2_out[31:16]), .out(n32bit_decoder_10div_6_out), .num_out(_0));
  Multiplexer #(.width(32), .enable("false")) multiplexer_2 (
    .in0(out_1), .in1(negator_2_out), .out(multiplexer_2_out), .sel(out_1[31]));
  buf buffer_7 (sign[3], out_1[31]);
  buf buffer_8 (buffer_8_out, add1_2);
  buf buffer_9 (buffer_8_out, sub1_2);
  Adder #(.width(32)) adder_3 (.a(out_1), .b(32'h10000), .out(adder_3_out));  // open: cin, cout
  assign controlled_buffer_5_out = add1_2 ? adder_3_out : 32'bz;  // Controlled_Buffer controlled_buffer_5
  Adder #(.width(32)) adder_4 (.a(out_1), .b(32'ha0000), .out(adder_4_out));  // open: cin, cout
  assign controlled_buffer_5_out = sub1_2 ? adder_4_out : 32'bz;  // Controlled_Buffer controlled_buffer_6
  Subtractor #(.width(32)) subtractor_3 (.a(out_1), .b(32'h10000), .out(subtractor_3_out));  // open: bin, bout
  Subtractor #(.width(32)) subtractor_4 (.a(out_1), .b(32'ha0000), .out(subtractor_4_out));  // open: bin, bout
  Pull_Resistor pull_resistor_3 (.node(out_28));
  buf buffer_10 (out_28, buffer_8_out);
  buf buffer_11 (buffer_8_out, sub10_2);
  Pull_Resistor pull_resistor_4 (.node(buffer_8_out));
  buf buffer_12 (buffer_8_out, add10_2);
  assign controlled_buffer_5_out = add10_2 ? subtractor_3_out : 32'bz;  // Controlled_Buffer controlled_buffer_7
  assign controlled_buffer_5_out = sub10_2 ? subtractor_4_out : 32'bz;  // Controlled_Buffer controlled_buffer_8
  rising_edge_pulse rising_edge_pulse_3 (.signal(buffer_14_out), .out(rising_edge_pulse_3_out));
  Register #(.width(32)) register_3 (
    .D(controlled_buffer_9_out), .Q(out_1_2), .clk(rising_edge_pulse_3_out));  // open: en, clr
  _32bit_decoder_10div u_32bit_decoder_10div_7 (.in(n32bit_decoder_10div_8_out), .num_out(_2_2));  // open: out
  Negator #(.width(32)) negator_3 (.in(out_1_2), .out(negator_3_out));
  _32bit_decoder_10div u_32bit_decoder_10div_8 (
    .in(n32bit_decoder_10div_9_out), .out(n32bit_decoder_10div_8_out), .num_out(_1_2));
  _32bit_decoder_10div u_32bit_decoder_10div_9 (
    .in(multiplexer_3_out[31:16]), .out(n32bit_decoder_10div_9_out), .num_out(_0_2));
  Multiplexer #(.width(32), .enable("false")) multiplexer_3 (
    .in0(out_1_2), .in1(negator_3_out), .out(multiplexer_3_out), .sel(out_1_2[31]));
  buf buffer_13 (sign_2[3], out_1_2[31]);
  buf buffer_14 (buffer_14_out, add1_3);
  buf buffer_15 (buffer_14_out, sub1_3);
  Adder #(.width(32)) adder_5 (.a(out_1_2), .b(32'h10000), .out(adder_5_out));  // open: cin, cout
  assign controlled_buffer_9_out = add1_3 ? adder_5_out : 32'bz;  // Controlled_Buffer controlled_buffer_9
  assign controlled_buffer_9_out = sub1_3 ? adder_6_out : 32'bz;  // Controlled_Buffer controlled_buffer_10
  Adder #(.width(32)) adder_6 (.a(out_1_2), .b(32'ha0000), .out(adder_6_out));  // open: cin, cout
  Subtractor #(.width(32)) subtractor_5 (.a(out_1_2), .b(32'h10000), .out(subtractor_5_out));  // open: bin, bout
  Subtractor #(.width(32)) subtractor_6 (.a(out_1_2), .b(32'ha0000), .out(subtractor_6_out));  // open: bin, bout
  Pull_Resistor pull_resistor_5 (.node(out_28));
  buf buffer_16 (out_28, buffer_14_out);
  buf buffer_17 (buffer_14_out, sub10_3);
  buf buffer_18 (buffer_14_out, add10_3);
  Pull_Resistor pull_resistor_6 (.node(buffer_14_out));
  assign controlled_buffer_9_out = add10_3 ? subtractor_5_out : 32'bz;  // Controlled_Buffer controlled_buffer_11
  assign controlled_buffer_9_out = sub10_3 ? subtractor_6_out : 32'bz;  // Controlled_Buffer controlled_buffer_12

  assign sign[2:0] = {3{sign[3]}};
  assign sign_2[2:0] = {3{sign_2[3]}};
  assign sign_3[2:0] = {3{sign_3[3]}};

  // Notes on the sheet:
  //   _1_3: pull=down
  //   sub10_3: pull=down
  //   _0_3: pull=down
  //   sub1: pull=down
  //   add1: pull=down
  //   add10_3: pull=down
  //   _1_2: pull=down
  //   _2_2: pull=down
  //   add10_2: pull=down
  //   sub10_2: pull=down
  //   _0: pull=down
  //   _1: pull=down
  //   out_28: pull=down
  //   sub1_2: pull=down
  //   _0_2: pull=down
  //   _2_3: pull=down
  //   add1_2: pull=down
  //   _2: pull=down
  //   add10: pull=down
  //   sub10: pull=down
  //   add1_3: pull=down
  //   sub1_3: pull=down
  //   buffer_1 drives only 0 and floats otherwise
  //   buffer_2 drives only 1 and floats otherwise
  //   buffer_3 drives only 1 and floats otherwise
  //   buffer_4 drives only 1 and floats otherwise
  //   buffer_5 drives only 1 and floats otherwise
  //   buffer_6 drives only 1 and floats otherwise
  //   buffer_7 drives only 0 and floats otherwise
  //   buffer_8 drives only 1 and floats otherwise
  //   buffer_9 drives only 1 and floats otherwise
  //   buffer_10 drives only 1 and floats otherwise
  //   buffer_11 drives only 1 and floats otherwise
  //   buffer_12 drives only 1 and floats otherwise
  //   buffer_13 drives only 0 and floats otherwise
  //   buffer_14 drives only 1 and floats otherwise
  //   buffer_15 drives only 1 and floats otherwise
  //   buffer_16 drives only 1 and floats otherwise
  //   buffer_17 drives only 1 and floats otherwise
  //   buffer_18 drives only 1 and floats otherwise
endmodule
