// Logisim project Dodane_rejestry_4x4 (1).circ as structural Verilog: 9 circuits, main circuit matrix_mult
module matrix_mult (
  input  [31:0] in_1,
  input  [31:0] in_2,
  input  [31:0] in_3,
  input  [31:0] in_4,
  input  [31:0] in_5,
  input  [31:0] in_6,
  input  [31:0] in_7,
  input  [31:0] in_8,
  input  [31:0] in_9,
  input  [31:0] in_10,
  input  [31:0] in_11,
  input  [31:0] in_12,
  input  [31:0] in_13,
  input  [31:0] in_14,
  input  [31:0] in_15,
  input  [31:0] in_16,
  input  [31:0] in_17,
  input  [31:0] in_18,
  output [31:0] out11,
  output [31:0] out21,
  output [31:0] out31,
  output [31:0] out12,
  output [31:0] out22,
  output [31:0] out32,
  output [31:0] out13,
  output [31:0] out23,
  output [31:0] out33
);

  matrix_mult_sub matrix_mult_sub_1 (
    .in_a1(in_10), .in_b1(in_1), .in_a2(in_11), .in_b2(in_4), .in_a3(in_12), .in_b3(in_7), .out_ab(out11));
  matrix_mult_sub matrix_mult_sub_2 (
    .in_a1(in_13), .in_b1(in_1), .in_a2(in_14), .in_b2(in_4), .in_a3(in_15), .in_b3(in_7), .out_ab(out12));
  matrix_mult_sub matrix_mult_sub_3 (
    .in_a1(in_16), .in_b1(in_1), .in_a2(in_17), .in_b2(in_4), .in_a3(in_18), .in_b3(in_7), .out_ab(out13));
  matrix_mult_sub matrix_mult_sub_4 (
    .in_a1(in_10), .in_b1(in_2), .in_a2(in_11), .in_b2(in_5), .in_a3(in_12), .in_b3(in_8), .out_ab(out21));
  matrix_mult_sub matrix_mult_sub_5 (
    .in_a1(in_13), .in_b1(in_2), .in_a2(in_14), .in_b2(in_5), .in_a3(in_15), .in_b3(in_8), .out_ab(out22));
  matrix_mult_sub matrix_mult_sub_6 (
    .in_a1(in_16), .in_b1(in_2), .in_a2(in_17), .in_b2(in_5), .in_a3(in_18), .in_b3(in_8), .out_ab(out23));
  matrix_mult_sub matrix_mult_sub_7 (
    .in_a1(in_10), .in_b1(in_3), .in_a2(in_11), .in_b2(in_6), .in_a3(in_12), .in_b3(in_9), .out_ab(out31));
  matrix_mult_sub matrix_mult_sub_8 (
    .in_a1(in_13), .in_b1(in_3), .in_a2(in_14), .in_b2(in_6), .in_a3(in_15), .in_b3(in_9), .out_ab(out32));
  matrix_mult_sub matrix_mult_sub_9 (
    .in_a1(in_16), .in_b1(in_3), .in_a2(in_17), .in_b2(in_6), .in_a3(in_18), .in_b3(in_9), .out_ab(out33));

  // Other names for the same wires on the sheet: A11[31:0] = in_10; A12[31:0] = in_13; A13[31:0] = in_16;
  //   A21[31:0] = in_11; A22[31:0] = in_14; A23[31:0] = in_17; A31[31:0] = in_12; A32[31:0] = in_15;
  //   A33[31:0] = in_18; B11[31:0] = in_1; B12[31:0] = in_4; B13[31:0] = in_7; B21[31:0] = in_2; B22[31:0] = in_5;
  //   B23[31:0] = in_8; B31[31:0] = in_3; B32[31:0] = in_6; B33[31:0] = in_9

  // Notes on the sheet:
  //   out32: pull=down
  //   out31: pull=down
  //   in_10: pull=down
  //   in_17: pull=down
  //   out13: pull=down
  //   out11: pull=down
  //   in_18: pull=down
  //   in_1: pull=down
  //   in_2: pull=down
  //   out33: pull=down
  //   in_16: pull=down
  //   out21: pull=down
  //   out23: pull=down
  //   in_5: pull=down
  //   in_9: pull=down
  //   in_11: pull=down
  //   in_3: pull=down
  //   in_6: pull=down
  //   out12: pull=down
  //   in_13: pull=down
  //   in_4: pull=down
  //   in_12: pull=down
  //   in_8: pull=down
  //   in_7: pull=down
  //   in_15: pull=down
  //   out22: pull=down
  //   in_14: pull=down
endmodule

module matrix_mult_sub (
  input  [31:0] in_a1,
  input  [31:0] in_b1,
  input  [31:0] in_a2,
  input  [31:0] in_b2,
  input  [31:0] in_a3,
  input  [31:0] in_b3,
  output [31:0] out_ab
);

  wire [31:0] adder_1_out, fp_mult_1_out, fp_mult_2_out, fp_mult_3_out;

  fp_mult fp_mult_1 (.in1(in_a1), .in2(in_b1), .out(fp_mult_1_out));
  fp_mult fp_mult_2 (.in1(in_a2), .in2(in_b2), .out(fp_mult_2_out));
  fp_mult fp_mult_3 (.in1(in_a3), .in2(in_b3), .out(fp_mult_3_out));
  Adder #(.width(32)) adder_1 (.a(fp_mult_1_out), .b(fp_mult_2_out), .out(adder_1_out));  // open: cin, cout
  Adder #(.width(32)) adder_2 (.a(adder_1_out), .b(fp_mult_3_out), .out(out_ab));  // open: cin, cout

  // Notes on the sheet:
  //   in_b1: pull=down
  //   out_ab: pull=down
  //   in_b3: pull=down
  //   in_a2: pull=down
  //   in_a3: pull=down
  //   in_a1: pull=down
  //   in_b2: pull=down
endmodule

module matrix_reg_4x4 (
  input  in_1,
  input  rst,
  input  [31:0] in_41,
  input  [31:0] in_11,
  input  [31:0] in_21,
  input  [31:0] in_31,
  input  [31:0] in_12,
  input  [31:0] in_22,
  input  [31:0] in_32,
  input  [31:0] in_42,
  input  [31:0] in_13,
  input  [31:0] in_23,
  input  [31:0] in_33,
  input  [31:0] in_43,
  input  [31:0] in_14,
  input  [31:0] in_24,
  input  [31:0] in_34,
  input  [31:0] in_44,
  input  _1__store_by_address_0__store_all,
  input  [3:0] val___XXYY_address,
  input  ignone,
  output [31:0] out_41,
  output [31:0] out_11,
  output [31:0] out_21,
  output [31:0] out_31,
  output [31:0] out_12,
  output [31:0] out_22,
  output [31:0] out_32,
  output [31:0] out_42,
  output [31:0] out_13,
  output [31:0] out_23,
  output [31:0] out_33,
  output [31:0] out_43,
  output [31:0] out_14,
  output [31:0] out_24,
  output [31:0] out_34,
  output [31:0] out_44
);

  wire and_1_out, and_2_out, and_3_out, and_4_out, and_5_out, and_6_out, and_7_out, and_8_out, and_9_out,
       and_10_out, and_11_out, and_12_out, and_13_out, and_14_out, and_15_out, and_16_out,
       demultiplexer_1_out0, demultiplexer_1_out1, demultiplexer_1_out2, demultiplexer_1_out3,
       demultiplexer_2_out0, demultiplexer_2_out1, demultiplexer_2_out2, demultiplexer_2_out3, not_1_out,
       sel_11, sel_12, sel_13, sel_14, sel_21, sel_22, sel_23, sel_24, sel_31, sel_32, sel_33, sel_34,
       sel_41, sel_42, sel_43, sel_44;

  Register #(.width(32)) register_1 (.D(in_11), .en(sel_11), .Q(out_11), .clk(in_1), .clr(rst));
  Register #(.width(32)) register_2 (.D(in_12), .en(sel_12), .Q(out_12), .clk(in_1), .clr(rst));
  Register #(.width(32)) register_3 (.D(in_13), .en(sel_13), .Q(out_13), .clk(in_1), .clr(rst));
  Register #(.width(32)) register_4 (.D(in_14), .en(sel_14), .Q(out_14), .clk(in_1), .clr(rst));
  Pull_Resistor pull_resistor_1 (.node(rst));
  Register #(.width(32)) register_5 (.D(in_21), .en(sel_21), .Q(out_21), .clk(in_1), .clr(rst));
  Register #(.width(32)) register_6 (.D(in_22), .en(sel_22), .Q(out_22), .clk(in_1), .clr(rst));
  Register #(.width(32)) register_7 (.D(in_23), .en(sel_23), .Q(out_23), .clk(in_1), .clr(rst));
  Register #(.width(32)) register_8 (.D(in_24), .en(sel_24), .Q(out_24), .clk(in_1), .clr(rst));
  Register #(.width(32)) register_9 (.D(in_31), .en(sel_31), .Q(out_31), .clk(in_1), .clr(rst));
  Register #(.width(32)) register_10 (.D(in_32), .en(sel_32), .Q(out_32), .clk(in_1), .clr(rst));
  Register #(.width(32)) register_11 (.D(in_33), .en(sel_33), .Q(out_33), .clk(in_1), .clr(rst));
  Register #(.width(32)) register_12 (.D(in_34), .en(sel_34), .Q(out_34), .clk(in_1), .clr(rst));
  Pull_Resistor pull_resistor_2 (.node(_1__store_by_address_0__store_all));
  Pull_Resistor pull_resistor_3 (.node(val___XXYY_address));
  Demultiplexer #(.select(2)) demultiplexer_1 (
    .out0(demultiplexer_1_out0), .out1(demultiplexer_1_out1), .out2(demultiplexer_1_out2),
    .out3(demultiplexer_1_out3), .sel(val___XXYY_address[1:0]), .en(ignone));  // open: in
  not not_1 (not_1_out, _1__store_by_address_0__store_all);
  Demultiplexer #(.select(2)) demultiplexer_2 (
    .out0(demultiplexer_2_out0), .out1(demultiplexer_2_out1), .out2(demultiplexer_2_out2),
    .out3(demultiplexer_2_out3), .in(1'b1), .sel(val___XXYY_address[3:2]), .en(ignone));
  Register #(.width(32)) register_13 (.D(in_41), .en(sel_41), .Q(out_41), .clk(in_1), .clr(rst));
  Register #(.width(32)) register_14 (.D(in_42), .en(sel_42), .Q(out_42), .clk(in_1), .clr(rst));
  Register #(.width(32)) register_15 (.D(in_43), .en(sel_43), .Q(out_43), .clk(in_1), .clr(rst));
  Register #(.width(32)) register_16 (.D(in_44), .en(sel_44), .Q(out_44), .clk(in_1), .clr(rst));
  and and_1 (and_1_out, _1__store_by_address_0__store_all, demultiplexer_2_out0, demultiplexer_1_out0);
  and and_2 (and_2_out, _1__store_by_address_0__store_all, demultiplexer_2_out0, demultiplexer_1_out1);
  and and_3 (and_3_out, _1__store_by_address_0__store_all, demultiplexer_2_out0, demultiplexer_1_out2);
  and and_4 (and_4_out, _1__store_by_address_0__store_all, demultiplexer_2_out0, demultiplexer_1_out3);
  and and_5 (and_5_out, _1__store_by_address_0__store_all, demultiplexer_2_out1, demultiplexer_1_out0);
  and and_6 (and_6_out, _1__store_by_address_0__store_all, demultiplexer_2_out1, demultiplexer_1_out1);
  and and_7 (and_7_out, _1__store_by_address_0__store_all, demultiplexer_2_out1, demultiplexer_1_out2);
  and and_8 (and_8_out, _1__store_by_address_0__store_all, demultiplexer_2_out1, demultiplexer_1_out3);
  and and_9 (and_9_out, _1__store_by_address_0__store_all, demultiplexer_2_out2, demultiplexer_1_out0);
  and and_10 (and_10_out, _1__store_by_address_0__store_all, demultiplexer_2_out2, demultiplexer_1_out1);
  and and_11 (and_11_out, _1__store_by_address_0__store_all, demultiplexer_2_out2, demultiplexer_1_out2);
  and and_12 (and_12_out, _1__store_by_address_0__store_all, demultiplexer_2_out2, demultiplexer_1_out3);
  and and_13 (and_13_out, _1__store_by_address_0__store_all, demultiplexer_2_out3, demultiplexer_1_out0);
  and and_14 (and_14_out, _1__store_by_address_0__store_all, demultiplexer_2_out3, demultiplexer_1_out1);
  and and_15 (and_15_out, _1__store_by_address_0__store_all, demultiplexer_2_out3, demultiplexer_1_out2);
  and and_16 (and_16_out, _1__store_by_address_0__store_all, demultiplexer_2_out3, demultiplexer_1_out3);
  or or_1 (sel_11, and_1_out, not_1_out);
  or or_2 (sel_12, and_2_out, not_1_out);
  or or_3 (sel_13, and_3_out, not_1_out);
  or or_4 (sel_14, and_4_out, not_1_out);
  or or_5 (sel_21, and_5_out, not_1_out);
  or or_6 (sel_22, and_6_out, not_1_out);
  or or_7 (sel_23, and_7_out, not_1_out);
  or or_8 (sel_24, and_8_out, not_1_out);
  or or_9 (sel_31, and_9_out, not_1_out);
  or or_10 (sel_32, and_10_out, not_1_out);
  or or_11 (sel_33, and_11_out, not_1_out);
  or or_12 (sel_34, and_12_out, not_1_out);
  or or_13 (sel_41, and_13_out, not_1_out);
  or or_14 (sel_42, and_14_out, not_1_out);
  or or_15 (sel_43, and_15_out, not_1_out);
  or or_16 (sel_44, and_16_out, not_1_out);

  // Other names for the same wires on the sheet: clk = in_1
endmodule

module matrix_reg_rev_4x4 (
  input  in_1,
  input  rst,
  input  [31:0] in_41,
  input  [31:0] in_11,
  input  [31:0] in_21,
  input  [31:0] in_31,
  input  [31:0] in_12,
  input  [31:0] in_22,
  input  [31:0] in_32,
  input  [31:0] in_42,
  input  [31:0] in_13,
  input  [31:0] in_23,
  input  [31:0] in_33,
  input  [31:0] in_43,
  input  [31:0] in_14,
  input  [31:0] in_24,
  input  [31:0] in_34,
  input  [31:0] in_44,
  input  _1__store_by_address_0__store_all,
  input  [3:0] val___XXYY_address,
  input  ignone,
  output [31:0] out_41,
  output [31:0] out_11,
  output [31:0] out_21,
  output [31:0] out_31,
  output [31:0] out_12,
  output [31:0] out_22,
  output [31:0] out_32,
  output [31:0] out_42,
  output [31:0] out_13,
  output [31:0] out_23,
  output [31:0] out_33,
  output [31:0] out_43,
  output [31:0] out_14,
  output [31:0] out_24,
  output [31:0] out_34,
  output [31:0] out_44
);

  wire and_1_out, and_2_out, and_3_out, and_4_out, and_5_out, and_6_out, and_7_out, and_8_out, and_9_out,
       and_10_out, and_11_out, and_12_out, and_13_out, and_14_out, and_15_out, and_16_out,
       demultiplexer_1_out0, demultiplexer_1_out1, demultiplexer_1_out2, demultiplexer_1_out3,
       demultiplexer_2_out0, demultiplexer_2_out1, demultiplexer_2_out2, demultiplexer_2_out3, not_1_out,
       sel_11, sel_12, sel_13, sel_14, sel_21, sel_22, sel_23, sel_24, sel_31, sel_32, sel_33, sel_34,
       sel_41, sel_42, sel_43, sel_44;

  Register #(.width(32)) register_1 (.D(in_11), .en(sel_11), .Q(out_11), .clk(in_1), .clr(rst));
  Register #(.width(32)) register_2 (.D(in_12), .en(sel_12), .Q(out_12), .clk(in_1), .clr(rst));
  Register #(.width(32)) register_3 (.D(in_13), .en(sel_13), .Q(out_13), .clk(in_1), .clr(rst));
  Register #(.width(32)) register_4 (.D(in_14), .en(sel_14), .Q(out_14), .clk(in_1), .clr(rst));
  Pull_Resistor pull_resistor_1 (.node(rst));
  Register #(.width(32)) register_5 (.D(in_21), .en(sel_21), .Q(out_21), .clk(in_1), .clr(rst));
  Register #(.width(32)) register_6 (.D(in_22), .en(sel_22), .Q(out_22), .clk(in_1), .clr(rst));
  Register #(.width(32)) register_7 (.D(in_23), .en(sel_23), .Q(out_23), .clk(in_1), .clr(rst));
  Register #(.width(32)) register_8 (.D(in_24), .en(sel_24), .Q(out_24), .clk(in_1), .clr(rst));
  Register #(.width(32)) register_9 (.D(in_31), .en(sel_31), .Q(out_31), .clk(in_1), .clr(rst));
  Register #(.width(32)) register_10 (.D(in_32), .en(sel_32), .Q(out_32), .clk(in_1), .clr(rst));
  Register #(.width(32)) register_11 (.D(in_33), .en(sel_33), .Q(out_33), .clk(in_1), .clr(rst));
  Register #(.width(32)) register_12 (.D(in_34), .en(sel_34), .Q(out_34), .clk(in_1), .clr(rst));
  Pull_Resistor pull_resistor_2 (.node(_1__store_by_address_0__store_all));
  Pull_Resistor pull_resistor_3 (.node(val___XXYY_address));
  Demultiplexer #(.select(2)) demultiplexer_1 (
    .out0(demultiplexer_1_out0), .out1(demultiplexer_1_out1), .out2(demultiplexer_1_out2),
    .out3(demultiplexer_1_out3), .sel(val___XXYY_address[1:0]), .en(ignone));  // open: in
  not not_1 (not_1_out, _1__store_by_address_0__store_all);
  Demultiplexer #(.select(2)) demultiplexer_2 (
    .out0(demultiplexer_2_out0), .out1(demultiplexer_2_out1), .out2(demultiplexer_2_out2),
    .out3(demultiplexer_2_out3), .in(1'b1), .sel(val___XXYY_address[3:2]), .en(ignone));
  Register #(.width(32)) register_13 (.D(in_41), .en(sel_41), .Q(out_41), .clk(in_1), .clr(rst));
  Register #(.width(32)) register_14 (.D(in_42), .en(sel_42), .Q(out_42), .clk(in_1), .clr(rst));
  Register #(.width(32)) register_15 (.D(in_43), .en(sel_43), .Q(out_43), .clk(in_1), .clr(rst));
  Register #(.width(32)) register_16 (.D(in_44), .en(sel_44), .Q(out_44), .clk(in_1), .clr(rst));
  and and_1 (and_1_out, _1__store_by_address_0__store_all, demultiplexer_2_out0, demultiplexer_1_out0);
  and and_2 (and_2_out, _1__store_by_address_0__store_all, demultiplexer_2_out0, demultiplexer_1_out1);
  and and_3 (and_3_out, _1__store_by_address_0__store_all, demultiplexer_2_out0, demultiplexer_1_out2);
  and and_4 (and_4_out, _1__store_by_address_0__store_all, demultiplexer_2_out0, demultiplexer_1_out3);
  and and_5 (and_5_out, _1__store_by_address_0__store_all, demultiplexer_2_out1, demultiplexer_1_out0);
  and and_6 (and_6_out, _1__store_by_address_0__store_all, demultiplexer_2_out1, demultiplexer_1_out1);
  and and_7 (and_7_out, _1__store_by_address_0__store_all, demultiplexer_2_out1, demultiplexer_1_out2);
  and and_8 (and_8_out, _1__store_by_address_0__store_all, demultiplexer_2_out1, demultiplexer_1_out3);
  and and_9 (and_9_out, _1__store_by_address_0__store_all, demultiplexer_2_out2, demultiplexer_1_out0);
  and and_10 (and_10_out, _1__store_by_address_0__store_all, demultiplexer_2_out2, demultiplexer_1_out1);
  and and_11 (and_11_out, _1__store_by_address_0__store_all, demultiplexer_2_out2, demultiplexer_1_out2);
  and and_12 (and_12_out, _1__store_by_address_0__store_all, demultiplexer_2_out2, demultiplexer_1_out3);
  and and_13 (and_13_out, _1__store_by_address_0__store_all, demultiplexer_2_out3, demultiplexer_1_out0);
  and and_14 (and_14_out, _1__store_by_address_0__store_all, demultiplexer_2_out3, demultiplexer_1_out1);
  and and_15 (and_15_out, _1__store_by_address_0__store_all, demultiplexer_2_out3, demultiplexer_1_out2);
  and and_16 (and_16_out, _1__store_by_address_0__store_all, demultiplexer_2_out3, demultiplexer_1_out3);
  or or_1 (sel_11, and_1_out, not_1_out);
  or or_2 (sel_12, and_2_out, not_1_out);
  or or_3 (sel_13, and_3_out, not_1_out);
  or or_4 (sel_14, and_4_out, not_1_out);
  or or_5 (sel_21, and_5_out, not_1_out);
  or or_6 (sel_22, and_6_out, not_1_out);
  or or_7 (sel_23, and_7_out, not_1_out);
  or or_8 (sel_24, and_8_out, not_1_out);
  or or_9 (sel_31, and_9_out, not_1_out);
  or or_10 (sel_32, and_10_out, not_1_out);
  or or_11 (sel_33, and_11_out, not_1_out);
  or or_12 (sel_34, and_12_out, not_1_out);
  or or_13 (sel_41, and_13_out, not_1_out);
  or or_14 (sel_42, and_14_out, not_1_out);
  or or_15 (sel_43, and_15_out, not_1_out);
  or or_16 (sel_44, and_16_out, not_1_out);

  // Other names for the same wires on the sheet: clk = in_1
endmodule

module matrix_add (
  input  [31:0] in_1,
  input  [31:0] in_2,
  input  [31:0] in_3,
  input  [31:0] in_4,
  input  [31:0] in_5,
  input  [31:0] in_6,
  input  [31:0] in_7,
  input  [31:0] in_8,
  input  [31:0] in_9,
  input  [31:0] in_10,
  input  [31:0] in_11,
  input  [31:0] in_12,
  input  [31:0] in_13,
  input  [31:0] in_14,
  input  [31:0] in_15,
  input  [31:0] in_16,
  input  [31:0] in_17,
  input  [31:0] in_18,
  output [31:0] out11,
  output [31:0] out21,
  output [31:0] out31,
  output [31:0] out12,
  output [31:0] out22,
  output [31:0] out32,
  output [31:0] out13,
  output [31:0] out23,
  output [31:0] out33
);

  Adder #(.width(32)) adder_1 (.a(in_10), .b(in_1), .out(out11));  // open: cin, cout
  Adder #(.width(32)) adder_2 (.a(in_13), .b(in_4), .out(out12));  // open: cin, cout
  Adder #(.width(32)) adder_3 (.a(in_16), .b(in_7), .out(out13));  // open: cin, cout
  Adder #(.width(32)) adder_4 (.a(in_11), .b(in_2), .out(out21));  // open: cin, cout
  Adder #(.width(32)) adder_5 (.a(in_14), .b(in_5), .out(out22));  // open: cin, cout
  Adder #(.width(32)) adder_6 (.a(in_17), .b(in_8), .out(out23));  // open: cin, cout
  Adder #(.width(32)) adder_7 (.a(in_12), .b(in_3), .out(out31));  // open: cin, cout
  Adder #(.width(32)) adder_8 (.a(in_15), .b(in_6), .out(out32));  // open: cin, cout
  Adder #(.width(32)) adder_9 (.a(in_18), .b(in_9), .out(out33));  // open: cin, cout

  // Other names for the same wires on the sheet: A11[31:0] = in_10; A12[31:0] = in_13; A13[31:0] = in_16;
  //   A21[31:0] = in_11; A22[31:0] = in_14; A23[31:0] = in_17; A31[31:0] = in_12; A32[31:0] = in_15;
  //   A33[31:0] = in_18; B11[31:0] = in_1; B12[31:0] = in_4; B13[31:0] = in_7; B21[31:0] = in_2; B22[31:0] = in_5;
  //   B23[31:0] = in_8; B31[31:0] = in_3; B32[31:0] = in_6; B33[31:0] = in_9

  // Notes on the sheet:
  //   in_17: pull=down
  //   in_14: pull=down
  //   out33: pull=down
  //   out11: pull=down
  //   out12: pull=down
  //   in_9: pull=down
  //   in_12: pull=down
  //   in_18: pull=down
  //   out31: pull=down
  //   in_10: pull=down
  //   in_15: pull=down
  //   in_4: pull=down
  //   in_6: pull=down
  //   out23: pull=down
  //   in_5: pull=down
  //   in_2: pull=down
  //   out13: pull=down
  //   in_16: pull=down
  //   out22: pull=down
  //   in_8: pull=down
  //   in_3: pull=down
  //   in_1: pull=down
  //   in_7: pull=down
  //   out21: pull=down
  //   in_11: pull=down
  //   in_13: pull=down
  //   out32: pull=down
endmodule

module matrix_sub (
  input  [31:0] in_1,
  input  [31:0] in_2,
  input  [31:0] in_3,
  input  [31:0] in_4,
  input  [31:0] in_5,
  input  [31:0] in_6,
  input  [31:0] in_7,
  input  [31:0] in_8,
  input  [31:0] in_9,
  input  [31:0] in_10,
  input  [31:0] in_11,
  input  [31:0] in_12,
  input  [31:0] in_13,
  input  [31:0] in_14,
  input  [31:0] in_15,
  input  [31:0] in_16,
  input  [31:0] in_17,
  input  [31:0] in_18,
  output [31:0] out11,
  output [31:0] out21,
  output [31:0] out31,
  output [31:0] out12,
  output [31:0] out22,
  output [31:0] out32,
  output [31:0] out13,
  output [31:0] out23,
  output [31:0] out33
);

  Subtractor #(.width(32)) subtractor_1 (.a(in_10), .b(in_1), .out(out11));  // open: bin, bout
  Subtractor #(.width(32)) subtractor_2 (.a(in_13), .b(in_4), .out(out12));  // open: bin, bout
  Subtractor #(.width(32)) subtractor_3 (.a(in_16), .b(in_7), .out(out13));  // open: bin, bout
  Subtractor #(.width(32)) subtractor_4 (.a(in_11), .b(in_2), .out(out21));  // open: bin, bout
  Subtractor #(.width(32)) subtractor_5 (.a(in_14), .b(in_5), .out(out22));  // open: bin, bout
  Subtractor #(.width(32)) subtractor_6 (.a(in_17), .b(in_8), .out(out23));  // open: bin, bout
  Subtractor #(.width(32)) subtractor_7 (.a(in_12), .b(in_3), .out(out31));  // open: bin, bout
  Subtractor #(.width(32)) subtractor_8 (.a(in_15), .b(in_6), .out(out32));  // open: bin, bout
  Subtractor #(.width(32)) subtractor_9 (.a(in_18), .b(in_9), .out(out33));  // open: bin, bout

  // Other names for the same wires on the sheet: A11[31:0] = in_10; A12[31:0] = in_13; A13[31:0] = in_16;
  //   A21[31:0] = in_11; A22[31:0] = in_14; A23[31:0] = in_17; A31[31:0] = in_12; A32[31:0] = in_15;
  //   A33[31:0] = in_18; B11[31:0] = in_1; B12[31:0] = in_4; B13[31:0] = in_7; B21[31:0] = in_2; B22[31:0] = in_5;
  //   B23[31:0] = in_8; B31[31:0] = in_3; B32[31:0] = in_6; B33[31:0] = in_9

  // Notes on the sheet:
  //   in_18: pull=down
  //   out32: pull=down
  //   in_13: pull=down
  //   out23: pull=down
  //   out31: pull=down
  //   in_2: pull=down
  //   out21: pull=down
  //   in_1: pull=down
  //   in_17: pull=down
  //   in_6: pull=down
  //   in_15: pull=down
  //   in_14: pull=down
  //   in_9: pull=down
  //   in_8: pull=down
  //   out22: pull=down
  //   out12: pull=down
  //   in_4: pull=down
  //   in_11: pull=down
  //   in_3: pull=down
  //   out13: pull=down
  //   in_12: pull=down
  //   in_10: pull=down
  //   out33: pull=down
  //   out11: pull=down
  //   in_5: pull=down
  //   in_7: pull=down
  //   in_16: pull=down
endmodule

module matrix_mult_4x4 (
  input  [31:0] in_1,
  input  [31:0] in_2,
  input  [31:0] in_3,
  input  [31:0] in_4,
  input  [31:0] in_5,
  input  [31:0] in_6,
  input  [31:0] in_7,
  input  [31:0] in_8,
  input  [31:0] in_9,
  input  [31:0] in_10,
  input  [31:0] in_11,
  input  [31:0] in_12,
  input  [31:0] in_13,
  input  [31:0] in_14,
  input  [31:0] in_15,
  input  [31:0] in_16,
  input  [31:0] in_17,
  input  [31:0] in_18,
  input  [31:0] in_19,
  input  [31:0] in_20,
  input  [31:0] in_21,
  input  [31:0] in_22,
  input  [31:0] in_23,
  input  [31:0] in_24,
  input  [31:0] in_25,
  input  [31:0] in_26,
  input  [31:0] in_27,
  input  [31:0] in_28,
  input  [31:0] in_29,
  input  [31:0] in_30,
  input  [31:0] in_31,
  input  [31:0] in_32,
  output [31:0] out11,
  output [31:0] out21,
  output [31:0] out31,
  output [31:0] out41,
  output [31:0] out12,
  output [31:0] out22,
  output [31:0] out32,
  output [31:0] out42,
  output [31:0] out13,
  output [31:0] out23,
  output [31:0] out33,
  output [31:0] out43,
  output [31:0] out14,
  output [31:0] out24,
  output [31:0] out34,
  output [31:0] out44
);

  matrix_mult_sub_4 matrix_mult_sub_4_1 (
    .in_a1(in_17), .in_b1(in_1), .in_a2(in_18), .in_b2(in_5), .in_a3(in_19), .in_b3(in_9), .in_a4(in_20),
    .in_b4(in_13), .out_ab(out11));
  matrix_mult_sub_4 matrix_mult_sub_4_2 (
    .in_a1(in_21), .in_b1(in_1), .in_a2(in_22), .in_b2(in_5), .in_a3(in_23), .in_b3(in_9), .in_a4(in_24),
    .in_b4(in_13), .out_ab(out12));
  matrix_mult_sub_4 matrix_mult_sub_4_3 (
    .in_a1(in_25), .in_b1(in_1), .in_a2(in_26), .in_b2(in_5), .in_a3(in_27), .in_b3(in_9), .in_a4(in_28),
    .in_b4(in_13), .out_ab(out13));
  matrix_mult_sub_4 matrix_mult_sub_4_4 (
    .in_a1(in_29), .in_b1(in_1), .in_a2(in_30), .in_b2(in_5), .in_a3(in_31), .in_b3(in_9), .in_a4(in_32),
    .in_b4(in_13), .out_ab(out14));
  matrix_mult_sub_4 matrix_mult_sub_4_5 (
    .in_a1(in_17), .in_b1(in_2), .in_a2(in_18), .in_b2(in_6), .in_a3(in_19), .in_b3(in_10), .in_a4(in_20),
    .in_b4(in_14), .out_ab(out21));
  matrix_mult_sub_4 matrix_mult_sub_4_6 (
    .in_a1(in_21), .in_b1(in_2), .in_a2(in_22), .in_b2(in_6), .in_a3(in_23), .in_b3(in_10), .in_a4(in_24),
    .in_b4(in_14), .out_ab(out22));
  matrix_mult_sub_4 matrix_mult_sub_4_7 (
    .in_a1(in_25), .in_b1(in_2), .in_a2(in_26), .in_b2(in_6), .in_a3(in_27), .in_b3(in_10), .in_a4(in_28),
    .in_b4(in_14), .out_ab(out23));
  matrix_mult_sub_4 matrix_mult_sub_4_8 (
    .in_a1(in_29), .in_b1(in_2), .in_a2(in_30), .in_b2(in_6), .in_a3(in_31), .in_b3(in_10), .in_a4(in_32),
    .in_b4(in_14), .out_ab(out24));
  matrix_mult_sub_4 matrix_mult_sub_4_9 (
    .in_a1(in_17), .in_b1(in_3), .in_a2(in_18), .in_b2(in_7), .in_a3(in_19), .in_b3(in_11), .in_a4(in_20),
    .in_b4(in_15), .out_ab(out31));
  matrix_mult_sub_4 matrix_mult_sub_4_10 (
    .in_a1(in_21), .in_b1(in_3), .in_a2(in_22), .in_b2(in_7), .in_a3(in_23), .in_b3(in_11), .in_a4(in_24),
    .in_b4(in_15), .out_ab(out32));
  matrix_mult_sub_4 matrix_mult_sub_4_11 (
    .in_a1(in_25), .in_b1(in_3), .in_a2(in_26), .in_b2(in_7), .in_a3(in_27), .in_b3(in_11), .in_a4(in_28),
    .in_b4(in_15), .out_ab(out33));
  matrix_mult_sub_4 matrix_mult_sub_4_12 (
    .in_a1(in_29), .in_b1(in_3), .in_a2(in_30), .in_b2(in_7), .in_a3(in_31), .in_b3(in_11), .in_a4(in_32),
    .in_b4(in_15), .out_ab(out34));
  matrix_mult_sub_4 matrix_mult_sub_4_13 (
    .in_a1(in_17), .in_b1(in_4), .in_a2(in_18), .in_b2(in_8), .in_a3(in_19), .in_b3(in_12), .in_a4(in_20),
    .in_b4(in_16), .out_ab(out41));
  matrix_mult_sub_4 matrix_mult_sub_4_14 (
    .in_a1(in_21), .in_b1(in_4), .in_a2(in_22), .in_b2(in_8), .in_a3(in_23), .in_b3(in_12), .in_a4(in_24),
    .in_b4(in_16), .out_ab(out42));
  matrix_mult_sub_4 matrix_mult_sub_4_15 (
    .in_a1(in_25), .in_b1(in_4), .in_a2(in_26), .in_b2(in_8), .in_a3(in_27), .in_b3(in_12), .in_a4(in_28),
    .in_b4(in_16), .out_ab(out43));
  matrix_mult_sub_4 matrix_mult_sub_4_16 (
    .in_a1(in_29), .in_b1(in_4), .in_a2(in_30), .in_b2(in_8), .in_a3(in_31), .in_b3(in_12), .in_a4(in_32),
    .in_b4(in_16), .out_ab(out44));

  // Other names for the same wires on the sheet: A11[31:0] = in_17; A12[31:0] = in_21; A13[31:0] = in_25;
  //   A14[31:0] = in_29; A21[31:0] = in_18; A22[31:0] = in_22; A23[31:0] = in_26; A24[31:0] = in_30;
  //   A31[31:0] = in_19; A32[31:0] = in_23; A33[31:0] = in_27; A34[31:0] = in_31; A41[31:0] = in_20;
  //   A42[31:0] = in_24; A43[31:0] = in_28; A44[31:0] = in_32; B11[31:0] = in_1; B12[31:0] = in_5; B13[31:0] = in_9;
  //   B14[31:0] = in_13; B21[31:0] = in_2; B22[31:0] = in_6; B23[31:0] = in_10; B24[31:0] = in_14; B31[31:0] = in_3;
  //   B32[31:0] = in_7; B33[31:0] = in_11; B34[31:0] = in_15; B41[31:0] = in_4; B42[31:0] = in_8; B43[31:0] = in_12;
  //   B44[31:0] = in_16

  // Notes on the sheet:
  //   in_26: pull=down
  //   in_11: pull=down
  //   out44: pull=down
  //   out34: pull=down
  //   in_4: pull=down
  //   in_30: pull=down
  //   in_24: pull=down
  //   in_19: pull=down
  //   in_8: pull=down
  //   in_32: pull=down
  //   out23: pull=down
  //   in_1: pull=down
  //   in_25: pull=down
  //   in_5: pull=down
  //   in_9: pull=down
  //   in_12: pull=down
  //   in_27: pull=down
  //   in_22: pull=down
  //   in_21: pull=down
  //   out12: pull=down
  //   out24: pull=down
  //   in_10: pull=down
  //   out43: pull=down
  //   in_31: pull=down
  //   in_18: pull=down
  //   out13: pull=down
  //   in_15: pull=down
  //   in_14: pull=down
  //   out14: pull=down
  //   in_6: pull=down
  //   in_3: pull=down
  //   out22: pull=down
  //   in_20: pull=down
  //   out42: pull=down
  //   out11: pull=down
  //   out32: pull=down
  //   in_7: pull=down
  //   out31: pull=down
  //   in_29: pull=down
  //   in_2: pull=down
  //   in_23: pull=down
  //   in_28: pull=down
  //   in_16: pull=down
  //   out21: pull=down
  //   out33: pull=down
  //   out41: pull=down
  //   in_17: pull=down
  //   in_13: pull=down
endmodule

module matrix_mult_sub_4 (
  input  [31:0] in_a1,
  input  [31:0] in_b1,
  input  [31:0] in_a2,
  input  [31:0] in_b2,
  input  [31:0] in_a3,
  input  [31:0] in_b3,
  input  [31:0] in_a4,
  input  [31:0] in_b4,
  output [31:0] out_ab
);

  wire [31:0] adder_1_out, adder_3_out, fp_mult_1_out, fp_mult_2_out, fp_mult_3_out, fp_mult_4_out;

  fp_mult fp_mult_1 (.in1(in_a1), .in2(in_b1), .out(fp_mult_1_out));
  fp_mult fp_mult_2 (.in1(in_a2), .in2(in_b2), .out(fp_mult_2_out));
  fp_mult fp_mult_3 (.in1(in_a3), .in2(in_b3), .out(fp_mult_3_out));
  fp_mult fp_mult_4 (.in1(in_a4), .in2(in_b4), .out(fp_mult_4_out));
  Adder #(.width(32)) adder_1 (.a(fp_mult_1_out), .b(fp_mult_2_out), .out(adder_1_out));  // open: cin, cout
  Adder #(.width(32)) adder_2 (.a(adder_1_out), .b(adder_3_out), .out(out_ab));  // open: cin, cout
  Adder #(.width(32)) adder_3 (.a(fp_mult_3_out), .b(fp_mult_4_out), .out(adder_3_out));  // open: cin, cout

  // Notes on the sheet:
  //   in_b2: pull=down
  //   in_b4: pull=down
  //   out_ab: pull=down
  //   in_a3: pull=down
  //   in_b3: pull=down
  //   in_a4: pull=down
  //   in_a2: pull=down
  //   in_b1: pull=down
  //   in_a1: pull=down
endmodule

module vec4_to_vec3 (
  input  [31:0] in1,
  input  [31:0] in2,
  input  [31:0] in3,
  input  [31:0] in4,
  output [31:0] out1,
  output [31:0] out2,
  output [31:0] out3
);

  fp_div fp_div_1 (.in1(in1), .in2(in4), .out(out1));
  fp_div fp_div_2 (.in1(in2), .in2(in4), .out(out2));
  fp_div fp_div_3 (.in1(in3), .in2(in4), .out(out3));
endmodule
