// Logisim project algorythms.circ as structural Verilog
module DDA_async (
  input  sync,
  input  new_data,
  input  lock,
  input  [31:0] x2,
  input  [31:0] x1,
  input  [31:0] y2,
  input  [31:0] y1,
  output set_point,
  output [31:0] out_y,
  output [31:0] out_x,
  output done
);

  wire and_2_out, and_5_out, and_7_out, and_9_out, and_13_out, and_14_out, and_15_out, and_16_out,
       and_17_out, and_18_out, and_19_out, and_20_out, and_21_out, and_22_out, and_23_out, and_24_out,
       and_25_out, and_27_out, and_28_out, and_29_out, and_30_out, clear, clear_wait_counter, clk,
       comparator_2_gt, comparator_2_lt, comparator_4_lt, comparator_5_lt, done_t, inc_loop_counter,
       inc_stage_counter, inc_stored_values, inc_wait_counter, load, load_x1y1, load_x2y2, loop_counter,
       loop_stopper_counter, new_data_t, or_3_out, pull_resistor_3_node, pull_resistor_9_node, reset,
       rising_edge_detector_async_1_out, rising_edge_detector_async_2_out, s_r_ff_1_q, set, skip_loop, start,
       wait_counter;
  wire [1:0] comparator_1_gt, or_2_out, stage;
  wire [1:1] comparator_1_lt;
  wire [3:0] address, register_1_q, register_2_q, register_3_q, register_6_q, register_7_q, register_8_q,
       register_9_q, register_10_q, register_11_q, register_12_q, register_13_q, register_14_q,
       register_15_q, register_16_q, register_17_q, register_18_q, register_19_q, register_20_q,
       register_21_q, register_22_q, register_23_q, register_24_q, register_25_q, register_26_q,
       register_27_q, register_28_q, register_29_q, register_30_q, register_31_q, register_32_q;
  wire [7:0] counter_1_q, counter_3_q, counter_4_q;
  wire [31:0] adder_3_out, adder_4_out, adder_5_out, dx, dy, fp_abs_1_abs, fp_abs_2_abs, loop_count,
       multiplexer_1_out, out_x_t, out_y_t, steps_count, x, x_dx, x_step, y, y_dy, y_step;

  Register #(.width(4), .trigger("low")) register_1 (.D(address), .Q(register_1_q), .clk(1'b0));  // open: en, clr
  Register #(.width(4), .trigger("low")) register_2 (.D(address), .Q(register_2_q), .clk(1'b0));  // open: en, clr
  rising_edge_pulse rising_edge_pulse_1 (.signal(sync), .out(clk));
  Pull_Resistor pull_resistor_1 (.node(sync));
  rising_edge_detector_async rising_edge_detector_async_1 (
    .signal(new_data), .clear(clear), .out(rising_edge_detector_async_1_out));
  Pull_Resistor pull_resistor_2 (.node(lock));
  Pull_Resistor pull_resistor_3 (.node(pull_resistor_3_node));
  and and_1 (pull_resistor_3_node, ~register_1_q[0], ~register_1_q[1], ~register_1_q[2], ~register_1_q[3], start);  // AND_Gate
  assign address = pull_resistor_3_node ? 4'b0001 : 4'bz;  // Controlled_Buffer controlled_buffer_1
  assign address = and_2_out ? 4'b0000 : 4'bz;  // Controlled_Buffer controlled_buffer_2
  and and_2 (and_2_out, ~start, ~register_2_q[0], ~register_2_q[1], ~register_2_q[2], ~register_2_q[3]);  // AND_Gate
  Pull_Resistor pull_resistor_4 (.node(and_2_out));
  and and_3 (new_data_t, rising_edge_detector_async_1_out, ~lock);  // AND_Gate
  assign x = load_x2y2 ? x2 : 32'bz;  // Controlled_Buffer controlled_buffer_3
  assign x = inc_stored_values ? x_dx : 32'bz;  // Controlled_Buffer controlled_buffer_4
  assign y = load_x2y2 ? y2 : 32'bz;  // Controlled_Buffer controlled_buffer_5
  assign y = inc_stored_values ? y_dy : 32'bz;  // Controlled_Buffer controlled_buffer_6
  assign x = load_x1y1 ? x1 : 32'bz;  // Controlled_Buffer controlled_buffer_7
  or or_1 (load, load_x1y1, load_x2y2, inc_stored_values);
  assign y = load_x1y1 ? y1 : 32'bz;  // Controlled_Buffer controlled_buffer_8
  Register #(.width(4), .trigger("low")) register_3 (.D(address), .Q(register_3_q), .clk(1'b0));  // open: en, clr
  // fp_round_ones fp_round_ones_1: pin names not known; wires that end beside it: out_x_t, out_y
  // fp_round_ones fp_round_ones_2: pin names not known; wires that end beside it: out_y_t, out_x
  Subtractor #(.width(32)) subtractor_1 (.a(x2), .b(x1), .out(dx));  // open: bin, bout
  Subtractor #(.width(32)) subtractor_2 (.a(y2), .b(y1), .out(dy));  // open: bin, bout
  Adder #(.width(32)) adder_1 (.a(out_x_t), .b(x_step), .out(x_dx));  // open: cin, cout
  Adder #(.width(32)) adder_2 (.a(out_y_t), .b(y_step), .out(y_dy));  // open: cin, cout
  and and_4 (load_x1y1, register_3_q[0], ~register_3_q[1], ~register_3_q[2], ~register_3_q[3]);  // AND_Gate
  fp_abs fp_abs_1 (.in(dx), .abs(fp_abs_1_abs));
  fp_abs fp_abs_2 (.in(dy), .abs(fp_abs_2_abs));
  assign address = load_x1y1 ? 4'b0010 : 4'bz;  // Controlled_Buffer controlled_buffer_9
  Pull_Resistor pull_resistor_5 (.node(load_x1y1));
  Comparator #(.width(32)) comparator_1 (
    .a(fp_abs_1_abs), .b(fp_abs_2_abs), .gt(comparator_1_gt[0]), .eq(comparator_1_gt[1]),
    .lt(comparator_1_lt[1]));
  S_R_Flip_Flop s_r_ff_1 (.Q(s_r_ff_1_q), .Qn(done), .preset(and_5_out), .reset(done_t));  // open: S, clk, R, en
  Multiplexer #(.select(2), .width(32), .enable("false")) multiplexer_1 (
    .in1(fp_abs_1_abs), .in2(fp_abs_1_abs), .in3(fp_abs_2_abs), .out(multiplexer_1_out), .sel(or_2_out));  // open: in0
  assign or_2_out = comparator_1_gt | {2{comparator_1_lt[1]}};  // OR_Gate or_2, 2 bits wide
  fp_div fp_div_1 (.in1(dx), .in2(steps_count), .out(x_step));
  fp_div fp_div_2 (.in1(dy), .in2(steps_count), .out(y_step));
  Register #(.width(32)) register_4 (.D(x), .Q(out_x_t), .clk(load), .clr(clear));  // open: en
  Register #(.width(32)) register_5 (.D(y), .Q(out_y_t), .clk(load), .clr(clear));  // open: en
  Register #(.width(4), .trigger("low")) register_6 (.D(address), .Q(register_6_q), .clk(1'b0));  // open: en, clr
  S_R_Flip_Flop s_r_ff_2 (.Q(set_point), .preset(set), .reset(reset));  // open: S, clk, R, Qn, en
  and and_5 (and_5_out, new_data_t, ~s_r_ff_1_q);  // AND_Gate
  // fp_round_ones fp_round_ones_3: pin names not known; wires that end beside it: multiplexer_1_out, steps_count
  assign address = set ? 4'b0011 : 4'bz;  // Controlled_Buffer controlled_buffer_10
  and and_6 (set, ~register_6_q[0], register_6_q[1], ~register_6_q[2], ~register_6_q[3]);  // AND_Gate
  Pull_Resistor pull_resistor_6 (.node(set));
  Adder #(.width(32)) adder_3 (.a({{31{1'b0}}, new_data_t}), .b({32{1'b0}}), .out(adder_3_out));  // open: cin, cout
  Adder #(.width(32)) adder_4 (.a(adder_3_out), .b({32{1'b0}}), .out(adder_4_out));  // open: cin, cout
  Subtractor #(.width(32)) subtractor_3 (.a(steps_count), .b(32'h20000), .out(loop_count));  // open: bin, bout
  Comparator #(.width(32)) comparator_2 (
    .a(steps_count), .b(32'h10000), .gt(comparator_2_gt), .lt(comparator_2_lt));  // open: eq
  rising_edge_detector_async rising_edge_detector_async_2 (
    .signal(new_data_t), .clear(and_7_out), .out(rising_edge_detector_async_2_out));
  Adder #(.width(32)) adder_5 (.a(adder_4_out), .b({32{1'b0}}), .out(adder_5_out));  // open: cin, cout
  not not_1 (skip_loop, comparator_2_gt);
  and and_7 (and_7_out, comparator_2_lt, rising_edge_detector_async_2_out);
  rising_edge_detector rising_edge_detector_1 (.signal(adder_5_out[0]), .clear(clear), .sync(clk), .out(start));
  buf buffer_1 (inc_stage_counter, and_7_out);
  Register #(.width(4), .trigger("low")) register_7 (.D(address), .Q(register_7_q), .clk(1'b0));  // open: en, clr
  Register #(.width(4), .trigger("low")) register_8 (.D(address), .Q(register_8_q), .clk(1'b0));  // open: en, clr
  assign address = clear_wait_counter ? 4'b1101 : 4'bz;  // Controlled_Buffer controlled_buffer_11
  and and_8 (clear_wait_counter, register_7_q[0], register_7_q[1], ~register_7_q[2], ~register_7_q[3]);  // AND_Gate
  Pull_Resistor pull_resistor_7 (.node(clear_wait_counter));
  assign address = and_9_out ? 4'b0100 : 4'bz;  // Controlled_Buffer controlled_buffer_12
  and and_9 (and_9_out, register_8_q[0], ~register_8_q[1], register_8_q[2], register_8_q[3]);  // AND_Gate
  Pull_Resistor pull_resistor_8 (.node(and_9_out));
  Counter counter_1 (.Q(counter_1_q), .clk(inc_wait_counter), .clr(clear_wait_counter));  // open: load, D, count, carry
  Comparator comparator_3 (.a(counter_1_q), .b({8{1'b0}}), .eq(wait_counter));  // open: gt, lt
  Register #(.width(4), .trigger("low")) register_9 (.D(address), .Q(register_9_q), .clk(1'b0));  // open: en, clr
  Register #(.width(4), .trigger("low")) register_10 (.D(address), .Q(register_10_q), .clk(1'b0));  // open: en, clr
  Pull_Resistor pull_resistor_9 (.node(pull_resistor_9_node));
  and and_10 (pull_resistor_9_node, ~register_9_q[0], ~register_9_q[1], register_9_q[2], ~register_9_q[3], wait_counter);  // AND_Gate
  assign address = pull_resistor_9_node ? 4'b0110 : 4'bz;  // Controlled_Buffer controlled_buffer_13
  assign address = inc_wait_counter ? 4'b1101 : 4'bz;  // Controlled_Buffer controlled_buffer_14
  and and_11 (inc_wait_counter, ~wait_counter, ~register_10_q[0], ~register_10_q[1], register_10_q[2], ~register_10_q[3]);  // AND_Gate
  Pull_Resistor pull_resistor_10 (.node(inc_wait_counter));
  Counter #(.width(2), .max('h3)) counter_2 (
    .Q(stage), .clk(inc_stage_counter), .clr(done_t));  // open: load, D, count, carry
  Pull_Resistor pull_resistor_11 (.node(inc_stage_counter));
  Register #(.width(4), .trigger("low")) register_11 (.D(address), .Q(register_11_q), .clk(1'b0));  // open: en, clr
  Register #(.width(4), .trigger("low")) register_12 (.D(address), .Q(register_12_q), .clk(1'b0));  // open: en, clr
  Register #(.width(4), .trigger("low")) register_13 (.D(address), .Q(register_13_q), .clk(1'b0));  // open: en, clr
  Register #(.width(4), .trigger("low")) register_14 (.D(address), .Q(register_14_q), .clk(1'b0));  // open: en, clr
  Register #(.width(4), .trigger("low")) register_15 (.D(address), .Q(register_15_q), .clk(1'b0));  // open: en, clr
  Register #(.width(4), .trigger("low")) register_16 (.D(address), .Q(register_16_q), .clk(1'b0));  // open: en, clr
  Register #(.width(4), .trigger("low")) register_17 (.D(address), .Q(register_17_q), .clk(1'b0));  // open: en, clr
  Register #(.width(4), .trigger("low")) register_18 (.D(address), .Q(register_18_q), .clk(1'b0));  // open: en, clr
  and and_12 (reset, ~register_18_q[0], register_18_q[1], register_18_q[2], ~register_18_q[3]);  // AND_Gate
  assign address = and_13_out ? 4'b1111 : 4'bz;  // Controlled_Buffer controlled_buffer_15
  and and_13 (and_13_out, skip_loop, ~stage[0], stage[1], ~register_11_q[0], register_11_q[1], register_11_q[2], ~register_11_q[3]);  // AND_Gate
  Pull_Resistor pull_resistor_12 (.node(and_13_out));
  assign address = and_14_out ? 4'b0111 : 4'bz;  // Controlled_Buffer controlled_buffer_16
  and and_14 (and_14_out, skip_loop, stage[0], ~stage[1], ~register_12_q[0], register_12_q[1], register_12_q[2], ~register_12_q[3]);  // AND_Gate
  Pull_Resistor pull_resistor_13 (.node(and_14_out));
  assign address = and_15_out ? 4'b0111 : 4'bz;  // Controlled_Buffer controlled_buffer_17
  and and_15 (and_15_out, skip_loop, ~stage[0], ~stage[1], ~register_13_q[0], register_13_q[1], register_13_q[2], ~register_13_q[3]);  // AND_Gate
  Pull_Resistor pull_resistor_14 (.node(and_15_out));
  assign address = and_16_out ? 4'b1111 : 4'bz;  // Controlled_Buffer controlled_buffer_18
  and and_16 (and_16_out, ~skip_loop, stage[0], stage[1], ~register_14_q[0], register_14_q[1], register_14_q[2], ~register_14_q[3]);  // AND_Gate
  Pull_Resistor pull_resistor_15 (.node(and_16_out));
  assign address = and_17_out ? 4'b0111 : 4'bz;  // Controlled_Buffer controlled_buffer_19
  and and_17 (and_17_out, ~skip_loop, ~stage[0], stage[1], ~register_15_q[0], register_15_q[1], register_15_q[2], ~register_15_q[3]);  // AND_Gate
  Pull_Resistor pull_resistor_16 (.node(and_17_out));
  assign address = and_18_out ? 4'b1010 : 4'bz;  // Controlled_Buffer controlled_buffer_20
  and and_18 (and_18_out, ~skip_loop, stage[0], ~stage[1], ~register_16_q[0], register_16_q[1], register_16_q[2], ~register_16_q[3]);  // AND_Gate
  Pull_Resistor pull_resistor_17 (.node(and_18_out));
  assign address = and_19_out ? 4'b0111 : 4'bz;  // Controlled_Buffer controlled_buffer_21
  and and_19 (and_19_out, ~skip_loop, ~stage[0], ~stage[1], ~register_17_q[0], register_17_q[1], register_17_q[2], ~register_17_q[3]);  // AND_Gate
  Pull_Resistor pull_resistor_18 (.node(and_19_out));
  Register #(.width(4), .trigger("low")) register_19 (.D(address), .Q(register_19_q), .clk(1'b0));  // open: en, clr
  Register #(.width(4), .trigger("low")) register_20 (.D(address), .Q(register_20_q), .clk(1'b0));  // open: en, clr
  Register #(.width(4), .trigger("low")) register_21 (.D(address), .Q(register_21_q), .clk(1'b0));  // open: en, clr
  Register #(.width(4), .trigger("low")) register_22 (.D(address), .Q(register_22_q), .clk(1'b0));  // open: en, clr
  Register #(.width(4), .trigger("low")) register_23 (.D(address), .Q(register_23_q), .clk(1'b0));  // open: en, clr
  Register #(.width(4), .trigger("low")) register_24 (.D(address), .Q(register_24_q), .clk(1'b0));  // open: en, clr
  and and_20 (and_20_out, register_19_q[0], register_19_q[1], register_19_q[2], ~register_19_q[3]);  // AND_Gate
  Pull_Resistor pull_resistor_19 (.node(and_20_out));
  buf buffer_2 (inc_stage_counter, and_20_out);
  assign address = and_21_out ? 4'b1100 : 4'bz;  // Controlled_Buffer controlled_buffer_22
  and and_21 (and_21_out, skip_loop, stage[0], ~stage[1], register_20_q[0], register_20_q[1], register_20_q[2], ~register_20_q[3]);  // AND_Gate
  Pull_Resistor pull_resistor_20 (.node(and_21_out));
  assign address = and_22_out ? 4'b1011 : 4'bz;  // Controlled_Buffer controlled_buffer_23
  and and_22 (and_22_out, skip_loop, ~stage[0], ~stage[1], register_21_q[0], register_21_q[1], register_21_q[2], ~register_21_q[3]);  // AND_Gate
  Pull_Resistor pull_resistor_21 (.node(and_22_out));
  assign address = and_23_out ? 4'b1100 : 4'bz;  // Controlled_Buffer controlled_buffer_24
  and and_23 (and_23_out, ~skip_loop, ~stage[0], stage[1], register_22_q[0], register_22_q[1], register_22_q[2], ~register_22_q[3]);  // AND_Gate
  Pull_Resistor pull_resistor_22 (.node(and_23_out));
  assign address = and_24_out ? 4'b1011 : 4'bz;  // Controlled_Buffer controlled_buffer_25
  and and_24 (and_24_out, ~skip_loop, stage[0], ~stage[1], register_23_q[0], register_23_q[1], register_23_q[2], ~register_23_q[3]);  // AND_Gate
  Pull_Resistor pull_resistor_23 (.node(and_24_out));
  assign address = and_25_out ? 4'b1000 : 4'bz;  // Controlled_Buffer controlled_buffer_26
  and and_25 (and_25_out, ~skip_loop, ~stage[0], ~stage[1], register_24_q[0], register_24_q[1], register_24_q[2], ~register_24_q[3]);  // AND_Gate
  Pull_Resistor pull_resistor_24 (.node(and_25_out));
  Register #(.width(4), .trigger("low")) register_25 (.D(address), .Q(register_25_q), .clk(1'b0));  // open: en, clr
  assign address = inc_stored_values ? 4'b0010 : 4'bz;  // Controlled_Buffer controlled_buffer_27
  and and_26 (inc_stored_values, ~register_25_q[0], ~register_25_q[1], ~register_25_q[2], register_25_q[3]);  // AND_Gate
  Pull_Resistor pull_resistor_25 (.node(inc_stored_values));
  Counter counter_3 (.Q(counter_3_q), .clk(inc_loop_counter), .clr(clear));  // open: load, D, count, carry
  Counter counter_4 (.Q(counter_4_q), .clk(inc_loop_counter), .clr(or_3_out));  // open: load, D, count, carry
  or or_3 (or_3_out, and_27_out, clear);
  Comparator comparator_4 (.a(counter_3_q), .b(loop_count[23:16]), .lt(comparator_4_lt));  // open: gt, eq
  not not_2 (loop_counter, comparator_4_lt);
  Comparator comparator_5 (.a(counter_4_q), .b(8'ha), .lt(comparator_5_lt));  // open: gt, eq
  not not_3 (loop_stopper_counter, comparator_5_lt);
  and and_27 (and_27_out, loop_stopper_counter, clk);
  Register #(.width(4), .trigger("low")) register_26 (.D(address), .Q(register_26_q), .clk(1'b0));  // open: en, clr
  Register #(.width(4), .trigger("low")) register_27 (.D(address), .Q(register_27_q), .clk(1'b0));  // open: en, clr
  Register #(.width(4), .trigger("low")) register_28 (.D(address), .Q(register_28_q), .clk(1'b0));  // open: en, clr
  Register #(.width(4), .trigger("low")) register_29 (.D(address), .Q(register_29_q), .clk(1'b0));  // open: en, clr
  assign address = and_28_out ? 4'b1010 : 4'bz;  // Controlled_Buffer controlled_buffer_28
  and and_28 (and_28_out, loop_counter, loop_stopper_counter, ~register_26_q[0], register_26_q[1], ~register_26_q[2], register_26_q[3]);  // AND_Gate
  Pull_Resistor pull_resistor_26 (.node(and_28_out));
  assign address = and_29_out ? 4'b1010 : 4'bz;  // Controlled_Buffer controlled_buffer_29
  and and_29 (and_29_out, ~loop_counter, loop_stopper_counter, ~register_27_q[0], register_27_q[1], ~register_27_q[2], register_27_q[3]);  // AND_Gate
  Pull_Resistor pull_resistor_27 (.node(and_29_out));
  assign address = and_30_out ? 4'b0111 : 4'bz;  // Controlled_Buffer controlled_buffer_30
  and and_30 (and_30_out, loop_counter, ~loop_stopper_counter, ~register_28_q[0], register_28_q[1], ~register_28_q[2], register_28_q[3]);  // AND_Gate
  Pull_Resistor pull_resistor_28 (.node(and_30_out));
  assign address = inc_loop_counter ? 4'b1000 : 4'bz;  // Controlled_Buffer controlled_buffer_31
  and and_31 (inc_loop_counter, ~loop_counter, ~loop_stopper_counter, ~register_29_q[0], register_29_q[1], ~register_29_q[2], register_29_q[3]);  // AND_Gate
  Pull_Resistor pull_resistor_29 (.node(inc_loop_counter));
  Register #(.width(4), .trigger("low")) register_30 (.D(address), .Q(register_30_q), .clk(1'b0));  // open: en, clr
  and and_32 (load_x2y2, register_30_q[0], register_30_q[1], ~register_30_q[2], register_30_q[3]);  // AND_Gate
  Pull_Resistor pull_resistor_30 (.node(load_x2y2));
  assign address = load_x2y2 ? 4'b0010 : 4'bz;  // Controlled_Buffer controlled_buffer_32
  Register #(.width(4), .trigger("low")) register_31 (.D(address), .Q(register_31_q), .clk(1'b0));  // open: en, clr
  assign address = clear ? 4'b0011 : 4'bz;  // Controlled_Buffer controlled_buffer_33
  and and_33 (clear, ~register_31_q[0], ~register_31_q[1], register_31_q[2], register_31_q[3]);  // AND_Gate
  Pull_Resistor pull_resistor_31 (.node(clear));
  Register #(.width(4), .trigger("low")) register_32 (.D(address), .Q(register_32_q), .clk(1'b0));  // open: en, clr
  and and_34 (done_t, register_32_q[0], register_32_q[1], register_32_q[2], register_32_q[3]);
  assign address = done_t ? 4'b0000 : 4'bz;  // Controlled_Buffer controlled_buffer_34
  Pull_Resistor pull_resistor_32 (.node(done_t));

  // Notes on the sheet:
  //   set_point: pull=up
  //   done: pull=up
  //   Config
  //   In
  //   halt
  //   Mission decoder
  //   load x1y1
  //   Math
  //   Out
  //   Out reg
  //   set
  //   buffer_1 drives only 1 and floats otherwise
  //   clear wait counter
  //   (wait buff)
  //   wait
  //   Main logic 
  //   reset
  //   stage
  //   buffer_2 drives only 1 and floats otherwise
  //   inc
  //   loop
  //   load x2y2
  //   clear
  //   done
  //   kek
endmodule

module DDA_sync (
  input  clk,
  input  new_data,
  input  [31:0] x2,
  input  [31:0] x1,
  input  [31:0] y2,
  input  [31:0] y1,
  output [31:0] out_x,
  output [3:0] status,
  output [31:0] out_y,
  output set_point,
  output done
);

  wire and_1_out, and_2_out, and_4_out, and_5_out, buffer_1_out, button_1_out, comparator_2_eq,
       comparator_2_lt, comparator_3_eq, controlled_buffer_7_out, d_ff_1_q, d_ff_2_q, done_t, mission_2,
       nand_1_out, nand_2_out, nand_3_out, nand_4_out, nand_5_out, nand_6_out, nand_7_out, nand_8_out,
       nand_9_out, nand_11_out, nand_12_out, nand_14_out, nand_15_out, nand_17_out, nand_18_out, nand_20_out,
       nand_21_out, nand_22_out, nand_23_out, nand_24_out, nand_25_out, nand_27_out, nand_29_out, new_data_t,
       not_1_out, not_2_out, not_3_out, or_2_out, rising_edge_detector_async_1_out,
       rising_edge_detector_async_2_out;
  wire [1:0] comparator_1_gt, control, mission, or_1_out, state;
  wire [1:1] comparator_1_lt;
  wire [31:0] counter_1_q, dx, dy, fp_abs_1_abs, fp_abs_2_abs, fp_round_ones_3_p1, out_x_t, out_y_t,
       steps_count, x, x1_t, x2_t, x_dx, x_step, y, y1_t, y2_t, y_dy, y_step;

  rising_edge_detector rising_edge_detector_1 (.signal(new_data), .clear(done_t), .sync(clk), .out(new_data_t));
  and and_1 (and_1_out, ~mission[1], mission[0]);  // AND_Gate
  and and_2 (and_2_out, mission[1], mission[0]);
  and and_3 (mission_2, mission[1], ~mission[0]);  // AND_Gate
  Register #(.width(32)) register_1 (.D(x2), .Q(x2_t), .clk(new_data_t));  // open: en, clr
  Register #(.width(32)) register_2 (.D(x1), .Q(x1_t), .clk(new_data_t));  // open: en, clr
  Register #(.width(32)) register_3 (.D(y2), .Q(y2_t), .clk(new_data_t));  // open: en, clr
  Register #(.width(32)) register_4 (.D(y1), .Q(y1_t), .clk(new_data_t));  // open: en, clr
  assign x = and_1_out ? x1_t : 32'bz;  // Controlled_Buffer controlled_buffer_1
  assign x = and_2_out ? x2_t : 32'bz;  // Controlled_Buffer controlled_buffer_2
  assign x = mission_2 ? x_dx : 32'bz;  // Controlled_Buffer controlled_buffer_3
  assign y = and_1_out ? y1_t : 32'bz;  // Controlled_Buffer controlled_buffer_4
  assign y = and_2_out ? y2_t : 32'bz;  // Controlled_Buffer controlled_buffer_5
  assign y = mission_2 ? y_dy : 32'bz;  // Controlled_Buffer controlled_buffer_6
  rising_edge_detector_async rising_edge_detector_async_1 (
    .signal(1'b1), .clear(rising_edge_detector_async_2_out), .out(rising_edge_detector_async_1_out));
  buf buffer_1 (buffer_1_out, done_t);
  Pull_Resistor pull_resistor_1 (.node(buffer_1_out));
  buf buffer_2 (buffer_1_out, rising_edge_detector_async_1_out);
  fp_abs fp_abs_1 (.in(dx), .abs(fp_abs_1_abs));
  Subtractor #(.width(32)) subtractor_1 (.a(x2_t), .b(x1_t), .out(dx));  // open: bin, bout
  Subtractor #(.width(32)) subtractor_2 (.a(y2_t), .b(y1_t), .out(dy));  // open: bin, bout
  fp_abs fp_abs_2 (.in(dy), .abs(fp_abs_2_abs));
  Adder #(.width(32)) adder_1 (.a(out_x_t), .b(x_step), .out(x_dx));  // open: cin, cout
  Adder #(.width(32)) adder_2 (.a(out_y_t), .b(y_step), .out(y_dy));  // open: cin, cout
  // fp_round_ones fp_round_ones_1: pin names not known; wires that end beside it: out_x_t, out_x
  // fp_round_ones fp_round_ones_2: pin names not known; wires that end beside it: out_y_t, out_y
  D_Flip_Flop d_ff_1 (.clk(clk), .D(buffer_1_out), .Q(d_ff_1_q));  // open: Qn, preset, en, reset
  Comparator #(.width(32)) comparator_1 (
    .a(fp_abs_1_abs), .b(fp_abs_2_abs), .gt(comparator_1_gt[0]), .eq(comparator_1_gt[1]),
    .lt(comparator_1_lt[1]));
  buf buffer_3 (done, rising_edge_detector_async_2_out);
  rising_edge_detector_async rising_edge_detector_async_2 (
    .signal(d_ff_1_q), .clear(new_data_t), .out(rising_edge_detector_async_2_out));
  assign or_1_out = comparator_1_gt | {2{comparator_1_lt[1]}};  // OR_Gate or_1, 2 bits wide
  fp_div fp_div_1 (.in1(dx), .in2(steps_count), .out(x_step));
  fp_div fp_div_2 (.in1(dy), .in2(steps_count), .out(y_step));
  // fp_round_ones fp_round_ones_3: pin names not known; wires that end beside it: fp_round_ones_3_p1, steps_count
  Multiplexer #(.select(2), .width(32), .enable("false")) multiplexer_1 (
    .in1(fp_abs_1_abs), .in2(fp_abs_1_abs), .in3(fp_abs_2_abs), .out(fp_round_ones_3_p1), .sel(or_1_out));  // open: in0
  Register #(.width(32)) register_5 (.D(x), .Q(out_x_t), .clk(clk), .clr(button_1_out));  // open: en
  Register #(.width(32)) register_6 (.D(y), .Q(out_y_t), .clk(clk), .clr(button_1_out));  // open: en
  Button button_1 (.out(button_1_out));
  assign controlled_buffer_7_out = and_4_out ? clk : 1'bz;  // Controlled_Buffer controlled_buffer_7
  and and_4 (and_4_out, ~comparator_3_eq, mission_2);  // AND_Gate
  Counter #(.width(32), .max('hffffffff)) counter_1 (
    .Q(counter_1_q), .clk(controlled_buffer_7_out), .clr(done_t));  // open: load, D, count, carry
  or or_2 (or_2_out, comparator_2_eq, comparator_2_lt);
  Comparator #(.width(32)) comparator_2 (
    .a(steps_count), .b(32'h10000), .eq(comparator_2_eq), .lt(comparator_2_lt));  // open: gt
  nand nand_1 (nand_1_out, control[0], state[0]);
  not not_1 (not_1_out, nand_1_out);
  nand nand_2 (nand_2_out, ~control[0], ~control[1]);  // NAND_Gate
  nand nand_3 (nand_3_out, nand_2_out, ~state[0]);  // NAND_Gate
  nand nand_4 (nand_4_out, control[0], ~state[1]);  // NAND_Gate
  nand nand_5 (nand_5_out, nand_4_out, nand_6_out);
  nand nand_6 (nand_6_out, control[1], state[1]);
  nand nand_7 (nand_7_out, control[0], nand_8_out);
  nand nand_8 (nand_8_out, ~control[1], ~state[1]);  // NAND_Gate
  and and_5 (and_5_out, ~or_2_out, comparator_3_eq);  // AND_Gate
  Comparator #(.width(32)) comparator_3 (
    .a({counter_1_q[15:0], {16{1'b0}}}), .b(steps_count), .eq(comparator_3_eq));  // open: gt, lt
  J_K_Flip_Flop j_k_ff_1 (.J(not_1_out), .clk(clk), .K(nand_3_out), .Q(state[1]));  // open: Qn, preset, en, reset
  J_K_Flip_Flop j_k_ff_2 (.J(nand_5_out), .clk(clk), .K(nand_7_out), .Q(state[0]));  // open: Qn, preset, en, reset
  nand nand_9 (nand_9_out, control[1], ~control[0], ~state[1]);  // NAND_Gate
  nand nand_10 (status[1], nand_9_out, nand_11_out);
  nand nand_11 (nand_11_out, control[1], ~control[0], state[0]);  // NAND_Gate
  nand nand_12 (nand_12_out, control[1], state[1], ~state[0]);  // NAND_Gate
  nand nand_13 (status[0], nand_12_out, not_2_out);
  not not_2 (not_2_out, control[0]);
  nand nand_14 (nand_14_out, control[0], ~state[1], state[0]);  // NAND_Gate
  nand nand_15 (nand_15_out, control[0], state[1], ~state[0]);  // NAND_Gate
  nand nand_16 (mission[1], nand_14_out, nand_15_out, nand_17_out);
  nand nand_17 (nand_17_out, control[1], state[1], ~state[0]);  // NAND_Gate
  nand nand_18 (nand_18_out, control[0], ~state[1], ~state[0]);  // NAND_Gate
  nand nand_19 (mission[0], nand_18_out, nand_20_out, nand_21_out);
  nand nand_20 (nand_20_out, control[1], control[0]);
  nand nand_21 (nand_21_out, control[1], state[1], ~state[0]);  // NAND_Gate
  nand nand_22 (nand_22_out, control[1], control[0], ~state[1], state[0]);  // NAND_Gate
  nand nand_23 (nand_23_out, nand_22_out, nand_24_out);
  nand nand_24 (nand_24_out, control[1], state[1], ~state[0]);  // NAND_Gate
  nand nand_25 (nand_25_out, control[0], state[0]);
  nand nand_26 (set_point, nand_25_out, nand_27_out);
  nand nand_27 (nand_27_out, state[1], ~state[0]);  // NAND_Gate
  D_Flip_Flop d_ff_2 (.clk(clk), .D(nand_23_out), .Q(d_ff_2_q));  // open: Qn, preset, en, reset
  not not_3 (not_3_out, and_5_out);
  nand nand_28 (control[1], not_3_out, nand_29_out);
  nand nand_29 (nand_29_out, or_2_out, new_data_t);
  nand nand_30 (control[0], ~new_data_t, ~and_5_out);  // NAND_Gate
  D_Flip_Flop d_ff_3 (.clk(clk), .D(d_ff_2_q), .Q(done_t));  // open: Qn, preset, en, reset
  Hex_Digit_Display hex_digit_display_1 (.value({2'b00, status[1:0]}));  // open: dp

  assign status[3:2] = 2'b00;

  // Other names for the same wires on the sheet: status_t[1:0] = status[1:0]

  // Notes on the sheet:
  //   done: pull=up
  //   set_point: pull=up
  //   In
  //   Mission decoder
  //   buffer_1 drives only 1 and floats otherwise
  //   buffer_2 drives only 1 and floats otherwise
  //   Out
  //   Math
  //   buffer_3 drives only 0 and floats otherwise
  //   Out reg
  //   State machine
  //   Main logic
  //   00 - halt do nothg
  //   01 - load x1y1
  //   10 - increment by step
  //   11 - load x2y2
  //   Status
  //   0: halt
  //   1: run
  //   2: error
endmodule

module projection_matrix (
  input  [31:0] FOV,
  input  [31:0] far_plane,
  input  [31:0] near_plane,
  output [31:0] out_4,
  output [31:0] out_5,
  output [31:0] out_6,
  output [31:0] out_7,
  output [31:0] out_8
);

  wire [31:0] far_near, fp_mult_1_out, fp_mult_2_out;

  tg tg_1 (.in_fp(FOV), .tg(out_5));
  fp_mult fp_mult_1 (.in1(far_plane), .in2(32'hffff0000), .out(fp_mult_1_out));
  fp_mult fp_mult_2 (.in1(fp_mult_1_out), .in2(near_plane), .out(fp_mult_2_out));
  Subtractor #(.width(32)) subtractor_1 (.a(far_plane), .b(near_plane), .out(far_near));  // open: bin, bout
  fp_mult fp_mult_3 (.in1(32'h10000), .in2(out_5), .out(out_4));
  fp_div fp_div_1 (.in1(far_plane), .in2(far_near), .out(out_6));
  fp_div fp_div_2 (.in1(fp_mult_2_out), .in2(far_near), .out(out_8));

  assign out_7 = 32'h10000;

  // Other names for the same wires on the sheet: f_far[31:0] = far_plane; f_fov_rad[31:0] = out_5;
  //   f_near[31:0] = near_plane
endmodule

module point_projector_x4 (
  input  [31:0] line1_x1,
  input  [31:0] line2_x1,
  input  [31:0] line1_y1,
  input  [31:0] line2_y1,
  input  [31:0] FOV,
  input  [31:0] line1_z1,
  input  [31:0] line2_z1,
  input  [31:0] far_plane,
  input  [31:0] line1_x2,
  input  [31:0] line2_x2,
  input  [31:0] near_plane,
  input  [31:0] line1_y2,
  input  [31:0] line2_y2,
  input  [31:0] line1_z2,
  input  [31:0] line2_z2,
  output [31:0] line1_x1_2,
  output [31:0] line1_y1_2,
  output [31:0] line1_x2_2,
  output [31:0] line1_y2_2,
  output [31:0] line2_x1_2,
  output [31:0] line2_y1_2,
  output [31:0] FOV_bypass,
  output [31:0] line2_x2_2,
  output [31:0] far_plane_bypass,
  output [31:0] line2_y2_2,
  output [31:0] near_plane_bypass
);

  wire [31:0] matrix_mult_4x4_1_out11, matrix_mult_4x4_1_out12, matrix_mult_4x4_1_out14,
       matrix_mult_4x4_1_out21, matrix_mult_4x4_1_out22, matrix_mult_4x4_1_out24, matrix_mult_4x4_1_out31,
       matrix_mult_4x4_1_out32, matrix_mult_4x4_1_out34, matrix_mult_4x4_1_out41, matrix_mult_4x4_1_out42,
       matrix_mult_4x4_1_out44, projection_matrix_v2_1_out_4, projection_matrix_v2_1_out_5,
       projection_matrix_v2_1_out_6, projection_matrix_v2_1_out_7, projection_matrix_v2_1_out_8;

  projection_matrix_v2 projection_matrix_v2_1 (
    .FOV(FOV), .far_plane(far_plane), .near_plane(near_plane), .out_4(projection_matrix_v2_1_out_4),
    .out_5(projection_matrix_v2_1_out_5), .out_6(projection_matrix_v2_1_out_6),
    .out_7(projection_matrix_v2_1_out_7), .out_8(projection_matrix_v2_1_out_8));
  matrix_mult_4x4 matrix_mult_4x4_1 (
    .in_1(line1_x1), .in_2(line1_x2), .in_3(line2_x1), .in_4(line2_x2), .in_5(line1_y1), .in_6(line1_y2),
    .in_7(line2_y1), .in_8(line2_y2), .in_9(line1_z1), .in_10(line1_z2), .in_11(line2_z1), .in_12(line2_z2),
    .in_13(32'h10000), .in_14(32'h10000), .in_15(32'h10000), .in_16(32'h10000),
    .in_17(projection_matrix_v2_1_out_4), .in_22(projection_matrix_v2_1_out_5),
    .in_27(projection_matrix_v2_1_out_6), .in_28(projection_matrix_v2_1_out_8),
    .in_31(projection_matrix_v2_1_out_7), .out11(matrix_mult_4x4_1_out11), .out21(matrix_mult_4x4_1_out21),
    .out31(matrix_mult_4x4_1_out31), .out41(matrix_mult_4x4_1_out41), .out12(matrix_mult_4x4_1_out12),
    .out22(matrix_mult_4x4_1_out22), .out32(matrix_mult_4x4_1_out32), .out42(matrix_mult_4x4_1_out42),
    .out14(matrix_mult_4x4_1_out14), .out24(matrix_mult_4x4_1_out24), .out34(matrix_mult_4x4_1_out34),
    .out44(matrix_mult_4x4_1_out44));  // open: in_18, in_19, in_20, in_21, in_23, in_24, in_25, in_26, in_29, in_30, in_32, out13, out23, out33, out43
  vec4_to_vec2 vec4_to_vec2_1 (
    .in1(matrix_mult_4x4_1_out11), .in2(matrix_mult_4x4_1_out12), .in4(matrix_mult_4x4_1_out14),
    .out1(line1_x1_2), .out2(line1_y1_2));
  vec4_to_vec2 vec4_to_vec2_2 (
    .in1(matrix_mult_4x4_1_out21), .in2(matrix_mult_4x4_1_out22), .in4(matrix_mult_4x4_1_out24),
    .out1(line1_x2_2), .out2(line1_y2_2));
  vec4_to_vec2 vec4_to_vec2_3 (
    .in1(matrix_mult_4x4_1_out31), .in2(matrix_mult_4x4_1_out32), .in4(matrix_mult_4x4_1_out34),
    .out1(line2_x1_2), .out2(line2_y1_2));
  vec4_to_vec2 vec4_to_vec2_4 (
    .in1(matrix_mult_4x4_1_out41), .in2(matrix_mult_4x4_1_out42), .in4(matrix_mult_4x4_1_out44),
    .out1(line2_x2_2), .out2(line2_y2_2));

  assign far_plane_bypass = far_plane;
  assign FOV_bypass = FOV;
  assign near_plane_bypass = near_plane;
endmodule

module projection_matrix_v2 (
  input  [31:0] FOV,
  input  [31:0] far_plane,
  input  [31:0] near_plane,
  output [31:0] out_4,
  output [31:0] out_5,
  output [31:0] out_6,
  output [31:0] out_7,
  output [31:0] out_8
);

  wire [31:0] far_near, fp_div_1_out, fp_mult_1_out, fp_mult_2_out;

  fp_div fp_div_1 (.in1(FOV), .in2(32'h20000), .out(fp_div_1_out));
  tg tg_1 (.in_fp(fp_div_1_out), .tg(out_5));
  fp_mult fp_mult_1 (.in1(far_plane), .in2(32'hffff0000), .out(fp_mult_1_out));
  fp_mult fp_mult_2 (.in1(fp_mult_1_out), .in2(near_plane), .out(fp_mult_2_out));
  Subtractor #(.width(32)) subtractor_1 (.a(far_plane), .b(near_plane), .out(far_near));  // open: bin, bout
  fp_mult fp_mult_3 (.in1(32'h10000), .in2(out_5), .out(out_4));
  fp_div fp_div_2 (.in1(far_plane), .in2(far_near), .out(out_6));
  fp_div fp_div_3 (.in1(fp_mult_2_out), .in2(far_near), .out(out_8));

  assign out_7 = 32'h10000;

  // Other names for the same wires on the sheet: f_far[31:0] = far_plane; f_fov_rad[31:0] = out_5;
  //   f_near[31:0] = near_plane
endmodule

module point_projector_x4_optimized (
  input  [31:0] line1_x1,
  input  [31:0] line2_x1,
  input  [31:0] line1_y1,
  input  [31:0] line2_y1,
  input  [31:0] FOV,
  input  [31:0] line1_z1,
  input  [31:0] line2_z1,
  input  [31:0] far_plane,
  input  [31:0] line1_x2,
  input  [31:0] line2_x2,
  input  [31:0] near_plane,
  input  [31:0] line1_y2,
  input  [31:0] line2_y2,
  input  [31:0] line1_z2,
  input  [31:0] line2_z2,
  output [31:0] line1_x1_2,
  output [31:0] line1_y1_2,
  output [31:0] line1_x2_2,
  output [31:0] line1_y2_2,
  output [31:0] line2_x1_2,
  output [31:0] line2_y1_2,
  output [31:0] FOV_bypass,
  output [31:0] line2_x2_2,
  output [31:0] far_plane_bypass,
  output [31:0] line2_y2_2,
  output [31:0] near_plane_bypass
);

  wire [31:0] matrix_mul_4x4_optimized_for_projection_1_out11,
       matrix_mul_4x4_optimized_for_projection_1_out12, matrix_mul_4x4_optimized_for_projection_1_out14,
       matrix_mul_4x4_optimized_for_projection_1_out21, matrix_mul_4x4_optimized_for_projection_1_out22,
       matrix_mul_4x4_optimized_for_projection_1_out24, matrix_mul_4x4_optimized_for_projection_1_out31,
       matrix_mul_4x4_optimized_for_projection_1_out32, matrix_mul_4x4_optimized_for_projection_1_out34,
       matrix_mul_4x4_optimized_for_projection_1_out41, matrix_mul_4x4_optimized_for_projection_1_out42,
       matrix_mul_4x4_optimized_for_projection_1_out44, projection_matrix_v2_1_out_4,
       projection_matrix_v2_1_out_5, projection_matrix_v2_1_out_6, projection_matrix_v2_1_out_7,
       projection_matrix_v2_1_out_8;

  projection_matrix_v2 projection_matrix_v2_1 (
    .FOV(FOV), .far_plane(far_plane), .near_plane(near_plane), .out_4(projection_matrix_v2_1_out_4),
    .out_5(projection_matrix_v2_1_out_5), .out_6(projection_matrix_v2_1_out_6),
    .out_7(projection_matrix_v2_1_out_7), .out_8(projection_matrix_v2_1_out_8));
  matrix_mul_4x4_optimized_for_projection matrix_mul_4x4_optimized_for_projection_1 (
    .in_1(line1_x1), .in_2(line1_x2), .in_3(line2_x1), .in_4(line2_x2), .in_5(line1_y1), .in_6(line1_y2),
    .in_7(line2_y1), .in_8(line2_y2), .in_9(line1_z1), .in_10(line1_z2), .in_11(line2_z1), .in_12(line2_z2),
    .in_13(projection_matrix_v2_1_out_4), .in_14(projection_matrix_v2_1_out_5),
    .in_15(projection_matrix_v2_1_out_6), .in_16(projection_matrix_v2_1_out_8),
    .in_17(projection_matrix_v2_1_out_7), .out11(matrix_mul_4x4_optimized_for_projection_1_out11),
    .out21(matrix_mul_4x4_optimized_for_projection_1_out21),
    .out31(matrix_mul_4x4_optimized_for_projection_1_out31),
    .out41(matrix_mul_4x4_optimized_for_projection_1_out41),
    .out12(matrix_mul_4x4_optimized_for_projection_1_out12),
    .out22(matrix_mul_4x4_optimized_for_projection_1_out22),
    .out32(matrix_mul_4x4_optimized_for_projection_1_out32),
    .out42(matrix_mul_4x4_optimized_for_projection_1_out42),
    .out14(matrix_mul_4x4_optimized_for_projection_1_out14),
    .out24(matrix_mul_4x4_optimized_for_projection_1_out24),
    .out34(matrix_mul_4x4_optimized_for_projection_1_out34),
    .out44(matrix_mul_4x4_optimized_for_projection_1_out44));
  vec4_to_vec2 vec4_to_vec2_1 (
    .in1(matrix_mul_4x4_optimized_for_projection_1_out11),
    .in2(matrix_mul_4x4_optimized_for_projection_1_out12),
    .in4(matrix_mul_4x4_optimized_for_projection_1_out14), .out1(line1_x1_2), .out2(line1_y1_2));
  vec4_to_vec2 vec4_to_vec2_2 (
    .in1(matrix_mul_4x4_optimized_for_projection_1_out21),
    .in2(matrix_mul_4x4_optimized_for_projection_1_out22),
    .in4(matrix_mul_4x4_optimized_for_projection_1_out24), .out1(line1_x2_2), .out2(line1_y2_2));
  vec4_to_vec2 vec4_to_vec2_3 (
    .in1(matrix_mul_4x4_optimized_for_projection_1_out31),
    .in2(matrix_mul_4x4_optimized_for_projection_1_out32),
    .in4(matrix_mul_4x4_optimized_for_projection_1_out34), .out1(line2_x1_2), .out2(line2_y1_2));
  vec4_to_vec2 vec4_to_vec2_4 (
    .in1(matrix_mul_4x4_optimized_for_projection_1_out41),
    .in2(matrix_mul_4x4_optimized_for_projection_1_out42),
    .in4(matrix_mul_4x4_optimized_for_projection_1_out44), .out1(line2_x2_2), .out2(line2_y2_2));

  assign far_plane_bypass = far_plane;
  assign FOV_bypass = FOV;
  assign near_plane_bypass = near_plane;
endmodule

module translator_x4_optimized (
  input  [31:0] line1_x1,
  input  [31:0] line1_y1,
  input  [31:0] line1_z1,
  input  [31:0] line1_x2,
  input  [31:0] line1_y2,
  input  [31:0] line1_z2,
  input  [31:0] line2_x1,
  input  [31:0] line2_y1,
  input  [31:0] line2_z1,
  input  [31:0] line2_x2,
  input  [31:0] line2_y2,
  input  [31:0] line2_z2,
  input  [31:0] x,
  input  [31:0] y,
  input  [31:0] z,
  output [31:0] line1_x1_2,
  output [31:0] line1_y1_2,
  output [31:0] line1_z1_2,
  output [31:0] line1_x2_2,
  output [31:0] line1_y2_2,
  output [31:0] line1_z2_2,
  output [31:0] line2_x1_2,
  output [31:0] line2_y1_2,
  output [31:0] line2_z1_2,
  output [31:0] line2_x2_2,
  output [31:0] line2_y2_2,
  output [31:0] line2_z2_2,
  output [31:0] bypass,
  output [31:0] bypass_2,
  output [31:0] bypass_3
);

  matrix_mul_4x4_optimized_for_translation matrix_mul_4x4_optimized_for_translation_1 (
    .in_1(x), .in_2(line1_x1), .in_3(line1_x2), .in_4(line2_x1), .in_5(line2_x2), .in_6(y), .in_7(line1_y1),
    .in_8(line1_y2), .in_9(line2_y1), .in_10(line2_y2), .in_11(z), .in_12(line1_z1), .in_13(line1_z2),
    .in_14(line2_z1), .in_15(line2_z2), .out11(line1_x1_2), .out21(line1_x2_2), .out31(line2_x1_2),
    .out41(line2_x2_2), .out12(line1_y1_2), .out22(line1_y2_2), .out32(line2_y1_2), .out42(line2_y2_2),
    .out13(line1_z1_2), .out23(line1_z2_2), .out33(line2_z1_2), .out43(line2_z2_2));

  assign bypass = x;
  assign bypass_2 = y;
  assign bypass_3 = z;
endmodule

module rotator_x4_optimized (
  input  [31:0] line1_x1,
  input  [31:0] line2_x1,
  input  [31:0] line1_y1,
  input  [31:0] line2_y1,
  input  [31:0] Rx,
  input  [31:0] line1_z1,
  input  [31:0] line2_z1,
  input  [31:0] Ry,
  input  [31:0] Rz,
  input  [31:0] line1_x2,
  input  [31:0] line2_x2,
  input  [31:0] line1_y2,
  input  [31:0] line2_y2,
  input  [31:0] line1_z2,
  input  [31:0] line2_z2,
  output [31:0] line1_x1_2,
  output [31:0] line1_y1_2,
  output [31:0] line1_z1_2,
  output [31:0] line1_x2_2,
  output [31:0] line1_y2_2,
  output [31:0] line1_z2_2,
  output [31:0] line2_x1_2,
  output [31:0] line2_y1_2,
  output [31:0] bypass,
  output [31:0] line2_z1_2,
  output [31:0] bypass_2,
  output [31:0] line2_x2_2,
  output [31:0] bypass_3,
  output [31:0] line2_y2_2,
  output [31:0] line2_z2_2
);

  wire [31:0] rotation_matrix_1_out_4, rotation_matrix_1_out_5, rotation_matrix_1_out_6,
       rotation_matrix_1_out_7, rotation_matrix_1_out_8, rotation_matrix_1_out_9, rotation_matrix_1_out_10,
       rotation_matrix_1_out_11, rotation_matrix_1_out_12;

  rotation_matrix rotation_matrix_1 (
    .Rx(Rx), .Ry(Ry), .Rz(Rz), .out_4(rotation_matrix_1_out_4), .out_5(rotation_matrix_1_out_5),
    .out_6(rotation_matrix_1_out_6), .out_7(rotation_matrix_1_out_7), .out_8(rotation_matrix_1_out_8),
    .out_9(rotation_matrix_1_out_9), .out_10(rotation_matrix_1_out_10), .out_11(rotation_matrix_1_out_11),
    .out_12(rotation_matrix_1_out_12));
  matrix_mul_4x4_optimized_for_rotation matrix_mul_4x4_optimized_for_rotation_1 (
    .in_1(rotation_matrix_1_out_4), .in_2(rotation_matrix_1_out_5), .in_3(rotation_matrix_1_out_6),
    .in_4(line1_x1), .in_5(line1_x2), .in_6(line2_x1), .in_7(line2_x2), .in_8(rotation_matrix_1_out_7),
    .in_9(rotation_matrix_1_out_8), .in_10(rotation_matrix_1_out_9), .in_11(line1_y1), .in_12(line1_y2),
    .in_13(line2_y1), .in_14(line2_y2), .in_15(rotation_matrix_1_out_10), .in_16(rotation_matrix_1_out_11),
    .in_17(rotation_matrix_1_out_12), .in_18(line1_z1), .in_19(line1_z2), .in_20(line2_z1), .in_21(line2_z2),
    .out11(line1_x1_2), .out21(line1_x2_2), .out31(line2_x1_2), .out41(line2_x2_2), .out12(line1_y1_2),
    .out22(line1_y2_2), .out32(line2_y1_2), .out42(line2_y2_2), .out13(line1_z1_2), .out23(line1_z2_2),
    .out33(line2_z1_2), .out43(line2_z2_2));

  assign bypass = Rx;
  assign bypass_2 = Ry;
  assign bypass_3 = Rz;
endmodule

module rotation_matrix (
  input  [31:0] Rx,
  input  [31:0] Ry,
  input  [31:0] Rz,
  output [31:0] out_4,
  output [31:0] out_5,
  output [31:0] out_6,
  output [31:0] out_7,
  output [31:0] out_8,
  output [31:0] out_9,
  output [31:0] out_10,
  output [31:0] out_11,
  output [31:0] out_12
);

  wire [31:0] cosinusx, cosinusy, cosinusz, fp_mult_3_out, fp_mult_4_out, fp_mult_5_out, fp_mult_6_out,
       fp_mult_7_out, fp_mult_8_out, fp_mult_10_out, fp_mult_11_out, fp_mult_12_out, fp_mult_13_out,
       fp_mult_14_out, fp_mult_15_out, sinusx, sinusy, sinusz;

  sin sin_1 (.in_fp(Rx), .sin(sinusx));
  cos cos_1 (.cos(cosinusx), .in_fp(Rx));
  sin sin_2 (.in_fp(Ry), .sin(sinusy));
  cos cos_2 (.cos(cosinusy), .in_fp(Ry));
  sin sin_3 (.in_fp(Rz), .sin(sinusz));
  cos cos_3 (.cos(cosinusz), .in_fp(Rz));
  fp_mult fp_mult_1 (.in1(cosinusy), .in2(cosinusz), .out(out_4));
  fp_mult fp_mult_2 (.in1(cosinusy), .in2(sinusz), .out(out_7));
  Negator #(.width(32)) negator_1 (.in(sinusy), .out(out_10));
  fp_mult fp_mult_3 (.in1(sinusx), .in2(sinusy), .out(fp_mult_3_out));
  fp_mult fp_mult_4 (.in1(sinusx), .in2(sinusy), .out(fp_mult_4_out));
  fp_mult fp_mult_5 (.in1(fp_mult_3_out), .in2(cosinusy), .out(fp_mult_5_out));
  Subtractor #(.width(32)) subtractor_1 (.a(fp_mult_5_out), .b(fp_mult_6_out), .out(out_5));  // open: bin, bout
  fp_mult fp_mult_6 (.in1(cosinusx), .in2(sinusz), .out(fp_mult_6_out));
  fp_mult fp_mult_7 (.in1(fp_mult_4_out), .in2(sinusz), .out(fp_mult_7_out));
  Adder #(.width(32)) adder_1 (.a(fp_mult_7_out), .b(fp_mult_8_out), .out(out_8));  // open: cin, cout
  fp_mult fp_mult_8 (.in1(cosinusx), .in2(cosinusz), .out(fp_mult_8_out));
  fp_mult fp_mult_9 (.in1(sinusx), .in2(cosinusy), .out(out_11));
  fp_mult fp_mult_10 (.in1(cosinusx), .in2(sinusy), .out(fp_mult_10_out));
  fp_mult fp_mult_11 (.in1(fp_mult_10_out), .in2(cosinusz), .out(fp_mult_11_out));
  fp_mult fp_mult_12 (.in1(sinusx), .in2(sinusz), .out(fp_mult_12_out));
  fp_mult fp_mult_13 (.in1(cosinusx), .in2(sinusy), .out(fp_mult_13_out));
  fp_mult fp_mult_14 (.in1(fp_mult_13_out), .in2(sinusz), .out(fp_mult_14_out));
  fp_mult fp_mult_15 (.in1(sinusx), .in2(cosinusz), .out(fp_mult_15_out));
  Adder #(.width(32)) adder_2 (.a(fp_mult_11_out), .b(fp_mult_12_out), .out(out_6));  // open: cin, cout
  Subtractor #(.width(32)) subtractor_2 (.a(fp_mult_14_out), .b(fp_mult_15_out), .out(out_9));  // open: bin, bout
  fp_mult fp_mult_16 (.in1(cosinusx), .in2(cosinusy), .out(out_12));
endmodule
