// Logisim project funkcje_sin_cos (1).circ as structural Verilog: 1 circuit, main circuit main
module main (
  input  [6:0] in_1,
  input  [6:0] in_2,
  input  [6:0] in_3,
  input  [6:0] in_4,
  input  [6:0] in_5
);

  wire n32bit_decoder_short_1_dot, n32bit_decoder_short_1_sign, n32bit_decoder_short_2_dot,
       n32bit_decoder_short_2_sign, n32bit_decoder_short_3_dot, n32bit_decoder_short_3_sign,
       n32bit_decoder_short_4_dot, n32bit_decoder_short_4_sign, n32bit_decoder_short_5_dot,
       n32bit_decoder_short_5_sign, n32bit_decoder_short_6_dot, n32bit_decoder_short_6_sign,
       n32bit_decoder_short_7_dot, n32bit_decoder_short_7_sign, n32bit_decoder_short_8_dot,
       n32bit_decoder_short_8_sign, n32bit_decoder_short_9_dot, n32bit_decoder_short_9_sign;
  wire [3:0] n32bit_decoder_short_1__0, n32bit_decoder_short_1__1, n32bit_decoder_short_1__1_2,
       n32bit_decoder_short_1__2, n32bit_decoder_short_1__2_2, n32bit_decoder_short_1__3,
       n32bit_decoder_short_1__3_2, n32bit_decoder_short_1__4, n32bit_decoder_short_1__4_2,
       n32bit_decoder_short_1__5, n32bit_decoder_short_2__0, n32bit_decoder_short_2__1,
       n32bit_decoder_short_2__1_2, n32bit_decoder_short_2__2, n32bit_decoder_short_2__2_2,
       n32bit_decoder_short_2__3, n32bit_decoder_short_2__3_2, n32bit_decoder_short_2__4,
       n32bit_decoder_short_2__4_2, n32bit_decoder_short_2__5, n32bit_decoder_short_3__0,
       n32bit_decoder_short_3__1, n32bit_decoder_short_3__1_2, n32bit_decoder_short_3__2,
       n32bit_decoder_short_3__2_2, n32bit_decoder_short_3__3, n32bit_decoder_short_3__3_2,
       n32bit_decoder_short_3__4, n32bit_decoder_short_3__4_2, n32bit_decoder_short_3__5,
       n32bit_decoder_short_4__0, n32bit_decoder_short_4__1, n32bit_decoder_short_4__1_2,
       n32bit_decoder_short_4__2, n32bit_decoder_short_4__2_2, n32bit_decoder_short_4__3,
       n32bit_decoder_short_4__3_2, n32bit_decoder_short_4__4, n32bit_decoder_short_4__4_2,
       n32bit_decoder_short_4__5, n32bit_decoder_short_5__0, n32bit_decoder_short_5__1,
       n32bit_decoder_short_5__1_2, n32bit_decoder_short_5__2, n32bit_decoder_short_5__2_2,
       n32bit_decoder_short_5__3, n32bit_decoder_short_5__3_2, n32bit_decoder_short_5__4,
       n32bit_decoder_short_5__4_2, n32bit_decoder_short_5__5, n32bit_decoder_short_6__0,
       n32bit_decoder_short_6__1, n32bit_decoder_short_6__1_2, n32bit_decoder_short_6__2,
       n32bit_decoder_short_6__2_2, n32bit_decoder_short_6__3, n32bit_decoder_short_6__3_2,
       n32bit_decoder_short_6__4, n32bit_decoder_short_6__4_2, n32bit_decoder_short_6__5,
       n32bit_decoder_short_7__0, n32bit_decoder_short_7__1, n32bit_decoder_short_7__1_2,
       n32bit_decoder_short_7__2, n32bit_decoder_short_7__2_2, n32bit_decoder_short_7__3,
       n32bit_decoder_short_7__3_2, n32bit_decoder_short_7__4, n32bit_decoder_short_7__4_2,
       n32bit_decoder_short_7__5, n32bit_decoder_short_8__0, n32bit_decoder_short_8__1,
       n32bit_decoder_short_8__1_2, n32bit_decoder_short_8__2, n32bit_decoder_short_8__2_2,
       n32bit_decoder_short_8__3, n32bit_decoder_short_8__3_2, n32bit_decoder_short_8__4,
       n32bit_decoder_short_8__4_2, n32bit_decoder_short_8__5, n32bit_decoder_short_9__0,
       n32bit_decoder_short_9__1, n32bit_decoder_short_9__1_2, n32bit_decoder_short_9__2,
       n32bit_decoder_short_9__2_2, n32bit_decoder_short_9__3, n32bit_decoder_short_9__3_2,
       n32bit_decoder_short_9__4, n32bit_decoder_short_9__4_2, n32bit_decoder_short_9__5;
  wire [31:0] fp_div_1_out, not_1_out, not_2_out, not_3_out, not_4_out, rom_1_data, rom_2_data, rom_3_data,
       rom_4_data, rom_5_data, rom_6_data, rom_7_data, rom_8_data, rom_9_data, rom_10_data;

  ROM #(.addrWidth(7), .dataWidth(32)) rom_1 (.addr(in_1), .data(rom_1_data));  // open: sel
  ROM #(.addrWidth(7), .dataWidth(32)) rom_2 (.addr(in_2), .data(rom_2_data));  // open: sel
  ROM #(.addrWidth(7), .dataWidth(32)) rom_3 (.addr(in_3), .data(rom_3_data));  // open: sel
  ROM #(.addrWidth(7), .dataWidth(32)) rom_4 (.addr(in_4), .data(rom_4_data));  // open: sel
  ROM #(.addrWidth(7), .dataWidth(32)) rom_5 (.addr(in_4), .data(rom_5_data));  // open: sel
  ROM #(.addrWidth(7), .dataWidth(32)) rom_6 (.addr(in_5), .data(rom_6_data));  // open: sel
  ROM #(.addrWidth(7), .dataWidth(32)) rom_7 (.addr(in_1), .data(rom_7_data));  // open: sel
  ROM #(.addrWidth(7), .dataWidth(32)) rom_8 (.addr(in_2), .data(rom_8_data));  // open: sel
  ROM #(.addrWidth(7), .dataWidth(32)) rom_9 (.addr(in_3), .data(rom_9_data));  // open: sel
  assign not_1_out = ~rom_5_data;  // NOT_Gate not_1, 32 bits wide
  ROM #(.addrWidth(7), .dataWidth(32)) rom_10 (.addr(in_5), .data(rom_10_data));  // open: sel
  assign not_2_out = ~rom_2_data;  // NOT_Gate not_2, 32 bits wide
  assign not_3_out = ~rom_9_data;  // NOT_Gate not_3, 32 bits wide
  assign not_4_out = ~rom_3_data;  // NOT_Gate not_4, 32 bits wide
  _7_Segment_Display u_7_segment_display_1 (.g(n32bit_decoder_short_2_sign));  // open: f, a, b, e, d, c, dp
  _7_Segment_Display u_7_segment_display_2 (.g(n32bit_decoder_short_4_sign));  // open: f, a, b, e, d, c, dp
  _7_Segment_Display u_7_segment_display_3 (.g(n32bit_decoder_short_6_sign));  // open: f, a, b, e, d, c, dp
  _7_Segment_Display u_7_segment_display_4 (.g(n32bit_decoder_short_1_sign));  // open: f, a, b, e, d, c, dp
  Hex_Digit_Display hex_digit_display_1 (.value(n32bit_decoder_short_1__4));  // open: dp
  _7_Segment_Display u_7_segment_display_5 (.g(n32bit_decoder_short_8_sign));  // open: f, a, b, e, d, c, dp
  Hex_Digit_Display hex_digit_display_2 (.value(n32bit_decoder_short_2__4));  // open: dp
  _7_Segment_Display u_7_segment_display_6 (.g(n32bit_decoder_short_3_sign));  // open: f, a, b, e, d, c, dp
  Hex_Digit_Display hex_digit_display_3 (.value(n32bit_decoder_short_4__4));  // open: dp
  _7_Segment_Display u_7_segment_display_7 (.g(n32bit_decoder_short_5_sign));  // open: f, a, b, e, d, c, dp
  Hex_Digit_Display hex_digit_display_4 (.value(n32bit_decoder_short_6__3));  // open: dp
  Hex_Digit_Display hex_digit_display_5 (.value(n32bit_decoder_short_6__4));  // open: dp
  _7_Segment_Display u_7_segment_display_8 (.g(n32bit_decoder_short_7_sign));  // open: f, a, b, e, d, c, dp
  Hex_Digit_Display hex_digit_display_6 (.value(n32bit_decoder_short_7__4));  // open: dp
  Hex_Digit_Display hex_digit_display_7 (.value(n32bit_decoder_short_1__3));  // open: dp
  Hex_Digit_Display hex_digit_display_8 (.value(n32bit_decoder_short_1__2_2));  // open: dp
  Hex_Digit_Display hex_digit_display_9 (.value(n32bit_decoder_short_8__3));  // open: dp
  Hex_Digit_Display hex_digit_display_10 (.value(n32bit_decoder_short_8__4));  // open: dp
  fp_div fp_div_1 (.in1(rom_10_data), .in2(rom_6_data), .out(fp_div_1_out));
  Hex_Digit_Display hex_digit_display_11 (.value(n32bit_decoder_short_2__3));  // open: dp
  Hex_Digit_Display hex_digit_display_12 (.value(n32bit_decoder_short_2__2_2));  // open: dp
  Hex_Digit_Display hex_digit_display_13 (.value(n32bit_decoder_short_3__4));  // open: dp
  Hex_Digit_Display hex_digit_display_14 (.value(n32bit_decoder_short_3__3));  // open: dp
  Hex_Digit_Display hex_digit_display_15 (.value(n32bit_decoder_short_4__2_2));  // open: dp
  Hex_Digit_Display hex_digit_display_16 (.value(n32bit_decoder_short_4__3));  // open: dp
  Hex_Digit_Display hex_digit_display_17 (.value(n32bit_decoder_short_5__4));  // open: dp
  Hex_Digit_Display hex_digit_display_18 (.value(n32bit_decoder_short_5__3));  // open: dp
  Hex_Digit_Display hex_digit_display_19 (.value(n32bit_decoder_short_6__2_2));  // open: dp
  Hex_Digit_Display hex_digit_display_20 (.value(n32bit_decoder_short_6__1_2));  // open: dp
  Hex_Digit_Display hex_digit_display_21 (.value(n32bit_decoder_short_7__3));  // open: dp
  Hex_Digit_Display hex_digit_display_22 (.value(n32bit_decoder_short_7__2_2));  // open: dp
  Hex_Digit_Display hex_digit_display_23 (.value(n32bit_decoder_short_1__1_2));  // open: dp
  Hex_Digit_Display hex_digit_display_24 (.value(n32bit_decoder_short_1__0), .dp(n32bit_decoder_short_1_dot));
  Hex_Digit_Display hex_digit_display_25 (.value(n32bit_decoder_short_8__1_2));  // open: dp
  Hex_Digit_Display hex_digit_display_26 (.value(n32bit_decoder_short_8__2_2));  // open: dp
  Hex_Digit_Display hex_digit_display_27 (.value(n32bit_decoder_short_2__0), .dp(n32bit_decoder_short_2_dot));
  Hex_Digit_Display hex_digit_display_28 (.value(n32bit_decoder_short_2__1_2));  // open: dp
  Hex_Digit_Display hex_digit_display_29 (.value(n32bit_decoder_short_3__2_2));  // open: dp
  Hex_Digit_Display hex_digit_display_30 (.value(n32bit_decoder_short_3__1_2));  // open: dp
  Hex_Digit_Display hex_digit_display_31 (.value(n32bit_decoder_short_4__1_2));  // open: dp
  Hex_Digit_Display hex_digit_display_32 (.value(n32bit_decoder_short_4__0), .dp(n32bit_decoder_short_4_dot));
  Hex_Digit_Display hex_digit_display_33 (.value(n32bit_decoder_short_5__2_2));  // open: dp
  Hex_Digit_Display hex_digit_display_34 (.value(n32bit_decoder_short_5__1_2));  // open: dp
  Hex_Digit_Display hex_digit_display_35 (.value(n32bit_decoder_short_6__0), .dp(n32bit_decoder_short_6_dot));
  Hex_Digit_Display hex_digit_display_36 (.value(n32bit_decoder_short_6__1));  // open: dp
  Hex_Digit_Display hex_digit_display_37 (.value(n32bit_decoder_short_7__0), .dp(n32bit_decoder_short_7_dot));
  Hex_Digit_Display hex_digit_display_38 (.value(n32bit_decoder_short_7__1_2));  // open: dp
  Hex_Digit_Display hex_digit_display_39 (.value(n32bit_decoder_short_1__1));  // open: dp
  Hex_Digit_Display hex_digit_display_40 (.value(n32bit_decoder_short_1__2));  // open: dp
  Hex_Digit_Display hex_digit_display_41 (.value(n32bit_decoder_short_8__1));  // open: dp
  Hex_Digit_Display hex_digit_display_42 (.value(n32bit_decoder_short_8__0), .dp(n32bit_decoder_short_8_dot));
  Hex_Digit_Display hex_digit_display_43 (.value(n32bit_decoder_short_2__1));  // open: dp
  Hex_Digit_Display hex_digit_display_44 (.value(n32bit_decoder_short_2__2));  // open: dp
  Hex_Digit_Display hex_digit_display_45 (.value(n32bit_decoder_short_3__1));  // open: dp
  Hex_Digit_Display hex_digit_display_46 (.value(n32bit_decoder_short_3__0), .dp(n32bit_decoder_short_3_dot));
  Hex_Digit_Display hex_digit_display_47 (.value(n32bit_decoder_short_4__2));  // open: dp
  Hex_Digit_Display hex_digit_display_48 (.value(n32bit_decoder_short_4__1));  // open: dp
  Hex_Digit_Display hex_digit_display_49 (.value(n32bit_decoder_short_5__0), .dp(n32bit_decoder_short_5_dot));
  Hex_Digit_Display hex_digit_display_50 (.value(n32bit_decoder_short_5__1));  // open: dp
  Hex_Digit_Display hex_digit_display_51 (.value(n32bit_decoder_short_6__3_2));  // open: dp
  Hex_Digit_Display hex_digit_display_52 (.value(n32bit_decoder_short_6__2));  // open: dp
  Hex_Digit_Display hex_digit_display_53 (.value(n32bit_decoder_short_7__1));  // open: dp
  Hex_Digit_Display hex_digit_display_54 (.value(n32bit_decoder_short_7__2));  // open: dp
  Hex_Digit_Display hex_digit_display_55 (.value(n32bit_decoder_short_1__4_2));  // open: dp
  Hex_Digit_Display hex_digit_display_56 (.value(n32bit_decoder_short_1__3_2));  // open: dp
  Hex_Digit_Display hex_digit_display_57 (.value(n32bit_decoder_short_8__3_2));  // open: dp
  Hex_Digit_Display hex_digit_display_58 (.value(n32bit_decoder_short_8__2));  // open: dp
  Hex_Digit_Display hex_digit_display_59 (.value(n32bit_decoder_short_2__4_2));  // open: dp
  Hex_Digit_Display hex_digit_display_60 (.value(n32bit_decoder_short_2__3_2));  // open: dp
  Hex_Digit_Display hex_digit_display_61 (.value(n32bit_decoder_short_3__3_2));  // open: dp
  Hex_Digit_Display hex_digit_display_62 (.value(n32bit_decoder_short_3__2));  // open: dp
  Hex_Digit_Display hex_digit_display_63 (.value(n32bit_decoder_short_4__3_2));  // open: dp
  Hex_Digit_Display hex_digit_display_64 (.value(n32bit_decoder_short_4__4_2));  // open: dp
  Hex_Digit_Display hex_digit_display_65 (.value(n32bit_decoder_short_5__2));  // open: dp
  Hex_Digit_Display hex_digit_display_66 (.value(n32bit_decoder_short_5__3_2));  // open: dp
  Hex_Digit_Display hex_digit_display_67 (.value(n32bit_decoder_short_6__5));  // open: dp
  Hex_Digit_Display hex_digit_display_68 (.value(n32bit_decoder_short_6__4_2));  // open: dp
  Hex_Digit_Display hex_digit_display_69 (.value(n32bit_decoder_short_7__3_2));  // open: dp
  Hex_Digit_Display hex_digit_display_70 (.value(n32bit_decoder_short_7__4_2));  // open: dp
  Hex_Digit_Display hex_digit_display_71 (.value(n32bit_decoder_short_1__5));  // open: dp
  _32bit_decoder_short u_32bit_decoder_short_1 (
    .sign(n32bit_decoder_short_1_sign), ._4(n32bit_decoder_short_1__4), ._3(n32bit_decoder_short_1__3),
    ._2_2(n32bit_decoder_short_1__2_2), ._1_2(n32bit_decoder_short_1__1_2), ._0(n32bit_decoder_short_1__0),
    .dot(n32bit_decoder_short_1_dot), .in(rom_4_data), ._1(n32bit_decoder_short_1__1),
    ._2(n32bit_decoder_short_1__2), ._3_2(n32bit_decoder_short_1__3_2), ._4_2(n32bit_decoder_short_1__4_2),
    ._5(n32bit_decoder_short_1__5));
  Hex_Digit_Display hex_digit_display_72 (.value(n32bit_decoder_short_8__4_2));  // open: dp
  Hex_Digit_Display hex_digit_display_73 (.value(n32bit_decoder_short_8__5));  // open: dp
  _7_Segment_Display u_7_segment_display_9 (.g(n32bit_decoder_short_9_sign));  // open: f, a, b, e, d, c, dp
  Hex_Digit_Display hex_digit_display_74 (.value(n32bit_decoder_short_9__4));  // open: dp
  Hex_Digit_Display hex_digit_display_75 (.value(n32bit_decoder_short_2__5));  // open: dp
  _32bit_decoder_short u_32bit_decoder_short_2 (
    .sign(n32bit_decoder_short_2_sign), ._4(n32bit_decoder_short_2__4), ._3(n32bit_decoder_short_2__3),
    ._2_2(n32bit_decoder_short_2__2_2), ._1_2(n32bit_decoder_short_2__1_2), ._0(n32bit_decoder_short_2__0),
    .dot(n32bit_decoder_short_2_dot), .in(rom_7_data), ._1(n32bit_decoder_short_2__1),
    ._2(n32bit_decoder_short_2__2), ._3_2(n32bit_decoder_short_2__3_2), ._4_2(n32bit_decoder_short_2__4_2),
    ._5(n32bit_decoder_short_2__5));
  Hex_Digit_Display hex_digit_display_76 (.value(n32bit_decoder_short_3__5));  // open: dp
  Hex_Digit_Display hex_digit_display_77 (.value(n32bit_decoder_short_3__4_2));  // open: dp
  _32bit_decoder_short u_32bit_decoder_short_3 (
    .sign(n32bit_decoder_short_3_sign), ._4(n32bit_decoder_short_3__4), ._3(n32bit_decoder_short_3__3),
    ._2_2(n32bit_decoder_short_3__2_2), ._1_2(n32bit_decoder_short_3__1_2), ._0(n32bit_decoder_short_3__0),
    .dot(n32bit_decoder_short_3_dot), .in(rom_1_data), ._1(n32bit_decoder_short_3__1),
    ._2(n32bit_decoder_short_3__2), ._3_2(n32bit_decoder_short_3__3_2), ._4_2(n32bit_decoder_short_3__4_2),
    ._5(n32bit_decoder_short_3__5));
  Hex_Digit_Display hex_digit_display_78 (.value(n32bit_decoder_short_4__5));  // open: dp
  _32bit_decoder_short u_32bit_decoder_short_4 (
    .sign(n32bit_decoder_short_4_sign), ._4(n32bit_decoder_short_4__4), ._3(n32bit_decoder_short_4__3),
    ._2_2(n32bit_decoder_short_4__2_2), ._1_2(n32bit_decoder_short_4__1_2), ._0(n32bit_decoder_short_4__0),
    .dot(n32bit_decoder_short_4_dot), .in(rom_8_data), ._1(n32bit_decoder_short_4__1),
    ._2(n32bit_decoder_short_4__2), ._3_2(n32bit_decoder_short_4__3_2), ._4_2(n32bit_decoder_short_4__4_2),
    ._5(n32bit_decoder_short_4__5));
  Hex_Digit_Display hex_digit_display_79 (.value(n32bit_decoder_short_5__4_2));  // open: dp
  Hex_Digit_Display hex_digit_display_80 (.value(n32bit_decoder_short_5__5));  // open: dp
  _32bit_decoder_short u_32bit_decoder_short_5 (
    .sign(n32bit_decoder_short_5_sign), ._4(n32bit_decoder_short_5__4), ._3(n32bit_decoder_short_5__3),
    ._2_2(n32bit_decoder_short_5__2_2), ._1_2(n32bit_decoder_short_5__1_2), ._0(n32bit_decoder_short_5__0),
    .dot(n32bit_decoder_short_5_dot), .in(not_2_out), ._1(n32bit_decoder_short_5__1),
    ._2(n32bit_decoder_short_5__2), ._3_2(n32bit_decoder_short_5__3_2), ._4_2(n32bit_decoder_short_5__4_2),
    ._5(n32bit_decoder_short_5__5));
  _32bit_decoder_short u_32bit_decoder_short_6 (
    .sign(n32bit_decoder_short_6_sign), ._4(n32bit_decoder_short_6__4), ._3(n32bit_decoder_short_6__3),
    ._2_2(n32bit_decoder_short_6__2_2), ._1_2(n32bit_decoder_short_6__1_2), ._0(n32bit_decoder_short_6__0),
    .dot(n32bit_decoder_short_6_dot), .in(not_3_out), ._1(n32bit_decoder_short_6__1),
    ._2(n32bit_decoder_short_6__2), ._3_2(n32bit_decoder_short_6__3_2), ._4_2(n32bit_decoder_short_6__4_2),
    ._5(n32bit_decoder_short_6__5));
  Hex_Digit_Display hex_digit_display_81 (.value(n32bit_decoder_short_7__5));  // open: dp
  _32bit_decoder_short u_32bit_decoder_short_7 (
    .sign(n32bit_decoder_short_7_sign), ._4(n32bit_decoder_short_7__4), ._3(n32bit_decoder_short_7__3),
    ._2_2(n32bit_decoder_short_7__2_2), ._1_2(n32bit_decoder_short_7__1_2), ._0(n32bit_decoder_short_7__0),
    .dot(n32bit_decoder_short_7_dot), .in(not_4_out), ._1(n32bit_decoder_short_7__1),
    ._2(n32bit_decoder_short_7__2), ._3_2(n32bit_decoder_short_7__3_2), ._4_2(n32bit_decoder_short_7__4_2),
    ._5(n32bit_decoder_short_7__5));
  _32bit_decoder_short u_32bit_decoder_short_8 (
    .sign(n32bit_decoder_short_8_sign), ._4(n32bit_decoder_short_8__4), ._3(n32bit_decoder_short_8__3),
    ._2_2(n32bit_decoder_short_8__2_2), ._1_2(n32bit_decoder_short_8__1_2), ._0(n32bit_decoder_short_8__0),
    .dot(n32bit_decoder_short_8_dot), .in(not_1_out), ._1(n32bit_decoder_short_8__1),
    ._2(n32bit_decoder_short_8__2), ._3_2(n32bit_decoder_short_8__3_2), ._4_2(n32bit_decoder_short_8__4_2),
    ._5(n32bit_decoder_short_8__5));
  Hex_Digit_Display hex_digit_display_82 (.value(n32bit_decoder_short_9__2_2));  // open: dp
  Hex_Digit_Display hex_digit_display_83 (.value(n32bit_decoder_short_9__3));  // open: dp
  Hex_Digit_Display hex_digit_display_84 (.value(n32bit_decoder_short_9__1_2));  // open: dp
  Hex_Digit_Display hex_digit_display_85 (.value(n32bit_decoder_short_9__0), .dp(n32bit_decoder_short_9_dot));
  Hex_Digit_Display hex_digit_display_86 (.value(n32bit_decoder_short_9__1));  // open: dp
  Hex_Digit_Display hex_digit_display_87 (.value(n32bit_decoder_short_9__2));  // open: dp
  Hex_Digit_Display hex_digit_display_88 (.value(n32bit_decoder_short_9__4_2));  // open: dp
  Hex_Digit_Display hex_digit_display_89 (.value(n32bit_decoder_short_9__3_2));  // open: dp
  Hex_Digit_Display hex_digit_display_90 (.value(n32bit_decoder_short_9__5));  // open: dp
  _32bit_decoder_short u_32bit_decoder_short_9 (
    .sign(n32bit_decoder_short_9_sign), ._4(n32bit_decoder_short_9__4), ._3(n32bit_decoder_short_9__3),
    ._2_2(n32bit_decoder_short_9__2_2), ._1_2(n32bit_decoder_short_9__1_2), ._0(n32bit_decoder_short_9__0),
    .dot(n32bit_decoder_short_9_dot), .in(fp_div_1_out), ._1(n32bit_decoder_short_9__1),
    ._2(n32bit_decoder_short_9__2), ._3_2(n32bit_decoder_short_9__3_2), ._4_2(n32bit_decoder_short_9__4_2),
    ._5(n32bit_decoder_short_9__5));

  // Notes on the sheet:
  //   IV Cwiara
  //   I Cwiara
  //   I Cwiara
  //   II Cwiara
  //   III Cwiara
  //   COSINUS
  //   COSINUS
  //   COSINUS
  //   COSINUS
  //   SINUS
  //   COSINUS
  //   SINUS
  //   contents of rom_1 (hex, n*v repeats v):
  //   10000 fff2 ffd8 ffa4 ff62 ff06 fe97 fe14 fd84 fcd9 fc1b fb4a fa64 f972 f865 f745 f617 f4d0 f37b f20c
  //   f090 ef00 ed5c eba5 e9db e803 e617 e418 e205 dfe5 ddb2 db71 d916 d6b5 d439 d1b7 cf1a cc71 c9ba c6f0
  //   c418 c134 be3b bb3d b824 b504 b1d7 ae97 ab4a a7f6 a48e a119 9d9e 9a0f 967a 92d7 8f27 8b6a 87a7 83d7
  //   8000 7c1b 7831 7439 703a 6c2f 681d 6404 5fe5 5bc0 578d 535a 4f1a 4ada 468d 4240 3ded 3999 3538 30d8
  //   2c71 2809 23a2 1f34 1ac0 1652 11de d63 8ef 47a
  //   SINUS
  //   contents of rom_2 (hex, n*v repeats v):
  //   0 47a 8ef d63 11de 1652 1ac0 1f34 23a2 2809 2c71 30d8 3538 3999 3ded 4240 468d 4ada 4f1a 535a 578d
  //   5bc0 5fe5 6404 681d 6c2f 703a 7439 7831 7c1b 8000 83d7 87a7 8b6a 8f27 92d7 967a 9a0f 9d9e a119 a48e
  //   a7f6 ab4a ae97 b1d7 b504 b824 bb3d be3b c134 c418 c6f0 c9ba cc71 cf1a d1b7 d439 d6b5 d916 db71 ddb2
  //   dfe5 e205 e418 e617 e803 e9db eba5 ed5c ef00 f090 f20c f37b f4d0 f617 f745 f865 f972 fa64 fb4a fc1b
  //   fcd9 fd84 fe14 fe97 ff06 ff62 ffa4 ffd8 fff2 10000
  //   SINUS
  //   contents of rom_3 (hex, n*v repeats v):
  //   10000 fff2 ffd8 ffa4 ff62 ff06 fe97 fe14 fd84 fcd9 fc1b fb4a fa64 f972 f865 f745 f617 f4d0 f37b f20c
  //   f090 ef00 ed5c eba5 e9db e803 e617 e418 e205 dfe5 ddb2 db71 d916 d6b5 d439 d1b7 cf1a cc71 c9ba c6f0
  //   c418 c134 be3b bb3d b824 b504 b1d7 ae97 ab4a a7f6 a48e a119 9d9e 9a0f 967a 92d7 8f27 8b6a 87a7 83d7
  //   8000 7c1b 7831 7439 703a 6c2f 681d 6404 5fe5 5bc0 578d 535a 4f1a 4ada 468d 4240 3ded 3999 3538 30d8
  //   2c71 2809 23a2 1f34 1ac0 1652 11de d63 8ef 47a
  //   contents of rom_4 (hex, n*v repeats v):
  //   0 47a 8ef d63 11de 1652 1ac0 1f34 23a2 2809 2c71 30d8 3538 3999 3ded 4240 468d 4ada 4f1a 535a 578d
  //   5bc0 5fe5 6404 681d 6c2f 703a 7439 7831 7c1b 8000 83d7 87a7 8b6a 8f27 92d7 967a 9a0f 9d9e a119 a48e
  //   a7f6 ab4a ae97 b1d7 b504 b824 bb3d be3b c134 c418 c6f0 c9ba cc71 cf1a d1b7 d439 d6b5 d916 db71 ddb2
  //   dfe5 e205 e418 e617 e803 e9db eba5 ed5c ef00 f090 f20c f37b f4d0 f617 f745 f865 f972 fa64 fb4a fc1b
  //   fcd9 fd84 fe14 fe97 ff06 ff62 ffa4 ffd8 fff2 10000
  //   contents of rom_5 (hex, n*v repeats v):
  //   10000 fff2 ffd8 ffa4 ff62 ff06 fe97 fe14 fd84 fcd9 fc1b fb4a fa64 f972 f865 f745 f617 f4d0 f37b f20c
  //   f090 ef00 ed5c eba5 e9db e803 e617 e418 e205 dfe5 ddb2 db71 d916 d6b5 d439 d1b7 cf1a cc71 c9ba c6f0
  //   c418 c134 be3b bb3d b824 b504 b1d7 ae97 ab4a a7f6 a48e a119 9d9e 9a0f 967a 92d7 8f27 8b6a 87a7 83d7
  //   8000 7c1b 7831 7439 703a 6c2f 681d 6404 5fe5 5bc0 578d 535a 4f1a 4ada 468d 4240 3ded 3999 3538 30d8
  //   2c71 2809 23a2 1f34 1ac0 1652 11de d63 8ef 47a
  //   SINUS
  //   contents of rom_6 (hex, n*v repeats v):
  //   10000 fff2 ffd8 ffa4 ff62 ff06 fe97 fe14 fd84 fcd9 fc1b fb4a fa64 f972 f865 f745 f617 f4d0 f37b f20c
  //   f090 ef00 ed5c eba5 e9db e803 e617 e418 e205 dfe5 ddb2 db71 d916 d6b5 d439 d1b7 cf1a cc71 c9ba c6f0
  //   c418 c134 be3b bb3d b824 b504 b1d7 ae97 ab4a a7f6 a48e a119 9d9e 9a0f 967a 92d7 8f27 8b6a 87a7 83d7
  //   8000 7c1b 7831 7439 703a 6c2f 681d 6404 5fe5 5bc0 578d 535a 4f1a 4ada 468d 4240 3ded 3999 3538 30d8
  //   2c71 2809 23a2 1f34 1ac0 1652 11de d63 8ef 47a
  //   contents of rom_7 (hex, n*v repeats v):
  //   0 47a 8ef d63 11de 1652 1ac0 1f34 23a2 2809 2c71 30d8 3538 3999 3ded 4240 468d 4ada 4f1a 535a 578d
  //   5bc0 5fe5 6404 681d 6c2f 703a 7439 7831 7c1b 8000 83d7 87a7 8b6a 8f27 92d7 967a 9a0f 9d9e a119 a48e
  //   a7f6 ab4a ae97 b1d7 b504 b824 bb3d be3b c134 c418 c6f0 c9ba cc71 cf1a d1b7 d439 d6b5 d916 db71 ddb2
  //   dfe5 e205 e418 e617 e803 e9db eba5 ed5c ef00 f090 f20c f37b f4d0 f617 f745 f865 f972 fa64 fb4a fc1b
  //   fcd9 fd84 fe14 fe97 ff06 ff62 ffa4 ffd8 fff2 10000
  //   contents of rom_8 (hex, n*v repeats v):
  //   10000 fff2 ffd8 ffa4 ff62 ff06 fe97 fe14 fd84 fcd9 fc1b fb4a fa64 f972 f865 f745 f617 f4d0 f37b f20c
  //   f090 ef00 ed5c eba5 e9db e803 e617 e418 e205 dfe5 ddb2 db71 d916 d6b5 d439 d1b7 cf1a cc71 c9ba c6f0
  //   c418 c134 be3b bb3d b824 b504 b1d7 ae97 ab4a a7f6 a48e a119 9d9e 9a0f 967a 92d7 8f27 8b6a 87a7 83d7
  //   8000 7c1b 7831 7439 703a 6c2f 681d 6404 5fe5 5bc0 578d 535a 4f1a 4ada 468d 4240 3ded 3999 3538 30d8
  //   2c71 2809 23a2 1f34 1ac0 1652 11de d63 8ef 47a
  //   contents of rom_9 (hex, n*v repeats v):
  //   0 47a 8ef d63 11de 1652 1ac0 1f34 23a2 2809 2c71 30d8 3538 3999 3ded 4240 468d 4ada 4f1a 535a 578d
  //   5bc0 5fe5 6404 681d 6c2f 703a 7439 7831 7c1b 8000 83d7 87a7 8b6a 8f27 92d7 967a 9a0f 9d9e a119 a48e
  //   a7f6 ab4a ae97 b1d7 b504 b824 bb3d be3b c134 c418 c6f0 c9ba cc71 cf1a d1b7 d439 d6b5 d916 db71 ddb2
  //   dfe5 e205 e418 e617 e803 e9db eba5 ed5c ef00 f090 f20c f37b f4d0 f617 f745 f865 f972 fa64 fb4a fc1b
  //   fcd9 fd84 fe14 fe97 ff06 ff62 ffa4 ffd8 fff2 10000
  //   contents of rom_10 (hex, n*v repeats v):
  //   0 47a 8ef d63 11de 1652 1ac0 1f34 23a2 2809 2c71 30d8 3538 3999 3ded 4240 468d 4ada 4f1a 535a 578d
  //   5bc0 5fe5 6404 681d 6c2f 703a 7439 7831 7c1b 8000 83d7 87a7 8b6a 8f27 92d7 967a 9a0f 9d9e a119 a48e
  //   a7f6 ab4a ae97 b1d7 b504 b824 bb3d be3b c134 c418 c6f0 c9ba cc71 cf1a d1b7 d439 d6b5 d916 db71 ddb2
  //   dfe5 e205 e418 e617 e803 e9db eba5 ed5c ef00 f090 f20c f37b f4d0 f617 f745 f865 f972 fa64 fb4a fc1b
  //   fcd9 fd84 fe14 fe97 ff06 ff62 ffa4 ffd8 fff2 10000
endmodule
