// Logisim project main - kopia (3).circ as structural Verilog: 11 circuits, main circuit main
module main (
  input  in_1,
  input  in_2
);

  wire buffer_1_out, clk, dda_sync_1_set_point, dda_sync_2_p7, dda_sync_2_p8, dda_sync_2_p9, dda_sync_2_p11,
       dda_sync_3_p7, dda_sync_3_p8, dda_sync_3_p9, dda_sync_4_p7, dda_sync_4_p8, dda_sync_4_p9,
       dda_sync_5_set_point, dda_sync_6_p7, dda_sync_6_p8, dda_sync_6_p9, dda_sync_7_p7, dda_sync_7_p8,
       dda_sync_7_p9, dda_sync_8_p7, dda_sync_8_p8, dda_sync_8_p9, merger_x8_1_p1, merger_x8_1_p2,
       merger_x8_1_p3, merger_x8_1_p4, pull_resistor_1_node, rising_edge_pulse_1_out, start_DDA_out,
       update_2d_points, update_3d_points, update_out, vram_ss_1_p4, vram_ss_1_p5, vram_ss_1_p6,
       vram_ss_1_p7, vram_ss_2_p5, vram_ss_2_p6, vram_ss_2_p7, vram_ss_2_p8, vram_ss_3_p5, vram_ss_3_p6,
       vram_ss_3_p7, vram_ss_3_p8, vram_ss_4_p5, vram_ss_4_p6, vram_ss_4_p7, vram_ss_4_p8, vram_ss_5_p5,
       vram_ss_5_p6, vram_ss_5_p7, vram_ss_5_p8, vram_ss_6_p5, vram_ss_6_p6, vram_ss_6_p7, vram_ss_6_p8,
       vram_ss_7_p5, vram_ss_7_p6, vram_ss_7_p7, vram_ss_7_p8, vram_ss_8_p8, vram_ss_8_p9, vram_ss_8_p10,
       vram_ss_8_p11;
  wire [31:0] dda_sync_1_out_x, dda_sync_1_out_y, dda_sync_5_out_x, dda_sync_5_out_y, ex_2_1_out_3,
       ex_2_1_out_4, ex_2_1_out_5, ex_2_1_out_6, ex_2_1_out_7, ex_2_1_out_8, ex_2_1_out_9, ex_2_1_out_10,
       ex_2_1_out_11, ex_2_1_out_12, ex_2_1_out_13, ex_2_1_out_14, ex_2_1_out_15, ex_2_1_out_16,
       ex_2_1_out_17, ex_2_1_out_18, ex_2_1_out_19, ex_2_1_out_20, ex_2_1_out_21, ex_2_1_out_22,
       ex_2_1_out_23, ex_2_1_out_24, ex_2_1_out_25, ex_2_1_out_26, ex_2_1_out_27, ex_2_1_out_28,
       ex_2_1_out_29, ex_2_1_out_30, ex_2_1_out_31, ex_2_1_out_32, ex_2_1_out_33, ex_2_1_out_34,
       ex_2_1_out_35, ex_2_1_out_36, ex_2_1_out_37, ex_2_1_out_38, ex_2_1_out_39, ex_2_1_out_40,
       ex_2_1_out_41, ex_2_1_out_42, ex_2_1_out_43, ex_2_1_out_44, ex_2_1_out_45, ex_2_1_out_46,
       ex_2_1_out_47, ex_2_1_out_48, ex_2_1_out_49, ex_2_1_out_50, matrix_2x2_reg_1_out_11,
       matrix_2x2_reg_1_out_12, matrix_2x2_reg_1_out_21, matrix_2x2_reg_1_out_22, matrix_2x2_reg_2_out_11,
       matrix_2x2_reg_2_out_12, matrix_2x2_reg_2_out_21, matrix_2x2_reg_2_out_22, matrix_2x2_reg_3_out_11,
       matrix_2x2_reg_3_out_12, matrix_2x2_reg_3_out_21, matrix_2x2_reg_3_out_22, matrix_2x2_reg_4_out_11,
       matrix_2x2_reg_4_out_12, matrix_2x2_reg_4_out_21, matrix_2x2_reg_4_out_22, matrix_2x2_reg_5_out_11,
       matrix_2x2_reg_5_out_12, matrix_2x2_reg_5_out_21, matrix_2x2_reg_5_out_22, matrix_2x2_reg_6_out_11,
       matrix_2x2_reg_6_out_12, matrix_2x2_reg_6_out_21, matrix_2x2_reg_6_out_22, matrix_2x2_reg_7_out_11,
       matrix_2x2_reg_7_out_12, matrix_2x2_reg_7_out_21, matrix_2x2_reg_7_out_22, matrix_2x2_reg_8_out_11,
       matrix_2x2_reg_8_out_12, matrix_2x2_reg_8_out_21, matrix_2x2_reg_8_out_22, matrix_4x3_reg_1_out_11,
       matrix_4x3_reg_1_out_12, matrix_4x3_reg_1_out_13, matrix_4x3_reg_1_out_21, matrix_4x3_reg_1_out_22,
       matrix_4x3_reg_1_out_23, matrix_4x3_reg_1_out_31, matrix_4x3_reg_1_out_32, matrix_4x3_reg_1_out_33,
       matrix_4x3_reg_1_out_41, matrix_4x3_reg_1_out_42, matrix_4x3_reg_1_out_43, matrix_4x3_reg_2_out_11,
       matrix_4x3_reg_2_out_12, matrix_4x3_reg_2_out_13, matrix_4x3_reg_2_out_21, matrix_4x3_reg_2_out_22,
       matrix_4x3_reg_2_out_23, matrix_4x3_reg_2_out_31, matrix_4x3_reg_2_out_32, matrix_4x3_reg_2_out_33,
       matrix_4x3_reg_2_out_41, matrix_4x3_reg_2_out_42, matrix_4x3_reg_2_out_43, matrix_4x3_reg_3_out_11,
       matrix_4x3_reg_3_out_12, matrix_4x3_reg_3_out_13, matrix_4x3_reg_3_out_21, matrix_4x3_reg_3_out_22,
       matrix_4x3_reg_3_out_23, matrix_4x3_reg_3_out_31, matrix_4x3_reg_3_out_32, matrix_4x3_reg_3_out_33,
       matrix_4x3_reg_3_out_41, matrix_4x3_reg_3_out_42, matrix_4x3_reg_3_out_43, matrix_4x3_reg_4_out_11,
       matrix_4x3_reg_4_out_12, matrix_4x3_reg_4_out_13, matrix_4x3_reg_4_out_21, matrix_4x3_reg_4_out_22,
       matrix_4x3_reg_4_out_23, matrix_4x3_reg_4_out_31, matrix_4x3_reg_4_out_32, matrix_4x3_reg_4_out_33,
       matrix_4x3_reg_4_out_41, matrix_4x3_reg_4_out_42, matrix_4x3_reg_4_out_43,
       point_projector_x4_1_far_plane_bypass, point_projector_x4_1_fov_bypass,
       point_projector_x4_1_line1_x1_2, point_projector_x4_1_line1_x2_2, point_projector_x4_1_line1_y1_2,
       point_projector_x4_1_line1_y2_2, point_projector_x4_1_line2_x1_2, point_projector_x4_1_line2_x2_2,
       point_projector_x4_1_line2_y1_2, point_projector_x4_1_line2_y2_2,
       point_projector_x4_1_near_plane_bypass, point_projector_x4_2_far_plane_bypass,
       point_projector_x4_2_fov_bypass, point_projector_x4_2_line1_x1_2, point_projector_x4_2_line1_x2_2,
       point_projector_x4_2_line1_y1_2, point_projector_x4_2_line1_y2_2, point_projector_x4_2_line2_x1_2,
       point_projector_x4_2_line2_x2_2, point_projector_x4_2_line2_y1_2, point_projector_x4_2_line2_y2_2,
       point_projector_x4_2_near_plane_bypass, point_projector_x4_3_far_plane_bypass,
       point_projector_x4_3_fov_bypass, point_projector_x4_3_line1_x1_2, point_projector_x4_3_line1_x2_2,
       point_projector_x4_3_line1_y1_2, point_projector_x4_3_line1_y2_2, point_projector_x4_3_line2_x1_2,
       point_projector_x4_3_line2_x2_2, point_projector_x4_3_line2_y1_2, point_projector_x4_3_line2_y2_2,
       point_projector_x4_3_near_plane_bypass, point_projector_x4_4_line1_x1_2,
       point_projector_x4_4_line1_x2_2, point_projector_x4_4_line1_y1_2, point_projector_x4_4_line1_y2_2,
       point_projector_x4_4_line2_x1_2, point_projector_x4_4_line2_x2_2, point_projector_x4_4_line2_y1_2,
       point_projector_x4_4_line2_y2_2, test_rot_1_out_6, test_rot_1_out_7, test_rot_1_out_8,
       test_rot_2_out_6, test_rot_2_out_7, test_rot_2_out_8, test_rot_3_out_6, test_rot_3_out_7,
       test_rot_3_out_8, test_rot_4_out_6, test_rot_4_out_7, test_rot_4_out_8, test_rot_5_out_6,
       test_rot_5_out_7, test_rot_5_out_8, test_rot_6_out_6, test_rot_6_out_7, test_rot_6_out_8,
       test_rot_7_out_6, test_rot_7_out_7, test_rot_7_out_8, test_rot_8_out_6, test_rot_8_out_7,
       test_rot_8_out_8, test_rot_9_out_6, test_rot_9_out_7, test_rot_9_out_8, test_rot_10_out_6,
       test_rot_10_out_7, test_rot_10_out_8, test_rot_11_out_6, test_rot_11_out_7, test_rot_11_out_8,
       test_rot_12_out_6, test_rot_12_out_7, test_rot_12_out_8, test_rot_13_out_6, test_rot_13_out_7,
       test_rot_13_out_8, test_rot_14_out_6, test_rot_14_out_7, test_rot_14_out_8, test_rot_15_out_6,
       test_rot_15_out_7, test_rot_15_out_8, test_rot_16_out_6, test_rot_16_out_7, test_rot_16_out_8;

  Clock clock_1 (.out(clk));
  ex_2 ex_2_1 (
    .distance(32'h40000), .side_size(32'h10000), .out_3(ex_2_1_out_3), .out_4(ex_2_1_out_4),
    .out_5(ex_2_1_out_5), .out_6(ex_2_1_out_6), .out_7(ex_2_1_out_7), .out_8(ex_2_1_out_8),
    .out_9(ex_2_1_out_9), .out_10(ex_2_1_out_10), .out_11(ex_2_1_out_11), .out_12(ex_2_1_out_12),
    .out_13(ex_2_1_out_13), .out_14(ex_2_1_out_14), .out_15(ex_2_1_out_15), .out_16(ex_2_1_out_16),
    .out_17(ex_2_1_out_17), .out_18(ex_2_1_out_18), .out_19(ex_2_1_out_19), .out_20(ex_2_1_out_20),
    .out_21(ex_2_1_out_21), .out_22(ex_2_1_out_22), .out_23(ex_2_1_out_23), .out_24(ex_2_1_out_24),
    .out_25(ex_2_1_out_25), .out_26(ex_2_1_out_26), .out_27(ex_2_1_out_27), .out_28(ex_2_1_out_28),
    .out_29(ex_2_1_out_29), .out_30(ex_2_1_out_30), .out_31(ex_2_1_out_31), .out_32(ex_2_1_out_32),
    .out_33(ex_2_1_out_33), .out_34(ex_2_1_out_34), .out_35(ex_2_1_out_35), .out_36(ex_2_1_out_36),
    .out_37(ex_2_1_out_37), .out_38(ex_2_1_out_38), .out_39(ex_2_1_out_39), .out_40(ex_2_1_out_40),
    .out_41(ex_2_1_out_41), .out_42(ex_2_1_out_42), .out_43(ex_2_1_out_43), .out_44(ex_2_1_out_44),
    .out_45(ex_2_1_out_45), .out_46(ex_2_1_out_46), .out_47(ex_2_1_out_47), .out_48(ex_2_1_out_48),
    .out_49(ex_2_1_out_49), .out_50(ex_2_1_out_50));
  Button u_update_3d_points (.out(update_3d_points));
  test_rot test_rot_1 (
    .distance(32'h40000), .rotation(32'h2d0000), .in_3(ex_2_1_out_3), .in_4(ex_2_1_out_7),
    .in_5(ex_2_1_out_11), .out_6(test_rot_1_out_6), .out_7(test_rot_1_out_7), .out_8(test_rot_1_out_8));
  test_rot test_rot_2 (
    .distance(32'h40000), .rotation(32'h2d0000), .in_3(ex_2_1_out_15), .in_4(ex_2_1_out_19),
    .in_5(ex_2_1_out_23), .out_6(test_rot_2_out_6), .out_7(test_rot_2_out_7), .out_8(test_rot_2_out_8));
  test_rot test_rot_3 (
    .distance(32'h40000), .rotation(32'h2d0000), .in_3(ex_2_1_out_4), .in_4(ex_2_1_out_8),
    .in_5(ex_2_1_out_12), .out_6(test_rot_3_out_6), .out_7(test_rot_3_out_7), .out_8(test_rot_3_out_8));
  test_rot test_rot_4 (
    .distance(32'h40000), .rotation(32'h2d0000), .in_3(ex_2_1_out_16), .in_4(ex_2_1_out_20),
    .in_5(ex_2_1_out_24), .out_6(test_rot_4_out_6), .out_7(test_rot_4_out_7), .out_8(test_rot_4_out_8));
  test_rot test_rot_5 (
    .distance(32'h40000), .rotation(32'h2d0000), .in_3(ex_2_1_out_5), .in_4(ex_2_1_out_9),
    .in_5(ex_2_1_out_13), .out_6(test_rot_5_out_6), .out_7(test_rot_5_out_7), .out_8(test_rot_5_out_8));
  test_rot test_rot_6 (
    .distance(32'h40000), .rotation(32'h2d0000), .in_3(ex_2_1_out_17), .in_4(ex_2_1_out_21),
    .in_5(ex_2_1_out_25), .out_6(test_rot_6_out_6), .out_7(test_rot_6_out_7), .out_8(test_rot_6_out_8));
  test_rot test_rot_7 (
    .distance(32'h40000), .rotation(32'h2d0000), .in_3(ex_2_1_out_6), .in_4(ex_2_1_out_10),
    .in_5(ex_2_1_out_14), .out_6(test_rot_7_out_6), .out_7(test_rot_7_out_7), .out_8(test_rot_7_out_8));
  test_rot test_rot_8 (
    .distance(32'h40000), .rotation(32'h2d0000), .in_3(ex_2_1_out_18), .in_4(ex_2_1_out_22),
    .in_5(ex_2_1_out_26), .out_6(test_rot_8_out_6), .out_7(test_rot_8_out_7), .out_8(test_rot_8_out_8));
  test_rot test_rot_9 (
    .distance(32'h40000), .rotation(32'h2d0000), .in_3(ex_2_1_out_27), .in_4(ex_2_1_out_31),
    .in_5(ex_2_1_out_35), .out_6(test_rot_9_out_6), .out_7(test_rot_9_out_7), .out_8(test_rot_9_out_8));
  test_rot test_rot_10 (
    .distance(32'h40000), .rotation(32'h2d0000), .in_3(ex_2_1_out_39), .in_4(ex_2_1_out_43),
    .in_5(ex_2_1_out_47), .out_6(test_rot_10_out_6), .out_7(test_rot_10_out_7), .out_8(test_rot_10_out_8));
  test_rot test_rot_11 (
    .distance(32'h40000), .rotation(32'h2d0000), .in_3(ex_2_1_out_28), .in_4(ex_2_1_out_32),
    .in_5(ex_2_1_out_36), .out_6(test_rot_11_out_6), .out_7(test_rot_11_out_7), .out_8(test_rot_11_out_8));
  test_rot test_rot_12 (
    .distance(32'h40000), .rotation(32'h2d0000), .in_3(ex_2_1_out_40), .in_4(ex_2_1_out_44),
    .in_5(ex_2_1_out_48), .out_6(test_rot_12_out_6), .out_7(test_rot_12_out_7), .out_8(test_rot_12_out_8));
  test_rot test_rot_13 (
    .distance(32'h40000), .rotation(32'h2d0000), .in_3(ex_2_1_out_29), .in_4(ex_2_1_out_33),
    .in_5(ex_2_1_out_37), .out_6(test_rot_13_out_6), .out_7(test_rot_13_out_7), .out_8(test_rot_13_out_8));
  test_rot test_rot_14 (
    .distance(32'h40000), .rotation(32'h2d0000), .in_3(ex_2_1_out_41), .in_4(ex_2_1_out_45),
    .in_5(ex_2_1_out_49), .out_6(test_rot_14_out_6), .out_7(test_rot_14_out_7), .out_8(test_rot_14_out_8));
  test_rot test_rot_15 (
    .distance(32'h40000), .rotation(32'h2d0000), .in_3(ex_2_1_out_30), .in_4(ex_2_1_out_34),
    .in_5(ex_2_1_out_38), .out_6(test_rot_15_out_6), .out_7(test_rot_15_out_7), .out_8(test_rot_15_out_8));
  test_rot test_rot_16 (
    .distance(32'h40000), .rotation(32'h2d0000), .in_3(ex_2_1_out_42), .in_4(ex_2_1_out_46),
    .in_5(ex_2_1_out_50), .out_6(test_rot_16_out_6), .out_7(test_rot_16_out_7), .out_8(test_rot_16_out_8));
  matrix_4x3_reg matrix_4x3_reg_1 (
    .clk(update_3d_points), .in_11(test_rot_1_out_6), .in_21(test_rot_2_out_6), .in_31(test_rot_3_out_6),
    .in_41(test_rot_4_out_6), .in_12(test_rot_1_out_7), .in_22(test_rot_2_out_7), .in_32(test_rot_3_out_7),
    .in_42(test_rot_4_out_7), .in_13(test_rot_1_out_8), .in_23(test_rot_2_out_8), .in_33(test_rot_3_out_8),
    .in_43(test_rot_4_out_8), .out_11(matrix_4x3_reg_1_out_11), .out_21(matrix_4x3_reg_1_out_21),
    .out_31(matrix_4x3_reg_1_out_31), .out_41(matrix_4x3_reg_1_out_41), .out_12(matrix_4x3_reg_1_out_12),
    .out_22(matrix_4x3_reg_1_out_22), .out_32(matrix_4x3_reg_1_out_32), .out_42(matrix_4x3_reg_1_out_42),
    .out_13(matrix_4x3_reg_1_out_13), .out_23(matrix_4x3_reg_1_out_23), .out_33(matrix_4x3_reg_1_out_33),
    .out_43(matrix_4x3_reg_1_out_43));  // open: rst
  matrix_4x3_reg matrix_4x3_reg_2 (
    .clk(update_3d_points), .in_11(test_rot_5_out_6), .in_21(test_rot_6_out_6), .in_31(test_rot_7_out_6),
    .in_41(test_rot_8_out_6), .in_12(test_rot_5_out_7), .in_22(test_rot_6_out_7), .in_32(test_rot_7_out_7),
    .in_42(test_rot_8_out_7), .in_13(test_rot_5_out_8), .in_23(test_rot_6_out_8), .in_33(test_rot_7_out_8),
    .in_43(test_rot_8_out_8), .out_11(matrix_4x3_reg_2_out_11), .out_21(matrix_4x3_reg_2_out_21),
    .out_31(matrix_4x3_reg_2_out_31), .out_41(matrix_4x3_reg_2_out_41), .out_12(matrix_4x3_reg_2_out_12),
    .out_22(matrix_4x3_reg_2_out_22), .out_32(matrix_4x3_reg_2_out_32), .out_42(matrix_4x3_reg_2_out_42),
    .out_13(matrix_4x3_reg_2_out_13), .out_23(matrix_4x3_reg_2_out_23), .out_33(matrix_4x3_reg_2_out_33),
    .out_43(matrix_4x3_reg_2_out_43));  // open: rst
  matrix_4x3_reg matrix_4x3_reg_3 (
    .clk(update_3d_points), .in_11(test_rot_9_out_6), .in_21(test_rot_10_out_6), .in_31(test_rot_11_out_6),
    .in_41(test_rot_12_out_6), .in_12(test_rot_9_out_7), .in_22(test_rot_10_out_7),
    .in_32(test_rot_11_out_7), .in_42(test_rot_12_out_7), .in_13(test_rot_9_out_8),
    .in_23(test_rot_10_out_8), .in_33(test_rot_11_out_8), .in_43(test_rot_12_out_8),
    .out_11(matrix_4x3_reg_3_out_11), .out_21(matrix_4x3_reg_3_out_21), .out_31(matrix_4x3_reg_3_out_31),
    .out_41(matrix_4x3_reg_3_out_41), .out_12(matrix_4x3_reg_3_out_12), .out_22(matrix_4x3_reg_3_out_22),
    .out_32(matrix_4x3_reg_3_out_32), .out_42(matrix_4x3_reg_3_out_42), .out_13(matrix_4x3_reg_3_out_13),
    .out_23(matrix_4x3_reg_3_out_23), .out_33(matrix_4x3_reg_3_out_33), .out_43(matrix_4x3_reg_3_out_43));  // open: rst
  matrix_4x3_reg matrix_4x3_reg_4 (
    .clk(update_3d_points), .in_11(test_rot_13_out_6), .in_21(test_rot_14_out_6), .in_31(test_rot_15_out_6),
    .in_41(test_rot_16_out_6), .in_12(test_rot_13_out_7), .in_22(test_rot_14_out_7),
    .in_32(test_rot_15_out_7), .in_42(test_rot_16_out_7), .in_13(test_rot_13_out_8),
    .in_23(test_rot_14_out_8), .in_33(test_rot_15_out_8), .in_43(test_rot_16_out_8),
    .out_11(matrix_4x3_reg_4_out_11), .out_21(matrix_4x3_reg_4_out_21), .out_31(matrix_4x3_reg_4_out_31),
    .out_41(matrix_4x3_reg_4_out_41), .out_12(matrix_4x3_reg_4_out_12), .out_22(matrix_4x3_reg_4_out_22),
    .out_32(matrix_4x3_reg_4_out_32), .out_42(matrix_4x3_reg_4_out_42), .out_13(matrix_4x3_reg_4_out_13),
    .out_23(matrix_4x3_reg_4_out_23), .out_33(matrix_4x3_reg_4_out_33), .out_43(matrix_4x3_reg_4_out_43));  // open: rst
  Button u_update_2d_points (.out(update_2d_points));
  point_projector_x4 point_projector_x4_1 (
    .line1_x1(matrix_4x3_reg_1_out_11), .line2_x1(matrix_4x3_reg_1_out_31),
    .line1_y1(matrix_4x3_reg_1_out_12), .line2_y1(matrix_4x3_reg_1_out_32), .FOV(32'h5a0000),
    .line1_z1(matrix_4x3_reg_1_out_13), .line2_z1(matrix_4x3_reg_1_out_33), .far_plane(32'h3e80000),
    .line1_x2(matrix_4x3_reg_1_out_21), .line2_x2(matrix_4x3_reg_1_out_41), .near_plane(32'h1999),
    .line1_y2(matrix_4x3_reg_1_out_22), .line2_y2(matrix_4x3_reg_1_out_42),
    .line1_z2(matrix_4x3_reg_1_out_23), .line2_z2(matrix_4x3_reg_1_out_43),
    .line1_x1_2(point_projector_x4_1_line1_x1_2), .line1_y1_2(point_projector_x4_1_line1_y1_2),
    .line1_x2_2(point_projector_x4_1_line1_x2_2), .line1_y2_2(point_projector_x4_1_line1_y2_2),
    .line2_x1_2(point_projector_x4_1_line2_x1_2), .line2_y1_2(point_projector_x4_1_line2_y1_2),
    .line2_x2_2(point_projector_x4_1_line2_x2_2), .line2_y2_2(point_projector_x4_1_line2_y2_2),
    .FOV_bypass(point_projector_x4_1_fov_bypass), .far_plane_bypass(point_projector_x4_1_far_plane_bypass),
    .near_plane_bypass(point_projector_x4_1_near_plane_bypass));
  point_projector_x4 point_projector_x4_2 (
    .line1_x1(matrix_4x3_reg_2_out_11), .line2_x1(matrix_4x3_reg_2_out_31),
    .line1_y1(matrix_4x3_reg_2_out_12), .line2_y1(matrix_4x3_reg_2_out_32),
    .FOV(point_projector_x4_1_fov_bypass), .line1_z1(matrix_4x3_reg_2_out_13),
    .line2_z1(matrix_4x3_reg_2_out_33), .far_plane(point_projector_x4_1_far_plane_bypass),
    .line1_x2(matrix_4x3_reg_2_out_21), .line2_x2(matrix_4x3_reg_2_out_41),
    .near_plane(point_projector_x4_1_near_plane_bypass), .line1_y2(matrix_4x3_reg_2_out_22),
    .line2_y2(matrix_4x3_reg_2_out_42), .line1_z2(matrix_4x3_reg_2_out_23),
    .line2_z2(matrix_4x3_reg_2_out_43), .line1_x1_2(point_projector_x4_2_line1_x1_2),
    .line1_y1_2(point_projector_x4_2_line1_y1_2), .line1_x2_2(point_projector_x4_2_line1_x2_2),
    .line1_y2_2(point_projector_x4_2_line1_y2_2), .line2_x1_2(point_projector_x4_2_line2_x1_2),
    .line2_y1_2(point_projector_x4_2_line2_y1_2), .line2_x2_2(point_projector_x4_2_line2_x2_2),
    .line2_y2_2(point_projector_x4_2_line2_y2_2), .FOV_bypass(point_projector_x4_2_fov_bypass),
    .far_plane_bypass(point_projector_x4_2_far_plane_bypass),
    .near_plane_bypass(point_projector_x4_2_near_plane_bypass));
  point_projector_x4 point_projector_x4_3 (
    .line1_x1(matrix_4x3_reg_3_out_11), .line2_x1(matrix_4x3_reg_3_out_31),
    .line1_y1(matrix_4x3_reg_3_out_12), .line2_y1(matrix_4x3_reg_3_out_32),
    .FOV(point_projector_x4_2_fov_bypass), .line1_z1(matrix_4x3_reg_3_out_13),
    .line2_z1(matrix_4x3_reg_3_out_33), .far_plane(point_projector_x4_2_far_plane_bypass),
    .line1_x2(matrix_4x3_reg_3_out_21), .line2_x2(matrix_4x3_reg_3_out_41),
    .near_plane(point_projector_x4_2_near_plane_bypass), .line1_y2(matrix_4x3_reg_3_out_22),
    .line2_y2(matrix_4x3_reg_3_out_42), .line1_z2(matrix_4x3_reg_3_out_23),
    .line2_z2(matrix_4x3_reg_3_out_43), .line1_x1_2(point_projector_x4_3_line1_x1_2),
    .line1_y1_2(point_projector_x4_3_line1_y1_2), .line1_x2_2(point_projector_x4_3_line1_x2_2),
    .line1_y2_2(point_projector_x4_3_line1_y2_2), .line2_x1_2(point_projector_x4_3_line2_x1_2),
    .line2_y1_2(point_projector_x4_3_line2_y1_2), .line2_x2_2(point_projector_x4_3_line2_x2_2),
    .line2_y2_2(point_projector_x4_3_line2_y2_2), .FOV_bypass(point_projector_x4_3_fov_bypass),
    .far_plane_bypass(point_projector_x4_3_far_plane_bypass),
    .near_plane_bypass(point_projector_x4_3_near_plane_bypass));
  point_projector_x4 point_projector_x4_4 (
    .line1_x1(matrix_4x3_reg_4_out_11), .line2_x1(matrix_4x3_reg_4_out_31),
    .line1_y1(matrix_4x3_reg_4_out_12), .line2_y1(matrix_4x3_reg_4_out_32),
    .FOV(point_projector_x4_3_fov_bypass), .line1_z1(matrix_4x3_reg_4_out_13),
    .line2_z1(matrix_4x3_reg_4_out_33), .far_plane(point_projector_x4_3_far_plane_bypass),
    .line1_x2(matrix_4x3_reg_4_out_21), .line2_x2(matrix_4x3_reg_4_out_41),
    .near_plane(point_projector_x4_3_near_plane_bypass), .line1_y2(matrix_4x3_reg_4_out_22),
    .line2_y2(matrix_4x3_reg_4_out_42), .line1_z2(matrix_4x3_reg_4_out_23),
    .line2_z2(matrix_4x3_reg_4_out_43), .line1_x1_2(point_projector_x4_4_line1_x1_2),
    .line1_y1_2(point_projector_x4_4_line1_y1_2), .line1_x2_2(point_projector_x4_4_line1_x2_2),
    .line1_y2_2(point_projector_x4_4_line1_y2_2), .line2_x1_2(point_projector_x4_4_line2_x1_2),
    .line2_y1_2(point_projector_x4_4_line2_y1_2), .line2_x2_2(point_projector_x4_4_line2_x2_2),
    .line2_y2_2(point_projector_x4_4_line2_y2_2));  // open: FOV_bypass, far_plane_bypass, near_plane_bypass
  Button start_DDA (.out(start_DDA_out));
  matrix_2x2_reg matrix_2x2_reg_1 (
    .in_11(point_projector_x4_1_line1_x1_2), .in_21(point_projector_x4_1_line1_y1_2),
    .in_12(point_projector_x4_1_line1_x2_2), .in_22(point_projector_x4_1_line1_y2_2), .clk(update_2d_points),
    .out_11(matrix_2x2_reg_1_out_11), .out_21(matrix_2x2_reg_1_out_21), .out_12(matrix_2x2_reg_1_out_12),
    .out_22(matrix_2x2_reg_1_out_22));
  matrix_2x2_reg matrix_2x2_reg_2 (
    .in_11(point_projector_x4_1_line2_x1_2), .in_21(point_projector_x4_1_line2_y1_2),
    .in_12(point_projector_x4_1_line2_x2_2), .in_22(point_projector_x4_1_line2_y2_2), .clk(update_2d_points),
    .out_11(matrix_2x2_reg_2_out_11), .out_21(matrix_2x2_reg_2_out_21), .out_12(matrix_2x2_reg_2_out_12),
    .out_22(matrix_2x2_reg_2_out_22));
  matrix_2x2_reg matrix_2x2_reg_3 (
    .in_11(point_projector_x4_2_line1_x1_2), .in_21(point_projector_x4_2_line1_y1_2),
    .in_12(point_projector_x4_2_line1_x2_2), .in_22(point_projector_x4_2_line1_y2_2), .clk(update_2d_points),
    .out_11(matrix_2x2_reg_3_out_11), .out_21(matrix_2x2_reg_3_out_21), .out_12(matrix_2x2_reg_3_out_12),
    .out_22(matrix_2x2_reg_3_out_22));
  matrix_2x2_reg matrix_2x2_reg_4 (
    .in_11(point_projector_x4_2_line2_x1_2), .in_21(point_projector_x4_2_line2_y1_2),
    .in_12(point_projector_x4_2_line2_x2_2), .in_22(point_projector_x4_2_line2_y2_2), .clk(update_2d_points),
    .out_11(matrix_2x2_reg_4_out_11), .out_21(matrix_2x2_reg_4_out_21), .out_12(matrix_2x2_reg_4_out_12),
    .out_22(matrix_2x2_reg_4_out_22));
  matrix_2x2_reg matrix_2x2_reg_5 (
    .in_11(point_projector_x4_3_line1_x1_2), .in_21(point_projector_x4_3_line1_y1_2),
    .in_12(point_projector_x4_3_line1_x2_2), .in_22(point_projector_x4_3_line1_y2_2), .clk(update_2d_points),
    .out_11(matrix_2x2_reg_5_out_11), .out_21(matrix_2x2_reg_5_out_21), .out_12(matrix_2x2_reg_5_out_12),
    .out_22(matrix_2x2_reg_5_out_22));
  matrix_2x2_reg matrix_2x2_reg_6 (
    .in_11(point_projector_x4_3_line2_x1_2), .in_21(point_projector_x4_3_line2_y1_2),
    .in_12(point_projector_x4_3_line2_x2_2), .in_22(point_projector_x4_3_line2_y2_2), .clk(update_2d_points),
    .out_11(matrix_2x2_reg_6_out_11), .out_21(matrix_2x2_reg_6_out_21), .out_12(matrix_2x2_reg_6_out_12),
    .out_22(matrix_2x2_reg_6_out_22));
  matrix_2x2_reg matrix_2x2_reg_7 (
    .in_11(point_projector_x4_4_line1_x1_2), .in_21(point_projector_x4_4_line1_y1_2),
    .in_12(point_projector_x4_4_line1_x2_2), .in_22(point_projector_x4_4_line1_y2_2), .clk(update_2d_points),
    .out_11(matrix_2x2_reg_7_out_11), .out_21(matrix_2x2_reg_7_out_21), .out_12(matrix_2x2_reg_7_out_12),
    .out_22(matrix_2x2_reg_7_out_22));
  matrix_2x2_reg matrix_2x2_reg_8 (
    .in_11(point_projector_x4_4_line2_x1_2), .in_21(point_projector_x4_4_line2_y1_2),
    .in_12(point_projector_x4_4_line2_x2_2), .in_22(point_projector_x4_4_line2_y2_2), .clk(update_2d_points),
    .out_11(matrix_2x2_reg_8_out_11), .out_21(matrix_2x2_reg_8_out_21), .out_12(matrix_2x2_reg_8_out_12),
    .out_22(matrix_2x2_reg_8_out_22));
  Pull_Resistor #(.pull(1)) pull_resistor_1 (.node(pull_resistor_1_node));
  DDA_sync dda_sync_1 (
    .clk(clk), .new_data(start_DDA_out), .x2(matrix_2x2_reg_1_out_12), .x1(matrix_2x2_reg_1_out_11),
    .y2(matrix_2x2_reg_1_out_22), .y1(matrix_2x2_reg_1_out_21), .out_y(dda_sync_1_out_y),
    .out_x(dda_sync_1_out_x), .set_point(dda_sync_1_set_point), .done(pull_resistor_1_node));  // open: status
  // DDA_sync dda_sync_2: pin names not known; wires that end beside it: matrix_2x2_reg_2_out_11, matrix_2x2_reg_2_out_21, matrix_2x2_reg_2_out_12, matrix_2x2_reg_2_out_22, start_DDA_out, clk, dda_sync_2_p7, dda_sync_2_p8, dda_sync_2_p9, pull_resistor_1_node, dda_sync_2_p11, dda_sync_2_p11
  // DDA_sync dda_sync_3: pin names not known; wires that end beside it: matrix_2x2_reg_3_out_11, matrix_2x2_reg_3_out_21, matrix_2x2_reg_3_out_12, matrix_2x2_reg_3_out_22, start_DDA_out, clk, dda_sync_3_p7, dda_sync_3_p8, dda_sync_3_p9, pull_resistor_1_node, dda_sync_2_p11, dda_sync_2_p11
  // DDA_sync dda_sync_4: pin names not known; wires that end beside it: matrix_2x2_reg_4_out_11, matrix_2x2_reg_4_out_21, matrix_2x2_reg_4_out_12, matrix_2x2_reg_4_out_22, start_DDA_out, clk, dda_sync_4_p7, dda_sync_4_p8, dda_sync_4_p9, pull_resistor_1_node, dda_sync_2_p11, dda_sync_2_p11
  DDA_sync dda_sync_5 (
    .clk(clk), .new_data(start_DDA_out), .x2(matrix_2x2_reg_5_out_12), .x1(matrix_2x2_reg_5_out_11),
    .y2(matrix_2x2_reg_5_out_22), .y1(matrix_2x2_reg_5_out_21), .out_y(dda_sync_5_out_y),
    .out_x(dda_sync_5_out_x), .set_point(dda_sync_5_set_point), .done(pull_resistor_1_node));  // open: status
  // DDA_sync dda_sync_6: pin names not known; wires that end beside it: matrix_2x2_reg_6_out_11, matrix_2x2_reg_6_out_21, matrix_2x2_reg_6_out_12, matrix_2x2_reg_6_out_22, start_DDA_out, clk, dda_sync_6_p7, dda_sync_6_p8, dda_sync_6_p9, pull_resistor_1_node, dda_sync_2_p11, dda_sync_2_p11
  // DDA_sync dda_sync_7: pin names not known; wires that end beside it: matrix_2x2_reg_7_out_11, matrix_2x2_reg_7_out_21, matrix_2x2_reg_7_out_12, matrix_2x2_reg_7_out_22, start_DDA_out, clk, dda_sync_7_p7, dda_sync_7_p8, dda_sync_7_p9, pull_resistor_1_node, dda_sync_2_p11, dda_sync_2_p11
  // DDA_sync dda_sync_8: pin names not known; wires that end beside it: matrix_2x2_reg_8_out_11, matrix_2x2_reg_8_out_21, matrix_2x2_reg_8_out_12, matrix_2x2_reg_8_out_22, start_DDA_out, clk, dda_sync_8_p7, dda_sync_8_p8, dda_sync_8_p9, pull_resistor_1_node, dda_sync_2_p11, dda_sync_2_p11, dda_sync_2_p11
  Button update (.out(update_out));
  buf buffer_1 (buffer_1_out, update_out);
  rising_edge_pulse rising_edge_pulse_1 (.signal(pull_resistor_1_node), .out(rising_edge_pulse_1_out));
  buf buffer_2 (buffer_1_out, rising_edge_pulse_1_out);
  // VRAM_ss vram_ss_1: pin names not known; wires that end beside it: dda_sync_1_out_y, dda_sync_1_out_x, dda_sync_1_set_point, vram_ss_1_p4, vram_ss_1_p5, vram_ss_1_p6, vram_ss_1_p7, vram_ss_1_p4, vram_ss_1_p5, vram_ss_1_p6, vram_ss_1_p7, buffer_1_out, dda_sync_2_p11
  // VRAM_ss vram_ss_2: pin names not known; wires that end beside it: dda_sync_2_p7, dda_sync_2_p8, dda_sync_2_p9, clk, vram_ss_2_p5, vram_ss_2_p6, vram_ss_2_p7, vram_ss_2_p8, vram_ss_2_p5, vram_ss_2_p6, vram_ss_2_p7, vram_ss_2_p8
  // VRAM_ss vram_ss_3: pin names not known; wires that end beside it: dda_sync_3_p7, dda_sync_3_p8, dda_sync_3_p9, clk, vram_ss_3_p5, vram_ss_3_p6, vram_ss_3_p7, vram_ss_3_p8, vram_ss_3_p5, vram_ss_3_p6, vram_ss_3_p7, vram_ss_3_p8
  // VRAM_ss vram_ss_4: pin names not known; wires that end beside it: dda_sync_4_p7, dda_sync_4_p8, dda_sync_4_p9, clk, vram_ss_4_p5, vram_ss_4_p6, vram_ss_4_p7, vram_ss_4_p8, vram_ss_4_p5, vram_ss_4_p6, vram_ss_4_p7, vram_ss_4_p8
  // VRAM_ss vram_ss_5: pin names not known; wires that end beside it: dda_sync_5_out_y, dda_sync_5_out_x, dda_sync_5_set_point, clk, vram_ss_5_p5, vram_ss_5_p6, vram_ss_5_p7, vram_ss_5_p8, vram_ss_5_p5, vram_ss_5_p6, vram_ss_5_p7, vram_ss_5_p8
  // VRAM_ss vram_ss_6: pin names not known; wires that end beside it: dda_sync_6_p7, dda_sync_6_p8, dda_sync_6_p9, clk, vram_ss_6_p5, vram_ss_6_p6, vram_ss_6_p7, vram_ss_6_p8, vram_ss_6_p5, vram_ss_6_p6, vram_ss_6_p7, vram_ss_6_p8
  // VRAM_ss vram_ss_7: pin names not known; wires that end beside it: dda_sync_7_p7, dda_sync_7_p8, dda_sync_7_p9, clk, vram_ss_7_p5, vram_ss_7_p6, vram_ss_7_p7, vram_ss_7_p8, vram_ss_7_p5, vram_ss_7_p6, vram_ss_7_p7, vram_ss_7_p8
  // VRAM_ss vram_ss_8: pin names not known; wires that end beside it: start_DDA_out, pull_resistor_1_node, dda_sync_8_p7, dda_sync_8_p8, dda_sync_8_p9, clk, clk, vram_ss_8_p8, vram_ss_8_p9, vram_ss_8_p10, vram_ss_8_p11, vram_ss_8_p8, vram_ss_8_p9, vram_ss_8_p10, vram_ss_8_p11, clk
  Button clear (.out(dda_sync_2_p11));
  Pull_Resistor pull_resistor_2 (.node(buffer_1_out));
  // Merger_x8 merger_x8_1: pin names not known; wires that end beside it: merger_x8_1_p1, merger_x8_1_p2, merger_x8_1_p3, merger_x8_1_p4, merger_x8_1_p1, merger_x8_1_p2, merger_x8_1_p3, merger_x8_1_p4
  // DotMatrix #(.inputtype("select"), .matrixcols(32), .matrixrows(32), .persist(128)) dotmatrix_1: pin names not known
  // DotMatrix #(.inputtype("select"), .matrixcols(32), .matrixrows(32), .persist(128)) dotmatrix_2: pin names not known
  // DotMatrix #(.inputtype("select"), .matrixcols(32), .matrixrows(32), .persist(128)) dotmatrix_3: pin names not known
  // DotMatrix #(.inputtype("select"), .matrixcols(32), .matrixrows(32), .persist(128)) dotmatrix_4: pin names not known
  // _64_display_v3 64_display_v3_1: pin names not known

  // Notes on the sheet:
  //   buffer_1 drives only 1 and floats otherwise
  //   buffer_2 drives only 1 and floats otherwise
endmodule

module fp_to_int (
  input  [31:0] in,
  output [31:0] out
);

  Shifter #(.width(32), .shift("lr")) shifter_1 (.in(in), .\dist (5'b10000), .out(out));

  // Notes on the sheet:
  //   out: pull=down
  //   in: pull=down
endmodule

module _64x64_display_controller (
  input  [5:0] y,
  input  [5:0] x,
  input  state,
  input  clear,
  input  update_frame,
  input  clk,
  output [31:0] x12,
  output [31:0] x22,
  output [31:0] x11,
  output [31:0] x21,
  output [31:0] y12,
  output [31:0] y22,
  output [31:0] y11,
  output [31:0] y21
);

  wire counter_1_carry, counter_2_carry, falling_edge_pulse_1_out, falling_edge_pulse_2_out,
       multiplexer_1_out, multiplexer_2_out, multiplexer_3_out, multiplexer_6_out, not_1_out, not_2_out,
       not_3_out, not_4_out, not_5_out, or_1_out, or_2_out, rising_edge_detector_1_out,
       rising_edge_pulse_1_out;
  wire [5:0] counter_2_q, multiplexer_5_out;
  wire [31:0] decoder_1_out0, decoder_2_out0, multiplexer_7_out, multiplexer_8_out, or_3_out,
       pull_resistor_2_node, ram_1_data, ram_2_data, ram_3_data, ram_4_data;

  Register #(.width(6)) register_1 ();  // open: D, en, Q, clk, clr
  rising_edge_pulse rising_edge_pulse_1 (.signal(clear), .out(rising_edge_pulse_1_out));
  falling_edge_pulse falling_edge_pulse_1 (.signal(counter_1_carry), .out(falling_edge_pulse_1_out));
  falling_edge_pulse falling_edge_pulse_2 (.signal(counter_2_carry), .out(falling_edge_pulse_2_out));
  Decoder #(.select(5)) decoder_1 (
    .out0(decoder_1_out0[0]), .out1(decoder_1_out0[1]), .out2(decoder_1_out0[2]), .out3(decoder_1_out0[3]),
    .out4(decoder_1_out0[4]), .out5(decoder_1_out0[5]), .out6(decoder_1_out0[6]), .out7(decoder_1_out0[7]),
    .out8(decoder_1_out0[8]), .out9(decoder_1_out0[9]), .out10(decoder_1_out0[10]),
    .out11(decoder_1_out0[11]), .out12(decoder_1_out0[12]), .out13(decoder_1_out0[13]),
    .out14(decoder_1_out0[14]), .out15(decoder_1_out0[15]), .out16(decoder_1_out0[16]),
    .out17(decoder_1_out0[17]), .out18(decoder_1_out0[18]), .out19(decoder_1_out0[19]),
    .out20(decoder_1_out0[20]), .out21(decoder_1_out0[21]), .out22(decoder_1_out0[22]),
    .out23(decoder_1_out0[23]), .out24(decoder_1_out0[24]), .out25(decoder_1_out0[25]),
    .out26(decoder_1_out0[26]), .out27(decoder_1_out0[27]), .out28(decoder_1_out0[28]),
    .out29(decoder_1_out0[29]), .out30(decoder_1_out0[30]), .out31(decoder_1_out0[31]), .sel(x[4:0]),
    .en(state));
  rising_edge_detector rising_edge_detector_1 (
    .signal(update_frame), .clear(falling_edge_pulse_1_out), .sync(falling_edge_pulse_2_out),
    .out(rising_edge_detector_1_out));
  or or_1 (or_1_out, rising_edge_detector_1_out, counter_1_carry);
  Pull_Resistor pull_resistor_1 (.node(decoder_1_out0));
  Counter #(.width(6), .max('h3f)) counter_1 (
    .count(or_1_out), .carry(counter_1_carry), .clk(clk));  // open: load, D, Q, clr
  Multiplexer #(.enable("false")) multiplexer_1 (
    .in0(state), .in1(1'b0), .out(multiplexer_1_out), .sel(rising_edge_detector_1_out));
  Pull_Resistor pull_resistor_2 (.node(pull_resistor_2_node));
  not not_1 (not_1_out, x[5]);
  or or_2 (or_2_out, rising_edge_pulse_1_out, rising_edge_pulse_1_out);
  assign or_3_out = pull_resistor_2_node | decoder_1_out0;  // OR_Gate or_3, 32 bits wide
  Multiplexer #(.enable("false")) multiplexer_2 (
    .in0(x[5]), .in1(1'b1), .out(multiplexer_2_out), .sel(rising_edge_detector_1_out));
  Multiplexer #(.enable("false")) multiplexer_3 (
    .in0(not_1_out), .in1(1'b1), .out(multiplexer_3_out), .sel(rising_edge_detector_1_out));
  Multiplexer #(.width(32)) multiplexer_4 (
    .in0(ram_3_data), .in1(ram_1_data), .out(pull_resistor_2_node), .sel(multiplexer_3_out), .en(not_2_out));
  Multiplexer #(.width(6), .enable("false")) multiplexer_5 (
    .in0(y), .in1(counter_2_q), .out(multiplexer_5_out), .sel(rising_edge_detector_1_out));
  Counter #(.width(6), .max('h3f)) counter_2 (
    .Q(counter_2_q), .carry(counter_2_carry), .clk(clk));  // open: load, D, count, clr
  not not_2 (not_2_out, rising_edge_detector_1_out);
  Decoder #(.select(5), .enable("false")) decoder_2 (
    .out0(decoder_2_out0[0]), .out1(decoder_2_out0[1]), .out2(decoder_2_out0[2]), .out3(decoder_2_out0[3]),
    .out4(decoder_2_out0[4]), .out5(decoder_2_out0[5]), .out6(decoder_2_out0[6]), .out7(decoder_2_out0[7]),
    .out8(decoder_2_out0[8]), .out9(decoder_2_out0[9]), .out10(decoder_2_out0[10]),
    .out11(decoder_2_out0[11]), .out12(decoder_2_out0[12]), .out13(decoder_2_out0[13]),
    .out14(decoder_2_out0[14]), .out15(decoder_2_out0[15]), .out16(decoder_2_out0[16]),
    .out17(decoder_2_out0[17]), .out18(decoder_2_out0[18]), .out19(decoder_2_out0[19]),
    .out20(decoder_2_out0[20]), .out21(decoder_2_out0[21]), .out22(decoder_2_out0[22]),
    .out23(decoder_2_out0[23]), .out24(decoder_2_out0[24]), .out25(decoder_2_out0[25]),
    .out26(decoder_2_out0[26]), .out27(decoder_2_out0[27]), .out28(decoder_2_out0[28]),
    .out29(decoder_2_out0[29]), .out30(decoder_2_out0[30]), .out31(decoder_2_out0[31]), .sel(counter_2_q[4:0]));
  Multiplexer #(.enable("false")) multiplexer_6 (
    .in0(state), .in1(1'b1), .out(multiplexer_6_out), .sel(rising_edge_detector_1_out));
  not not_3 (not_3_out, rising_edge_detector_1_out);
  RAM #(.addrWidth(6), .dataWidth(32), .bus("separate")) ram_1 (
    .addr(multiplexer_5_out), .din(or_3_out), .data(ram_1_data), .str(multiplexer_1_out),
    .sel(multiplexer_3_out), .clk(clk), .ld(multiplexer_6_out), .clr(or_2_out));
  RAM #(.addrWidth(6), .dataWidth(32), .bus("separate")) ram_2 (
    .addr(counter_2_q), .din(ram_1_data), .data(ram_2_data), .str(rising_edge_detector_1_out), .clk(clk),
    .ld(not_3_out));  // open: sel, clr
  not not_4 (not_4_out, rising_edge_detector_1_out);
  RAM #(.addrWidth(6), .dataWidth(32), .bus("separate")) ram_3 (
    .addr(multiplexer_5_out), .din(or_3_out), .data(ram_3_data), .str(multiplexer_1_out),
    .sel(multiplexer_2_out), .clk(clk), .ld(multiplexer_6_out), .clr(or_2_out));
  RAM #(.addrWidth(6), .dataWidth(32), .bus("separate")) ram_4 (
    .addr(counter_2_q), .din(ram_3_data), .data(ram_4_data), .str(rising_edge_detector_1_out), .clk(clk),
    .ld(not_4_out));  // open: sel, clr
  Multiplexer #(.width(32), .enable("false")) multiplexer_7 (
    .in0(ram_4_data), .in1(ram_3_data), .out(multiplexer_7_out), .sel(rising_edge_detector_1_out));
  Multiplexer #(.width(32), .enable("false")) multiplexer_8 (
    .in0(ram_2_data), .in1(ram_1_data), .out(multiplexer_8_out), .sel(rising_edge_detector_1_out));
  not not_5 (not_5_out, counter_2_q[5]);
  Register #(.width(32), .trigger("falling")) register_2 (
    .D(multiplexer_7_out), .en(not_5_out), .Q(x22), .clk(clk), .clr(counter_2_q[5]));
  Register #(.width(32), .trigger("falling")) register_3 (
    .D(multiplexer_7_out), .en(counter_2_q[5]), .Q(x21), .clk(clk), .clr(not_5_out));
  Register #(.width(32), .trigger("falling")) register_4 (
    .D(decoder_2_out0), .en(not_5_out), .Q(y12), .clk(clk), .clr(counter_2_q[5]));
  Register #(.width(32), .trigger("falling")) register_5 (
    .D(decoder_2_out0), .en(counter_2_q[5]), .Q(y11), .clk(clk), .clr(not_5_out));
  Register #(.width(32), .trigger("falling")) register_6 (
    .D(multiplexer_8_out), .en(not_5_out), .Q(x12), .clk(clk), .clr(counter_2_q[5]));
  Register #(.width(32), .trigger("falling")) register_7 (
    .D(multiplexer_8_out), .en(counter_2_q[5]), .Q(x11), .clk(clk), .clr(not_5_out));
  Register #(.width(32), .trigger("falling")) register_8 (
    .D(decoder_2_out0), .en(not_5_out), .Q(y22), .clk(clk), .clr(counter_2_q[5]));
  Register #(.width(32), .trigger("falling")) register_9 (
    .D(decoder_2_out0), .en(counter_2_q[5]), .Q(y21), .clk(clk), .clr(not_5_out));

  // Notes on the sheet:
  //   y11: pull=down
  //   y12: pull=down
  //   x12: pull=down
  //   x11: pull=down
  //   y21: pull=down
  //   clear: pull=down
  //   y22: pull=down
  //   y: pull=down
  //   clk: pull=down
  //   x22: pull=down
  //   x: pull=down
  //   x21: pull=down
  //   update_frame: pull=down
  //   state: pull=down
endmodule

module int_to_fp (
  input  [31:0] in,
  output [31:0] out
);

  Shifter #(.width(32)) shifter_1 (.in(in), .\dist (5'b10000), .out(out));

  // Notes on the sheet:
  //   out: pull=down
  //   in: pull=down
endmodule

module DDA_test_sync (
  input  clk,
  input  new_data,
  input  [31:0] x2,
  input  [31:0] x1,
  input  [31:0] y2,
  input  [31:0] y1,
  output [31:0] out_y,
  output [3:0] status,
  output [31:0] out_x,
  output set_point,
  output done
);

  wire and_1_out, and_2_out, and_4_out, and_5_out, button_1_out, comparator_2_eq, comparator_2_lt,
       comparator_3_eq, controlled_buffer_7_out, mission_2, nand_1_out, nand_2_out, nand_3_out, nand_4_out,
       nand_5_out, nand_6_out, nand_7_out, nand_8_out, nand_9_out, nand_11_out, nand_12_out, nand_14_out,
       nand_15_out, nand_17_out, nand_18_out, nand_19_out, nand_21_out, nand_22_out, nand_23_out,
       nand_24_out, nand_25_out, nand_27_out, nand_29_out, new_data_t, not_1_out, not_2_out, not_3_out,
       or_2_out;
  wire [1:0] comparator_1_gt, control, mission, or_1_out, state;
  wire [1:1] comparator_1_lt;
  wire [31:0] counter_1_q, dx, dy, fp_abs_1_abs, fp_abs_2_abs, multiplexer_1_out, out_x_t, out_y_t,
       steps_count, x, x1_t, x2_t, x_dx, x_step, y, y1_t, y2_t, y_dy, y_step;

  rising_edge_detector rising_edge_detector_1 (.signal(new_data), .clear(done), .sync(clk), .out(new_data_t));
  and and_1 (and_1_out, ~mission[1], mission[0]);  // AND_Gate
  and and_2 (and_2_out, mission[1], mission[0]);
  and and_3 (mission_2, mission[1], ~mission[0]);  // AND_Gate
  Register #(.width(32)) register_1 (.D(x2), .Q(x2_t), .clk(new_data_t));  // open: en, clr
  Register #(.width(32)) register_2 (.D(x1), .Q(x1_t), .clk(new_data_t));  // open: en, clr
  Register #(.width(32)) register_3 (.D(y2), .Q(y2_t), .clk(new_data_t));  // open: en, clr
  Register #(.width(32)) register_4 (.D(y1), .Q(y1_t), .clk(new_data_t));  // open: en, clr
  assign x = and_1_out ? x1_t : 32'bz;  // Controlled_Buffer controlled_buffer_1
  assign x = and_2_out ? x2_t : 32'bz;  // Controlled_Buffer controlled_buffer_2
  assign x = mission_2 ? x_dx : 32'bz;  // Controlled_Buffer controlled_buffer_3
  assign y = and_1_out ? y1_t : 32'bz;  // Controlled_Buffer controlled_buffer_4
  assign y = and_2_out ? y2_t : 32'bz;  // Controlled_Buffer controlled_buffer_5
  assign y = mission_2 ? y_dy : 32'bz;  // Controlled_Buffer controlled_buffer_6
  Subtractor #(.width(32)) subtractor_1 (.a(x2_t), .b(x1_t), .out(dx));  // open: bin, bout
  fp_abs fp_abs_1 (.in(dx), .abs(fp_abs_1_abs));
  Subtractor #(.width(32)) subtractor_2 (.a(y2_t), .b(y1_t), .out(dy));  // open: bin, bout
  fp_abs fp_abs_2 (.in(dy), .abs(fp_abs_2_abs));
  Adder #(.width(32)) adder_1 (.a(out_x_t), .b(x_step), .out(x_dx));  // open: cin, cout
  Adder #(.width(32)) adder_2 (.a(out_y_t), .b(y_step), .out(y_dy));  // open: cin, cout
  fp_round_ones fp_round_ones_1 (.num(out_x_t), .out(out_y));
  fp_round_ones fp_round_ones_2 (.num(out_y_t), .out(out_x));
  Comparator #(.width(32)) comparator_1 (
    .a(fp_abs_1_abs), .b(fp_abs_2_abs), .gt(comparator_1_gt[0]), .eq(comparator_1_gt[1]),
    .lt(comparator_1_lt[1]));
  assign or_1_out = comparator_1_gt | {2{comparator_1_lt[1]}};  // OR_Gate or_1, 2 bits wide
  fp_div fp_div_1 (.in1(dx), .in2(steps_count), .out(x_step));
  fp_div fp_div_2 (.in1(dy), .in2(steps_count), .out(y_step));
  fp_round_ones fp_round_ones_3 (.num(multiplexer_1_out), .out(steps_count));
  Multiplexer #(.select(2), .width(32), .enable("false")) multiplexer_1 (
    .in1(fp_abs_1_abs), .in2(fp_abs_1_abs), .in3(fp_abs_2_abs), .out(multiplexer_1_out), .sel(or_1_out));  // open: in0
  Register #(.width(32)) register_5 (.D(x), .Q(out_x_t), .clk(clk), .clr(button_1_out));  // open: en
  Register #(.width(32)) register_6 (.D(y), .Q(out_y_t), .clk(clk), .clr(button_1_out));  // open: en
  Button button_1 (.out(button_1_out));
  assign controlled_buffer_7_out = and_4_out ? clk : 1'bz;  // Controlled_Buffer controlled_buffer_7
  and and_4 (and_4_out, ~comparator_3_eq, mission_2);  // AND_Gate
  Counter #(.width(32), .max('hffffffff)) counter_1 (
    .Q(counter_1_q), .clk(controlled_buffer_7_out), .clr(done));  // open: load, D, count, carry
  or or_2 (or_2_out, comparator_2_eq, comparator_2_lt);
  Comparator #(.width(32)) comparator_2 (
    .a(steps_count), .b(32'h10000), .eq(comparator_2_eq), .lt(comparator_2_lt));  // open: gt
  not not_1 (not_1_out, nand_1_out);
  nand nand_1 (nand_1_out, control[0], state[0]);
  nand nand_2 (nand_2_out, ~control[0], ~control[1]);  // NAND_Gate
  nand nand_3 (nand_3_out, nand_2_out, ~state[0]);  // NAND_Gate
  nand nand_4 (nand_4_out, control[0], ~state[1]);  // NAND_Gate
  nand nand_5 (nand_5_out, nand_4_out, nand_6_out);
  nand nand_6 (nand_6_out, control[1], state[1]);
  nand nand_7 (nand_7_out, control[0], nand_8_out);
  nand nand_8 (nand_8_out, ~control[1], ~state[1]);  // NAND_Gate
  Button button_2 ();  // open: out
  and and_5 (and_5_out, ~or_2_out, comparator_3_eq);  // AND_Gate
  Comparator #(.width(32)) comparator_3 (
    .a({counter_1_q[15:0], {16{1'b0}}}), .b(steps_count), .eq(comparator_3_eq));  // open: gt, lt
  J_K_Flip_Flop j_k_ff_1 (.J(not_1_out), .clk(clk), .K(nand_3_out), .Q(state[1]));  // open: Qn, preset, en, reset
  J_K_Flip_Flop j_k_ff_2 (.J(nand_5_out), .clk(clk), .K(nand_7_out), .Q(state[0]));  // open: Qn, preset, en, reset
  nand nand_9 (nand_9_out, control[1], ~control[0], ~state[1]);  // NAND_Gate
  nand nand_10 (status[1], nand_9_out, nand_11_out);
  nand nand_11 (nand_11_out, control[1], ~control[0], state[0]);  // NAND_Gate
  nand nand_12 (nand_12_out, control[1], state[1], ~state[0]);  // NAND_Gate
  nand nand_13 (status[0], nand_12_out, not_2_out);
  not not_2 (not_2_out, control[0]);
  nand nand_14 (nand_14_out, control[0], ~state[1], state[0]);  // NAND_Gate
  nand nand_15 (nand_15_out, control[0], state[1], ~state[0]);  // NAND_Gate
  nand nand_16 (mission[1], nand_14_out, nand_15_out, nand_17_out);
  nand nand_17 (nand_17_out, control[1], state[1], ~state[0]);  // NAND_Gate
  nand nand_18 (nand_18_out, control[0], ~state[1], ~state[0]);  // NAND_Gate
  nand nand_19 (nand_19_out, control[1], control[0]);
  nand nand_20 (mission[0], nand_18_out, nand_19_out, nand_21_out);
  nand nand_21 (nand_21_out, control[1], state[1], ~state[0]);  // NAND_Gate
  nand nand_22 (nand_22_out, control[1], control[0], ~state[1], state[0]);  // NAND_Gate
  nand nand_23 (nand_23_out, nand_22_out, nand_24_out);
  nand nand_24 (nand_24_out, control[1], state[1], ~state[0]);  // NAND_Gate
  nand nand_25 (nand_25_out, control[0], state[0]);
  nand nand_26 (set_point, nand_25_out, nand_27_out);
  nand nand_27 (nand_27_out, state[1], ~state[0]);  // NAND_Gate
  Shift_Register #(.length(2)) shift_register_1 (
    .in(nand_23_out), .clk(clk), .out(done));  // open: shift, load, clr, d0, q0, d1, q1
  not not_3 (not_3_out, and_5_out);
  nand nand_28 (control[1], not_3_out, nand_29_out);
  nand nand_29 (nand_29_out, or_2_out, new_data_t);
  nand nand_30 (control[0], ~new_data_t, ~and_5_out);  // NAND_Gate
  Hex_Digit_Display hex_digit_display_1 (.value({2'b00, status[1:0]}));  // open: dp

  assign status[3:2] = 2'b00;

  // Other names for the same wires on the sheet: status_t[1:0] = status[1:0]

  // Notes on the sheet:
  //   set_point: pull=up
  //   done: pull=up
  //   In
  //   Mission decoder
  //   Out
  //   Math
  //   Out reg
  //   State machine
  //   Main logic
  //   00 - halt do nothg
  //   01 - load x1y1
  //   10 - increment by step
  //   11 - load x2y2
  //   Status
  //   0: halt
  //   1: run
  //   2: error
endmodule

module DDA_test_async (
  input  sync,
  input  new_data,
  input  lock,
  input  [31:0] x2,
  input  [31:0] x1,
  input  [31:0] y2,
  input  [31:0] y1,
  input  load,
  output set_point,
  output [31:0] out_y,
  output [31:0] out_x,
  output done
);

  wire and_2_out, and_5_out, and_7_out, and_9_out, and_12_out, and_14_out, and_15_out, and_16_out,
       and_17_out, and_18_out, and_19_out, and_20_out, and_21_out, and_22_out, and_23_out, and_24_out,
       and_25_out, and_26_out, and_28_out, and_29_out, and_30_out, and_31_out, buffer_2_out, buffer_3_out,
       buffer_4_out, buffer_5_out, buffer_6_out, buffer_7_out, buffer_8_out, buffer_9_out, buffer_10_out,
       buffer_11_out, buffer_12_out, buffer_13_out, buffer_14_out, buffer_15_out, buffer_16_out,
       buffer_17_out, buffer_28_out, buffer_29_out, buffer_32_out, buffer_33_out, clear, clear_wait_counter,
       comparator_2_gt, comparator_2_lt, comparator_4_lt, comparator_5_lt, controlled_buffer_15_out,
       counter_2_carry, done_t, inc_loop_counter, inc_stage_counter, inc_stored_values, inc_wait_counter,
       load_t, load_x1y1, load_x2y2, loop_counter, loop_stopper_counter, new_data_t, not_2_out, not_3_out,
       not_4_out, or_5_out, pull_resistor_3_node, pull_resistor_9_node, pull_resistor_15_node,
       pull_resistor_17_node, reset, rising_edge_detector_async_1_out, rising_edge_detector_async_2_out,
       rising_edge_detector_async_3_out, rising_edge_pulse_1_out, s_r_ff_1_q, set, skip_loop, start,
       wait_counter;
  wire [1:0] comparator_1_gt, or_2_out, stage;
  wire [1:1] comparator_1_lt;
  wire [3:0] address, register_1_q, register_2_q, register_3_q, register_6_q, register_7_q, register_8_q,
       register_9_q, register_10_q, register_11_q, register_12_q, register_13_q, register_14_q,
       register_15_q, register_16_q, register_17_q, register_18_q, register_19_q, register_20_q,
       register_21_q, register_22_q, register_23_q, register_24_q, register_25_q, register_26_q,
       register_27_q, register_28_q, register_29_q, register_30_q, register_31_q, register_32_q;
  wire [5:0] buffer_18_out, buffer_19_out, buffer_20_out, buffer_21_out, buffer_22_out, buffer_23_out,
       buffer_24_out, buffer_25_out, buffer_26_out, counter_2_q, multiplexer_2_out;
  wire [7:0] counter_1_q, counter_4_q, counter_5_q;
  wire [31:0] adder_3_out, adder_4_out, adder_5_out, adder_6_out, adder_7_out, adder_8_out, decoder_1_out31,
       dx, dy, fp_abs_1_abs, fp_abs_2_abs, loop_count, multiplexer_1_out, or_3_out, or_4_out, out_x_t,
       out_y_t, ram_1_data, ram_2_data, steps_count, subtractor_4_out, x, x_dx, x_step, y, y_dy, y_step;

  Register #(.width(4), .trigger("low")) register_1 (.D(address), .Q(register_1_q), .clk(1'b0));  // open: en, clr
  Register #(.width(4), .trigger("low")) register_2 (.D(address), .Q(register_2_q), .clk(1'b0));  // open: en, clr
  Pull_Resistor pull_resistor_1 (.node(sync));
  rising_edge_detector_async rising_edge_detector_async_1 (
    .signal(new_data), .clear(clear), .out(rising_edge_detector_async_1_out));
  Pull_Resistor pull_resistor_2 (.node(lock));
  Pull_Resistor pull_resistor_3 (.node(pull_resistor_3_node));
  and and_1 (pull_resistor_3_node, ~register_1_q[0], ~register_1_q[1], ~register_1_q[2], ~register_1_q[3], start);  // AND_Gate
  assign address = pull_resistor_3_node ? 4'b0001 : 4'bz;  // Controlled_Buffer controlled_buffer_1
  assign address = and_2_out ? 4'b0000 : 4'bz;  // Controlled_Buffer controlled_buffer_2
  and and_2 (and_2_out, ~start, ~register_2_q[0], ~register_2_q[1], ~register_2_q[2], ~register_2_q[3]);  // AND_Gate
  Pull_Resistor pull_resistor_4 (.node(and_2_out));
  and and_3 (new_data_t, rising_edge_detector_async_1_out, ~lock);  // AND_Gate
  assign x = load_x2y2 ? x2 : 32'bz;  // Controlled_Buffer controlled_buffer_3
  assign x = inc_stored_values ? x_dx : 32'bz;  // Controlled_Buffer controlled_buffer_4
  assign y = load_x2y2 ? y2 : 32'bz;  // Controlled_Buffer controlled_buffer_5
  assign y = inc_stored_values ? y_dy : 32'bz;  // Controlled_Buffer controlled_buffer_6
  assign x = load_x1y1 ? x1 : 32'bz;  // Controlled_Buffer controlled_buffer_7
  or or_1 (load_t, load_x1y1, load_x2y2, inc_stored_values);
  assign y = load_x1y1 ? y1 : 32'bz;  // Controlled_Buffer controlled_buffer_8
  Register #(.width(4), .trigger("low")) register_3 (.D(address), .Q(register_3_q), .clk(1'b0));  // open: en, clr
  fp_round_ones fp_round_ones_1 (.num(out_x_t), .out(out_y));
  fp_round_ones fp_round_ones_2 (.num(out_y_t), .out(out_x));
  Subtractor #(.width(32)) subtractor_1 (.a(x2), .b(x1), .out(dx));  // open: bin, bout
  Subtractor #(.width(32)) subtractor_2 (.a(y2), .b(y1), .out(dy));  // open: bin, bout
  Adder #(.width(32)) adder_1 (.a(out_x_t), .b(x_step), .out(x_dx));  // open: cin, cout
  Adder #(.width(32)) adder_2 (.a(out_y_t), .b(y_step), .out(y_dy));  // open: cin, cout
  and and_4 (load_x1y1, register_3_q[0], ~register_3_q[1], ~register_3_q[2], ~register_3_q[3]);  // AND_Gate
  fp_abs fp_abs_1 (.in(dx), .abs(fp_abs_1_abs));
  fp_abs fp_abs_2 (.in(dy), .abs(fp_abs_2_abs));
  assign address = load_x1y1 ? 4'b0010 : 4'bz;  // Controlled_Buffer controlled_buffer_9
  Pull_Resistor pull_resistor_5 (.node(load_x1y1));
  Comparator #(.width(32)) comparator_1 (
    .a(fp_abs_1_abs), .b(fp_abs_2_abs), .gt(comparator_1_gt[0]), .eq(comparator_1_gt[1]),
    .lt(comparator_1_lt[1]));
  S_R_Flip_Flop s_r_ff_1 (.Q(s_r_ff_1_q), .Qn(done), .preset(and_5_out), .reset(done_t));  // open: S, clk, R, en
  Multiplexer #(.select(2), .width(32), .enable("false")) multiplexer_1 (
    .in1(fp_abs_1_abs), .in2(fp_abs_1_abs), .in3(fp_abs_2_abs), .out(multiplexer_1_out), .sel(or_2_out));  // open: in0
  assign or_2_out = comparator_1_gt | {2{comparator_1_lt[1]}};  // OR_Gate or_2, 2 bits wide
  fp_div fp_div_1 (.in1(dx), .in2(steps_count), .out(x_step));
  fp_div fp_div_2 (.in1(dy), .in2(steps_count), .out(y_step));
  Register #(.width(32)) register_4 (.D(x), .Q(out_x_t), .clk(load_t), .clr(clear));  // open: en
  Register #(.width(32)) register_5 (.D(y), .Q(out_y_t), .clk(load_t), .clr(clear));  // open: en
  Register #(.width(4), .trigger("low")) register_6 (.D(address), .Q(register_6_q), .clk(1'b0));  // open: en, clr
  S_R_Flip_Flop s_r_ff_2 (.Q(set_point), .preset(set), .reset(reset));  // open: S, clk, R, Qn, en
  and and_5 (and_5_out, new_data_t, ~s_r_ff_1_q);  // AND_Gate
  fp_round_ones fp_round_ones_3 (.num(multiplexer_1_out), .out(steps_count));
  assign address = set ? 4'b0011 : 4'bz;  // Controlled_Buffer controlled_buffer_10
  and and_6 (set, ~register_6_q[0], register_6_q[1], ~register_6_q[2], ~register_6_q[3]);  // AND_Gate
  Pull_Resistor pull_resistor_6 (.node(set));
  Adder #(.width(32)) adder_3 (.a(adder_4_out), .b({32{1'b0}}), .out(adder_3_out));  // open: cin, cout
  Adder #(.width(32)) adder_4 (.a({{31{1'b0}}, new_data_t}), .b({32{1'b0}}), .out(adder_4_out));  // open: cin, cout
  Subtractor #(.width(32)) subtractor_3 (.a(steps_count), .b(32'h20000), .out(loop_count));  // open: bin, bout
  Comparator #(.width(32)) comparator_2 (
    .a(steps_count), .b(32'h10000), .gt(comparator_2_gt), .lt(comparator_2_lt));  // open: eq
  rising_edge_detector_async rising_edge_detector_async_2 (
    .signal(new_data_t), .clear(and_7_out), .out(rising_edge_detector_async_2_out));
  Adder #(.width(32)) adder_5 (.a(adder_3_out), .b({32{1'b0}}), .out(adder_5_out));  // open: cin, cout
  not not_1 (skip_loop, comparator_2_gt);
  and and_7 (and_7_out, comparator_2_lt, rising_edge_detector_async_2_out);
  rising_edge_detector rising_edge_detector_1 (.signal(adder_5_out[0]), .clear(clear), .sync(sync), .out(start));
  buf buffer_1 (inc_stage_counter, and_7_out);
  Register #(.width(4), .trigger("low")) register_7 (.D(address), .Q(register_7_q), .clk(1'b0));  // open: en, clr
  Register #(.width(4), .trigger("low")) register_8 (.D(address), .Q(register_8_q), .clk(1'b0));  // open: en, clr
  assign address = clear_wait_counter ? 4'b1101 : 4'bz;  // Controlled_Buffer controlled_buffer_11
  and and_8 (clear_wait_counter, register_7_q[0], register_7_q[1], ~register_7_q[2], ~register_7_q[3]);  // AND_Gate
  Pull_Resistor pull_resistor_7 (.node(clear_wait_counter));
  assign address = and_9_out ? 4'b0100 : 4'bz;  // Controlled_Buffer controlled_buffer_12
  and and_9 (and_9_out, register_8_q[0], ~register_8_q[1], register_8_q[2], register_8_q[3]);  // AND_Gate
  Pull_Resistor pull_resistor_8 (.node(and_9_out));
  Counter counter_1 (.Q(counter_1_q), .clk(inc_wait_counter), .clr(clear_wait_counter));  // open: load, D, count, carry
  Comparator comparator_3 (.a(counter_1_q), .b({8{1'b0}}), .eq(wait_counter));  // open: gt, lt
  rising_edge_detector_async rising_edge_detector_async_3 (
    .signal(load), .clear(buffer_11_out), .out(rising_edge_detector_async_3_out));
  Register #(.width(4), .trigger("low")) register_9 (.D(address), .Q(register_9_q), .clk(1'b0));  // open: en, clr
  Register #(.width(4), .trigger("low")) register_10 (.D(address), .Q(register_10_q), .clk(1'b0));  // open: en, clr
  not not_2 (not_2_out, rising_edge_detector_async_3_out);
  buf buffer_2 (buffer_2_out, buffer_3_out);
  buf buffer_3 (buffer_3_out, buffer_6_out);
  buf buffer_4 (buffer_4_out, buffer_2_out);
  buf buffer_5 (buffer_5_out, buffer_15_out);
  buf buffer_6 (buffer_6_out, buffer_7_out);
  buf buffer_7 (buffer_7_out, buffer_8_out);
  buf buffer_8 (buffer_8_out, buffer_5_out);
  buf buffer_9 (buffer_9_out, buffer_12_out);
  buf buffer_10 (buffer_10_out, buffer_9_out);
  buf buffer_11 (buffer_11_out, buffer_10_out);
  buf buffer_12 (buffer_12_out, buffer_17_out);
  not not_3 (not_3_out, rising_edge_detector_async_3_out);
  Pull_Resistor pull_resistor_9 (.node(pull_resistor_9_node));
  and and_10 (pull_resistor_9_node, ~register_9_q[0], ~register_9_q[1], register_9_q[2], ~register_9_q[3], wait_counter);  // AND_Gate
  assign address = pull_resistor_9_node ? 4'b0110 : 4'bz;  // Controlled_Buffer controlled_buffer_13
  assign address = inc_wait_counter ? 4'b1101 : 4'bz;  // Controlled_Buffer controlled_buffer_14
  and and_11 (inc_wait_counter, ~wait_counter, ~register_10_q[0], ~register_10_q[1], register_10_q[2], ~register_10_q[3]);  // AND_Gate
  Pull_Resistor pull_resistor_10 (.node(inc_wait_counter));
  buf buffer_13 (buffer_13_out, adder_6_out[0]);
  Adder #(.width(32)) adder_6 (.a({{31{1'b0}}, set_point}), .b({32{1'b0}}), .out(adder_6_out));  // open: cin, cout
  Subtractor #(.width(32)) subtractor_4 (.a(adder_6_out), .b({32{1'b0}}), .out(subtractor_4_out));  // open: bin, bout
  Adder #(.width(32)) adder_7 (.a(out_x_t), .b(32'h8000), .out(adder_7_out));  // open: cin, cout
  rising_edge_pulse rising_edge_pulse_1 (.signal(start), .out(rising_edge_pulse_1_out));
  Adder #(.width(32)) adder_8 (.a(out_y_t), .b(32'h8000), .out(adder_8_out));  // open: cin, cout
  Pull_Resistor #(.pull(1)) pull_resistor_11 (.node(not_2_out));
  and and_12 (and_12_out, ~not_2_out, ~buffer_4_out);  // AND_Gate
  buf buffer_14 (buffer_14_out, and_12_out);
  buf buffer_15 (buffer_15_out, buffer_14_out);
  buf buffer_16 (buffer_16_out, counter_2_carry);
  buf buffer_17 (buffer_17_out, buffer_16_out);
  Decoder #(.select(5), .enable("false")) decoder_1 (
    .out0(decoder_1_out31[31]), .out1(decoder_1_out31[30]), .out2(decoder_1_out31[29]),
    .out3(decoder_1_out31[28]), .out4(decoder_1_out31[27]), .out5(decoder_1_out31[26]),
    .out6(decoder_1_out31[25]), .out7(decoder_1_out31[24]), .out8(decoder_1_out31[23]),
    .out9(decoder_1_out31[22]), .out10(decoder_1_out31[21]), .out11(decoder_1_out31[20]),
    .out12(decoder_1_out31[19]), .out13(decoder_1_out31[18]), .out14(decoder_1_out31[17]),
    .out15(decoder_1_out31[16]), .out16(decoder_1_out31[15]), .out17(decoder_1_out31[14]),
    .out18(decoder_1_out31[13]), .out19(decoder_1_out31[12]), .out20(decoder_1_out31[11]),
    .out21(decoder_1_out31[10]), .out22(decoder_1_out31[9]), .out23(decoder_1_out31[8]),
    .out24(decoder_1_out31[7]), .out25(decoder_1_out31[6]), .out26(decoder_1_out31[5]),
    .out27(decoder_1_out31[4]), .out28(decoder_1_out31[3]), .out29(decoder_1_out31[2]),
    .out30(decoder_1_out31[1]), .out31(decoder_1_out31[0]), .sel(adder_7_out[20:16]));
  Pull_Resistor pull_resistor_12 (.node(buffer_13_out));
  assign controlled_buffer_15_out = not_4_out ? subtractor_4_out[0] : 1'bz;  // Controlled_Buffer controlled_buffer_15
  not not_4 (not_4_out, load);
  Counter #(.width(6), .max('h3f)) counter_2 (
    .Q(counter_2_q), .carry(counter_2_carry), .clk(and_12_out), .clr(not_3_out));  // open: load, D, count
  assign buffer_18_out = counter_2_q;  // Buffer buffer_18, 6 bits wide
  assign buffer_19_out = buffer_18_out;  // Buffer buffer_19, 6 bits wide
  assign buffer_20_out = buffer_19_out;  // Buffer buffer_20, 6 bits wide
  assign buffer_21_out = buffer_20_out;  // Buffer buffer_21, 6 bits wide
  assign buffer_22_out = buffer_21_out;  // Buffer buffer_22, 6 bits wide
  assign buffer_23_out = buffer_22_out;  // Buffer buffer_23, 6 bits wide
  assign buffer_24_out = buffer_23_out;  // Buffer buffer_24, 6 bits wide
  assign buffer_25_out = buffer_24_out;  // Buffer buffer_25, 6 bits wide
  assign buffer_26_out = buffer_25_out;  // Buffer buffer_26, 6 bits wide
  // Buffer buffer_27 has open pins: in=buffer_26_out, out=open
  Pull_Resistor pull_resistor_13 (.node(controlled_buffer_15_out));
  Multiplexer #(.width(6), .enable("false")) multiplexer_2 (
    .in0(adder_8_out[21:16]), .in1(counter_2_q), .out(multiplexer_2_out), .sel(load));
  Pull_Resistor pull_resistor_14 (.node(load));
  assign or_3_out = ram_1_data | decoder_1_out31;  // OR_Gate or_3, 32 bits wide
  buf buffer_28 (buffer_28_out, buffer_29_out);
  buf buffer_29 (buffer_29_out, subtractor_4_out[0]);
  Pull_Resistor pull_resistor_15 (.node(pull_resistor_15_node));
  not not_5 (pull_resistor_15_node, adder_7_out[21]);
  buf buffer_30 (pull_resistor_15_node, load);
  // Probe on stage
  RAM #(.addrWidth(6), .dataWidth(32), .bus("separate")) ram_1 (
    .addr(multiplexer_2_out), .din(or_3_out), .data(ram_1_data), .str(controlled_buffer_15_out),
    .sel(pull_resistor_15_node), .clk(buffer_28_out), .ld(buffer_13_out), .clr(rising_edge_pulse_1_out));
  buf buffer_31 (buffer_13_out, load);
  assign or_4_out = ram_2_data | decoder_1_out31;  // OR_Gate or_4, 32 bits wide
  Counter #(.width(2), .max('h3)) counter_3 (
    .Q(stage), .clk(inc_stage_counter), .clr(done_t));  // open: load, D, count, carry
  Pull_Resistor pull_resistor_16 (.node(inc_stage_counter));
  Register #(.width(4), .trigger("low")) register_11 (.D(address), .Q(register_11_q), .clk(1'b0));  // open: en, clr
  Register #(.width(4), .trigger("low")) register_12 (.D(address), .Q(register_12_q), .clk(1'b0));  // open: en, clr
  Register #(.width(4), .trigger("low")) register_13 (.D(address), .Q(register_13_q), .clk(1'b0));  // open: en, clr
  Register #(.width(4), .trigger("low")) register_14 (.D(address), .Q(register_14_q), .clk(1'b0));  // open: en, clr
  Register #(.width(4), .trigger("low")) register_15 (.D(address), .Q(register_15_q), .clk(1'b0));  // open: en, clr
  Register #(.width(4), .trigger("low")) register_16 (.D(address), .Q(register_16_q), .clk(1'b0));  // open: en, clr
  Register #(.width(4), .trigger("low")) register_17 (.D(address), .Q(register_17_q), .clk(1'b0));  // open: en, clr
  buf buffer_32 (buffer_32_out, buffer_33_out);
  buf buffer_33 (buffer_33_out, subtractor_4_out[0]);
  Pull_Resistor pull_resistor_17 (.node(pull_resistor_17_node));
  buf buffer_34 (pull_resistor_17_node, load);
  buf buffer_35 (pull_resistor_17_node, adder_7_out[21]);
  buf buffer_36 (buffer_13_out, load);
  Register #(.width(4), .trigger("low")) register_18 (.D(address), .Q(register_18_q), .clk(1'b0));  // open: en, clr
  RAM #(.addrWidth(6), .dataWidth(32), .bus("separate")) ram_2 (
    .addr(multiplexer_2_out), .din(or_4_out), .data(ram_2_data), .str(controlled_buffer_15_out),
    .sel(pull_resistor_17_node), .clk(buffer_32_out), .ld(buffer_13_out), .clr(rising_edge_pulse_1_out));
  and and_13 (reset, ~register_18_q[0], register_18_q[1], register_18_q[2], ~register_18_q[3]);  // AND_Gate
  assign address = and_14_out ? 4'b1111 : 4'bz;  // Controlled_Buffer controlled_buffer_16
  and and_14 (and_14_out, skip_loop, ~stage[0], stage[1], ~register_11_q[0], register_11_q[1], register_11_q[2], ~register_11_q[3]);  // AND_Gate
  Pull_Resistor pull_resistor_18 (.node(and_14_out));
  assign address = and_15_out ? 4'b0111 : 4'bz;  // Controlled_Buffer controlled_buffer_17
  and and_15 (and_15_out, skip_loop, stage[0], ~stage[1], ~register_12_q[0], register_12_q[1], register_12_q[2], ~register_12_q[3]);  // AND_Gate
  Pull_Resistor pull_resistor_19 (.node(and_15_out));
  assign address = and_16_out ? 4'b0111 : 4'bz;  // Controlled_Buffer controlled_buffer_18
  and and_16 (and_16_out, skip_loop, ~stage[0], ~stage[1], ~register_13_q[0], register_13_q[1], register_13_q[2], ~register_13_q[3]);  // AND_Gate
  Pull_Resistor pull_resistor_20 (.node(and_16_out));
  assign address = and_17_out ? 4'b1111 : 4'bz;  // Controlled_Buffer controlled_buffer_19
  and and_17 (and_17_out, ~skip_loop, stage[0], stage[1], ~register_14_q[0], register_14_q[1], register_14_q[2], ~register_14_q[3]);  // AND_Gate
  Pull_Resistor pull_resistor_21 (.node(and_17_out));
  assign address = and_18_out ? 4'b0111 : 4'bz;  // Controlled_Buffer controlled_buffer_20
  and and_18 (and_18_out, ~skip_loop, ~stage[0], stage[1], ~register_15_q[0], register_15_q[1], register_15_q[2], ~register_15_q[3]);  // AND_Gate
  Pull_Resistor pull_resistor_22 (.node(and_18_out));
  assign address = and_19_out ? 4'b1010 : 4'bz;  // Controlled_Buffer controlled_buffer_21
  and and_19 (and_19_out, ~skip_loop, stage[0], ~stage[1], ~register_16_q[0], register_16_q[1], register_16_q[2], ~register_16_q[3]);  // AND_Gate
  Pull_Resistor pull_resistor_23 (.node(and_19_out));
  assign address = and_20_out ? 4'b0111 : 4'bz;  // Controlled_Buffer controlled_buffer_22
  and and_20 (and_20_out, ~skip_loop, ~stage[0], ~stage[1], ~register_17_q[0], register_17_q[1], register_17_q[2], ~register_17_q[3]);  // AND_Gate
  Pull_Resistor pull_resistor_24 (.node(and_20_out));
  Register #(.width(4), .trigger("low")) register_19 (.D(address), .Q(register_19_q), .clk(1'b0));  // open: en, clr
  Register #(.width(4), .trigger("low")) register_20 (.D(address), .Q(register_20_q), .clk(1'b0));  // open: en, clr
  Register #(.width(4), .trigger("low")) register_21 (.D(address), .Q(register_21_q), .clk(1'b0));  // open: en, clr
  Register #(.width(4), .trigger("low")) register_22 (.D(address), .Q(register_22_q), .clk(1'b0));  // open: en, clr
  Register #(.width(4), .trigger("low")) register_23 (.D(address), .Q(register_23_q), .clk(1'b0));  // open: en, clr
  Register #(.width(4), .trigger("low")) register_24 (.D(address), .Q(register_24_q), .clk(1'b0));  // open: en, clr
  and and_21 (and_21_out, register_19_q[0], register_19_q[1], register_19_q[2], ~register_19_q[3]);  // AND_Gate
  Pull_Resistor pull_resistor_25 (.node(and_21_out));
  buf buffer_37 (inc_stage_counter, and_21_out);
  assign address = and_22_out ? 4'b1100 : 4'bz;  // Controlled_Buffer controlled_buffer_23
  and and_22 (and_22_out, skip_loop, stage[0], ~stage[1], register_20_q[0], register_20_q[1], register_20_q[2], ~register_20_q[3]);  // AND_Gate
  Pull_Resistor pull_resistor_26 (.node(and_22_out));
  assign address = and_23_out ? 4'b1011 : 4'bz;  // Controlled_Buffer controlled_buffer_24
  and and_23 (and_23_out, skip_loop, ~stage[0], ~stage[1], register_21_q[0], register_21_q[1], register_21_q[2], ~register_21_q[3]);  // AND_Gate
  Pull_Resistor pull_resistor_27 (.node(and_23_out));
  assign address = and_24_out ? 4'b1100 : 4'bz;  // Controlled_Buffer controlled_buffer_25
  and and_24 (and_24_out, ~skip_loop, ~stage[0], stage[1], register_22_q[0], register_22_q[1], register_22_q[2], ~register_22_q[3]);  // AND_Gate
  Pull_Resistor pull_resistor_28 (.node(and_24_out));
  assign address = and_25_out ? 4'b1011 : 4'bz;  // Controlled_Buffer controlled_buffer_26
  and and_25 (and_25_out, ~skip_loop, stage[0], ~stage[1], register_23_q[0], register_23_q[1], register_23_q[2], ~register_23_q[3]);  // AND_Gate
  Pull_Resistor pull_resistor_29 (.node(and_25_out));
  assign address = and_26_out ? 4'b1000 : 4'bz;  // Controlled_Buffer controlled_buffer_27
  and and_26 (and_26_out, ~skip_loop, ~stage[0], ~stage[1], register_24_q[0], register_24_q[1], register_24_q[2], ~register_24_q[3]);  // AND_Gate
  Pull_Resistor pull_resistor_30 (.node(and_26_out));
  Register #(.width(4), .trigger("low")) register_25 (.D(address), .Q(register_25_q), .clk(1'b0));  // open: en, clr
  assign address = inc_stored_values ? 4'b0010 : 4'bz;  // Controlled_Buffer controlled_buffer_28
  and and_27 (inc_stored_values, ~register_25_q[0], ~register_25_q[1], ~register_25_q[2], register_25_q[3]);  // AND_Gate
  Pull_Resistor pull_resistor_31 (.node(inc_stored_values));
  Counter counter_4 (.Q(counter_4_q), .clk(inc_loop_counter), .clr(clear));  // open: load, D, count, carry
  Counter counter_5 (.Q(counter_5_q), .clk(inc_loop_counter), .clr(or_5_out));  // open: load, D, count, carry
  or or_5 (or_5_out, and_28_out, clear);
  Comparator comparator_4 (.a(counter_4_q), .b(loop_count[23:16]), .lt(comparator_4_lt));  // open: gt, eq
  not not_6 (loop_counter, comparator_4_lt);
  Comparator comparator_5 (.a(counter_5_q), .b(8'ha), .lt(comparator_5_lt));  // open: gt, eq
  not not_7 (loop_stopper_counter, comparator_5_lt);
  and and_28 (and_28_out, loop_stopper_counter, sync);
  Register #(.width(4), .trigger("low")) register_26 (.D(address), .Q(register_26_q), .clk(1'b0));  // open: en, clr
  Register #(.width(4), .trigger("low")) register_27 (.D(address), .Q(register_27_q), .clk(1'b0));  // open: en, clr
  Register #(.width(4), .trigger("low")) register_28 (.D(address), .Q(register_28_q), .clk(1'b0));  // open: en, clr
  Register #(.width(4), .trigger("low")) register_29 (.D(address), .Q(register_29_q), .clk(1'b0));  // open: en, clr
  assign address = and_29_out ? 4'b1010 : 4'bz;  // Controlled_Buffer controlled_buffer_29
  and and_29 (and_29_out, loop_counter, loop_stopper_counter, ~register_26_q[0], register_26_q[1], ~register_26_q[2], register_26_q[3]);  // AND_Gate
  Pull_Resistor pull_resistor_32 (.node(and_29_out));
  assign address = and_30_out ? 4'b1010 : 4'bz;  // Controlled_Buffer controlled_buffer_30
  and and_30 (and_30_out, ~loop_counter, loop_stopper_counter, ~register_27_q[0], register_27_q[1], ~register_27_q[2], register_27_q[3]);  // AND_Gate
  Pull_Resistor pull_resistor_33 (.node(and_30_out));
  assign address = and_31_out ? 4'b0111 : 4'bz;  // Controlled_Buffer controlled_buffer_31
  and and_31 (and_31_out, loop_counter, ~loop_stopper_counter, ~register_28_q[0], register_28_q[1], ~register_28_q[2], register_28_q[3]);  // AND_Gate
  Pull_Resistor pull_resistor_34 (.node(and_31_out));
  assign address = inc_loop_counter ? 4'b1000 : 4'bz;  // Controlled_Buffer controlled_buffer_32
  and and_32 (inc_loop_counter, ~loop_counter, ~loop_stopper_counter, ~register_29_q[0], register_29_q[1], ~register_29_q[2], register_29_q[3]);  // AND_Gate
  Pull_Resistor pull_resistor_35 (.node(inc_loop_counter));
  Register #(.width(4), .trigger("low")) register_30 (.D(address), .Q(register_30_q), .clk(1'b0));  // open: en, clr
  and and_33 (load_x2y2, register_30_q[0], register_30_q[1], ~register_30_q[2], register_30_q[3]);  // AND_Gate
  Pull_Resistor pull_resistor_36 (.node(load_x2y2));
  assign address = load_x2y2 ? 4'b0010 : 4'bz;  // Controlled_Buffer controlled_buffer_33
  Register #(.width(4), .trigger("low")) register_31 (.D(address), .Q(register_31_q), .clk(1'b0));  // open: en, clr
  assign address = clear ? 4'b0011 : 4'bz;  // Controlled_Buffer controlled_buffer_34
  and and_34 (clear, ~register_31_q[0], ~register_31_q[1], register_31_q[2], register_31_q[3]);  // AND_Gate
  Pull_Resistor pull_resistor_37 (.node(clear));
  Register #(.width(4), .trigger("low")) register_32 (.D(address), .Q(register_32_q), .clk(1'b0));  // open: en, clr
  and and_35 (done_t, register_32_q[0], register_32_q[1], register_32_q[2], register_32_q[3]);
  assign address = done_t ? 4'b0000 : 4'bz;  // Controlled_Buffer controlled_buffer_35
  Pull_Resistor pull_resistor_38 (.node(done_t));

  // Other names for the same wires on the sheet: clk = sync

  // Notes on the sheet:
  //   set_point: pull=up
  //   done: pull=up
  //   Config
  //   In
  //   halt
  //   Mission decoder
  //   load x1y1
  //   Math
  //   Out
  //   Out reg
  //   set
  //   buffer_1 drives only 1 and floats otherwise
  //   clear wait counter
  //   (wait buff)
  //   wait
  //   not_2 drives only 0 and floats otherwise
  //   buffer_13 drives only 1 and floats otherwise
  //   Main logic 
  //   not_5 drives only 1 and floats otherwise
  //   buffer_30 drives only 1 and floats otherwise
  //   buffer_31 drives only 1 and floats otherwise
  //   buffer_34 drives only 1 and floats otherwise
  //   buffer_35 drives only 1 and floats otherwise
  //   buffer_36 drives only 1 and floats otherwise
  //   reset
  //   stage
  //   buffer_37 drives only 1 and floats otherwise
  //   inc
  //   loop
  //   load x2y2
  //   clear
  //   done
  //   kek
endmodule

module playground (
  input  [31:0] x1,
  input  [31:0] x2,
  input  [31:0] y1,
  input  [31:0] x1_2,
  input  [31:0] x2_2,
  input  [31:0] y2,
  input  [31:0] y2_2,
  input  [31:0] y1_2
);

  wire buffer_1_out, clear_out, clk, dda_test_sync_1_done, dda_test_sync_1_set_point, start_DDA_out,
       update_out;
  wire [31:0] dda_test_sync_1_out_x, dda_test_sync_1_out_y;

  Clock clock_1 (.out(clk));
  buf buffer_1 (buffer_1_out, update_out);
  Button update (.out(update_out));
  Button clear (.out(clear_out));
  Button start_DDA (.out(start_DDA_out));
  DDA_test_sync dda_test_sync_1 (
    .clk(clk), .new_data(start_DDA_out), .x2(x2), .x1(x1_2), .y2(y2), .y1(y1_2),
    .out_y(dda_test_sync_1_out_y), .out_x(dda_test_sync_1_out_x), .set_point(dda_test_sync_1_set_point),
    .done(dda_test_sync_1_done));  // open: status
  buf buffer_2 (buffer_1_out, dda_test_sync_1_done);
  Pull_Resistor pull_resistor_1 (.node(buffer_1_out));
  // DotMatrix #(.inputtype("select"), .matrixcols(32), .matrixrows(32), .persist(128)) dotmatrix_1: pin names not known; wires that end beside it: dda_test_sync_1_out_x[21:16]
  // DotMatrix #(.inputtype("select"), .matrixcols(32), .matrixrows(32), .persist(128)) dotmatrix_2: pin names not known; wires that end beside it: dda_test_sync_1_out_y[21:16], dda_test_sync_1_set_point, buffer_1_out, clear_out, clk
  // DotMatrix #(.inputtype("select"), .matrixcols(32), .matrixrows(32), .persist(128)) dotmatrix_3: pin names not known
  // DotMatrix #(.inputtype("select"), .matrixcols(32), .matrixrows(32), .persist(128)) dotmatrix_4: pin names not known
  // _64_display_v2 64_display_v2_1: pin names not known

  // Notes on the sheet:
  //   buffer_1 drives only 1 and floats otherwise
  //   buffer_2 drives only 1 and floats otherwise
endmodule

module _64x64_display_controller_new (
  output [31:0] out_1,
  output [31:0] out_2,
  output [31:0] out_3,
  output [31:0] out_4,
  output [31:0] out_5,
  output [31:0] out_6,
  output [31:0] out_7,
  output [31:0] out_8,
  output [31:0] out_9,
  output [31:0] out_10,
  output [31:0] out_11,
  output [31:0] out_12,
  output [31:0] out_13,
  output [31:0] out_14,
  output [31:0] out_15,
  output [31:0] out_16,
  output [31:0] out_17,
  output [31:0] out_18,
  output [31:0] out_19,
  output [31:0] out_20,
  output [31:0] out_21,
  output [31:0] out_22,
  output [31:0] out_23,
  output [31:0] out_24,
  output [31:0] out_25,
  output [31:0] out_26,
  output [31:0] out_27,
  output [31:0] out_28,
  output [31:0] out_29,
  output [31:0] out_30,
  output [31:0] out_31,
  output [31:0] out_32,
  output [31:0] out_33,
  output [31:0] out_34,
  output [31:0] out_35,
  output [31:0] out_36,
  output [31:0] out_37,
  output [31:0] out_38,
  output [31:0] out_39,
  output [31:0] out_40,
  output [31:0] out_41,
  output [31:0] out_42,
  output [31:0] out_43,
  output [31:0] out_44,
  output [31:0] out_45,
  output [31:0] out_46,
  output [31:0] out_47,
  output [31:0] out_48,
  output [31:0] out_49,
  output [31:0] out_50,
  output [31:0] out_51,
  output [31:0] out_52,
  output [31:0] out_53,
  output [31:0] out_54,
  output [31:0] out_55,
  output [31:0] out_56,
  output [31:0] out_57,
  output [31:0] out_58,
  output [31:0] out_59,
  output [31:0] out_60,
  output [31:0] out_61,
  output [31:0] out_62,
  output [31:0] out_63,
  output [31:0] out_64,
  output [31:0] out_65,
  output [31:0] out_66,
  output [31:0] out_67,
  output [31:0] out_68,
  output [31:0] out_69,
  output [31:0] out_70,
  output [31:0] out_71,
  output [31:0] out_72,
  output [31:0] out_73,
  output [31:0] out_74,
  output [31:0] out_75,
  output [31:0] out_76,
  output [31:0] out_77,
  output [31:0] out_78,
  output [31:0] out_79,
  output [31:0] out_80,
  output [31:0] out_81,
  output [31:0] out_82,
  output [31:0] out_83,
  output [31:0] out_84,
  output [31:0] out_85,
  output [31:0] out_86,
  output [31:0] out_87,
  output [31:0] out_88,
  output [31:0] out_89,
  output [31:0] out_90,
  output [31:0] out_91,
  output [31:0] out_92,
  output [31:0] out_93,
  output [31:0] out_94,
  output [31:0] out_95,
  output [31:0] out_96,
  output [31:0] out_97,
  output [31:0] out_98,
  output [31:0] out_99,
  output [31:0] out_100,
  output [31:0] out_101,
  output [31:0] out_102,
  output [31:0] out_103,
  output [31:0] out_104,
  output [31:0] out_105,
  output [31:0] out_106,
  output [31:0] out_107,
  output [31:0] out_108,
  output [31:0] out_109,
  output [31:0] out_110,
  output [31:0] out_111,
  output [31:0] out_112,
  output [31:0] out_113,
  output [31:0] out_114,
  output [31:0] out_115,
  output [31:0] out_116,
  output [31:0] out_117,
  output [31:0] out_118,
  output [31:0] out_119,
  output [31:0] out_120,
  output [31:0] out_121,
  output [31:0] out_122,
  output [31:0] out_123,
  output [31:0] out_124,
  output [31:0] out_125,
  output [31:0] out_126,
  output [31:0] out_127,
  output [31:0] out_128
);

  wire and_1_out, and_2_out, and_3_out, and_4_out, undriven_4;
  wire [5:0] undriven_3;
  wire [31:0] demultiplexer_1_out0, demultiplexer_1_out1, demultiplexer_1_out2, demultiplexer_1_out3,
       demultiplexer_1_out4, demultiplexer_1_out5, demultiplexer_1_out6, demultiplexer_1_out7,
       demultiplexer_1_out8, demultiplexer_1_out9, demultiplexer_1_out10, demultiplexer_1_out11,
       demultiplexer_1_out12, demultiplexer_1_out13, demultiplexer_1_out14, demultiplexer_1_out15,
       demultiplexer_1_out16, demultiplexer_1_out17, demultiplexer_1_out18, demultiplexer_1_out19,
       demultiplexer_1_out20, demultiplexer_1_out21, demultiplexer_1_out22, demultiplexer_1_out23,
       demultiplexer_1_out24, demultiplexer_1_out25, demultiplexer_1_out26, demultiplexer_1_out27,
       demultiplexer_1_out28, demultiplexer_1_out29, demultiplexer_1_out30, demultiplexer_1_out31,
       demultiplexer_2_out0, demultiplexer_2_out1, demultiplexer_2_out2, demultiplexer_2_out3,
       demultiplexer_2_out4, demultiplexer_2_out5, demultiplexer_2_out6, demultiplexer_2_out7,
       demultiplexer_2_out8, demultiplexer_2_out9, demultiplexer_2_out10, demultiplexer_2_out11,
       demultiplexer_2_out12, demultiplexer_2_out13, demultiplexer_2_out14, demultiplexer_2_out15,
       demultiplexer_2_out16, demultiplexer_2_out17, demultiplexer_2_out18, demultiplexer_2_out19,
       demultiplexer_2_out20, demultiplexer_2_out21, demultiplexer_2_out22, demultiplexer_2_out23,
       demultiplexer_2_out24, demultiplexer_2_out25, demultiplexer_2_out26, demultiplexer_2_out27,
       demultiplexer_2_out28, demultiplexer_2_out29, demultiplexer_2_out30, demultiplexer_2_out31,
       demultiplexer_3_out0, demultiplexer_3_out1, demultiplexer_3_out2, demultiplexer_3_out3,
       demultiplexer_3_out4, demultiplexer_3_out5, demultiplexer_3_out6, demultiplexer_3_out7,
       demultiplexer_3_out8, demultiplexer_3_out9, demultiplexer_3_out10, demultiplexer_3_out11,
       demultiplexer_3_out12, demultiplexer_3_out13, demultiplexer_3_out14, demultiplexer_3_out15,
       demultiplexer_3_out16, demultiplexer_3_out17, demultiplexer_3_out18, demultiplexer_3_out19,
       demultiplexer_3_out20, demultiplexer_3_out21, demultiplexer_3_out22, demultiplexer_3_out23,
       demultiplexer_3_out24, demultiplexer_3_out25, demultiplexer_3_out26, demultiplexer_3_out27,
       demultiplexer_3_out28, demultiplexer_3_out29, demultiplexer_3_out30, demultiplexer_3_out31,
       demultiplexer_4_out0, demultiplexer_4_out1, demultiplexer_4_out2, demultiplexer_4_out3,
       demultiplexer_4_out4, demultiplexer_4_out5, demultiplexer_4_out6, demultiplexer_4_out7,
       demultiplexer_4_out8, demultiplexer_4_out9, demultiplexer_4_out10, demultiplexer_4_out11,
       demultiplexer_4_out12, demultiplexer_4_out13, demultiplexer_4_out14, demultiplexer_4_out15,
       demultiplexer_4_out16, demultiplexer_4_out17, demultiplexer_4_out18, demultiplexer_4_out19,
       demultiplexer_4_out20, demultiplexer_4_out21, demultiplexer_4_out22, demultiplexer_4_out23,
       demultiplexer_4_out24, demultiplexer_4_out25, demultiplexer_4_out26, demultiplexer_4_out27,
       demultiplexer_4_out28, demultiplexer_4_out29, demultiplexer_4_out30, demultiplexer_4_out31, undriven,
       undriven_2;

  Demultiplexer #(.select(5), .width(32), .tristate("true")) demultiplexer_1 (
    .out0(demultiplexer_1_out0), .out1(demultiplexer_1_out1), .out2(demultiplexer_1_out2),
    .out3(demultiplexer_1_out3), .out4(demultiplexer_1_out4), .out5(demultiplexer_1_out5),
    .out6(demultiplexer_1_out6), .out7(demultiplexer_1_out7), .out8(demultiplexer_1_out8),
    .out9(demultiplexer_1_out9), .out10(demultiplexer_1_out10), .out11(demultiplexer_1_out11),
    .out12(demultiplexer_1_out12), .out13(demultiplexer_1_out13), .out14(demultiplexer_1_out14),
    .out15(demultiplexer_1_out15), .out16(demultiplexer_1_out16), .out17(demultiplexer_1_out17),
    .out18(demultiplexer_1_out18), .out19(demultiplexer_1_out19), .out20(demultiplexer_1_out20),
    .out21(demultiplexer_1_out21), .out22(demultiplexer_1_out22), .out23(demultiplexer_1_out23),
    .out24(demultiplexer_1_out24), .out25(demultiplexer_1_out25), .out26(demultiplexer_1_out26),
    .out27(demultiplexer_1_out27), .out28(demultiplexer_1_out28), .out29(demultiplexer_1_out29),
    .out30(demultiplexer_1_out30), .out31(demultiplexer_1_out31), .in(undriven), .sel(undriven_3[4:0]),
    .en(and_1_out));
  and and_1 (and_1_out, undriven_4, undriven_3[5]);
  Demultiplexer #(.select(5), .width(32), .tristate("true")) demultiplexer_2 (
    .out0(demultiplexer_2_out0), .out1(demultiplexer_2_out1), .out2(demultiplexer_2_out2),
    .out3(demultiplexer_2_out3), .out4(demultiplexer_2_out4), .out5(demultiplexer_2_out5),
    .out6(demultiplexer_2_out6), .out7(demultiplexer_2_out7), .out8(demultiplexer_2_out8),
    .out9(demultiplexer_2_out9), .out10(demultiplexer_2_out10), .out11(demultiplexer_2_out11),
    .out12(demultiplexer_2_out12), .out13(demultiplexer_2_out13), .out14(demultiplexer_2_out14),
    .out15(demultiplexer_2_out15), .out16(demultiplexer_2_out16), .out17(demultiplexer_2_out17),
    .out18(demultiplexer_2_out18), .out19(demultiplexer_2_out19), .out20(demultiplexer_2_out20),
    .out21(demultiplexer_2_out21), .out22(demultiplexer_2_out22), .out23(demultiplexer_2_out23),
    .out24(demultiplexer_2_out24), .out25(demultiplexer_2_out25), .out26(demultiplexer_2_out26),
    .out27(demultiplexer_2_out27), .out28(demultiplexer_2_out28), .out29(demultiplexer_2_out29),
    .out30(demultiplexer_2_out30), .out31(demultiplexer_2_out31), .in(undriven_2), .sel(undriven_3[4:0]),
    .en(and_2_out));
  and and_2 (and_2_out, undriven_4, undriven_3[5]);
  Demultiplexer #(.select(5), .width(32), .tristate("true")) demultiplexer_3 (
    .out0(demultiplexer_3_out0), .out1(demultiplexer_3_out1), .out2(demultiplexer_3_out2),
    .out3(demultiplexer_3_out3), .out4(demultiplexer_3_out4), .out5(demultiplexer_3_out5),
    .out6(demultiplexer_3_out6), .out7(demultiplexer_3_out7), .out8(demultiplexer_3_out8),
    .out9(demultiplexer_3_out9), .out10(demultiplexer_3_out10), .out11(demultiplexer_3_out11),
    .out12(demultiplexer_3_out12), .out13(demultiplexer_3_out13), .out14(demultiplexer_3_out14),
    .out15(demultiplexer_3_out15), .out16(demultiplexer_3_out16), .out17(demultiplexer_3_out17),
    .out18(demultiplexer_3_out18), .out19(demultiplexer_3_out19), .out20(demultiplexer_3_out20),
    .out21(demultiplexer_3_out21), .out22(demultiplexer_3_out22), .out23(demultiplexer_3_out23),
    .out24(demultiplexer_3_out24), .out25(demultiplexer_3_out25), .out26(demultiplexer_3_out26),
    .out27(demultiplexer_3_out27), .out28(demultiplexer_3_out28), .out29(demultiplexer_3_out29),
    .out30(demultiplexer_3_out30), .out31(demultiplexer_3_out31), .in(undriven_2), .sel(undriven_3[4:0]),
    .en(and_3_out));
  and and_3 (and_3_out, undriven_4, ~undriven_3[5]);  // AND_Gate
  Demultiplexer #(.select(5), .width(32), .tristate("true")) demultiplexer_4 (
    .out0(demultiplexer_4_out0), .out1(demultiplexer_4_out1), .out2(demultiplexer_4_out2),
    .out3(demultiplexer_4_out3), .out4(demultiplexer_4_out4), .out5(demultiplexer_4_out5),
    .out6(demultiplexer_4_out6), .out7(demultiplexer_4_out7), .out8(demultiplexer_4_out8),
    .out9(demultiplexer_4_out9), .out10(demultiplexer_4_out10), .out11(demultiplexer_4_out11),
    .out12(demultiplexer_4_out12), .out13(demultiplexer_4_out13), .out14(demultiplexer_4_out14),
    .out15(demultiplexer_4_out15), .out16(demultiplexer_4_out16), .out17(demultiplexer_4_out17),
    .out18(demultiplexer_4_out18), .out19(demultiplexer_4_out19), .out20(demultiplexer_4_out20),
    .out21(demultiplexer_4_out21), .out22(demultiplexer_4_out22), .out23(demultiplexer_4_out23),
    .out24(demultiplexer_4_out24), .out25(demultiplexer_4_out25), .out26(demultiplexer_4_out26),
    .out27(demultiplexer_4_out27), .out28(demultiplexer_4_out28), .out29(demultiplexer_4_out29),
    .out30(demultiplexer_4_out30), .out31(demultiplexer_4_out31), .in(undriven), .sel(undriven_3[4:0]),
    .en(and_4_out));
  and and_4 (and_4_out, undriven_4, ~undriven_3[5]);  // AND_Gate
  Register #(.width(32), .trigger("high")) register_1 (
    .D(demultiplexer_1_out0), .Q(out_1), .clk(and_1_out));  // open: en, clr
  Register #(.width(32), .trigger("high")) register_2 (
    .D(demultiplexer_2_out0), .Q(out_33), .clk(and_2_out));  // open: en, clr
  Register #(.width(32), .trigger("high")) register_3 (
    .D(demultiplexer_3_out0), .Q(out_65), .clk(and_3_out));  // open: en, clr
  Register #(.width(32), .trigger("high")) register_4 (
    .D(demultiplexer_4_out0), .Q(out_97), .clk(and_4_out));  // open: en, clr
  Register #(.width(32), .trigger("high")) register_5 (
    .D(demultiplexer_1_out1), .Q(out_2), .clk(and_1_out));  // open: en, clr
  Register #(.width(32), .trigger("high")) register_6 (
    .D(demultiplexer_2_out1), .Q(out_34), .clk(and_2_out));  // open: en, clr
  Register #(.width(32), .trigger("high")) register_7 (
    .D(demultiplexer_3_out1), .Q(out_66), .clk(and_3_out));  // open: en, clr
  Register #(.width(32), .trigger("high")) register_8 (
    .D(demultiplexer_4_out1), .Q(out_98), .clk(and_4_out));  // open: en, clr
  Register #(.width(32), .trigger("high")) register_9 (
    .D(demultiplexer_1_out2), .Q(out_3), .clk(and_1_out));  // open: en, clr
  Register #(.width(32), .trigger("high")) register_10 (
    .D(demultiplexer_2_out2), .Q(out_35), .clk(and_2_out));  // open: en, clr
  Register #(.width(32), .trigger("high")) register_11 (
    .D(demultiplexer_3_out2), .Q(out_67), .clk(and_3_out));  // open: en, clr
  Register #(.width(32), .trigger("high")) register_12 (
    .D(demultiplexer_4_out2), .Q(out_99), .clk(and_4_out));  // open: en, clr
  Register #(.width(32), .trigger("high")) register_13 (
    .D(demultiplexer_1_out3), .Q(out_4), .clk(and_1_out));  // open: en, clr
  Register #(.width(32), .trigger("high")) register_14 (
    .D(demultiplexer_2_out3), .Q(out_36), .clk(and_2_out));  // open: en, clr
  Register #(.width(32), .trigger("high")) register_15 (
    .D(demultiplexer_3_out3), .Q(out_68), .clk(and_3_out));  // open: en, clr
  Register #(.width(32), .trigger("high")) register_16 (
    .D(demultiplexer_4_out3), .Q(out_100), .clk(and_4_out));  // open: en, clr
  Register #(.width(32), .trigger("high")) register_17 (
    .D(demultiplexer_1_out4), .Q(out_5), .clk(and_1_out));  // open: en, clr
  Register #(.width(32), .trigger("high")) register_18 (
    .D(demultiplexer_2_out4), .Q(out_37), .clk(and_2_out));  // open: en, clr
  Register #(.width(32), .trigger("high")) register_19 (
    .D(demultiplexer_3_out4), .Q(out_69), .clk(and_3_out));  // open: en, clr
  Register #(.width(32), .trigger("high")) register_20 (
    .D(demultiplexer_4_out4), .Q(out_101), .clk(and_4_out));  // open: en, clr
  Register #(.width(32), .trigger("high")) register_21 (
    .D(demultiplexer_1_out5), .Q(out_6), .clk(and_1_out));  // open: en, clr
  Register #(.width(32), .trigger("high")) register_22 (
    .D(demultiplexer_2_out5), .Q(out_38), .clk(and_2_out));  // open: en, clr
  Register #(.width(32), .trigger("high")) register_23 (
    .D(demultiplexer_3_out5), .Q(out_70), .clk(and_3_out));  // open: en, clr
  Register #(.width(32), .trigger("high")) register_24 (
    .D(demultiplexer_4_out5), .Q(out_102), .clk(and_4_out));  // open: en, clr
  Register #(.width(32), .trigger("high")) register_25 (
    .D(demultiplexer_1_out6), .Q(out_7), .clk(and_1_out));  // open: en, clr
  Register #(.width(32), .trigger("high")) register_26 (
    .D(demultiplexer_2_out6), .Q(out_39), .clk(and_2_out));  // open: en, clr
  Register #(.width(32), .trigger("high")) register_27 (
    .D(demultiplexer_3_out6), .Q(out_71), .clk(and_3_out));  // open: en, clr
  Register #(.width(32), .trigger("high")) register_28 (
    .D(demultiplexer_4_out6), .Q(out_103), .clk(and_4_out));  // open: en, clr
  Register #(.width(32), .trigger("high")) register_29 (
    .D(demultiplexer_1_out7), .Q(out_8), .clk(and_1_out));  // open: en, clr
  Register #(.width(32), .trigger("high")) register_30 (
    .D(demultiplexer_2_out7), .Q(out_40), .clk(and_2_out));  // open: en, clr
  Register #(.width(32), .trigger("high")) register_31 (
    .D(demultiplexer_3_out7), .Q(out_72), .clk(and_3_out));  // open: en, clr
  Register #(.width(32), .trigger("high")) register_32 (
    .D(demultiplexer_4_out7), .Q(out_104), .clk(and_4_out));  // open: en, clr
  Register #(.width(32), .trigger("high")) register_33 (
    .D(demultiplexer_1_out8), .Q(out_9), .clk(and_1_out));  // open: en, clr
  Register #(.width(32), .trigger("high")) register_34 (
    .D(demultiplexer_2_out8), .Q(out_41), .clk(and_2_out));  // open: en, clr
  Register #(.width(32), .trigger("high")) register_35 (
    .D(demultiplexer_3_out8), .Q(out_73), .clk(and_3_out));  // open: en, clr
  Register #(.width(32), .trigger("high")) register_36 (
    .D(demultiplexer_4_out8), .Q(out_105), .clk(and_4_out));  // open: en, clr
  Register #(.width(32), .trigger("high")) register_37 (
    .D(demultiplexer_1_out9), .Q(out_10), .clk(and_1_out));  // open: en, clr
  Register #(.width(32), .trigger("high")) register_38 (
    .D(demultiplexer_2_out9), .Q(out_42), .clk(and_2_out));  // open: en, clr
  Register #(.width(32), .trigger("high")) register_39 (
    .D(demultiplexer_3_out9), .Q(out_74), .clk(and_3_out));  // open: en, clr
  Register #(.width(32), .trigger("high")) register_40 (
    .D(demultiplexer_4_out9), .Q(out_106), .clk(and_4_out));  // open: en, clr
  Register #(.width(32), .trigger("high")) register_41 (
    .D(demultiplexer_1_out10), .Q(out_11), .clk(and_1_out));  // open: en, clr
  Register #(.width(32), .trigger("high")) register_42 (
    .D(demultiplexer_2_out10), .Q(out_43), .clk(and_2_out));  // open: en, clr
  Register #(.width(32), .trigger("high")) register_43 (
    .D(demultiplexer_3_out10), .Q(out_75), .clk(and_3_out));  // open: en, clr
  Register #(.width(32), .trigger("high")) register_44 (
    .D(demultiplexer_4_out10), .Q(out_107), .clk(and_4_out));  // open: en, clr
  Register #(.width(32), .trigger("high")) register_45 (
    .D(demultiplexer_1_out11), .Q(out_12), .clk(and_1_out));  // open: en, clr
  Register #(.width(32), .trigger("high")) register_46 (
    .D(demultiplexer_2_out11), .Q(out_44), .clk(and_2_out));  // open: en, clr
  Register #(.width(32), .trigger("high")) register_47 (
    .D(demultiplexer_3_out11), .Q(out_76), .clk(and_3_out));  // open: en, clr
  Register #(.width(32), .trigger("high")) register_48 (
    .D(demultiplexer_4_out11), .Q(out_108), .clk(and_4_out));  // open: en, clr
  Register #(.width(32), .trigger("high")) register_49 (
    .D(demultiplexer_1_out12), .Q(out_13), .clk(and_1_out));  // open: en, clr
  Register #(.width(32), .trigger("high")) register_50 (
    .D(demultiplexer_2_out12), .Q(out_45), .clk(and_2_out));  // open: en, clr
  Register #(.width(32), .trigger("high")) register_51 (
    .D(demultiplexer_3_out12), .Q(out_77), .clk(and_3_out));  // open: en, clr
  Register #(.width(32), .trigger("high")) register_52 (
    .D(demultiplexer_4_out12), .Q(out_109), .clk(and_4_out));  // open: en, clr
  Register #(.width(32), .trigger("high")) register_53 (
    .D(demultiplexer_1_out13), .Q(out_14), .clk(and_1_out));  // open: en, clr
  Register #(.width(32), .trigger("high")) register_54 (
    .D(demultiplexer_2_out13), .Q(out_46), .clk(and_2_out));  // open: en, clr
  Register #(.width(32), .trigger("high")) register_55 (
    .D(demultiplexer_3_out13), .Q(out_78), .clk(and_3_out));  // open: en, clr
  Register #(.width(32), .trigger("high")) register_56 (
    .D(demultiplexer_4_out13), .Q(out_110), .clk(and_4_out));  // open: en, clr
  Register #(.width(32), .trigger("high")) register_57 (
    .D(demultiplexer_1_out14), .Q(out_15), .clk(and_1_out));  // open: en, clr
  Register #(.width(32), .trigger("high")) register_58 (
    .D(demultiplexer_2_out14), .Q(out_47), .clk(and_2_out));  // open: en, clr
  Register #(.width(32), .trigger("high")) register_59 (
    .D(demultiplexer_3_out14), .Q(out_79), .clk(and_3_out));  // open: en, clr
  Register #(.width(32), .trigger("high")) register_60 (
    .D(demultiplexer_4_out14), .Q(out_111), .clk(and_4_out));  // open: en, clr
  Register #(.width(32), .trigger("high")) register_61 (
    .D(demultiplexer_1_out15), .Q(out_16), .clk(and_1_out));  // open: en, clr
  Register #(.width(32), .trigger("high")) register_62 (
    .D(demultiplexer_2_out15), .Q(out_48), .clk(and_2_out));  // open: en, clr
  Register #(.width(32), .trigger("high")) register_63 (
    .D(demultiplexer_3_out15), .Q(out_80), .clk(and_3_out));  // open: en, clr
  Register #(.width(32), .trigger("high")) register_64 (
    .D(demultiplexer_4_out15), .Q(out_112), .clk(and_4_out));  // open: en, clr
  Register #(.width(32), .trigger("high")) register_65 (
    .D(demultiplexer_1_out16), .Q(out_17), .clk(and_1_out));  // open: en, clr
  Register #(.width(32), .trigger("high")) register_66 (
    .D(demultiplexer_2_out16), .Q(out_49), .clk(and_2_out));  // open: en, clr
  Register #(.width(32), .trigger("high")) register_67 (
    .D(demultiplexer_3_out16), .Q(out_81), .clk(and_3_out));  // open: en, clr
  Register #(.width(32), .trigger("high")) register_68 (
    .D(demultiplexer_4_out16), .Q(out_113), .clk(and_4_out));  // open: en, clr
  Register #(.width(32), .trigger("high")) register_69 (
    .D(demultiplexer_1_out17), .Q(out_18), .clk(and_1_out));  // open: en, clr
  Register #(.width(32), .trigger("high")) register_70 (
    .D(demultiplexer_2_out17), .Q(out_50), .clk(and_2_out));  // open: en, clr
  Register #(.width(32), .trigger("high")) register_71 (
    .D(demultiplexer_3_out17), .Q(out_82), .clk(and_3_out));  // open: en, clr
  Register #(.width(32), .trigger("high")) register_72 (
    .D(demultiplexer_4_out17), .Q(out_114), .clk(and_4_out));  // open: en, clr
  Register #(.width(32), .trigger("high")) register_73 (
    .D(demultiplexer_1_out18), .Q(out_19), .clk(and_1_out));  // open: en, clr
  Register #(.width(32), .trigger("high")) register_74 (
    .D(demultiplexer_2_out18), .Q(out_51), .clk(and_2_out));  // open: en, clr
  Register #(.width(32), .trigger("high")) register_75 (
    .D(demultiplexer_3_out18), .Q(out_83), .clk(and_3_out));  // open: en, clr
  Register #(.width(32), .trigger("high")) register_76 (
    .D(demultiplexer_4_out18), .Q(out_115), .clk(and_4_out));  // open: en, clr
  Register #(.width(32), .trigger("high")) register_77 (
    .D(demultiplexer_1_out19), .Q(out_20), .clk(and_1_out));  // open: en, clr
  Register #(.width(32), .trigger("high")) register_78 (
    .D(demultiplexer_2_out19), .Q(out_52), .clk(and_2_out));  // open: en, clr
  Register #(.width(32), .trigger("high")) register_79 (
    .D(demultiplexer_3_out19), .Q(out_84), .clk(and_3_out));  // open: en, clr
  Register #(.width(32), .trigger("high")) register_80 (
    .D(demultiplexer_4_out19), .Q(out_116), .clk(and_4_out));  // open: en, clr
  Register #(.width(32), .trigger("high")) register_81 (
    .D(demultiplexer_1_out20), .Q(out_21), .clk(and_1_out));  // open: en, clr
  Register #(.width(32), .trigger("high")) register_82 (
    .D(demultiplexer_2_out20), .Q(out_53), .clk(and_2_out));  // open: en, clr
  Register #(.width(32), .trigger("high")) register_83 (
    .D(demultiplexer_3_out20), .Q(out_85), .clk(and_3_out));  // open: en, clr
  Register #(.width(32), .trigger("high")) register_84 (
    .D(demultiplexer_4_out20), .Q(out_117), .clk(and_4_out));  // open: en, clr
  Register #(.width(32), .trigger("high")) register_85 (
    .D(demultiplexer_1_out21), .Q(out_22), .clk(and_1_out));  // open: en, clr
  Register #(.width(32), .trigger("high")) register_86 (
    .D(demultiplexer_2_out21), .Q(out_54), .clk(and_2_out));  // open: en, clr
  Register #(.width(32), .trigger("high")) register_87 (
    .D(demultiplexer_3_out21), .Q(out_86), .clk(and_3_out));  // open: en, clr
  Register #(.width(32), .trigger("high")) register_88 (
    .D(demultiplexer_4_out21), .Q(out_118), .clk(and_4_out));  // open: en, clr
  Register #(.width(32), .trigger("high")) register_89 (
    .D(demultiplexer_1_out22), .Q(out_23), .clk(and_1_out));  // open: en, clr
  Register #(.width(32), .trigger("high")) register_90 (
    .D(demultiplexer_2_out22), .Q(out_55), .clk(and_2_out));  // open: en, clr
  Register #(.width(32), .trigger("high")) register_91 (
    .D(demultiplexer_3_out22), .Q(out_87), .clk(and_3_out));  // open: en, clr
  Register #(.width(32), .trigger("high")) register_92 (
    .D(demultiplexer_4_out22), .Q(out_119), .clk(and_4_out));  // open: en, clr
  Register #(.width(32), .trigger("high")) register_93 (
    .D(demultiplexer_1_out23), .Q(out_24), .clk(and_1_out));  // open: en, clr
  Register #(.width(32), .trigger("high")) register_94 (
    .D(demultiplexer_2_out23), .Q(out_56), .clk(and_2_out));  // open: en, clr
  Register #(.width(32), .trigger("high")) register_95 (
    .D(demultiplexer_3_out23), .Q(out_88), .clk(and_3_out));  // open: en, clr
  Register #(.width(32), .trigger("high")) register_96 (
    .D(demultiplexer_4_out23), .Q(out_120), .clk(and_4_out));  // open: en, clr
  Register #(.width(32), .trigger("high")) register_97 (
    .D(demultiplexer_1_out24), .Q(out_25), .clk(and_1_out));  // open: en, clr
  Register #(.width(32), .trigger("high")) register_98 (
    .D(demultiplexer_2_out24), .Q(out_57), .clk(and_2_out));  // open: en, clr
  Register #(.width(32), .trigger("high")) register_99 (
    .D(demultiplexer_3_out24), .Q(out_89), .clk(and_3_out));  // open: en, clr
  Register #(.width(32), .trigger("high")) register_100 (
    .D(demultiplexer_4_out24), .Q(out_121), .clk(and_4_out));  // open: en, clr
  Register #(.width(32), .trigger("high")) register_101 (
    .D(demultiplexer_1_out25), .Q(out_26), .clk(and_1_out));  // open: en, clr
  Register #(.width(32), .trigger("high")) register_102 (
    .D(demultiplexer_2_out25), .Q(out_58), .clk(and_2_out));  // open: en, clr
  Register #(.width(32), .trigger("high")) register_103 (
    .D(demultiplexer_3_out25), .Q(out_90), .clk(and_3_out));  // open: en, clr
  Register #(.width(32), .trigger("high")) register_104 (
    .D(demultiplexer_4_out25), .Q(out_122), .clk(and_4_out));  // open: en, clr
  Register #(.width(32), .trigger("high")) register_105 (
    .D(demultiplexer_1_out26), .Q(out_27), .clk(and_1_out));  // open: en, clr
  Register #(.width(32), .trigger("high")) register_106 (
    .D(demultiplexer_2_out26), .Q(out_59), .clk(and_2_out));  // open: en, clr
  Register #(.width(32), .trigger("high")) register_107 (
    .D(demultiplexer_3_out26), .Q(out_91), .clk(and_3_out));  // open: en, clr
  Register #(.width(32), .trigger("high")) register_108 (
    .D(demultiplexer_4_out26), .Q(out_123), .clk(and_4_out));  // open: en, clr
  Register #(.width(32), .trigger("high")) register_109 (
    .D(demultiplexer_1_out27), .Q(out_28), .clk(and_1_out));  // open: en, clr
  Register #(.width(32), .trigger("high")) register_110 (
    .D(demultiplexer_2_out27), .Q(out_60), .clk(and_2_out));  // open: en, clr
  Register #(.width(32), .trigger("high")) register_111 (
    .D(demultiplexer_3_out27), .Q(out_92), .clk(and_3_out));  // open: en, clr
  Register #(.width(32), .trigger("high")) register_112 (
    .D(demultiplexer_4_out27), .Q(out_124), .clk(and_4_out));  // open: en, clr
  Register #(.width(32), .trigger("high")) register_113 (
    .D(demultiplexer_1_out28), .Q(out_29), .clk(and_1_out));  // open: en, clr
  Register #(.width(32), .trigger("high")) register_114 (
    .D(demultiplexer_2_out28), .Q(out_61), .clk(and_2_out));  // open: en, clr
  Register #(.width(32), .trigger("high")) register_115 (
    .D(demultiplexer_3_out28), .Q(out_93), .clk(and_3_out));  // open: en, clr
  Register #(.width(32), .trigger("high")) register_116 (
    .D(demultiplexer_4_out28), .Q(out_125), .clk(and_4_out));  // open: en, clr
  Register #(.width(32), .trigger("high")) register_117 (
    .D(demultiplexer_1_out29), .Q(out_30), .clk(and_1_out));  // open: en, clr
  Register #(.width(32), .trigger("high")) register_118 (
    .D(demultiplexer_2_out29), .Q(out_62), .clk(and_2_out));  // open: en, clr
  Register #(.width(32), .trigger("high")) register_119 (
    .D(demultiplexer_3_out29), .Q(out_94), .clk(and_3_out));  // open: en, clr
  Register #(.width(32), .trigger("high")) register_120 (
    .D(demultiplexer_4_out29), .Q(out_126), .clk(and_4_out));  // open: en, clr
  Register #(.width(32), .trigger("high")) register_121 (
    .D(demultiplexer_1_out30), .Q(out_31), .clk(and_1_out));  // open: en, clr
  Register #(.width(32), .trigger("high")) register_122 (
    .D(demultiplexer_2_out30), .Q(out_63), .clk(and_2_out));  // open: en, clr
  Register #(.width(32), .trigger("high")) register_123 (
    .D(demultiplexer_3_out30), .Q(out_95), .clk(and_3_out));  // open: en, clr
  Register #(.width(32), .trigger("high")) register_124 (
    .D(demultiplexer_4_out30), .Q(out_127), .clk(and_4_out));  // open: en, clr
  Register #(.width(32), .trigger("high")) register_125 (
    .D(demultiplexer_1_out31), .Q(out_32), .clk(and_1_out));  // open: en, clr
  Register #(.width(32), .trigger("high")) register_126 (
    .D(demultiplexer_2_out31), .Q(out_64), .clk(and_2_out));  // open: en, clr
  Register #(.width(32), .trigger("high")) register_127 (
    .D(demultiplexer_3_out31), .Q(out_96), .clk(and_3_out));  // open: en, clr
  Register #(.width(32), .trigger("high")) register_128 (
    .D(demultiplexer_4_out31), .Q(out_128), .clk(and_4_out));  // open: en, clr

  // Notes on the sheet:
  //   kek
  //   kek
endmodule
module ex_cube (
  input  [31:0] distance,
  input  [31:0] side_size,
  output [31:0] out_3,
  output [31:0] out_4,
  output [31:0] out_5,
  output [31:0] out_6,
  output [31:0] out_7,
  output [31:0] out_8,
  output [31:0] out_9,
  output [31:0] out_10,
  output [31:0] out_11,
  output [31:0] out_12,
  output [31:0] out_13,
  output [31:0] out_14,
  output [31:0] out_15,
  output [31:0] out_16,
  output [31:0] out_17,
  output [31:0] out_18,
  output [31:0] out_19,
  output [31:0] out_20,
  output [31:0] out_21,
  output [31:0] out_22,
  output [31:0] out_23,
  output [31:0] out_24,
  output [31:0] out_25,
  output [31:0] out_26,
  output [31:0] out_27,
  output [31:0] out_28,
  output [31:0] out_29,
  output [31:0] out_30,
  output [31:0] out_31,
  output [31:0] out_32,
  output [31:0] out_33,
  output [31:0] out_34,
  output [31:0] out_35,
  output [31:0] out_36,
  output [31:0] out_37,
  output [31:0] out_38,
  output [31:0] out_39,
  output [31:0] out_40,
  output [31:0] out_41,
  output [31:0] out_42,
  output [31:0] out_43,
  output [31:0] out_44,
  output [31:0] out_45,
  output [31:0] out_46,
  output [31:0] out_47,
  output [31:0] out_48,
  output [31:0] out_49,
  output [31:0] out_50
);

  fp_mult fp_mult_1 (.in1(32'hffff0000), .in2(side_size), .out(out_3));
  fp_mult fp_mult_2 (.in1(32'hffff0000), .in2(side_size), .out(out_7));
  Adder #(.width(32)) adder_1 (.a(32'hffff0000), .b(distance), .out(out_11));  // open: cin, cout
  fp_mult fp_mult_3 (.in1(32'hffff0000), .in2(side_size), .out(out_15));
  fp_mult fp_mult_4 (.in1(32'h10000), .in2(side_size), .out(out_19));
  Adder #(.width(32)) adder_2 (.a(32'hffff0000), .b(distance), .out(out_23));  // open: cin, cout
  fp_mult fp_mult_5 (.in1(32'hffff0000), .in2(side_size), .out(out_27));
  fp_mult fp_mult_6 (.in1(32'h10000), .in2(side_size), .out(out_31));
  Adder #(.width(32)) adder_3 (.a(32'hffff0000), .b(distance), .out(out_35));  // open: cin, cout
  fp_mult fp_mult_7 (.in1(32'hffff0000), .in2(side_size), .out(out_39));
  fp_mult fp_mult_8 (.in1(32'h10000), .in2(side_size), .out(out_43));
  Adder #(.width(32)) adder_4 (.a(32'h10000), .b(distance), .out(out_47));  // open: cin, cout
  fp_mult fp_mult_9 (.in1(32'hffff0000), .in2(side_size), .out(out_4));
  fp_mult fp_mult_10 (.in1(32'h10000), .in2(side_size), .out(out_8));
  Adder #(.width(32)) adder_5 (.a(32'hffff0000), .b(distance), .out(out_12));  // open: cin, cout
  fp_mult fp_mult_11 (.in1(32'h10000), .in2(side_size), .out(out_16));
  fp_mult fp_mult_12 (.in1(32'h10000), .in2(side_size), .out(out_20));
  Adder #(.width(32)) adder_6 (.a(32'hffff0000), .b(distance), .out(out_24));  // open: cin, cout
  fp_mult fp_mult_13 (.in1(32'h10000), .in2(side_size), .out(out_28));
  fp_mult fp_mult_14 (.in1(32'h10000), .in2(side_size), .out(out_32));
  Adder #(.width(32)) adder_7 (.a(32'hffff0000), .b(distance), .out(out_36));  // open: cin, cout
  fp_mult fp_mult_15 (.in1(32'h10000), .in2(side_size), .out(out_40));
  fp_mult fp_mult_16 (.in1(32'h10000), .in2(side_size), .out(out_44));
  Adder #(.width(32)) adder_8 (.a(32'h10000), .b(distance), .out(out_48));  // open: cin, cout
  fp_mult fp_mult_17 (.in1(32'h10000), .in2(side_size), .out(out_5));
  fp_mult fp_mult_18 (.in1(32'h10000), .in2(side_size), .out(out_9));
  Adder #(.width(32)) adder_9 (.a(32'hffff0000), .b(distance), .out(out_13));  // open: cin, cout
  fp_mult fp_mult_19 (.in1(32'h10000), .in2(side_size), .out(out_17));
  fp_mult fp_mult_20 (.in1(32'hffff0000), .in2(side_size), .out(out_21));
  Adder #(.width(32)) adder_10 (.a(32'hffff0000), .b(distance), .out(out_25));  // open: cin, cout
  fp_mult fp_mult_21 (.in1(32'h10000), .in2(side_size), .out(out_29));
  fp_mult fp_mult_22 (.in1(32'hffff0000), .in2(side_size), .out(out_33));
  Adder #(.width(32)) adder_11 (.a(32'hffff0000), .b(distance), .out(out_37));  // open: cin, cout
  fp_mult fp_mult_23 (.in1(32'h10000), .in2(side_size), .out(out_41));
  fp_mult fp_mult_24 (.in1(32'hffff0000), .in2(side_size), .out(out_45));
  Adder #(.width(32)) adder_12 (.a(32'h10000), .b(distance), .out(out_49));  // open: cin, cout
  fp_mult fp_mult_25 (.in1(32'h10000), .in2(side_size), .out(out_6));
  fp_mult fp_mult_26 (.in1(32'hffff0000), .in2(side_size), .out(out_10));
  Adder #(.width(32)) adder_13 (.a(32'hffff0000), .b(distance), .out(out_14));  // open: cin, cout
  fp_mult fp_mult_27 (.in1(32'hffff0000), .in2(side_size), .out(out_18));
  fp_mult fp_mult_28 (.in1(32'hffff0000), .in2(side_size), .out(out_22));
  Adder #(.width(32)) adder_14 (.a(32'hffff0000), .b(distance), .out(out_26));  // open: cin, cout
  fp_mult fp_mult_29 (.in1(32'hffff0000), .in2(side_size), .out(out_30));
  fp_mult fp_mult_30 (.in1(32'hffff0000), .in2(side_size), .out(out_34));
  Adder #(.width(32)) adder_15 (.a(32'hffff0000), .b(distance), .out(out_38));  // open: cin, cout
  fp_mult fp_mult_31 (.in1(32'hffff0000), .in2(side_size), .out(out_42));
  fp_mult fp_mult_32 (.in1(32'hffff0000), .in2(side_size), .out(out_46));
  Adder #(.width(32)) adder_16 (.a(32'h10000), .b(distance), .out(out_50));  // open: cin, cout

  // Other names for the same wires on the sheet: d[31:0] = distance; s[31:0] = side_size
endmodule

module ex_2 (
  input  [31:0] distance,
  input  [31:0] side_size,
  output [31:0] out_3,
  output [31:0] out_4,
  output [31:0] out_5,
  output [31:0] out_6,
  output [31:0] out_7,
  output [31:0] out_8,
  output [31:0] out_9,
  output [31:0] out_10,
  output [31:0] out_11,
  output [31:0] out_12,
  output [31:0] out_13,
  output [31:0] out_14,
  output [31:0] out_15,
  output [31:0] out_16,
  output [31:0] out_17,
  output [31:0] out_18,
  output [31:0] out_19,
  output [31:0] out_20,
  output [31:0] out_21,
  output [31:0] out_22,
  output [31:0] out_23,
  output [31:0] out_24,
  output [31:0] out_25,
  output [31:0] out_26,
  output [31:0] out_27,
  output [31:0] out_28,
  output [31:0] out_29,
  output [31:0] out_30,
  output [31:0] out_31,
  output [31:0] out_32,
  output [31:0] out_33,
  output [31:0] out_34,
  output [31:0] out_35,
  output [31:0] out_36,
  output [31:0] out_37,
  output [31:0] out_38,
  output [31:0] out_39,
  output [31:0] out_40,
  output [31:0] out_41,
  output [31:0] out_42,
  output [31:0] out_43,
  output [31:0] out_44,
  output [31:0] out_45,
  output [31:0] out_46,
  output [31:0] out_47,
  output [31:0] out_48,
  output [31:0] out_49,
  output [31:0] out_50
);

  fp_mult fp_mult_1 (.in1(32'hffff0000), .in2(side_size), .out(out_3));
  fp_mult fp_mult_2 (.in1(32'hffff0000), .in2(side_size), .out(out_7));
  Adder #(.width(32)) adder_1 (.a(32'hffff0000), .b(distance), .out(out_11));  // open: cin, cout
  fp_mult fp_mult_3 (.in1(32'h10000), .in2(side_size), .out(out_15));
  fp_mult fp_mult_4 (.in1(32'hffff0000), .in2(side_size), .out(out_19));
  Adder #(.width(32)) adder_2 (.a(32'hffff0000), .b(distance), .out(out_23));  // open: cin, cout
  fp_mult fp_mult_5 (.in1(32'h10000), .in2(side_size), .out(out_31));
  Adder #(.width(32)) adder_3 (.a({32{1'b0}}), .b(distance), .out(out_35));  // open: cin, cout
  fp_mult fp_mult_6 (.in1(32'h10000), .in2(side_size), .out(out_39));
  fp_mult fp_mult_7 (.in1(32'hffff0000), .in2(side_size), .out(out_43));
  Adder #(.width(32)) adder_4 (.a(32'hffff0000), .b(distance), .out(out_47));  // open: cin, cout
  fp_mult fp_mult_8 (.in1(32'h10000), .in2(side_size), .out(out_4));
  fp_mult fp_mult_9 (.in1(32'hffff0000), .in2(side_size), .out(out_8));
  Adder #(.width(32)) adder_5 (.a(32'hffff0000), .b(distance), .out(out_12));  // open: cin, cout
  fp_mult fp_mult_10 (.in1(32'h10000), .in2(side_size), .out(out_16));
  fp_mult fp_mult_11 (.in1(32'hffff0000), .in2(side_size), .out(out_20));
  Adder #(.width(32)) adder_6 (.a(32'h10000), .b(distance), .out(out_24));  // open: cin, cout
  fp_mult fp_mult_12 (.in1(32'h10000), .in2(side_size), .out(out_32));
  Adder #(.width(32)) adder_7 (.a({32{1'b0}}), .b(distance), .out(out_36));  // open: cin, cout
  fp_mult fp_mult_13 (.in1(32'h10000), .in2(side_size), .out(out_40));
  fp_mult fp_mult_14 (.in1(32'hffff0000), .in2(side_size), .out(out_44));
  Adder #(.width(32)) adder_8 (.a(32'h10000), .b(distance), .out(out_48));  // open: cin, cout
  fp_mult fp_mult_15 (.in1(32'h10000), .in2(side_size), .out(out_5));
  fp_mult fp_mult_16 (.in1(32'hffff0000), .in2(side_size), .out(out_9));
  Adder #(.width(32)) adder_9 (.a(32'h10000), .b(distance), .out(out_13));  // open: cin, cout
  fp_mult fp_mult_17 (.in1(32'hffff0000), .in2(side_size), .out(out_17));
  fp_mult fp_mult_18 (.in1(32'hffff0000), .in2(side_size), .out(out_21));
  Adder #(.width(32)) adder_10 (.a(32'h10000), .b(distance), .out(out_25));  // open: cin, cout
  fp_mult fp_mult_19 (.in1(32'h10000), .in2(side_size), .out(out_33));
  Adder #(.width(32)) adder_11 (.a({32{1'b0}}), .b(distance), .out(out_37));  // open: cin, cout
  fp_mult fp_mult_20 (.in1(32'hffff0000), .in2(side_size), .out(out_41));
  fp_mult fp_mult_21 (.in1(32'hffff0000), .in2(side_size), .out(out_45));
  Adder #(.width(32)) adder_12 (.a(32'h10000), .b(distance), .out(out_49));  // open: cin, cout
  fp_mult fp_mult_22 (.in1(32'hffff0000), .in2(side_size), .out(out_6));
  fp_mult fp_mult_23 (.in1(32'hffff0000), .in2(side_size), .out(out_10));
  Adder #(.width(32)) adder_13 (.a(32'h10000), .b(distance), .out(out_14));  // open: cin, cout
  fp_mult fp_mult_24 (.in1(32'hffff0000), .in2(side_size), .out(out_18));
  fp_mult fp_mult_25 (.in1(32'hffff0000), .in2(side_size), .out(out_22));
  Adder #(.width(32)) adder_14 (.a(32'hffff0000), .b(distance), .out(out_26));  // open: cin, cout
  fp_mult fp_mult_26 (.in1(32'h10000), .in2(side_size), .out(out_34));
  Adder #(.width(32)) adder_15 (.a({32{1'b0}}), .b(distance), .out(out_38));  // open: cin, cout
  fp_mult fp_mult_27 (.in1(32'hffff0000), .in2(side_size), .out(out_42));
  fp_mult fp_mult_28 (.in1(32'hffff0000), .in2(side_size), .out(out_46));
  Adder #(.width(32)) adder_16 (.a(32'hffff0000), .b(distance), .out(out_50));  // open: cin, cout

  assign out_27 = {32{1'b0}};
  assign out_28 = {32{1'b0}};
  assign out_29 = {32{1'b0}};
  assign out_30 = {32{1'b0}};

  // Other names for the same wires on the sheet: d[31:0] = distance; s[31:0] = side_size
endmodule

module test_rot (
  input  [31:0] distance,
  input  [31:0] rotation,
  input  [31:0] in_3,
  input  [31:0] in_4,
  input  [31:0] in_5,
  output [31:0] out_6,
  output [31:0] out_7,
  output [31:0] out_8
);

  wire [31:0] cos, matrix_mult_4x4_1_out11, matrix_mult_4x4_1_out12, matrix_mult_4x4_1_out13,
       matrix_mult_4x4_1_out14, matrix_mult_4x4_2_out11, matrix_mult_4x4_2_out12, matrix_mult_4x4_2_out13,
       matrix_mult_4x4_2_out14, matrix_mult_4x4_3_out11, matrix_mult_4x4_3_out12, matrix_mult_4x4_3_out13,
       matrix_mult_4x4_3_out14, minus_sin, negator_1_out, sin;

  Negator #(.width(32)) negator_1 (.in(distance), .out(negator_1_out));
  matrix_mult_4x4 matrix_mult_4x4_1 (
    .in_1(in_3), .in_5(in_4), .in_9(in_5), .in_13(32'h10000), .in_17(32'h10000), .in_22(32'h10000),
    .in_27(32'h10000), .in_28(negator_1_out), .in_32(32'h10000), .out11(matrix_mult_4x4_1_out11),
    .out12(matrix_mult_4x4_1_out12), .out13(matrix_mult_4x4_1_out13), .out14(matrix_mult_4x4_1_out14));  // open: in_2, in_3, in_4, in_6, in_7, in_8, in_10, in_11, in_12, in_14, in_15, in_16, in_18, in_19, in_20, in_21, in_23, in_24, in_25, in_26, in_29, in_30, in_31, out21, out31, out41, out22, out32, out42, out23, out33, out43, out24, out34, out44
  sin sin_1 (.in_fp(rotation), .sin(sin));
  cos cos_1 (.cos(cos), .in_fp(rotation));
  Negator #(.width(32)) negator_2 (.in(sin), .out(minus_sin));
  matrix_mult_4x4 matrix_mult_4x4_2 (
    .in_1(matrix_mult_4x4_1_out11), .in_5(matrix_mult_4x4_1_out12), .in_9(matrix_mult_4x4_1_out13),
    .in_13(matrix_mult_4x4_1_out14), .in_17(cos), .in_19(sin), .in_22(32'h10000), .in_25(minus_sin),
    .in_27(cos), .in_32(32'h10000), .out11(matrix_mult_4x4_2_out11), .out12(matrix_mult_4x4_2_out12),
    .out13(matrix_mult_4x4_2_out13), .out14(matrix_mult_4x4_2_out14));  // open: in_2, in_3, in_4, in_6, in_7, in_8, in_10, in_11, in_12, in_14, in_15, in_16, in_18, in_20, in_21, in_23, in_24, in_26, in_28, in_29, in_30, in_31, out21, out31, out41, out22, out32, out42, out23, out33, out43, out24, out34, out44
  matrix_mult_4x4 matrix_mult_4x4_3 (
    .in_1(matrix_mult_4x4_2_out11), .in_5(matrix_mult_4x4_2_out12), .in_9(matrix_mult_4x4_2_out13),
    .in_13(matrix_mult_4x4_2_out14), .in_17(32'h10000), .in_22(32'h10000), .in_27(32'h10000),
    .in_28(distance), .in_32(32'h10000), .out11(matrix_mult_4x4_3_out11), .out12(matrix_mult_4x4_3_out12),
    .out13(matrix_mult_4x4_3_out13), .out14(matrix_mult_4x4_3_out14));  // open: in_2, in_3, in_4, in_6, in_7, in_8, in_10, in_11, in_12, in_14, in_15, in_16, in_18, in_19, in_20, in_21, in_23, in_24, in_25, in_26, in_29, in_30, in_31, out21, out31, out41, out22, out32, out42, out23, out33, out43, out24, out34, out44
  vec4_to_vec3 vec4_to_vec3_1 (
    .in1(matrix_mult_4x4_3_out11), .in2(matrix_mult_4x4_3_out12), .in3(matrix_mult_4x4_3_out13),
    .in4(matrix_mult_4x4_3_out14), .out1(out_6), .out2(out_7), .out3(out_8));
endmodule
