// Logisim project main.circ as structural Verilog
module main (
  input  [31:0] in_1,
  input  [31:0] in_2,
  input  [5:0] x,
  input  [5:0] y,
  input  [31:0] Load_sample,
  input  state,
  input  in_7,
  input  Load_to_MR1,
  input  [31:0] x2,
  input  Load_to__MR2,
  input  [31:0] x1,
  input  [31:0] y2,
  input  [31:0] y1,
  input  [31:0] in_14,
  input  [31:0] in_15,
  input  [31:0] in_16,
  input  [31:0] in_17,
  input  [31:0] in_18,
  input  [31:0] in_19,
  input  [31:0] in_20,
  input  [31:0] in_21,
  input  [31:0] in_22
);

  wire and_1_out, button_1_out, button_2_out, clk, clock_x2_1_clk_x2, clock_x2_2_clk_x2, clock_x2_3_clk_x2,
       clock_x2_4_clk_x2, counter_1_carry, counter_2_carry, dda_async_1_done, dda_async_1_set_point,
       dda_test_sync_1_done, dda_test_sync_1_set_point, mission, n32bit_decoder_short_1_dot,
       n32bit_decoder_short_1_sign, n32bit_decoder_short_2_dot, n32bit_decoder_short_2_sign,
       n32bit_decoder_short_3_dot, n32bit_decoder_short_3_sign, n32bit_decoder_short_4_dot,
       n32bit_decoder_short_4_sign, n32bit_decoder_short_5_dot, n32bit_decoder_short_5_sign,
       n32bit_decoder_short_6_dot, n32bit_decoder_short_6_sign, n32bit_decoder_short_7_dot,
       n32bit_decoder_short_7_sign, n32bit_decoder_short_8_dot, n32bit_decoder_short_8_sign,
       n32bit_decoder_short_9_dot, n32bit_decoder_short_9_sign, n32bit_decoder_short_10_dot,
       n32bit_decoder_short_10_sign, n32bit_decoder_short_11_dot, n32bit_decoder_short_11_sign,
       n32bit_decoder_short_12_dot, n32bit_decoder_short_12_sign, n32bit_decoder_short_13_dot,
       n32bit_decoder_short_13_sign, n32bit_decoder_short_14_dot, n32bit_decoder_short_14_sign,
       n32bit_decoder_short_15_dot, n32bit_decoder_short_15_sign, n32bit_decoder_short_16_dot,
       n32bit_decoder_short_16_sign, n32bit_decoder_short_17_dot, n32bit_decoder_short_17_sign,
       n32bit_decoder_short_18_dot, n32bit_decoder_short_18_sign, n32bit_decoder_short_19_dot,
       n32bit_decoder_short_19_sign, n32bit_decoder_short_20_dot, n32bit_decoder_short_20_sign,
       n32bit_decoder_short_21_dot, n32bit_decoder_short_21_sign, n32bit_decoder_short_22_dot,
       n32bit_decoder_short_22_sign, reset_out, vram_as_1_mode;
  wire [3:0] adder_1_out, bit_extender_2_out, bit_extender_3_out, matrix_addr_offset, matrix_addr_R1,
       matrix_addr_R2, n32bit_decoder_short_1__0, n32bit_decoder_short_1__1, n32bit_decoder_short_1__1_2,
       n32bit_decoder_short_1__2, n32bit_decoder_short_1__2_2, n32bit_decoder_short_1__3,
       n32bit_decoder_short_1__3_2, n32bit_decoder_short_1__4, n32bit_decoder_short_1__4_2,
       n32bit_decoder_short_1__5, n32bit_decoder_short_2__0, n32bit_decoder_short_2__1,
       n32bit_decoder_short_2__1_2, n32bit_decoder_short_2__2, n32bit_decoder_short_2__2_2,
       n32bit_decoder_short_2__3, n32bit_decoder_short_2__3_2, n32bit_decoder_short_2__4,
       n32bit_decoder_short_2__4_2, n32bit_decoder_short_2__5, n32bit_decoder_short_3__0,
       n32bit_decoder_short_3__1, n32bit_decoder_short_3__1_2, n32bit_decoder_short_3__2,
       n32bit_decoder_short_3__2_2, n32bit_decoder_short_3__3, n32bit_decoder_short_3__3_2,
       n32bit_decoder_short_3__4, n32bit_decoder_short_3__4_2, n32bit_decoder_short_3__5,
       n32bit_decoder_short_4__0, n32bit_decoder_short_4__1, n32bit_decoder_short_4__1_2,
       n32bit_decoder_short_4__2, n32bit_decoder_short_4__2_2, n32bit_decoder_short_4__3,
       n32bit_decoder_short_4__3_2, n32bit_decoder_short_4__4, n32bit_decoder_short_4__4_2,
       n32bit_decoder_short_4__5, n32bit_decoder_short_5__0, n32bit_decoder_short_5__1,
       n32bit_decoder_short_5__1_2, n32bit_decoder_short_5__2, n32bit_decoder_short_5__2_2,
       n32bit_decoder_short_5__3, n32bit_decoder_short_5__3_2, n32bit_decoder_short_5__4,
       n32bit_decoder_short_5__4_2, n32bit_decoder_short_5__5, n32bit_decoder_short_6__0,
       n32bit_decoder_short_6__1, n32bit_decoder_short_6__1_2, n32bit_decoder_short_6__2,
       n32bit_decoder_short_6__2_2, n32bit_decoder_short_6__3, n32bit_decoder_short_6__3_2,
       n32bit_decoder_short_6__4, n32bit_decoder_short_6__4_2, n32bit_decoder_short_6__5,
       n32bit_decoder_short_7__0, n32bit_decoder_short_7__1, n32bit_decoder_short_7__1_2,
       n32bit_decoder_short_7__2, n32bit_decoder_short_7__2_2, n32bit_decoder_short_7__3,
       n32bit_decoder_short_7__3_2, n32bit_decoder_short_7__4, n32bit_decoder_short_7__4_2,
       n32bit_decoder_short_7__5, n32bit_decoder_short_8__0, n32bit_decoder_short_8__1,
       n32bit_decoder_short_8__1_2, n32bit_decoder_short_8__2, n32bit_decoder_short_8__2_2,
       n32bit_decoder_short_8__3, n32bit_decoder_short_8__3_2, n32bit_decoder_short_8__4,
       n32bit_decoder_short_8__4_2, n32bit_decoder_short_8__5, n32bit_decoder_short_9__0,
       n32bit_decoder_short_9__1, n32bit_decoder_short_9__1_2, n32bit_decoder_short_9__2,
       n32bit_decoder_short_9__2_2, n32bit_decoder_short_9__3, n32bit_decoder_short_9__3_2,
       n32bit_decoder_short_9__4, n32bit_decoder_short_9__4_2, n32bit_decoder_short_9__5,
       n32bit_decoder_short_10__0, n32bit_decoder_short_10__1, n32bit_decoder_short_10__1_2,
       n32bit_decoder_short_10__2, n32bit_decoder_short_10__2_2, n32bit_decoder_short_10__3,
       n32bit_decoder_short_10__3_2, n32bit_decoder_short_10__4, n32bit_decoder_short_10__4_2,
       n32bit_decoder_short_10__5, n32bit_decoder_short_11__0, n32bit_decoder_short_11__1,
       n32bit_decoder_short_11__1_2, n32bit_decoder_short_11__2, n32bit_decoder_short_11__2_2,
       n32bit_decoder_short_11__3, n32bit_decoder_short_11__3_2, n32bit_decoder_short_11__4,
       n32bit_decoder_short_11__4_2, n32bit_decoder_short_11__5, n32bit_decoder_short_12__0,
       n32bit_decoder_short_12__1, n32bit_decoder_short_12__1_2, n32bit_decoder_short_12__2,
       n32bit_decoder_short_12__2_2, n32bit_decoder_short_12__3, n32bit_decoder_short_12__3_2,
       n32bit_decoder_short_12__4, n32bit_decoder_short_12__4_2, n32bit_decoder_short_12__5,
       n32bit_decoder_short_13__0, n32bit_decoder_short_13__1, n32bit_decoder_short_13__1_2,
       n32bit_decoder_short_13__2, n32bit_decoder_short_13__2_2, n32bit_decoder_short_13__3,
       n32bit_decoder_short_13__3_2, n32bit_decoder_short_13__4, n32bit_decoder_short_13__4_2,
       n32bit_decoder_short_13__5, n32bit_decoder_short_14__0, n32bit_decoder_short_14__1,
       n32bit_decoder_short_14__1_2, n32bit_decoder_short_14__2, n32bit_decoder_short_14__2_2,
       n32bit_decoder_short_14__3, n32bit_decoder_short_14__3_2, n32bit_decoder_short_14__4,
       n32bit_decoder_short_14__4_2, n32bit_decoder_short_14__5, n32bit_decoder_short_15__0,
       n32bit_decoder_short_15__1, n32bit_decoder_short_15__1_2, n32bit_decoder_short_15__2,
       n32bit_decoder_short_15__2_2, n32bit_decoder_short_15__3, n32bit_decoder_short_15__3_2,
       n32bit_decoder_short_15__4, n32bit_decoder_short_15__4_2, n32bit_decoder_short_15__5,
       n32bit_decoder_short_16__0, n32bit_decoder_short_16__1, n32bit_decoder_short_16__1_2,
       n32bit_decoder_short_16__2, n32bit_decoder_short_16__2_2, n32bit_decoder_short_16__3,
       n32bit_decoder_short_16__3_2, n32bit_decoder_short_16__4, n32bit_decoder_short_16__4_2,
       n32bit_decoder_short_16__5, n32bit_decoder_short_17__0, n32bit_decoder_short_17__1,
       n32bit_decoder_short_17__1_2, n32bit_decoder_short_17__2, n32bit_decoder_short_17__2_2,
       n32bit_decoder_short_17__3, n32bit_decoder_short_17__3_2, n32bit_decoder_short_17__4,
       n32bit_decoder_short_17__4_2, n32bit_decoder_short_17__5, n32bit_decoder_short_18__0,
       n32bit_decoder_short_18__1, n32bit_decoder_short_18__1_2, n32bit_decoder_short_18__2,
       n32bit_decoder_short_18__2_2, n32bit_decoder_short_18__3, n32bit_decoder_short_18__3_2,
       n32bit_decoder_short_18__4, n32bit_decoder_short_18__4_2, n32bit_decoder_short_18__5,
       n32bit_decoder_short_19__0, n32bit_decoder_short_19__1, n32bit_decoder_short_19__1_2,
       n32bit_decoder_short_19__2, n32bit_decoder_short_19__2_2, n32bit_decoder_short_19__3,
       n32bit_decoder_short_19__3_2, n32bit_decoder_short_19__4, n32bit_decoder_short_19__4_2,
       n32bit_decoder_short_19__5, n32bit_decoder_short_20__0, n32bit_decoder_short_20__1,
       n32bit_decoder_short_20__1_2, n32bit_decoder_short_20__2, n32bit_decoder_short_20__2_2,
       n32bit_decoder_short_20__3, n32bit_decoder_short_20__3_2, n32bit_decoder_short_20__4,
       n32bit_decoder_short_20__4_2, n32bit_decoder_short_20__5, n32bit_decoder_short_21__0,
       n32bit_decoder_short_21__1, n32bit_decoder_short_21__1_2, n32bit_decoder_short_21__2,
       n32bit_decoder_short_21__2_2, n32bit_decoder_short_21__3, n32bit_decoder_short_21__3_2,
       n32bit_decoder_short_21__4, n32bit_decoder_short_21__4_2, n32bit_decoder_short_21__5,
       n32bit_decoder_short_22__0, n32bit_decoder_short_22__1, n32bit_decoder_short_22__1_2,
       n32bit_decoder_short_22__2, n32bit_decoder_short_22__2_2, n32bit_decoder_short_22__3,
       n32bit_decoder_short_22__3_2, n32bit_decoder_short_22__4, n32bit_decoder_short_22__4_2,
       n32bit_decoder_short_22__5, pull_resistor_1_node;
  wire [5:0] vram_as_1_y_out;
  wire [23:0] bit_extender_1_out;
  wire [31:0] _11, _12, _13, _21, _22, _23, _31, _32, _33, adder_3_out, adder_4_out, adder_5_out, addr,
       bit_extender_4_out, dda_async_1_out_x, dda_async_1_out_y, dda_test_sync_1_out_x,
       dda_test_sync_1_out_y, dotmatrix_1_p3, dotmatrix_1_p4, f_aspect_ratio, f_fov_rad, fp_div_1_out,
       fp_div_4_out, fp_div_5_out, fp_div_6_out, fp_div_7_out, fp_div_8_out, fp_div_9_out, fp_div_10_out,
       fp_div_11_out, fp_mult_1_out, fp_mult_4_out, fp_mult_5_out, fp_mult_8_out, fp_mult_9_out,
       fp_mult_10_out, fp_mult_11_out, fp_mult_12_out, fp_mult_13_out, fp_mult_14_out, fp_round_1_out, h_2,
       matrix_mult_4x4_1_out11, matrix_mult_4x4_1_out12, matrix_mult_4x4_1_out13, matrix_mult_4x4_1_out14,
       matrix_mult_4x4_2_out11, matrix_mult_4x4_2_out12, matrix_mult_4x4_2_out13, matrix_mult_4x4_2_out14,
       matrix_mult_4x4_4_out11, matrix_mult_4x4_4_out12, matrix_mult_4x4_4_out13, matrix_mult_4x4_4_out14,
       matrix_reg_rev_1_out_11, matrix_reg_rev_1_out_12, matrix_reg_rev_1_out_13, matrix_reg_rev_1_out_21,
       matrix_reg_rev_1_out_22, matrix_reg_rev_1_out_23, matrix_reg_rev_1_out_31, matrix_reg_rev_1_out_32,
       matrix_reg_rev_1_out_33, matrix_reg_rev_2_out_11, matrix_reg_rev_2_out_12, matrix_reg_rev_2_out_13,
       matrix_reg_rev_2_out_21, matrix_reg_rev_2_out_22, matrix_reg_rev_2_out_23, matrix_reg_rev_2_out_31,
       matrix_reg_rev_2_out_32, matrix_reg_rev_2_out_33, n64_display_1_out_6, n64_display_1_out_7,
       n64_display_1_out_8, n64_display_1_out_9, n64_display_1_out_10, n64_display_1_out_11,
       n64_display_1_out_12, n64_display_1_out_13, n64_display_1_out_14, n64_display_1_out_15,
       n64_display_1_out_16, n64_display_1_out_17, n64_display_1_out_18, n64_display_1_out_19,
       n64_display_1_out_20, n64_display_1_out_21, n64_display_1_out_22, n64_display_1_out_23,
       n64_display_1_out_24, n64_display_1_out_25, n64_display_1_out_26, n64_display_1_out_27,
       n64_display_1_out_28, n64_display_1_out_29, n64_display_1_out_30, n64_display_1_out_31,
       n64_display_1_out_32, n64_display_1_out_33, n64_display_1_out_34, n64_display_1_out_35,
       n64_display_1_out_36, n64_display_1_out_37, n64_display_1_out_38, n64_display_1_out_39,
       n64_display_1_out_40, n64_display_1_out_41, n64_display_1_out_42, n64_display_1_out_43,
       n64_display_1_out_44, n64_display_1_out_45, n64_display_1_out_46, n64_display_1_out_47,
       n64_display_1_out_48, n64_display_1_out_49, n64_display_1_out_50, n64_display_1_out_51,
       n64_display_1_out_52, n64_display_1_out_53, n64_display_1_out_54, n64_display_1_out_55,
       n64_display_1_out_56, n64_display_1_out_57, n64_display_1_out_58, n64_display_1_out_59,
       n64_display_1_out_60, n64_display_1_out_61, n64_display_1_out_62, n64_display_1_out_63,
       n64_display_1_out_64, n64_display_1_out_65, n64_display_1_out_66, n64_display_1_out_67,
       n64_display_1_out_68, n64_display_1_out_69, n64_display_1_out_70, n64_display_1_out_71,
       n64_display_1_out_72, n64_display_1_out_73, n64_display_1_out_74, n64_display_1_out_75,
       n64_display_1_out_76, n64_display_1_out_77, n64_display_1_out_78, n64_display_1_out_79,
       n64_display_1_out_80, n64_display_1_out_81, n64_display_1_out_82, n64_display_1_out_83,
       n64_display_1_out_84, n64_display_1_out_85, n64_display_1_out_86, n64_display_1_out_87,
       n64_display_1_out_88, n64_display_1_out_89, n64_display_1_out_90, n64_display_1_out_91,
       n64_display_1_out_92, n64_display_1_out_93, n64_display_1_out_94, n64_display_1_out_95,
       n64_display_1_out_96, n64_display_1_out_97, n64_display_1_out_98, n64_display_1_out_99,
       n64_display_1_out_100, n64_display_1_out_101, n64_display_1_out_102, n64_display_1_out_103,
       n64_display_1_out_104, n64_display_1_out_105, n64_display_1_out_106, n64_display_1_out_107,
       n64_display_1_out_108, n64_display_1_out_109, n64_display_1_out_110, n64_display_1_out_111,
       n64_display_1_out_112, n64_display_1_out_113, n64_display_1_out_114, n64_display_1_out_115,
       n64_display_1_out_116, n64_display_1_out_117, n64_display_1_out_118, n64_display_1_out_119,
       n64_display_1_out_120, n64_display_1_out_121, n64_display_1_out_122, n64_display_1_out_123,
       n64_display_1_out_124, n64_display_1_out_125, n64_display_1_out_126, n64_display_1_out_127,
       n64_display_1_out_128, n64_display_1_out_129, n64_display_1_out_130, n64_display_1_out_131,
       n64_display_1_out_132, n64_display_1_out_133, n64x64_display_controller_1_x12,
       n64x64_display_controller_1_x21, n64x64_display_controller_1_x22, n64x64_display_controller_1_y12,
       n64x64_display_controller_1_y21, n64x64_display_controller_1_y22, negator_1_out, r, R1_11, R2_11,
       rom_1_data, sample_m_addr, sin_co_1_cos, sin_co_1_sin, subtractor_1_out, subtractor_2_out,
       subtractor_3_out, t, vec4_to_vec3_1_out1, vec4_to_vec3_1_out2, vec4_to_vec3_2_out1,
       vec4_to_vec3_2_out2, vec4_to_vec3_2_out3, vec4_to_vec3_3_out1, vec4_to_vec3_3_out2,
       vec4_to_vec3_3_out3, vram_as_1_x_left_out, vram_as_1_x_right_out, w_2;

  Clock clock_1 (.out(clk));
  Pull_Resistor pull_resistor_1 (.node(pull_resistor_1_node));
  Transistor #(.\type ("n"), .width(4)) transistor_1 (.in(4'b0101), .out(pull_resistor_1_node), .gate(mission));
  Adder #(.width(4)) adder_1 (.a(pull_resistor_1_node), .b(matrix_addr_offset), .out(adder_1_out));  // open: cin, cout
  Bit_Extender #(.in_width(32), .out_width(24)) bit_extender_1 (.in(addr), .out(bit_extender_1_out));
  Multiplier #(.width(32)) multiplier_1 (.a(Load_sample), .b(32'h30), .out(sample_m_addr));  // open: cin, cout
  Button button_1 (.out(button_1_out));
  assign bit_extender_2_out = {{2{1'b0}}, matrix_addr_offset[1:0]};  // Bit_Extender bit_extender_2
  assign bit_extender_3_out = {{2{1'b0}}, matrix_addr_offset[3:2]};  // Bit_Extender bit_extender_3
  Transistor #(.\type ("n"), .width(4)) transistor_2 (.in(adder_1_out), .out(matrix_addr_R1), .gate(Load_to_MR1));
  Transistor #(.\type ("n"), .width(4)) transistor_3 (.in(adder_1_out), .out(matrix_addr_R2), .gate(Load_to__MR2));
  ROM #(.addrWidth(24), .dataWidth(32)) rom_1 (.addr(bit_extender_1_out), .data(rom_1_data));  // open: sel
  _7_Segment_Display u_7_segment_display_1 (.g(n32bit_decoder_short_1_sign));  // open: f, a, b, e, d, c, dp
  Hex_Digit_Display hex_digit_display_1 (.value(n32bit_decoder_short_1__4));  // open: dp
  fp_round fp_round_1 (.num(32'h8000), .rounding_number_eg__0_1__100_etc(32'h1999), .out(fp_round_1_out));
  _7_Segment_Display u_7_segment_display_2 (.g(n32bit_decoder_short_2_sign));  // open: f, a, b, e, d, c, dp
  Hex_Digit_Display hex_digit_display_2 (.value(n32bit_decoder_short_2__4));  // open: dp
  rising_edge_detector rising_edge_detector_1 (
    .signal(button_1_out), .clear(counter_2_carry), .sync(clk), .out(mission));
  and and_1 (and_1_out, mission, clk);
  assign bit_extender_4_out = {{24{1'b0}}, {bit_extender_3_out, bit_extender_2_out}};  // Bit_Extender bit_extender_4
  Pull_Resistor pull_resistor_2 (.node(R1_11));
  Transistor #(.\type ("n"), .width(32)) transistor_4 (.in(rom_1_data), .out(R1_11), .gate(Load_to_MR1));
  Pull_Resistor pull_resistor_3 (.node(R2_11));
  Transistor #(.\type ("n"), .width(32)) transistor_5 (.in(rom_1_data), .out(R2_11), .gate(Load_to__MR2));
  Hex_Digit_Display hex_digit_display_3 (.value(n32bit_decoder_short_1__2_2));  // open: dp
  Hex_Digit_Display hex_digit_display_4 (.value(n32bit_decoder_short_1__3));  // open: dp
  _7_Segment_Display u_7_segment_display_3 (.g(n32bit_decoder_short_3_sign));  // open: f, a, b, e, d, c, dp
  Hex_Digit_Display hex_digit_display_5 (.value(n32bit_decoder_short_3__4));  // open: dp
  Hex_Digit_Display hex_digit_display_6 (.value(n32bit_decoder_short_2__2_2));  // open: dp
  Hex_Digit_Display hex_digit_display_7 (.value(n32bit_decoder_short_2__3));  // open: dp
  Counter #(.width(2), .max('h3)) counter_1 (
    .Q(matrix_addr_offset[3:2]), .carry(counter_1_carry), .clk(and_1_out), .clr(counter_1_carry));  // open: load, D, count
  Counter #(.width(2), .max('h3)) counter_2 (
    .Q(matrix_addr_offset[1:0]), .carry(counter_2_carry), .clk(counter_1_carry), .clr(counter_2_carry));  // open: load, D, count
  Adder #(.width(32)) adder_2 (.a(bit_extender_4_out), .b(sample_m_addr), .out(addr));  // open: cin, cout
  Pull_Resistor pull_resistor_4 (.node(matrix_addr_R1));
  Pull_Resistor pull_resistor_5 (.node(matrix_addr_R2));
  Hex_Digit_Display hex_digit_display_8 (.value(n32bit_decoder_short_1__1_2));  // open: dp
  Hex_Digit_Display hex_digit_display_9 (.value(n32bit_decoder_short_1__0), .dp(n32bit_decoder_short_1_dot));
  Hex_Digit_Display hex_digit_display_10 (.value(n32bit_decoder_short_3__3));  // open: dp
  Hex_Digit_Display hex_digit_display_11 (.value(n32bit_decoder_short_3__2_2));  // open: dp
  Hex_Digit_Display hex_digit_display_12 (.value(n32bit_decoder_short_2__0), .dp(n32bit_decoder_short_2_dot));
  Hex_Digit_Display hex_digit_display_13 (.value(n32bit_decoder_short_2__1_2));  // open: dp
  _7_Segment_Display u_7_segment_display_4 (.g(n32bit_decoder_short_4_sign));  // open: f, a, b, e, d, c, dp
  _7_Segment_Display u_7_segment_display_5 (.g(n32bit_decoder_short_5_sign));  // open: f, a, b, e, d, c, dp
  _7_Segment_Display u_7_segment_display_6 (.g(n32bit_decoder_short_6_sign));  // open: f, a, b, e, d, c, dp
  Hex_Digit_Display hex_digit_display_14 (.value(n32bit_decoder_short_1__1));  // open: dp
  Hex_Digit_Display hex_digit_display_15 (.value(n32bit_decoder_short_1__2));  // open: dp
  Hex_Digit_Display hex_digit_display_16 (.value(n32bit_decoder_short_3__0), .dp(n32bit_decoder_short_3_dot));
  Hex_Digit_Display hex_digit_display_17 (.value(n32bit_decoder_short_3__1_2));  // open: dp
  Hex_Digit_Display hex_digit_display_18 (.value(n32bit_decoder_short_2__1));  // open: dp
  Hex_Digit_Display hex_digit_display_19 (.value(n32bit_decoder_short_2__2));  // open: dp
  fp_div fp_div_1 (.in1(32'h5a0000), .in2(32'h20000), .out(fp_div_1_out));
  Hex_Digit_Display hex_digit_display_20 (.value(n32bit_decoder_short_4__4));  // open: dp
  Hex_Digit_Display hex_digit_display_21 (.value(n32bit_decoder_short_4__3));  // open: dp
  Hex_Digit_Display hex_digit_display_22 (.value(n32bit_decoder_short_5__3));  // open: dp
  Hex_Digit_Display hex_digit_display_23 (.value(n32bit_decoder_short_5__4));  // open: dp
  Hex_Digit_Display hex_digit_display_24 (.value(n32bit_decoder_short_6__3));  // open: dp
  Hex_Digit_Display hex_digit_display_25 (.value(n32bit_decoder_short_6__4));  // open: dp
  Button reset (.out(reset_out));
  Hex_Digit_Display hex_digit_display_26 (.value(n32bit_decoder_short_1__3_2));  // open: dp
  Hex_Digit_Display hex_digit_display_27 (.value(n32bit_decoder_short_1__4_2));  // open: dp
  Hex_Digit_Display hex_digit_display_28 (.value(n32bit_decoder_short_3__2));  // open: dp
  Hex_Digit_Display hex_digit_display_29 (.value(n32bit_decoder_short_3__1));  // open: dp
  Hex_Digit_Display hex_digit_display_30 (.value(n32bit_decoder_short_2__4_2));  // open: dp
  Hex_Digit_Display hex_digit_display_31 (.value(n32bit_decoder_short_2__3_2));  // open: dp
  sin_co sin_co_1 (.in_1(fp_div_1_out), .sin(sin_co_1_sin), .cos(sin_co_1_cos));
  Hex_Digit_Display hex_digit_display_32 (.value(n32bit_decoder_short_4__1_2));  // open: dp
  Hex_Digit_Display hex_digit_display_33 (.value(n32bit_decoder_short_4__2_2));  // open: dp
  Hex_Digit_Display hex_digit_display_34 (.value(n32bit_decoder_short_5__2_2));  // open: dp
  Hex_Digit_Display hex_digit_display_35 (.value(n32bit_decoder_short_5__1_2));  // open: dp
  Hex_Digit_Display hex_digit_display_36 (.value(n32bit_decoder_short_6__1_2));  // open: dp
  Hex_Digit_Display hex_digit_display_37 (.value(n32bit_decoder_short_6__2_2));  // open: dp
  Hex_Digit_Display hex_digit_display_38 (.value(n32bit_decoder_short_1__5));  // open: dp
  _32bit_decoder_short u_32bit_decoder_short_1 (
    .sign(n32bit_decoder_short_1_sign), ._4(n32bit_decoder_short_1__4), ._3(n32bit_decoder_short_1__3),
    ._2_2(n32bit_decoder_short_1__2_2), ._1_2(n32bit_decoder_short_1__1_2), ._0(n32bit_decoder_short_1__0),
    .dot(n32bit_decoder_short_1_dot), .in(32'h8000), ._1(n32bit_decoder_short_1__1),
    ._2(n32bit_decoder_short_1__2), ._3_2(n32bit_decoder_short_1__3_2), ._4_2(n32bit_decoder_short_1__4_2),
    ._5(n32bit_decoder_short_1__5));
  Hex_Digit_Display hex_digit_display_39 (.value(n32bit_decoder_short_3__3_2));  // open: dp
  Hex_Digit_Display hex_digit_display_40 (.value(n32bit_decoder_short_3__4_2));  // open: dp
  Hex_Digit_Display hex_digit_display_41 (.value(n32bit_decoder_short_2__5));  // open: dp
  _32bit_decoder_short u_32bit_decoder_short_2 (
    .sign(n32bit_decoder_short_2_sign), ._4(n32bit_decoder_short_2__4), ._3(n32bit_decoder_short_2__3),
    ._2_2(n32bit_decoder_short_2__2_2), ._1_2(n32bit_decoder_short_2__1_2), ._0(n32bit_decoder_short_2__0),
    .dot(n32bit_decoder_short_2_dot), .in(32'h1999), ._1(n32bit_decoder_short_2__1),
    ._2(n32bit_decoder_short_2__2), ._3_2(n32bit_decoder_short_2__3_2), ._4_2(n32bit_decoder_short_2__4_2),
    ._5(n32bit_decoder_short_2__5));
  fp_div fp_div_2 (.in1(sin_co_1_cos), .in2(sin_co_1_sin), .out(f_fov_rad));
  Hex_Digit_Display hex_digit_display_42 (.value(n32bit_decoder_short_4__0), .dp(n32bit_decoder_short_4_dot));
  Hex_Digit_Display hex_digit_display_43 (.value(n32bit_decoder_short_4__1));  // open: dp
  Hex_Digit_Display hex_digit_display_44 (.value(n32bit_decoder_short_5__1));  // open: dp
  Hex_Digit_Display hex_digit_display_45 (.value(n32bit_decoder_short_5__0), .dp(n32bit_decoder_short_5_dot));
  Hex_Digit_Display hex_digit_display_46 (.value(n32bit_decoder_short_6__1));  // open: dp
  Hex_Digit_Display hex_digit_display_47 (.value(n32bit_decoder_short_6__0), .dp(n32bit_decoder_short_6_dot));
  Hex_Digit_Display hex_digit_display_48 (.value(n32bit_decoder_short_3__5));  // open: dp
  _32bit_decoder_short u_32bit_decoder_short_3 (
    .sign(n32bit_decoder_short_3_sign), ._4(n32bit_decoder_short_3__4), ._3(n32bit_decoder_short_3__3),
    ._2_2(n32bit_decoder_short_3__2_2), ._1_2(n32bit_decoder_short_3__1_2), ._0(n32bit_decoder_short_3__0),
    .dot(n32bit_decoder_short_3_dot), .in(fp_round_1_out), ._1(n32bit_decoder_short_3__1),
    ._2(n32bit_decoder_short_3__2), ._3_2(n32bit_decoder_short_3__3_2), ._4_2(n32bit_decoder_short_3__4_2),
    ._5(n32bit_decoder_short_3__5));
  _7_Segment_Display u_7_segment_display_7 (.g(n32bit_decoder_short_7_sign));  // open: f, a, b, e, d, c, dp
  Hex_Digit_Display hex_digit_display_49 (.value(n32bit_decoder_short_4__3_2));  // open: dp
  Hex_Digit_Display hex_digit_display_50 (.value(n32bit_decoder_short_4__2));  // open: dp
  Hex_Digit_Display hex_digit_display_51 (.value(n32bit_decoder_short_5__2));  // open: dp
  Hex_Digit_Display hex_digit_display_52 (.value(n32bit_decoder_short_5__3_2));  // open: dp
  Hex_Digit_Display hex_digit_display_53 (.value(n32bit_decoder_short_6__2));  // open: dp
  Hex_Digit_Display hex_digit_display_54 (.value(n32bit_decoder_short_6__3_2));  // open: dp
  matrix_reg_rev matrix_reg_rev_1 (
    .in_1(clk), .rst(reset_out), .in_11(R2_11), .in_21(R2_11), .in_31(R2_11), .in_12(R2_11), .in_22(R2_11),
    .in_32(R2_11), .in_13(R2_11), .in_23(R2_11), .in_33(R2_11), ._1__store_by_address_0__store_all(1'b1),
    .val___XXYY_address(matrix_addr_R2), .out_11(matrix_reg_rev_1_out_11), .out_21(matrix_reg_rev_1_out_21),
    .out_31(matrix_reg_rev_1_out_31), .out_12(matrix_reg_rev_1_out_12), .out_22(matrix_reg_rev_1_out_22),
    .out_32(matrix_reg_rev_1_out_32), .out_13(matrix_reg_rev_1_out_13), .out_23(matrix_reg_rev_1_out_23),
    .out_33(matrix_reg_rev_1_out_33));
  matrix_reg_rev matrix_reg_rev_2 (
    .in_1(clk), .rst(reset_out), .in_11(R1_11), .in_21(R1_11), .in_31(R1_11), .in_12(R1_11), .in_22(R1_11),
    .in_32(R1_11), .in_13(R1_11), .in_23(R1_11), .in_33(R1_11), ._1__store_by_address_0__store_all(1'b1),
    .val___XXYY_address(matrix_addr_R1), .out_11(matrix_reg_rev_2_out_11), .out_21(matrix_reg_rev_2_out_21),
    .out_31(matrix_reg_rev_2_out_31), .out_12(matrix_reg_rev_2_out_12), .out_22(matrix_reg_rev_2_out_22),
    .out_32(matrix_reg_rev_2_out_32), .out_13(matrix_reg_rev_2_out_13), .out_23(matrix_reg_rev_2_out_23),
    .out_33(matrix_reg_rev_2_out_33));
  Hex_Digit_Display hex_digit_display_55 (.value(n32bit_decoder_short_7__4));  // open: dp
  Hex_Digit_Display hex_digit_display_56 (.value(n32bit_decoder_short_4__4_2));  // open: dp
  Hex_Digit_Display hex_digit_display_57 (.value(n32bit_decoder_short_4__5));  // open: dp
  Hex_Digit_Display hex_digit_display_58 (.value(n32bit_decoder_short_5__4_2));  // open: dp
  Hex_Digit_Display hex_digit_display_59 (.value(n32bit_decoder_short_5__5));  // open: dp
  Hex_Digit_Display hex_digit_display_60 (.value(n32bit_decoder_short_6__5));  // open: dp
  Hex_Digit_Display hex_digit_display_61 (.value(n32bit_decoder_short_6__4_2));  // open: dp
  Hex_Digit_Display hex_digit_display_62 (.value(n32bit_decoder_short_7__2_2));  // open: dp
  Hex_Digit_Display hex_digit_display_63 (.value(n32bit_decoder_short_7__3));  // open: dp
  _7_Segment_Display u_7_segment_display_8 (.g(n32bit_decoder_short_8_sign));  // open: f, a, b, e, d, c, dp
  _32bit_decoder_short u_32bit_decoder_short_4 (
    .sign(n32bit_decoder_short_4_sign), ._4(n32bit_decoder_short_4__4), ._3(n32bit_decoder_short_4__3),
    ._2_2(n32bit_decoder_short_4__2_2), ._1_2(n32bit_decoder_short_4__1_2), ._0(n32bit_decoder_short_4__0),
    .dot(n32bit_decoder_short_4_dot), .in(_11), ._1(n32bit_decoder_short_4__1),
    ._2(n32bit_decoder_short_4__2), ._3_2(n32bit_decoder_short_4__3_2), ._4_2(n32bit_decoder_short_4__4_2),
    ._5(n32bit_decoder_short_4__5));
  _7_Segment_Display u_7_segment_display_9 (.g(n32bit_decoder_short_9_sign));  // open: f, a, b, e, d, c, dp
  _32bit_decoder_short u_32bit_decoder_short_5 (
    .sign(n32bit_decoder_short_5_sign), ._4(n32bit_decoder_short_5__4), ._3(n32bit_decoder_short_5__3),
    ._2_2(n32bit_decoder_short_5__2_2), ._1_2(n32bit_decoder_short_5__1_2), ._0(n32bit_decoder_short_5__0),
    .dot(n32bit_decoder_short_5_dot), .in(_12), ._1(n32bit_decoder_short_5__1),
    ._2(n32bit_decoder_short_5__2), ._3_2(n32bit_decoder_short_5__3_2), ._4_2(n32bit_decoder_short_5__4_2),
    ._5(n32bit_decoder_short_5__5));
  _7_Segment_Display u_7_segment_display_10 (.g(n32bit_decoder_short_10_sign));  // open: f, a, b, e, d, c, dp
  _32bit_decoder_short u_32bit_decoder_short_6 (
    .sign(n32bit_decoder_short_6_sign), ._4(n32bit_decoder_short_6__4), ._3(n32bit_decoder_short_6__3),
    ._2_2(n32bit_decoder_short_6__2_2), ._1_2(n32bit_decoder_short_6__1_2), ._0(n32bit_decoder_short_6__0),
    .dot(n32bit_decoder_short_6_dot), .in(_13), ._1(n32bit_decoder_short_6__1),
    ._2(n32bit_decoder_short_6__2), ._3_2(n32bit_decoder_short_6__3_2), ._4_2(n32bit_decoder_short_6__4_2),
    ._5(n32bit_decoder_short_6__5));
  matrix_mult matrix_mult_1 (
    .in_1(matrix_reg_rev_1_out_11), .in_2(matrix_reg_rev_1_out_21), .in_3(matrix_reg_rev_1_out_31),
    .in_4(matrix_reg_rev_1_out_12), .in_5(matrix_reg_rev_1_out_22), .in_6(matrix_reg_rev_1_out_32),
    .in_7(matrix_reg_rev_1_out_13), .in_8(matrix_reg_rev_1_out_23), .in_9(matrix_reg_rev_1_out_33),
    .in_10(matrix_reg_rev_2_out_11), .in_11(matrix_reg_rev_2_out_21), .in_12(matrix_reg_rev_2_out_31),
    .in_13(matrix_reg_rev_2_out_12), .in_14(matrix_reg_rev_2_out_22), .in_15(matrix_reg_rev_2_out_32),
    .in_16(matrix_reg_rev_2_out_13), .in_17(matrix_reg_rev_2_out_23), .in_18(matrix_reg_rev_2_out_33),
    .out11(_11), .out21(_21), .out31(_31), .out12(_12), .out22(_22), .out32(_32), .out13(_13), .out23(_23),
    .out33(_33));
  Hex_Digit_Display hex_digit_display_64 (.value(n32bit_decoder_short_7__0), .dp(n32bit_decoder_short_7_dot));
  Hex_Digit_Display hex_digit_display_65 (.value(n32bit_decoder_short_7__1_2));  // open: dp
  fp_mult fp_mult_1 (.in1(32'h1999), .in2(32'h3e80000), .out(fp_mult_1_out));
  Hex_Digit_Display hex_digit_display_66 (.value(n32bit_decoder_short_8__4));  // open: dp
  Hex_Digit_Display hex_digit_display_67 (.value(n32bit_decoder_short_9__4));  // open: dp
  Hex_Digit_Display hex_digit_display_68 (.value(n32bit_decoder_short_10__4));  // open: dp
  _7_Segment_Display u_7_segment_display_11 (.g(n32bit_decoder_short_11_sign));  // open: f, a, b, e, d, c, dp
  Hex_Digit_Display hex_digit_display_69 (.value(n32bit_decoder_short_11__4));  // open: dp
  fp_mult fp_mult_2 (.in1(32'h400000), .in2(32'h8000), .out(h_2));
  fp_mult fp_mult_3 (.in1(32'h400000), .in2(32'h8000), .out(w_2));
  fp_div fp_div_3 (.in1(32'h400000), .in2(32'h400000), .out(f_aspect_ratio));
  Hex_Digit_Display hex_digit_display_70 (.value(n32bit_decoder_short_7__1));  // open: dp
  Hex_Digit_Display hex_digit_display_71 (.value(n32bit_decoder_short_7__2));  // open: dp
  Adder #(.width(32)) adder_3 (.a(32'h3e80000), .b(32'h1999), .out(adder_3_out));  // open: cin, cout
  Subtractor #(.width(32)) subtractor_1 (.a(32'h1999), .b(32'h3e80000), .out(subtractor_1_out));  // open: bin, bout
  fp_mult fp_mult_4 (.in1(fp_mult_1_out), .in2(32'h20000), .out(fp_mult_4_out));
  Hex_Digit_Display hex_digit_display_72 (.value(n32bit_decoder_short_8__2_2));  // open: dp
  Hex_Digit_Display hex_digit_display_73 (.value(n32bit_decoder_short_8__3));  // open: dp
  Hex_Digit_Display hex_digit_display_74 (.value(n32bit_decoder_short_9__2_2));  // open: dp
  Hex_Digit_Display hex_digit_display_75 (.value(n32bit_decoder_short_9__3));  // open: dp
  Hex_Digit_Display hex_digit_display_76 (.value(n32bit_decoder_short_10__3));  // open: dp
  Hex_Digit_Display hex_digit_display_77 (.value(n32bit_decoder_short_10__2_2));  // open: dp
  Hex_Digit_Display hex_digit_display_78 (.value(n32bit_decoder_short_11__2_2));  // open: dp
  Hex_Digit_Display hex_digit_display_79 (.value(n32bit_decoder_short_11__3));  // open: dp
  fp_mult fp_mult_5 (.in1(32'h3e80000), .in2(32'hffff0000), .out(fp_mult_5_out));
  Hex_Digit_Display hex_digit_display_80 (.value(n32bit_decoder_short_7__3_2));  // open: dp
  Hex_Digit_Display hex_digit_display_81 (.value(n32bit_decoder_short_7__4_2));  // open: dp
  fp_mult fp_mult_6 (.in1(32'h400000), .in2(32'h8000), .out(t));
  fp_mult fp_mult_7 (.in1(32'h400000), .in2(32'h8000), .out(r));
  fp_div fp_div_4 (.in1(32'h1999), .in2(r), .out(fp_div_4_out));
  fp_div fp_div_5 (.in1(32'h1999), .in2(t), .out(fp_div_5_out));
  fp_div fp_div_6 (.in1(adder_3_out), .in2(subtractor_1_out), .out(fp_div_6_out));
  fp_div fp_div_7 (.in1(fp_mult_4_out), .in2(subtractor_1_out), .out(fp_div_7_out));
  Hex_Digit_Display hex_digit_display_82 (.value(n32bit_decoder_short_8__1_2));  // open: dp
  Hex_Digit_Display hex_digit_display_83 (.value(n32bit_decoder_short_8__0), .dp(n32bit_decoder_short_8_dot));
  Hex_Digit_Display hex_digit_display_84 (.value(n32bit_decoder_short_9__0), .dp(n32bit_decoder_short_9_dot));
  Hex_Digit_Display hex_digit_display_85 (.value(n32bit_decoder_short_9__1_2));  // open: dp
  Hex_Digit_Display hex_digit_display_86 (.value(n32bit_decoder_short_10__0), .dp(n32bit_decoder_short_10_dot));
  Hex_Digit_Display hex_digit_display_87 (.value(n32bit_decoder_short_10__1_2));  // open: dp
  Hex_Digit_Display hex_digit_display_88 (.value(n32bit_decoder_short_11__1_2));  // open: dp
  Hex_Digit_Display hex_digit_display_89 (.value(n32bit_decoder_short_11__0), .dp(n32bit_decoder_short_11_dot));
  fp_mult fp_mult_8 (.in1(f_aspect_ratio), .in2(f_fov_rad), .out(fp_mult_8_out));
  fp_mult fp_mult_9 (.in1(fp_mult_5_out), .in2(32'h1999), .out(fp_mult_9_out));
  fp_div fp_div_8 (.in1(fp_mult_9_out), .in2(subtractor_2_out), .out(fp_div_8_out));
  fp_div fp_div_9 (.in1(32'h3e80000), .in2(subtractor_2_out), .out(fp_div_9_out));
  Subtractor #(.width(32)) subtractor_2 (.a(32'h3e80000), .b(32'h1999), .out(subtractor_2_out));  // open: bin, bout
  Hex_Digit_Display hex_digit_display_90 (.value(n32bit_decoder_short_7__5));  // open: dp
  _32bit_decoder_short u_32bit_decoder_short_7 (
    .sign(n32bit_decoder_short_7_sign), ._4(n32bit_decoder_short_7__4), ._3(n32bit_decoder_short_7__3),
    ._2_2(n32bit_decoder_short_7__2_2), ._1_2(n32bit_decoder_short_7__1_2), ._0(n32bit_decoder_short_7__0),
    .dot(n32bit_decoder_short_7_dot), .in(f_fov_rad), ._1(n32bit_decoder_short_7__1),
    ._2(n32bit_decoder_short_7__2), ._3_2(n32bit_decoder_short_7__3_2), ._4_2(n32bit_decoder_short_7__4_2),
    ._5(n32bit_decoder_short_7__5));
  Hex_Digit_Display hex_digit_display_91 (.value(n32bit_decoder_short_8__2));  // open: dp
  Hex_Digit_Display hex_digit_display_92 (.value(n32bit_decoder_short_8__1));  // open: dp
  Hex_Digit_Display hex_digit_display_93 (.value(n32bit_decoder_short_9__2));  // open: dp
  Hex_Digit_Display hex_digit_display_94 (.value(n32bit_decoder_short_9__1));  // open: dp
  Hex_Digit_Display hex_digit_display_95 (.value(n32bit_decoder_short_10__2));  // open: dp
  Hex_Digit_Display hex_digit_display_96 (.value(n32bit_decoder_short_10__1));  // open: dp
  Hex_Digit_Display hex_digit_display_97 (.value(n32bit_decoder_short_11__1));  // open: dp
  Hex_Digit_Display hex_digit_display_98 (.value(n32bit_decoder_short_11__2));  // open: dp
  _7_Segment_Display u_7_segment_display_12 (.g(n32bit_decoder_short_12_sign));  // open: f, a, b, e, d, c, dp
  Hex_Digit_Display hex_digit_display_99 (.value(n32bit_decoder_short_8__4_2));  // open: dp
  Hex_Digit_Display hex_digit_display_100 (.value(n32bit_decoder_short_8__3_2));  // open: dp
  Hex_Digit_Display hex_digit_display_101 (.value(n32bit_decoder_short_9__3_2));  // open: dp
  Hex_Digit_Display hex_digit_display_102 (.value(n32bit_decoder_short_9__4_2));  // open: dp
  Hex_Digit_Display hex_digit_display_103 (.value(n32bit_decoder_short_10__4_2));  // open: dp
  Hex_Digit_Display hex_digit_display_104 (.value(n32bit_decoder_short_10__3_2));  // open: dp
  Hex_Digit_Display hex_digit_display_105 (.value(n32bit_decoder_short_11__4_2));  // open: dp
  Hex_Digit_Display hex_digit_display_106 (.value(n32bit_decoder_short_11__3_2));  // open: dp
  clock_x2 clock_x2_1 (.clk(clk), .clk_x2(clock_x2_1_clk_x2));
  Hex_Digit_Display hex_digit_display_107 (.value(n32bit_decoder_short_12__4));  // open: dp
  Hex_Digit_Display hex_digit_display_108 (.value(n32bit_decoder_short_12__3));  // open: dp
  Hex_Digit_Display hex_digit_display_109 (.value(n32bit_decoder_short_8__5));  // open: dp
  _32bit_decoder_short u_32bit_decoder_short_8 (
    .sign(n32bit_decoder_short_8_sign), ._4(n32bit_decoder_short_8__4), ._3(n32bit_decoder_short_8__3),
    ._2_2(n32bit_decoder_short_8__2_2), ._1_2(n32bit_decoder_short_8__1_2), ._0(n32bit_decoder_short_8__0),
    .dot(n32bit_decoder_short_8_dot), .in(_21), ._1(n32bit_decoder_short_8__1),
    ._2(n32bit_decoder_short_8__2), ._3_2(n32bit_decoder_short_8__3_2), ._4_2(n32bit_decoder_short_8__4_2),
    ._5(n32bit_decoder_short_8__5));
  Hex_Digit_Display hex_digit_display_110 (.value(n32bit_decoder_short_9__5));  // open: dp
  _32bit_decoder_short u_32bit_decoder_short_9 (
    .sign(n32bit_decoder_short_9_sign), ._4(n32bit_decoder_short_9__4), ._3(n32bit_decoder_short_9__3),
    ._2_2(n32bit_decoder_short_9__2_2), ._1_2(n32bit_decoder_short_9__1_2), ._0(n32bit_decoder_short_9__0),
    .dot(n32bit_decoder_short_9_dot), .in(_22), ._1(n32bit_decoder_short_9__1),
    ._2(n32bit_decoder_short_9__2), ._3_2(n32bit_decoder_short_9__3_2), ._4_2(n32bit_decoder_short_9__4_2),
    ._5(n32bit_decoder_short_9__5));
  Hex_Digit_Display hex_digit_display_111 (.value(n32bit_decoder_short_10__5));  // open: dp
  _32bit_decoder_short u_32bit_decoder_short_10 (
    .sign(n32bit_decoder_short_10_sign), ._4(n32bit_decoder_short_10__4), ._3(n32bit_decoder_short_10__3),
    ._2_2(n32bit_decoder_short_10__2_2), ._1_2(n32bit_decoder_short_10__1_2),
    ._0(n32bit_decoder_short_10__0), .dot(n32bit_decoder_short_10_dot), .in(_23),
    ._1(n32bit_decoder_short_10__1), ._2(n32bit_decoder_short_10__2), ._3_2(n32bit_decoder_short_10__3_2),
    ._4_2(n32bit_decoder_short_10__4_2), ._5(n32bit_decoder_short_10__5));
  Hex_Digit_Display hex_digit_display_112 (.value(n32bit_decoder_short_11__5));  // open: dp
  _32bit_decoder_short u_32bit_decoder_short_11 (
    .sign(n32bit_decoder_short_11_sign), ._4(n32bit_decoder_short_11__4), ._3(n32bit_decoder_short_11__3),
    ._2_2(n32bit_decoder_short_11__2_2), ._1_2(n32bit_decoder_short_11__1_2),
    ._0(n32bit_decoder_short_11__0), .dot(n32bit_decoder_short_11_dot), .in(in_2),
    ._1(n32bit_decoder_short_11__1), ._2(n32bit_decoder_short_11__2), ._3_2(n32bit_decoder_short_11__3_2),
    ._4_2(n32bit_decoder_short_11__4_2), ._5(n32bit_decoder_short_11__5));
  DDA_test_sync dda_test_sync_1 (
    .clk(clock_x2_1_clk_x2), .new_data(in_7), .x2(x2), .x1(x1), .y2(y2), .y1(y1),
    .out_y(dda_test_sync_1_out_y), .out_x(dda_test_sync_1_out_x), .set_point(dda_test_sync_1_set_point),
    .done(dda_test_sync_1_done));  // open: status
  Hex_Digit_Display hex_digit_display_113 (.value(n32bit_decoder_short_12__2_2));  // open: dp
  Hex_Digit_Display hex_digit_display_114 (.value(n32bit_decoder_short_12__1_2));  // open: dp
  _7_Segment_Display u_7_segment_display_13 (.g(n32bit_decoder_short_13_sign));  // open: f, a, b, e, d, c, dp
  _7_Segment_Display u_7_segment_display_14 (.g(n32bit_decoder_short_14_sign));  // open: f, a, b, e, d, c, dp
  _7_Segment_Display u_7_segment_display_15 (.g(n32bit_decoder_short_15_sign));  // open: f, a, b, e, d, c, dp
  Hex_Digit_Display hex_digit_display_115 (.value(n32bit_decoder_short_12__0), .dp(n32bit_decoder_short_12_dot));
  Hex_Digit_Display hex_digit_display_116 (.value(n32bit_decoder_short_12__1));  // open: dp
  Hex_Digit_Display hex_digit_display_117 (.value(n32bit_decoder_short_13__3));  // open: dp
  Hex_Digit_Display hex_digit_display_118 (.value(n32bit_decoder_short_13__4));  // open: dp
  Hex_Digit_Display hex_digit_display_119 (.value(n32bit_decoder_short_14__3));  // open: dp
  Hex_Digit_Display hex_digit_display_120 (.value(n32bit_decoder_short_14__4));  // open: dp
  Hex_Digit_Display hex_digit_display_121 (.value(n32bit_decoder_short_15__3));  // open: dp
  Hex_Digit_Display hex_digit_display_122 (.value(n32bit_decoder_short_15__4));  // open: dp
  Hex_Digit_Display hex_digit_display_123 (.value(n32bit_decoder_short_12__2));  // open: dp
  Hex_Digit_Display hex_digit_display_124 (.value(n32bit_decoder_short_12__3_2));  // open: dp
  matrix_mult_4x4 matrix_mult_4x4_1 (
    .in_1(in_14), .in_5(in_15), .in_9(in_16), .in_13(32'h10000), .in_17(fp_mult_8_out), .in_22(f_fov_rad),
    .in_27(fp_div_8_out), .in_28(fp_div_9_out), .in_31(32'h10000), .out11(matrix_mult_4x4_1_out11),
    .out12(matrix_mult_4x4_1_out12), .out13(matrix_mult_4x4_1_out13), .out14(matrix_mult_4x4_1_out14));  // open: in_2, in_3, in_4, in_6, in_7, in_8, in_10, in_11, in_12, in_14, in_15, in_16, in_18, in_19, in_20, in_21, in_23, in_24, in_25, in_26, in_29, in_30, in_32, out21, out31, out41, out22, out32, out42, out23, out33, out43, out24, out34, out44
  matrix_mult_4x4 matrix_mult_4x4_2 (
    .in_1(in_17), .in_5(in_19), .in_9(in_21), .in_13(32'h10000), .in_17(fp_div_4_out), .in_21(fp_div_4_out),
    .in_22(fp_div_5_out), .in_27(fp_div_6_out), .in_28(fp_div_7_out), .in_31(32'hffff0000),
    .out11(matrix_mult_4x4_2_out11), .out12(matrix_mult_4x4_2_out12), .out13(matrix_mult_4x4_2_out13),
    .out14(matrix_mult_4x4_2_out14));  // open: in_2, in_3, in_4, in_6, in_7, in_8, in_10, in_11, in_12, in_14, in_15, in_16, in_18, in_19, in_20, in_23, in_24, in_25, in_26, in_29, in_30, in_32, out21, out31, out41, out22, out32, out42, out23, out33, out43, out24, out34, out44
  Hex_Digit_Display hex_digit_display_125 (.value(n32bit_decoder_short_13__1_2));  // open: dp
  Hex_Digit_Display hex_digit_display_126 (.value(n32bit_decoder_short_13__2_2));  // open: dp
  Hex_Digit_Display hex_digit_display_127 (.value(n32bit_decoder_short_14__1_2));  // open: dp
  Hex_Digit_Display hex_digit_display_128 (.value(n32bit_decoder_short_14__2_2));  // open: dp
  Hex_Digit_Display hex_digit_display_129 (.value(n32bit_decoder_short_15__2_2));  // open: dp
  Hex_Digit_Display hex_digit_display_130 (.value(n32bit_decoder_short_15__1_2));  // open: dp
  Button update ();  // open: out
  Button reset_2 ();  // open: out
  Hex_Digit_Display hex_digit_display_131 (.value(n32bit_decoder_short_12__5));  // open: dp
  Hex_Digit_Display hex_digit_display_132 (.value(n32bit_decoder_short_12__4_2));  // open: dp
  _32bit_decoder_short u_32bit_decoder_short_12 (
    .sign(n32bit_decoder_short_12_sign), ._4(n32bit_decoder_short_12__4), ._3(n32bit_decoder_short_12__3),
    ._2_2(n32bit_decoder_short_12__2_2), ._1_2(n32bit_decoder_short_12__1_2),
    ._0(n32bit_decoder_short_12__0), .dot(n32bit_decoder_short_12_dot), .in(in_14),
    ._1(n32bit_decoder_short_12__1), ._2(n32bit_decoder_short_12__2), ._3_2(n32bit_decoder_short_12__3_2),
    ._4_2(n32bit_decoder_short_12__4_2), ._5(n32bit_decoder_short_12__5));
  vec4_to_vec3 vec4_to_vec3_1 (
    .in1(matrix_mult_4x4_2_out11), .in2(matrix_mult_4x4_2_out12), .in3(matrix_mult_4x4_2_out13),
    .in4(matrix_mult_4x4_2_out14), .out1(vec4_to_vec3_1_out1), .out2(vec4_to_vec3_1_out2));  // open: out3
  Hex_Digit_Display hex_digit_display_133 (.value(n32bit_decoder_short_13__0), .dp(n32bit_decoder_short_13_dot));
  Hex_Digit_Display hex_digit_display_134 (.value(n32bit_decoder_short_13__1));  // open: dp
  Hex_Digit_Display hex_digit_display_135 (.value(n32bit_decoder_short_14__0), .dp(n32bit_decoder_short_14_dot));
  Hex_Digit_Display hex_digit_display_136 (.value(n32bit_decoder_short_14__1));  // open: dp
  Hex_Digit_Display hex_digit_display_137 (.value(n32bit_decoder_short_15__0), .dp(n32bit_decoder_short_15_dot));
  Hex_Digit_Display hex_digit_display_138 (.value(n32bit_decoder_short_15__1));  // open: dp
  clock_x2 clock_x2_2 (.clk(clk), .clk_x2(clock_x2_2_clk_x2));
  vec4_to_vec3 vec4_to_vec3_2 (
    .in1(matrix_mult_4x4_1_out11), .in2(matrix_mult_4x4_1_out12), .in3(matrix_mult_4x4_1_out13),
    .in4(matrix_mult_4x4_1_out14), .out1(vec4_to_vec3_2_out1), .out2(vec4_to_vec3_2_out2),
    .out3(vec4_to_vec3_2_out3));
  Adder #(.width(32)) adder_4 (.a(32'h10000), .b(vec4_to_vec3_1_out1), .out(adder_4_out));  // open: cin, cout
  Adder #(.width(32)) adder_5 (.a(vec4_to_vec3_1_out2), .b(32'h10000), .out(adder_5_out));  // open: cin, cout
  Hex_Digit_Display hex_digit_display_139 (.value(n32bit_decoder_short_13__3_2));  // open: dp
  Hex_Digit_Display hex_digit_display_140 (.value(n32bit_decoder_short_13__2));  // open: dp
  Hex_Digit_Display hex_digit_display_141 (.value(n32bit_decoder_short_14__3_2));  // open: dp
  Hex_Digit_Display hex_digit_display_142 (.value(n32bit_decoder_short_14__2));  // open: dp
  Hex_Digit_Display hex_digit_display_143 (.value(n32bit_decoder_short_15__2));  // open: dp
  Hex_Digit_Display hex_digit_display_144 (.value(n32bit_decoder_short_15__3_2));  // open: dp
  // DotMatrix #(.inputtype("select"), .matrixcols(32), .matrixrows(32), .persist(64)) dotmatrix_1: pin names not known; wires that end beside it: y, x, dotmatrix_1_p3, dotmatrix_1_p4
  _64x64_display_controller u_64x64_display_controller_1 (
    .clk(clock_x2_2_clk_x2), .x11(dotmatrix_1_p3), .x21(n64x64_display_controller_1_x21),
    .x12(n64x64_display_controller_1_x12), .x22(n64x64_display_controller_1_x22), .y11(dotmatrix_1_p4),
    .y21(n64x64_display_controller_1_y21), .y12(n64x64_display_controller_1_y12),
    .y22(n64x64_display_controller_1_y22), .x(dda_test_sync_1_out_x[21:16]),
    .y(dda_test_sync_1_out_y[21:16]), .clear(in_7), .state(dda_test_sync_1_set_point),
    .update_frame(dda_test_sync_1_done));
  // DotMatrix #(.inputtype("select"), .matrixcols(32), .matrixrows(32), .persist(64)) dotmatrix_2: pin names not known; wires that end beside it: dda_test_sync_1_done, in_7, state, n64x64_display_controller_1_x12, n64x64_display_controller_1_y12
  _7_Segment_Display u_7_segment_display_16 (.g(n32bit_decoder_short_16_sign));  // open: f, a, b, e, d, c, dp
  Hex_Digit_Display hex_digit_display_145 (.value(n32bit_decoder_short_16__4));  // open: dp
  _7_Segment_Display u_7_segment_display_17 (.g(n32bit_decoder_short_17_sign));  // open: f, a, b, e, d, c, dp
  Hex_Digit_Display hex_digit_display_146 (.value(n32bit_decoder_short_17__4));  // open: dp
  Hex_Digit_Display hex_digit_display_147 (.value(n32bit_decoder_short_13__4_2));  // open: dp
  Hex_Digit_Display hex_digit_display_148 (.value(n32bit_decoder_short_13__5));  // open: dp
  _32bit_decoder_short u_32bit_decoder_short_13 (
    .sign(n32bit_decoder_short_13_sign), ._4(n32bit_decoder_short_13__4), ._3(n32bit_decoder_short_13__3),
    ._2_2(n32bit_decoder_short_13__2_2), ._1_2(n32bit_decoder_short_13__1_2),
    ._0(n32bit_decoder_short_13__0), .dot(n32bit_decoder_short_13_dot), .in(_31),
    ._1(n32bit_decoder_short_13__1), ._2(n32bit_decoder_short_13__2), ._3_2(n32bit_decoder_short_13__3_2),
    ._4_2(n32bit_decoder_short_13__4_2), ._5(n32bit_decoder_short_13__5));
  Hex_Digit_Display hex_digit_display_149 (.value(n32bit_decoder_short_14__4_2));  // open: dp
  Hex_Digit_Display hex_digit_display_150 (.value(n32bit_decoder_short_14__5));  // open: dp
  _32bit_decoder_short u_32bit_decoder_short_14 (
    .sign(n32bit_decoder_short_14_sign), ._4(n32bit_decoder_short_14__4), ._3(n32bit_decoder_short_14__3),
    ._2_2(n32bit_decoder_short_14__2_2), ._1_2(n32bit_decoder_short_14__1_2),
    ._0(n32bit_decoder_short_14__0), .dot(n32bit_decoder_short_14_dot), .in(_32),
    ._1(n32bit_decoder_short_14__1), ._2(n32bit_decoder_short_14__2), ._3_2(n32bit_decoder_short_14__3_2),
    ._4_2(n32bit_decoder_short_14__4_2), ._5(n32bit_decoder_short_14__5));
  Hex_Digit_Display hex_digit_display_151 (.value(n32bit_decoder_short_15__5));  // open: dp
  Hex_Digit_Display hex_digit_display_152 (.value(n32bit_decoder_short_15__4_2));  // open: dp
  _32bit_decoder_short u_32bit_decoder_short_15 (
    .sign(n32bit_decoder_short_15_sign), ._4(n32bit_decoder_short_15__4), ._3(n32bit_decoder_short_15__3),
    ._2_2(n32bit_decoder_short_15__2_2), ._1_2(n32bit_decoder_short_15__1_2),
    ._0(n32bit_decoder_short_15__0), .dot(n32bit_decoder_short_15_dot), .in(_33),
    ._1(n32bit_decoder_short_15__1), ._2(n32bit_decoder_short_15__2), ._3_2(n32bit_decoder_short_15__3_2),
    ._4_2(n32bit_decoder_short_15__4_2), ._5(n32bit_decoder_short_15__5));
  Hex_Digit_Display hex_digit_display_153 (.value(n32bit_decoder_short_16__2_2));  // open: dp
  Hex_Digit_Display hex_digit_display_154 (.value(n32bit_decoder_short_16__3));  // open: dp
  Hex_Digit_Display hex_digit_display_155 (.value(n32bit_decoder_short_17__3));  // open: dp
  Hex_Digit_Display hex_digit_display_156 (.value(n32bit_decoder_short_17__2_2));  // open: dp
  _7_Segment_Display u_7_segment_display_18 (.g(n32bit_decoder_short_18_sign));  // open: f, a, b, e, d, c, dp
  _7_Segment_Display u_7_segment_display_19 (.g(n32bit_decoder_short_19_sign));  // open: f, a, b, e, d, c, dp
  fp_mult fp_mult_10 (.in1(w_2), .in2(adder_4_out), .out(fp_mult_10_out));
  fp_mult fp_mult_11 (.in1(adder_5_out), .in2(h_2), .out(fp_mult_11_out));
  Hex_Digit_Display hex_digit_display_157 (.value(n32bit_decoder_short_16__1_2));  // open: dp
  Hex_Digit_Display hex_digit_display_158 (.value(n32bit_decoder_short_16__0), .dp(n32bit_decoder_short_16_dot));
  Hex_Digit_Display hex_digit_display_159 (.value(n32bit_decoder_short_17__0), .dp(n32bit_decoder_short_17_dot));
  Hex_Digit_Display hex_digit_display_160 (.value(n32bit_decoder_short_17__1_2));  // open: dp
  Hex_Digit_Display hex_digit_display_161 (.value(n32bit_decoder_short_18__4));  // open: dp
  Hex_Digit_Display hex_digit_display_162 (.value(n32bit_decoder_short_18__3));  // open: dp
  Hex_Digit_Display hex_digit_display_163 (.value(n32bit_decoder_short_19__3));  // open: dp
  Hex_Digit_Display hex_digit_display_164 (.value(n32bit_decoder_short_19__4));  // open: dp
  Hex_Digit_Display hex_digit_display_165 (.value(n32bit_decoder_short_16__1));  // open: dp
  Hex_Digit_Display hex_digit_display_166 (.value(n32bit_decoder_short_16__2));  // open: dp
  Hex_Digit_Display hex_digit_display_167 (.value(n32bit_decoder_short_17__2));  // open: dp
  Hex_Digit_Display hex_digit_display_168 (.value(n32bit_decoder_short_17__1));  // open: dp
  Hex_Digit_Display hex_digit_display_169 (.value(n32bit_decoder_short_18__2_2));  // open: dp
  Hex_Digit_Display hex_digit_display_170 (.value(n32bit_decoder_short_18__1_2));  // open: dp
  Hex_Digit_Display hex_digit_display_171 (.value(n32bit_decoder_short_19__2_2));  // open: dp
  Hex_Digit_Display hex_digit_display_172 (.value(n32bit_decoder_short_19__1_2));  // open: dp
  Negator #(.width(32)) negator_1 (.in(in_1), .out(negator_1_out));
  // DotMatrix #(.inputtype("select"), .matrixcols(32), .matrixrows(32), .persist(64)) dotmatrix_3: pin names not known; wires that end beside it: n64x64_display_controller_1_x21, n64x64_display_controller_1_y21
  // DotMatrix #(.inputtype("select"), .matrixcols(32), .matrixrows(32), .persist(64)) dotmatrix_4: pin names not known; wires that end beside it: n64x64_display_controller_1_x22, n64x64_display_controller_1_y22
  Hex_Digit_Display hex_digit_display_173 (.value(n32bit_decoder_short_16__4_2));  // open: dp
  Hex_Digit_Display hex_digit_display_174 (.value(n32bit_decoder_short_16__3_2));  // open: dp
  Hex_Digit_Display hex_digit_display_175 (.value(n32bit_decoder_short_17__4_2));  // open: dp
  Hex_Digit_Display hex_digit_display_176 (.value(n32bit_decoder_short_17__3_2));  // open: dp
  Hex_Digit_Display hex_digit_display_177 (.value(n32bit_decoder_short_18__0), .dp(n32bit_decoder_short_18_dot));
  Hex_Digit_Display hex_digit_display_178 (.value(n32bit_decoder_short_18__1));  // open: dp
  Hex_Digit_Display hex_digit_display_179 (.value(n32bit_decoder_short_19__0), .dp(n32bit_decoder_short_19_dot));
  Hex_Digit_Display hex_digit_display_180 (.value(n32bit_decoder_short_19__1));  // open: dp
  Hex_Digit_Display hex_digit_display_181 (.value(n32bit_decoder_short_16__5));  // open: dp
  _32bit_decoder_short u_32bit_decoder_short_16 (
    .sign(n32bit_decoder_short_16_sign), ._4(n32bit_decoder_short_16__4), ._3(n32bit_decoder_short_16__3),
    ._2_2(n32bit_decoder_short_16__2_2), ._1_2(n32bit_decoder_short_16__1_2),
    ._0(n32bit_decoder_short_16__0), .dot(n32bit_decoder_short_16_dot), .in(vec4_to_vec3_2_out1),
    ._1(n32bit_decoder_short_16__1), ._2(n32bit_decoder_short_16__2), ._3_2(n32bit_decoder_short_16__3_2),
    ._4_2(n32bit_decoder_short_16__4_2), ._5(n32bit_decoder_short_16__5));
  Hex_Digit_Display hex_digit_display_182 (.value(n32bit_decoder_short_17__5));  // open: dp
  _32bit_decoder_short u_32bit_decoder_short_17 (
    .sign(n32bit_decoder_short_17_sign), ._4(n32bit_decoder_short_17__4), ._3(n32bit_decoder_short_17__3),
    ._2_2(n32bit_decoder_short_17__2_2), ._1_2(n32bit_decoder_short_17__1_2),
    ._0(n32bit_decoder_short_17__0), .dot(n32bit_decoder_short_17_dot), .in(vec4_to_vec3_2_out2),
    ._1(n32bit_decoder_short_17__1), ._2(n32bit_decoder_short_17__2), ._3_2(n32bit_decoder_short_17__3_2),
    ._4_2(n32bit_decoder_short_17__4_2), ._5(n32bit_decoder_short_17__5));
  Hex_Digit_Display hex_digit_display_183 (.value(n32bit_decoder_short_18__3_2));  // open: dp
  Hex_Digit_Display hex_digit_display_184 (.value(n32bit_decoder_short_18__2));  // open: dp
  Hex_Digit_Display hex_digit_display_185 (.value(n32bit_decoder_short_19__3_2));  // open: dp
  Hex_Digit_Display hex_digit_display_186 (.value(n32bit_decoder_short_19__2));  // open: dp
  _7_Segment_Display u_7_segment_display_20 (.g(n32bit_decoder_short_20_sign));  // open: f, a, b, e, d, c, dp
  Hex_Digit_Display hex_digit_display_187 (.value(n32bit_decoder_short_18__4_2));  // open: dp
  Hex_Digit_Display hex_digit_display_188 (.value(n32bit_decoder_short_18__5));  // open: dp
  Hex_Digit_Display hex_digit_display_189 (.value(n32bit_decoder_short_19__4_2));  // open: dp
  Hex_Digit_Display hex_digit_display_190 (.value(n32bit_decoder_short_19__5));  // open: dp
  Hex_Digit_Display hex_digit_display_191 (.value(n32bit_decoder_short_20__4));  // open: dp
  _32bit_decoder_short u_32bit_decoder_short_18 (
    .sign(n32bit_decoder_short_18_sign), ._4(n32bit_decoder_short_18__4), ._3(n32bit_decoder_short_18__3),
    ._2_2(n32bit_decoder_short_18__2_2), ._1_2(n32bit_decoder_short_18__1_2),
    ._0(n32bit_decoder_short_18__0), .dot(n32bit_decoder_short_18_dot), .in(fp_mult_10_out),
    ._1(n32bit_decoder_short_18__1), ._2(n32bit_decoder_short_18__2), ._3_2(n32bit_decoder_short_18__3_2),
    ._4_2(n32bit_decoder_short_18__4_2), ._5(n32bit_decoder_short_18__5));
  _32bit_decoder_short u_32bit_decoder_short_19 (
    .sign(n32bit_decoder_short_19_sign), ._4(n32bit_decoder_short_19__4), ._3(n32bit_decoder_short_19__3),
    ._2_2(n32bit_decoder_short_19__2_2), ._1_2(n32bit_decoder_short_19__1_2),
    ._0(n32bit_decoder_short_19__0), .dot(n32bit_decoder_short_19_dot), .in(fp_mult_11_out),
    ._1(n32bit_decoder_short_19__1), ._2(n32bit_decoder_short_19__2), ._3_2(n32bit_decoder_short_19__3_2),
    ._4_2(n32bit_decoder_short_19__4_2), ._5(n32bit_decoder_short_19__5));
  Hex_Digit_Display hex_digit_display_192 (.value(n32bit_decoder_short_20__2_2));  // open: dp
  Hex_Digit_Display hex_digit_display_193 (.value(n32bit_decoder_short_20__3));  // open: dp
  Hex_Digit_Display hex_digit_display_194 (.value(n32bit_decoder_short_20__0), .dp(n32bit_decoder_short_20_dot));
  Hex_Digit_Display hex_digit_display_195 (.value(n32bit_decoder_short_20__1_2));  // open: dp
  fp_mult fp_mult_12 (.in1(32'h3e80000), .in2(32'hffff0000), .out(fp_mult_12_out));
  Hex_Digit_Display hex_digit_display_196 (.value(n32bit_decoder_short_20__2));  // open: dp
  Hex_Digit_Display hex_digit_display_197 (.value(n32bit_decoder_short_20__1));  // open: dp
  fp_mult fp_mult_13 (.in1(f_aspect_ratio), .in2(f_fov_rad), .out(fp_mult_13_out));
  fp_div fp_div_10 (.in1(32'h3e80000), .in2(subtractor_3_out), .out(fp_div_10_out));
  fp_mult fp_mult_14 (.in1(fp_mult_12_out), .in2(32'h1999), .out(fp_mult_14_out));
  fp_div fp_div_11 (.in1(fp_mult_14_out), .in2(subtractor_3_out), .out(fp_div_11_out));
  Subtractor #(.width(32)) subtractor_3 (.a(32'h3e80000), .b(32'h1999), .out(subtractor_3_out));  // open: bin, bout
  Hex_Digit_Display hex_digit_display_198 (.value(n32bit_decoder_short_20__4_2));  // open: dp
  Hex_Digit_Display hex_digit_display_199 (.value(n32bit_decoder_short_20__3_2));  // open: dp
  Button button_2 (.out(button_2_out));
  Hex_Digit_Display hex_digit_display_200 (.value(n32bit_decoder_short_20__5));  // open: dp
  _32bit_decoder_short u_32bit_decoder_short_20 (
    .sign(n32bit_decoder_short_20_sign), ._4(n32bit_decoder_short_20__4), ._3(n32bit_decoder_short_20__3),
    ._2_2(n32bit_decoder_short_20__2_2), ._1_2(n32bit_decoder_short_20__1_2),
    ._0(n32bit_decoder_short_20__0), .dot(n32bit_decoder_short_20_dot), .in(negator_1_out),
    ._1(n32bit_decoder_short_20__1), ._2(n32bit_decoder_short_20__2), ._3_2(n32bit_decoder_short_20__3_2),
    ._4_2(n32bit_decoder_short_20__4_2), ._5(n32bit_decoder_short_20__5));
  DDA_async dda_async_1 (
    .sync(clk), .new_data(button_2_out), .x2(x2), .x1(x1), .y2(y2), .y1(y1),
    .set_point(dda_async_1_set_point), .out_y(dda_async_1_out_y), .out_x(dda_async_1_out_x),
    .done(dda_async_1_done));  // open: lock
  clock_x2 clock_x2_3 (.clk(clk), .clk_x2(clock_x2_3_clk_x2));
  LED led_1 (.in(dda_async_1_done));
  VRAM_as vram_as_1 (
    .set(dda_async_1_set_point), .x1(dda_async_1_out_x), .clear(button_2_out), .y1(dda_async_1_out_y),
    .load_to_screen(dda_async_1_done), .clk(clock_x2_3_clk_x2), .x_right_out(vram_as_1_x_right_out),
    .x_left_out(vram_as_1_x_left_out), .y_out(vram_as_1_y_out), .mode(vram_as_1_mode));
  Button button_3 ();  // open: out
  clock_x2 clock_x2_4 (.clk(clk), .clk_x2(clock_x2_4_clk_x2));
  _64_display u_64_display_1 (
    .out_6(n64_display_1_out_6), .out_38(n64_display_1_out_38), .out_70(n64_display_1_out_70),
    .out_102(n64_display_1_out_102), .out_7(n64_display_1_out_7), .out_39(n64_display_1_out_39),
    .out_71(n64_display_1_out_71), .out_103(n64_display_1_out_103), .out_8(n64_display_1_out_8),
    .out_40(n64_display_1_out_40), .out_72(n64_display_1_out_72), .out_104(n64_display_1_out_104),
    .out_9(n64_display_1_out_9), .out_41(n64_display_1_out_41), .out_73(n64_display_1_out_73),
    .out_105(n64_display_1_out_105), .out_10(n64_display_1_out_10), .out_42(n64_display_1_out_42),
    .out_74(n64_display_1_out_74), .out_106(n64_display_1_out_106), .out_11(n64_display_1_out_11),
    .out_43(n64_display_1_out_43), .out_75(n64_display_1_out_75), .out_107(n64_display_1_out_107),
    .out_12(n64_display_1_out_12), .out_44(n64_display_1_out_44), .out_76(n64_display_1_out_76),
    .out_108(n64_display_1_out_108), .out_13(n64_display_1_out_13), .out_45(n64_display_1_out_45),
    .out_77(n64_display_1_out_77), .out_109(n64_display_1_out_109), .out_14(n64_display_1_out_14),
    .out_46(n64_display_1_out_46), .out_78(n64_display_1_out_78), .out_110(n64_display_1_out_110),
    .out_15(n64_display_1_out_15), .out_47(n64_display_1_out_47), .out_79(n64_display_1_out_79),
    .out_111(n64_display_1_out_111), .out_16(n64_display_1_out_16), .out_48(n64_display_1_out_48),
    .out_80(n64_display_1_out_80), .out_112(n64_display_1_out_112), .out_17(n64_display_1_out_17),
    .out_49(n64_display_1_out_49), .out_81(n64_display_1_out_81), .out_113(n64_display_1_out_113),
    .out_18(n64_display_1_out_18), .out_50(n64_display_1_out_50), .out_82(n64_display_1_out_82),
    .out_114(n64_display_1_out_114), .out_19(n64_display_1_out_19), .out_51(n64_display_1_out_51),
    .out_83(n64_display_1_out_83), .out_115(n64_display_1_out_115), .out_20(n64_display_1_out_20),
    .out_52(n64_display_1_out_52), .out_84(n64_display_1_out_84), .out_116(n64_display_1_out_116),
    .out_21(n64_display_1_out_21), .out_53(n64_display_1_out_53), .out_85(n64_display_1_out_85),
    .out_117(n64_display_1_out_117), .out_22(n64_display_1_out_22), .out_54(n64_display_1_out_54),
    .out_86(n64_display_1_out_86), .out_118(n64_display_1_out_118), .out_23(n64_display_1_out_23),
    .out_55(n64_display_1_out_55), .out_87(n64_display_1_out_87), .out_119(n64_display_1_out_119),
    .out_24(n64_display_1_out_24), .out_56(n64_display_1_out_56), .out_88(n64_display_1_out_88),
    .out_120(n64_display_1_out_120), .out_25(n64_display_1_out_25), .out_57(n64_display_1_out_57),
    .out_89(n64_display_1_out_89), .out_121(n64_display_1_out_121), .out_26(n64_display_1_out_26),
    .out_58(n64_display_1_out_58), .out_90(n64_display_1_out_90), .out_122(n64_display_1_out_122),
    .out_27(n64_display_1_out_27), .out_59(n64_display_1_out_59), .out_91(n64_display_1_out_91),
    .out_123(n64_display_1_out_123), .out_28(n64_display_1_out_28), .out_60(n64_display_1_out_60),
    .out_92(n64_display_1_out_92), .out_124(n64_display_1_out_124), .out_29(n64_display_1_out_29),
    .out_61(n64_display_1_out_61), .out_93(n64_display_1_out_93), .out_125(n64_display_1_out_125),
    .out_30(n64_display_1_out_30), .out_62(n64_display_1_out_62), .out_94(n64_display_1_out_94),
    .out_126(n64_display_1_out_126), .out_31(n64_display_1_out_31), .out_63(n64_display_1_out_63),
    .out_95(n64_display_1_out_95), .out_127(n64_display_1_out_127), .out_32(n64_display_1_out_32),
    .out_64(n64_display_1_out_64), .out_96(n64_display_1_out_96), .out_128(n64_display_1_out_128),
    .out_33(n64_display_1_out_33), .out_65(n64_display_1_out_65), .out_97(n64_display_1_out_97),
    .out_129(n64_display_1_out_129), .out_34(n64_display_1_out_34), .out_66(n64_display_1_out_66),
    .out_98(n64_display_1_out_98), .out_130(n64_display_1_out_130), .out_35(n64_display_1_out_35),
    .out_67(n64_display_1_out_67), .out_99(n64_display_1_out_99), .out_131(n64_display_1_out_131),
    .out_36(n64_display_1_out_36), .out_68(n64_display_1_out_68), .out_100(n64_display_1_out_100),
    .out_132(n64_display_1_out_132), .out_37(n64_display_1_out_37), .out_69(n64_display_1_out_69),
    .out_101(n64_display_1_out_101), .out_133(n64_display_1_out_133), .x_right_in(vram_as_1_x_right_out),
    .x_left_in(vram_as_1_x_left_out), .y_in(vram_as_1_y_out), .mode(vram_as_1_mode), .clk(clock_x2_4_clk_x2));
  DotMatrix #(.inputtype("row"), .matrixcols(32), .matrixrows(32)) dotmatrix_5 (
    .row0(n64_display_1_out_69), .row1(n64_display_1_out_68), .row2(n64_display_1_out_67),
    .row3(n64_display_1_out_66), .row4(n64_display_1_out_65), .row5(n64_display_1_out_64),
    .row6(n64_display_1_out_63), .row7(n64_display_1_out_62), .row8(n64_display_1_out_61),
    .row9(n64_display_1_out_60), .row10(n64_display_1_out_59), .row11(n64_display_1_out_58),
    .row12(n64_display_1_out_57), .row13(n64_display_1_out_56), .row14(n64_display_1_out_55),
    .row15(n64_display_1_out_54), .row16(n64_display_1_out_53), .row17(n64_display_1_out_52),
    .row18(n64_display_1_out_51), .row19(n64_display_1_out_50), .row20(n64_display_1_out_49),
    .row21(n64_display_1_out_48), .row22(n64_display_1_out_47), .row23(n64_display_1_out_46),
    .row24(n64_display_1_out_45), .row25(n64_display_1_out_44), .row26(n64_display_1_out_43),
    .row27(n64_display_1_out_42), .row28(n64_display_1_out_41), .row29(n64_display_1_out_40),
    .row30(n64_display_1_out_39), .row31(n64_display_1_out_38));
  DotMatrix #(.inputtype("row"), .matrixcols(32), .matrixrows(32)) dotmatrix_6 (
    .row0(n64_display_1_out_101), .row1(n64_display_1_out_100), .row2(n64_display_1_out_99),
    .row3(n64_display_1_out_98), .row4(n64_display_1_out_97), .row5(n64_display_1_out_96),
    .row6(n64_display_1_out_95), .row7(n64_display_1_out_94), .row8(n64_display_1_out_93),
    .row9(n64_display_1_out_92), .row10(n64_display_1_out_91), .row11(n64_display_1_out_90),
    .row12(n64_display_1_out_89), .row13(n64_display_1_out_88), .row14(n64_display_1_out_87),
    .row15(n64_display_1_out_86), .row16(n64_display_1_out_85), .row17(n64_display_1_out_84),
    .row18(n64_display_1_out_83), .row19(n64_display_1_out_82), .row20(n64_display_1_out_81),
    .row21(n64_display_1_out_80), .row22(n64_display_1_out_79), .row23(n64_display_1_out_78),
    .row24(n64_display_1_out_77), .row25(n64_display_1_out_76), .row26(n64_display_1_out_75),
    .row27(n64_display_1_out_74), .row28(n64_display_1_out_73), .row29(n64_display_1_out_72),
    .row30(n64_display_1_out_71), .row31(n64_display_1_out_70));
  // matrix_mult_4x4 matrix_mult_4x4_3: pin names not known
  matrix_mult_4x4 matrix_mult_4x4_4 (
    .in_1(in_18), .in_5(in_20), .in_9(in_22), .in_13(32'h10000), .in_17(fp_mult_13_out), .in_22(f_fov_rad),
    .in_27(fp_div_10_out), .in_28(fp_div_11_out), .in_31(32'h10000), .out11(matrix_mult_4x4_4_out11),
    .out12(matrix_mult_4x4_4_out12), .out13(matrix_mult_4x4_4_out13), .out14(matrix_mult_4x4_4_out14));  // open: in_2, in_3, in_4, in_6, in_7, in_8, in_10, in_11, in_12, in_14, in_15, in_16, in_18, in_19, in_20, in_21, in_23, in_24, in_25, in_26, in_29, in_30, in_32, out21, out31, out41, out22, out32, out42, out23, out33, out43, out24, out34, out44
  vec4_to_vec3 vec4_to_vec3_3 (
    .in1(matrix_mult_4x4_4_out11), .in2(matrix_mult_4x4_4_out12), .in3(matrix_mult_4x4_4_out13),
    .in4(matrix_mult_4x4_4_out14), .out1(vec4_to_vec3_3_out1), .out2(vec4_to_vec3_3_out2),
    .out3(vec4_to_vec3_3_out3));
  DotMatrix #(.inputtype("row"), .matrixcols(32), .matrixrows(32)) dotmatrix_7 (
    .row0(n64_display_1_out_37), .row1(n64_display_1_out_36), .row2(n64_display_1_out_35),
    .row3(n64_display_1_out_34), .row4(n64_display_1_out_33), .row5(n64_display_1_out_32),
    .row6(n64_display_1_out_31), .row7(n64_display_1_out_30), .row8(n64_display_1_out_29),
    .row9(n64_display_1_out_28), .row10(n64_display_1_out_27), .row11(n64_display_1_out_26),
    .row12(n64_display_1_out_25), .row13(n64_display_1_out_24), .row14(n64_display_1_out_23),
    .row15(n64_display_1_out_22), .row16(n64_display_1_out_21), .row17(n64_display_1_out_20),
    .row18(n64_display_1_out_19), .row19(n64_display_1_out_18), .row20(n64_display_1_out_17),
    .row21(n64_display_1_out_16), .row22(n64_display_1_out_15), .row23(n64_display_1_out_14),
    .row24(n64_display_1_out_13), .row25(n64_display_1_out_12), .row26(n64_display_1_out_11),
    .row27(n64_display_1_out_10), .row28(n64_display_1_out_9), .row29(n64_display_1_out_8),
    .row30(n64_display_1_out_7), .row31(n64_display_1_out_6));
  DotMatrix #(.inputtype("row"), .matrixcols(32), .matrixrows(32)) dotmatrix_8 (
    .row0(n64_display_1_out_133), .row1(n64_display_1_out_132), .row2(n64_display_1_out_131),
    .row3(n64_display_1_out_130), .row4(n64_display_1_out_129), .row5(n64_display_1_out_128),
    .row6(n64_display_1_out_127), .row7(n64_display_1_out_126), .row8(n64_display_1_out_125),
    .row9(n64_display_1_out_124), .row10(n64_display_1_out_123), .row11(n64_display_1_out_122),
    .row12(n64_display_1_out_121), .row13(n64_display_1_out_120), .row14(n64_display_1_out_119),
    .row15(n64_display_1_out_118), .row16(n64_display_1_out_117), .row17(n64_display_1_out_116),
    .row18(n64_display_1_out_115), .row19(n64_display_1_out_114), .row20(n64_display_1_out_113),
    .row21(n64_display_1_out_112), .row22(n64_display_1_out_111), .row23(n64_display_1_out_110),
    .row24(n64_display_1_out_109), .row25(n64_display_1_out_108), .row26(n64_display_1_out_107),
    .row27(n64_display_1_out_106), .row28(n64_display_1_out_105), .row29(n64_display_1_out_104),
    .row30(n64_display_1_out_103), .row31(n64_display_1_out_102));
  // vec4_to_vec3 vec4_to_vec3_4: pin names not known
  _7_Segment_Display u_7_segment_display_21 (.g(n32bit_decoder_short_21_sign));  // open: f, a, b, e, d, c, dp
  Hex_Digit_Display hex_digit_display_201 (.value(n32bit_decoder_short_21__4));  // open: dp
  _7_Segment_Display u_7_segment_display_22 (.g(n32bit_decoder_short_22_sign));  // open: f, a, b, e, d, c, dp
  Hex_Digit_Display hex_digit_display_202 (.value(n32bit_decoder_short_22__4));  // open: dp
  // matrix_mult_sub_4 matrix_mult_sub_4_1: pin names not known
  Hex_Digit_Display hex_digit_display_203 (.value(n32bit_decoder_short_21__3));  // open: dp
  Hex_Digit_Display hex_digit_display_204 (.value(n32bit_decoder_short_21__2_2));  // open: dp
  Hex_Digit_Display hex_digit_display_205 (.value(n32bit_decoder_short_22__3));  // open: dp
  Hex_Digit_Display hex_digit_display_206 (.value(n32bit_decoder_short_22__2_2));  // open: dp
  Hex_Digit_Display hex_digit_display_207 (.value(n32bit_decoder_short_21__1_2));  // open: dp
  Hex_Digit_Display hex_digit_display_208 (.value(n32bit_decoder_short_21__0), .dp(n32bit_decoder_short_21_dot));
  Hex_Digit_Display hex_digit_display_209 (.value(n32bit_decoder_short_22__1_2));  // open: dp
  Hex_Digit_Display hex_digit_display_210 (.value(n32bit_decoder_short_22__0), .dp(n32bit_decoder_short_22_dot));
  Hex_Digit_Display hex_digit_display_211 (.value(n32bit_decoder_short_21__1));  // open: dp
  Hex_Digit_Display hex_digit_display_212 (.value(n32bit_decoder_short_21__2));  // open: dp
  Hex_Digit_Display hex_digit_display_213 (.value(n32bit_decoder_short_22__2));  // open: dp
  Hex_Digit_Display hex_digit_display_214 (.value(n32bit_decoder_short_22__1));  // open: dp
  Hex_Digit_Display hex_digit_display_215 (.value(n32bit_decoder_short_21__4_2));  // open: dp
  Hex_Digit_Display hex_digit_display_216 (.value(n32bit_decoder_short_21__3_2));  // open: dp
  Hex_Digit_Display hex_digit_display_217 (.value(n32bit_decoder_short_22__3_2));  // open: dp
  Hex_Digit_Display hex_digit_display_218 (.value(n32bit_decoder_short_22__4_2));  // open: dp
  Hex_Digit_Display hex_digit_display_219 (.value(n32bit_decoder_short_21__5));  // open: dp
  _32bit_decoder_short u_32bit_decoder_short_21 (
    .sign(n32bit_decoder_short_21_sign), ._4(n32bit_decoder_short_21__4), ._3(n32bit_decoder_short_21__3),
    ._2_2(n32bit_decoder_short_21__2_2), ._1_2(n32bit_decoder_short_21__1_2),
    ._0(n32bit_decoder_short_21__0), .dot(n32bit_decoder_short_21_dot), .in(vec4_to_vec3_3_out1),
    ._1(n32bit_decoder_short_21__1), ._2(n32bit_decoder_short_21__2), ._3_2(n32bit_decoder_short_21__3_2),
    ._4_2(n32bit_decoder_short_21__4_2), ._5(n32bit_decoder_short_21__5));
  Hex_Digit_Display hex_digit_display_220 (.value(n32bit_decoder_short_22__5));  // open: dp
  _32bit_decoder_short u_32bit_decoder_short_22 (
    .sign(n32bit_decoder_short_22_sign), ._4(n32bit_decoder_short_22__4), ._3(n32bit_decoder_short_22__3),
    ._2_2(n32bit_decoder_short_22__2_2), ._1_2(n32bit_decoder_short_22__1_2),
    ._0(n32bit_decoder_short_22__0), .dot(n32bit_decoder_short_22_dot), .in(vec4_to_vec3_3_out2),
    ._1(n32bit_decoder_short_22__1), ._2(n32bit_decoder_short_22__2), ._3_2(n32bit_decoder_short_22__3_2),
    ._4_2(n32bit_decoder_short_22__4_2), ._5(n32bit_decoder_short_22__5));

  // Other names for the same wires on the sheet: R1_12[31:0] = R1_11; R1_13[31:0] = R1_11; R1_21[31:0] = R1_11;
  //   R1_22[31:0] = R1_11; R1_23[31:0] = R1_11; R1_31[31:0] = R1_11; R1_32[31:0] = R1_11; R1_33[31:0] = R1_11;
  //   R2_12[31:0] = R2_11; R2_13[31:0] = R2_11; R2_21[31:0] = R2_11; R2_22[31:0] = R2_11; R2_23[31:0] = R2_11;
  //   R2_31[31:0] = R2_11; R2_32[31:0] = R2_11; R2_33[31:0] = R2_11

  // Notes on the sheet:
  //   in_18: pull=down
  //   in_1: pull=down
  //   in_14: pull=down
  //   Load_sample: pull=down
  //   in_17: pull=down
  //   in_19: pull=down
  //   in_22: pull=down
  //   in_16: pull=down
  //   in_15: pull=down
  //   in_20: pull=down
  //   in_21: pull=down
  //   contents of rom_1 (hex, n*v repeats v):
  //   10000 10000 10000 13*0 10000 10000 10000 13*0 10000 10000 10000 13*0 10000 16*0 10000 16*0 10000
  //   13*0 1000 15*0 1000 15*0 1000 15*0 11000 11000 11000
  //   matrix couter
  //   projection matrix
endmodule

module fp_to_int (
  input  [31:0] in,
  output [31:0] out
);

  Shifter #(.width(32), .shift("lr")) shifter_1 (.in(in), .\dist (5'b10000), .out(out));

  // Notes on the sheet:
  //   in: pull=down
  //   out: pull=down
endmodule

module _64x64_display_controller (
  input  [5:0] y,
  input  [5:0] x,
  input  state,
  input  clear,
  input  update_frame,
  input  clk,
  output [31:0] x12,
  output [31:0] x22,
  output [31:0] x11,
  output [31:0] x21,
  output [31:0] y12,
  output [31:0] y22,
  output [31:0] y11,
  output [31:0] y21
);

  wire counter_1_carry, counter_2_carry, falling_edge_pulse_1_out, falling_edge_pulse_2_out,
       multiplexer_1_out, multiplexer_2_out, multiplexer_3_out, multiplexer_6_out, not_1_out, not_2_out,
       not_3_out, not_4_out, not_5_out, or_1_out, or_2_out, rising_edge_detector_1_out,
       rising_edge_pulse_1_out;
  wire [5:0] counter_2_q, multiplexer_5_out;
  wire [31:0] decoder_1_out0, decoder_2_out0, multiplexer_7_out, multiplexer_8_out, or_3_out,
       pull_resistor_2_node, ram_1_data, ram_2_data, ram_3_data, ram_4_data;

  Register #(.width(6)) register_1 ();  // open: D, en, Q, clk, clr
  rising_edge_pulse rising_edge_pulse_1 (.signal(clear), .out(rising_edge_pulse_1_out));
  falling_edge_pulse falling_edge_pulse_1 (.signal(counter_1_carry), .out(falling_edge_pulse_1_out));
  falling_edge_pulse falling_edge_pulse_2 (.signal(counter_2_carry), .out(falling_edge_pulse_2_out));
  Decoder #(.select(5)) decoder_1 (
    .out0(decoder_1_out0[0]), .out1(decoder_1_out0[1]), .out2(decoder_1_out0[2]), .out3(decoder_1_out0[3]),
    .out4(decoder_1_out0[4]), .out5(decoder_1_out0[5]), .out6(decoder_1_out0[6]), .out7(decoder_1_out0[7]),
    .out8(decoder_1_out0[8]), .out9(decoder_1_out0[9]), .out10(decoder_1_out0[10]),
    .out11(decoder_1_out0[11]), .out12(decoder_1_out0[12]), .out13(decoder_1_out0[13]),
    .out14(decoder_1_out0[14]), .out15(decoder_1_out0[15]), .out16(decoder_1_out0[16]),
    .out17(decoder_1_out0[17]), .out18(decoder_1_out0[18]), .out19(decoder_1_out0[19]),
    .out20(decoder_1_out0[20]), .out21(decoder_1_out0[21]), .out22(decoder_1_out0[22]),
    .out23(decoder_1_out0[23]), .out24(decoder_1_out0[24]), .out25(decoder_1_out0[25]),
    .out26(decoder_1_out0[26]), .out27(decoder_1_out0[27]), .out28(decoder_1_out0[28]),
    .out29(decoder_1_out0[29]), .out30(decoder_1_out0[30]), .out31(decoder_1_out0[31]), .sel(x[4:0]),
    .en(state));
  rising_edge_detector rising_edge_detector_1 (
    .signal(update_frame), .clear(falling_edge_pulse_1_out), .sync(falling_edge_pulse_2_out),
    .out(rising_edge_detector_1_out));
  or or_1 (or_1_out, rising_edge_detector_1_out, counter_1_carry);
  Pull_Resistor pull_resistor_1 (.node(decoder_1_out0));
  Counter #(.width(6), .max('h3f)) counter_1 (
    .count(or_1_out), .carry(counter_1_carry), .clk(clk));  // open: load, D, Q, clr
  Multiplexer #(.enable("false")) multiplexer_1 (
    .in0(state), .in1(1'b0), .out(multiplexer_1_out), .sel(rising_edge_detector_1_out));
  Pull_Resistor pull_resistor_2 (.node(pull_resistor_2_node));
  not not_1 (not_1_out, x[5]);
  or or_2 (or_2_out, rising_edge_pulse_1_out, rising_edge_pulse_1_out);
  assign or_3_out = pull_resistor_2_node | decoder_1_out0;  // OR_Gate or_3, 32 bits wide
  Multiplexer #(.enable("false")) multiplexer_2 (
    .in0(x[5]), .in1(1'b1), .out(multiplexer_2_out), .sel(rising_edge_detector_1_out));
  Multiplexer #(.enable("false")) multiplexer_3 (
    .in0(not_1_out), .in1(1'b1), .out(multiplexer_3_out), .sel(rising_edge_detector_1_out));
  Multiplexer #(.width(32)) multiplexer_4 (
    .in0(ram_3_data), .in1(ram_1_data), .out(pull_resistor_2_node), .sel(multiplexer_3_out), .en(not_2_out));
  Multiplexer #(.width(6), .enable("false")) multiplexer_5 (
    .in0(y), .in1(counter_2_q), .out(multiplexer_5_out), .sel(rising_edge_detector_1_out));
  Counter #(.width(6), .max('h3f)) counter_2 (
    .Q(counter_2_q), .carry(counter_2_carry), .clk(clk));  // open: load, D, count, clr
  not not_2 (not_2_out, rising_edge_detector_1_out);
  Decoder #(.select(5), .enable("false")) decoder_2 (
    .out0(decoder_2_out0[0]), .out1(decoder_2_out0[1]), .out2(decoder_2_out0[2]), .out3(decoder_2_out0[3]),
    .out4(decoder_2_out0[4]), .out5(decoder_2_out0[5]), .out6(decoder_2_out0[6]), .out7(decoder_2_out0[7]),
    .out8(decoder_2_out0[8]), .out9(decoder_2_out0[9]), .out10(decoder_2_out0[10]),
    .out11(decoder_2_out0[11]), .out12(decoder_2_out0[12]), .out13(decoder_2_out0[13]),
    .out14(decoder_2_out0[14]), .out15(decoder_2_out0[15]), .out16(decoder_2_out0[16]),
    .out17(decoder_2_out0[17]), .out18(decoder_2_out0[18]), .out19(decoder_2_out0[19]),
    .out20(decoder_2_out0[20]), .out21(decoder_2_out0[21]), .out22(decoder_2_out0[22]),
    .out23(decoder_2_out0[23]), .out24(decoder_2_out0[24]), .out25(decoder_2_out0[25]),
    .out26(decoder_2_out0[26]), .out27(decoder_2_out0[27]), .out28(decoder_2_out0[28]),
    .out29(decoder_2_out0[29]), .out30(decoder_2_out0[30]), .out31(decoder_2_out0[31]), .sel(counter_2_q[4:0]));
  Multiplexer #(.enable("false")) multiplexer_6 (
    .in0(state), .in1(1'b1), .out(multiplexer_6_out), .sel(rising_edge_detector_1_out));
  not not_3 (not_3_out, rising_edge_detector_1_out);
  RAM #(.addrWidth(6), .dataWidth(32), .bus("separate")) ram_1 (
    .addr(multiplexer_5_out), .din(or_3_out), .data(ram_1_data), .str(multiplexer_1_out),
    .sel(multiplexer_3_out), .clk(clk), .ld(multiplexer_6_out), .clr(or_2_out));
  RAM #(.addrWidth(6), .dataWidth(32), .bus("separate")) ram_2 (
    .addr(counter_2_q), .din(ram_1_data), .data(ram_2_data), .str(rising_edge_detector_1_out), .clk(clk),
    .ld(not_3_out));  // open: sel, clr
  not not_4 (not_4_out, rising_edge_detector_1_out);
  RAM #(.addrWidth(6), .dataWidth(32), .bus("separate")) ram_3 (
    .addr(multiplexer_5_out), .din(or_3_out), .data(ram_3_data), .str(multiplexer_1_out),
    .sel(multiplexer_2_out), .clk(clk), .ld(multiplexer_6_out), .clr(or_2_out));
  RAM #(.addrWidth(6), .dataWidth(32), .bus("separate")) ram_4 (
    .addr(counter_2_q), .din(ram_3_data), .data(ram_4_data), .str(rising_edge_detector_1_out), .clk(clk),
    .ld(not_4_out));  // open: sel, clr
  Multiplexer #(.width(32), .enable("false")) multiplexer_7 (
    .in0(ram_4_data), .in1(ram_3_data), .out(multiplexer_7_out), .sel(rising_edge_detector_1_out));
  Multiplexer #(.width(32), .enable("false")) multiplexer_8 (
    .in0(ram_2_data), .in1(ram_1_data), .out(multiplexer_8_out), .sel(rising_edge_detector_1_out));
  not not_5 (not_5_out, counter_2_q[5]);
  Register #(.width(32), .trigger("falling")) register_2 (
    .D(multiplexer_7_out), .en(not_5_out), .Q(x22), .clk(clk), .clr(counter_2_q[5]));
  Register #(.width(32), .trigger("falling")) register_3 (
    .D(multiplexer_7_out), .en(counter_2_q[5]), .Q(x21), .clk(clk), .clr(not_5_out));
  Register #(.width(32), .trigger("falling")) register_4 (
    .D(decoder_2_out0), .en(not_5_out), .Q(y12), .clk(clk), .clr(counter_2_q[5]));
  Register #(.width(32), .trigger("falling")) register_5 (
    .D(decoder_2_out0), .en(counter_2_q[5]), .Q(y11), .clk(clk), .clr(not_5_out));
  Register #(.width(32), .trigger("falling")) register_6 (
    .D(multiplexer_8_out), .en(not_5_out), .Q(x12), .clk(clk), .clr(counter_2_q[5]));
  Register #(.width(32), .trigger("falling")) register_7 (
    .D(multiplexer_8_out), .en(counter_2_q[5]), .Q(x11), .clk(clk), .clr(not_5_out));
  Register #(.width(32), .trigger("falling")) register_8 (
    .D(decoder_2_out0), .en(not_5_out), .Q(y22), .clk(clk), .clr(counter_2_q[5]));
  Register #(.width(32), .trigger("falling")) register_9 (
    .D(decoder_2_out0), .en(counter_2_q[5]), .Q(y21), .clk(clk), .clr(not_5_out));

  // Notes on the sheet:
  //   clear: pull=down
  //   update_frame: pull=down
  //   y22: pull=down
  //   y: pull=down
  //   y21: pull=down
  //   clk: pull=down
  //   state: pull=down
  //   x11: pull=down
  //   x21: pull=down
  //   x22: pull=down
  //   x12: pull=down
  //   x: pull=down
  //   y12: pull=down
  //   y11: pull=down
endmodule

module int_to_fp (
  input  [31:0] in,
  output [31:0] out
);

  Shifter #(.width(32)) shifter_1 (.in(in), .\dist (5'b10000), .out(out));

  // Notes on the sheet:
  //   in: pull=down
  //   out: pull=down
endmodule

module DDA_test_sync (
  input  clk,
  input  new_data,
  input  [31:0] x2,
  input  [31:0] x1,
  input  [31:0] y2,
  input  [31:0] y1,
  output [31:0] out_y,
  output [3:0] status,
  output [31:0] out_x,
  output set_point,
  output done
);

  wire and_1_out, and_2_out, and_4_out, and_5_out, button_1_out, comparator_2_eq, comparator_2_lt,
       comparator_3_eq, controlled_buffer_7_out, mission_2, nand_1_out, nand_2_out, nand_3_out, nand_4_out,
       nand_5_out, nand_6_out, nand_7_out, nand_8_out, nand_9_out, nand_11_out, nand_12_out, nand_14_out,
       nand_15_out, nand_17_out, nand_18_out, nand_20_out, nand_21_out, nand_22_out, nand_23_out,
       nand_24_out, nand_25_out, nand_27_out, nand_29_out, new_data_t, not_1_out, not_2_out, not_3_out,
       or_2_out;
  wire [1:0] comparator_1_gt, control, mission, or_1_out, state;
  wire [1:1] comparator_1_lt;
  wire [31:0] counter_1_q, dx, dy, fp_abs_1_abs, fp_abs_2_abs, fp_round_ones_3_p1, out_x_t, out_y_t,
       steps_count, x, x1_t, x2_t, x_dx, x_step, y, y1_t, y2_t, y_dy, y_step;

  rising_edge_detector rising_edge_detector_1 (.signal(new_data), .clear(done), .sync(clk), .out(new_data_t));
  and and_1 (and_1_out, ~mission[1], mission[0]);  // AND_Gate
  and and_2 (and_2_out, mission[1], mission[0]);
  and and_3 (mission_2, mission[1], ~mission[0]);  // AND_Gate
  Register #(.width(32)) register_1 (.D(x2), .Q(x2_t), .clk(new_data_t));  // open: en, clr
  Register #(.width(32)) register_2 (.D(x1), .Q(x1_t), .clk(new_data_t));  // open: en, clr
  Register #(.width(32)) register_3 (.D(y2), .Q(y2_t), .clk(new_data_t));  // open: en, clr
  Register #(.width(32)) register_4 (.D(y1), .Q(y1_t), .clk(new_data_t));  // open: en, clr
  assign x = and_1_out ? x1_t : 32'bz;  // Controlled_Buffer controlled_buffer_1
  assign x = and_2_out ? x2_t : 32'bz;  // Controlled_Buffer controlled_buffer_2
  assign x = mission_2 ? x_dx : 32'bz;  // Controlled_Buffer controlled_buffer_3
  assign y = and_1_out ? y1_t : 32'bz;  // Controlled_Buffer controlled_buffer_4
  assign y = and_2_out ? y2_t : 32'bz;  // Controlled_Buffer controlled_buffer_5
  assign y = mission_2 ? y_dy : 32'bz;  // Controlled_Buffer controlled_buffer_6
  fp_abs fp_abs_1 (.in(dx), .abs(fp_abs_1_abs));
  Subtractor #(.width(32)) subtractor_1 (.a(x2_t), .b(x1_t), .out(dx));  // open: bin, bout
  Subtractor #(.width(32)) subtractor_2 (.a(y2_t), .b(y1_t), .out(dy));  // open: bin, bout
  fp_abs fp_abs_2 (.in(dy), .abs(fp_abs_2_abs));
  Adder #(.width(32)) adder_1 (.a(out_x_t), .b(x_step), .out(x_dx));  // open: cin, cout
  Adder #(.width(32)) adder_2 (.a(out_y_t), .b(y_step), .out(y_dy));  // open: cin, cout
  // fp_round_ones fp_round_ones_1: pin names not known; wires that end beside it: out_x_t, out_y
  // fp_round_ones fp_round_ones_2: pin names not known; wires that end beside it: out_y_t, out_x
  Comparator #(.width(32)) comparator_1 (
    .a(fp_abs_1_abs), .b(fp_abs_2_abs), .gt(comparator_1_gt[0]), .eq(comparator_1_gt[1]),
    .lt(comparator_1_lt[1]));
  assign or_1_out = comparator_1_gt | {2{comparator_1_lt[1]}};  // OR_Gate or_1, 2 bits wide
  fp_div fp_div_1 (.in1(dx), .in2(steps_count), .out(x_step));
  fp_div fp_div_2 (.in1(dy), .in2(steps_count), .out(y_step));
  // fp_round_ones fp_round_ones_3: pin names not known; wires that end beside it: fp_round_ones_3_p1, steps_count
  Multiplexer #(.select(2), .width(32), .enable("false")) multiplexer_1 (
    .in1(fp_abs_1_abs), .in2(fp_abs_1_abs), .in3(fp_abs_2_abs), .out(fp_round_ones_3_p1), .sel(or_1_out));  // open: in0
  Register #(.width(32)) register_5 (.D(x), .Q(out_x_t), .clk(clk), .clr(button_1_out));  // open: en
  Register #(.width(32)) register_6 (.D(y), .Q(out_y_t), .clk(clk), .clr(button_1_out));  // open: en
  Button button_1 (.out(button_1_out));
  assign controlled_buffer_7_out = and_4_out ? clk : 1'bz;  // Controlled_Buffer controlled_buffer_7
  and and_4 (and_4_out, ~comparator_3_eq, mission_2);  // AND_Gate
  Counter #(.width(32), .max('hffffffff)) counter_1 (
    .Q(counter_1_q), .clk(controlled_buffer_7_out), .clr(done));  // open: load, D, count, carry
  or or_2 (or_2_out, comparator_2_eq, comparator_2_lt);
  Comparator #(.width(32)) comparator_2 (
    .a(steps_count), .b(32'h10000), .eq(comparator_2_eq), .lt(comparator_2_lt));  // open: gt
  not not_1 (not_1_out, nand_1_out);
  nand nand_1 (nand_1_out, control[0], state[0]);
  nand nand_2 (nand_2_out, ~control[0], ~control[1]);  // NAND_Gate
  nand nand_3 (nand_3_out, nand_2_out, ~state[0]);  // NAND_Gate
  nand nand_4 (nand_4_out, control[0], ~state[1]);  // NAND_Gate
  nand nand_5 (nand_5_out, nand_4_out, nand_6_out);
  nand nand_6 (nand_6_out, control[1], state[1]);
  nand nand_7 (nand_7_out, control[0], nand_8_out);
  nand nand_8 (nand_8_out, ~control[1], ~state[1]);  // NAND_Gate
  Button button_2 ();  // open: out
  and and_5 (and_5_out, ~or_2_out, comparator_3_eq);  // AND_Gate
  Comparator #(.width(32)) comparator_3 (
    .a({counter_1_q[15:0], {16{1'b0}}}), .b(steps_count), .eq(comparator_3_eq));  // open: gt, lt
  J_K_Flip_Flop j_k_ff_1 (.J(not_1_out), .clk(clk), .K(nand_3_out), .Q(state[1]));  // open: Qn, preset, en, reset
  J_K_Flip_Flop j_k_ff_2 (.J(nand_5_out), .clk(clk), .K(nand_7_out), .Q(state[0]));  // open: Qn, preset, en, reset
  nand nand_9 (nand_9_out, control[1], ~control[0], ~state[1]);  // NAND_Gate
  nand nand_10 (status[1], nand_9_out, nand_11_out);
  nand nand_11 (nand_11_out, control[1], ~control[0], state[0]);  // NAND_Gate
  nand nand_12 (nand_12_out, control[1], state[1], ~state[0]);  // NAND_Gate
  nand nand_13 (status[0], nand_12_out, not_2_out);
  not not_2 (not_2_out, control[0]);
  nand nand_14 (nand_14_out, control[0], ~state[1], state[0]);  // NAND_Gate
  nand nand_15 (nand_15_out, control[0], state[1], ~state[0]);  // NAND_Gate
  nand nand_16 (mission[1], nand_14_out, nand_15_out, nand_17_out);
  nand nand_17 (nand_17_out, control[1], state[1], ~state[0]);  // NAND_Gate
  nand nand_18 (nand_18_out, control[0], ~state[1], ~state[0]);  // NAND_Gate
  nand nand_19 (mission[0], nand_18_out, nand_20_out, nand_21_out);
  nand nand_20 (nand_20_out, control[1], control[0]);
  nand nand_21 (nand_21_out, control[1], state[1], ~state[0]);  // NAND_Gate
  nand nand_22 (nand_22_out, control[1], control[0], ~state[1], state[0]);  // NAND_Gate
  nand nand_23 (nand_23_out, nand_22_out, nand_24_out);
  nand nand_24 (nand_24_out, control[1], state[1], ~state[0]);  // NAND_Gate
  nand nand_25 (nand_25_out, control[0], state[0]);
  nand nand_26 (set_point, nand_25_out, nand_27_out);
  nand nand_27 (nand_27_out, state[1], ~state[0]);  // NAND_Gate
  Shift_Register #(.length(2)) shift_register_1 (
    .in(nand_23_out), .clk(clk), .out(done));  // open: shift, load, clr, d0, q0, d1, q1
  not not_3 (not_3_out, and_5_out);
  nand nand_28 (control[1], not_3_out, nand_29_out);
  nand nand_29 (nand_29_out, or_2_out, new_data_t);
  nand nand_30 (control[0], ~new_data_t, ~and_5_out);  // NAND_Gate
  Hex_Digit_Display hex_digit_display_1 (.value({2'b00, status[1:0]}));  // open: dp

  assign status[3:2] = 2'b00;

  // Other names for the same wires on the sheet: status_t[1:0] = status[1:0]

  // Notes on the sheet:
  //   done: pull=up
  //   set_point: pull=up
  //   In
  //   Mission decoder
  //   Out
  //   Math
  //   Out reg
  //   State machine
  //   Main logic
  //   00 - halt do nothg
  //   01 - load x1y1
  //   10 - increment by step
  //   11 - load x2y2
  //   Status
  //   0: halt
  //   1: run
  //   2: error
endmodule
module DDA_test_async (
  input  sync,
  input  new_data,
  input  lock,
  input  [31:0] x2,
  input  [31:0] x1,
  input  [31:0] y2,
  input  [31:0] y1,
  input  load,
  output set_point,
  output [31:0] out_y,
  output [31:0] out_x,
  output done
);

  wire and_2_out, and_5_out, and_7_out, and_9_out, and_12_out, and_14_out, and_15_out, and_16_out,
       and_17_out, and_18_out, and_19_out, and_20_out, and_21_out, and_22_out, and_23_out, and_24_out,
       and_25_out, and_26_out, and_28_out, and_29_out, and_30_out, and_31_out, buffer_2_out, buffer_3_out,
       buffer_4_out, buffer_5_out, buffer_6_out, buffer_7_out, buffer_8_out, buffer_9_out, buffer_10_out,
       buffer_11_out, buffer_12_out, buffer_13_out, buffer_14_out, buffer_15_out, buffer_16_out,
       buffer_17_out, buffer_28_out, buffer_29_out, buffer_32_out, buffer_33_out, clear, clear_wait_counter,
       comparator_2_gt, comparator_2_lt, comparator_4_lt, comparator_5_lt, controlled_buffer_15_out,
       counter_2_carry, done_t, inc_loop_counter, inc_stage_counter, inc_stored_values, inc_wait_counter,
       load_t, load_x1y1, load_x2y2, loop_counter, loop_stopper_counter, new_data_t, not_2_out, not_3_out,
       not_4_out, or_5_out, pull_resistor_3_node, pull_resistor_9_node, pull_resistor_15_node,
       pull_resistor_17_node, reset, rising_edge_detector_async_1_out, rising_edge_detector_async_2_out,
       rising_edge_detector_async_3_out, rising_edge_pulse_1_out, s_r_ff_1_q, set, skip_loop, start,
       wait_counter;
  wire [1:0] comparator_1_gt, or_2_out, stage;
  wire [1:1] comparator_1_lt;
  wire [3:0] address, register_1_q, register_2_q, register_3_q, register_6_q, register_7_q, register_8_q,
       register_9_q, register_10_q, register_11_q, register_12_q, register_13_q, register_14_q,
       register_15_q, register_16_q, register_17_q, register_18_q, register_19_q, register_20_q,
       register_21_q, register_22_q, register_23_q, register_24_q, register_25_q, register_26_q,
       register_27_q, register_28_q, register_29_q, register_30_q, register_31_q, register_32_q;
  wire [5:0] buffer_18_out, buffer_19_out, buffer_20_out, buffer_21_out, buffer_22_out, buffer_23_out,
       buffer_24_out, buffer_25_out, buffer_26_out, counter_2_q, multiplexer_2_out;
  wire [7:0] counter_1_q, counter_4_q, counter_5_q;
  wire [31:0] adder_3_out, adder_4_out, adder_5_out, adder_6_out, adder_7_out, adder_8_out, decoder_1_out31,
       dx, dy, fp_abs_1_abs, fp_abs_2_abs, loop_count, multiplexer_1_out, or_3_out, or_4_out, out_x_t,
       out_y_t, ram_1_data, ram_2_data, steps_count, subtractor_4_out, x, x_dx, x_step, y, y_dy, y_step;

  Register #(.width(4), .trigger("low")) register_1 (.D(address), .Q(register_1_q), .clk(1'b0));  // open: en, clr
  Register #(.width(4), .trigger("low")) register_2 (.D(address), .Q(register_2_q), .clk(1'b0));  // open: en, clr
  Pull_Resistor pull_resistor_1 (.node(sync));
  rising_edge_detector_async rising_edge_detector_async_1 (
    .signal(new_data), .clear(clear), .out(rising_edge_detector_async_1_out));
  Pull_Resistor pull_resistor_2 (.node(lock));
  Pull_Resistor pull_resistor_3 (.node(pull_resistor_3_node));
  and and_1 (pull_resistor_3_node, ~register_1_q[0], ~register_1_q[1], ~register_1_q[2], ~register_1_q[3], start);  // AND_Gate
  assign address = pull_resistor_3_node ? 4'b0001 : 4'bz;  // Controlled_Buffer controlled_buffer_1
  assign address = and_2_out ? 4'b0000 : 4'bz;  // Controlled_Buffer controlled_buffer_2
  and and_2 (and_2_out, ~start, ~register_2_q[0], ~register_2_q[1], ~register_2_q[2], ~register_2_q[3]);  // AND_Gate
  Pull_Resistor pull_resistor_4 (.node(and_2_out));
  and and_3 (new_data_t, rising_edge_detector_async_1_out, ~lock);  // AND_Gate
  assign x = load_x2y2 ? x2 : 32'bz;  // Controlled_Buffer controlled_buffer_3
  assign x = inc_stored_values ? x_dx : 32'bz;  // Controlled_Buffer controlled_buffer_4
  assign y = load_x2y2 ? y2 : 32'bz;  // Controlled_Buffer controlled_buffer_5
  assign y = inc_stored_values ? y_dy : 32'bz;  // Controlled_Buffer controlled_buffer_6
  assign x = load_x1y1 ? x1 : 32'bz;  // Controlled_Buffer controlled_buffer_7
  or or_1 (load_t, load_x1y1, load_x2y2, inc_stored_values);
  assign y = load_x1y1 ? y1 : 32'bz;  // Controlled_Buffer controlled_buffer_8
  Register #(.width(4), .trigger("low")) register_3 (.D(address), .Q(register_3_q), .clk(1'b0));  // open: en, clr
  // fp_round_ones fp_round_ones_1: pin names not known; wires that end beside it: out_x_t, out_y
  // fp_round_ones fp_round_ones_2: pin names not known; wires that end beside it: out_y_t, out_x
  Subtractor #(.width(32)) subtractor_1 (.a(x2), .b(x1), .out(dx));  // open: bin, bout
  Subtractor #(.width(32)) subtractor_2 (.a(y2), .b(y1), .out(dy));  // open: bin, bout
  Adder #(.width(32)) adder_1 (.a(out_x_t), .b(x_step), .out(x_dx));  // open: cin, cout
  Adder #(.width(32)) adder_2 (.a(out_y_t), .b(y_step), .out(y_dy));  // open: cin, cout
  and and_4 (load_x1y1, register_3_q[0], ~register_3_q[1], ~register_3_q[2], ~register_3_q[3]);  // AND_Gate
  fp_abs fp_abs_1 (.in(dx), .abs(fp_abs_1_abs));
  fp_abs fp_abs_2 (.in(dy), .abs(fp_abs_2_abs));
  assign address = load_x1y1 ? 4'b0010 : 4'bz;  // Controlled_Buffer controlled_buffer_9
  Pull_Resistor pull_resistor_5 (.node(load_x1y1));
  Comparator #(.width(32)) comparator_1 (
    .a(fp_abs_1_abs), .b(fp_abs_2_abs), .gt(comparator_1_gt[0]), .eq(comparator_1_gt[1]),
    .lt(comparator_1_lt[1]));
  S_R_Flip_Flop s_r_ff_1 (.Q(s_r_ff_1_q), .Qn(done), .preset(and_5_out), .reset(done_t));  // open: S, clk, R, en
  Multiplexer #(.select(2), .width(32), .enable("false")) multiplexer_1 (
    .in1(fp_abs_1_abs), .in2(fp_abs_1_abs), .in3(fp_abs_2_abs), .out(multiplexer_1_out), .sel(or_2_out));  // open: in0
  assign or_2_out = comparator_1_gt | {2{comparator_1_lt[1]}};  // OR_Gate or_2, 2 bits wide
  fp_div fp_div_1 (.in1(dx), .in2(steps_count), .out(x_step));
  fp_div fp_div_2 (.in1(dy), .in2(steps_count), .out(y_step));
  Register #(.width(32)) register_4 (.D(x), .Q(out_x_t), .clk(load_t), .clr(clear));  // open: en
  Register #(.width(32)) register_5 (.D(y), .Q(out_y_t), .clk(load_t), .clr(clear));  // open: en
  Register #(.width(4), .trigger("low")) register_6 (.D(address), .Q(register_6_q), .clk(1'b0));  // open: en, clr
  S_R_Flip_Flop s_r_ff_2 (.Q(set_point), .preset(set), .reset(reset));  // open: S, clk, R, Qn, en
  and and_5 (and_5_out, new_data_t, ~s_r_ff_1_q);  // AND_Gate
  // fp_round_ones fp_round_ones_3: pin names not known; wires that end beside it: multiplexer_1_out, steps_count
  assign address = set ? 4'b0011 : 4'bz;  // Controlled_Buffer controlled_buffer_10
  and and_6 (set, ~register_6_q[0], register_6_q[1], ~register_6_q[2], ~register_6_q[3]);  // AND_Gate
  Pull_Resistor pull_resistor_6 (.node(set));
  Adder #(.width(32)) adder_3 (.a(adder_4_out), .b({32{1'b0}}), .out(adder_3_out));  // open: cin, cout
  Adder #(.width(32)) adder_4 (.a({{31{1'b0}}, new_data_t}), .b({32{1'b0}}), .out(adder_4_out));  // open: cin, cout
  Subtractor #(.width(32)) subtractor_3 (.a(steps_count), .b(32'h20000), .out(loop_count));  // open: bin, bout
  Comparator #(.width(32)) comparator_2 (
    .a(steps_count), .b(32'h10000), .gt(comparator_2_gt), .lt(comparator_2_lt));  // open: eq
  rising_edge_detector_async rising_edge_detector_async_2 (
    .signal(new_data_t), .clear(and_7_out), .out(rising_edge_detector_async_2_out));
  Adder #(.width(32)) adder_5 (.a(adder_3_out), .b({32{1'b0}}), .out(adder_5_out));  // open: cin, cout
  not not_1 (skip_loop, comparator_2_gt);
  and and_7 (and_7_out, comparator_2_lt, rising_edge_detector_async_2_out);
  rising_edge_detector rising_edge_detector_1 (.signal(adder_5_out[0]), .clear(clear), .sync(sync), .out(start));
  buf buffer_1 (inc_stage_counter, and_7_out);
  Register #(.width(4), .trigger("low")) register_7 (.D(address), .Q(register_7_q), .clk(1'b0));  // open: en, clr
  Register #(.width(4), .trigger("low")) register_8 (.D(address), .Q(register_8_q), .clk(1'b0));  // open: en, clr
  assign address = clear_wait_counter ? 4'b1101 : 4'bz;  // Controlled_Buffer controlled_buffer_11
  and and_8 (clear_wait_counter, register_7_q[0], register_7_q[1], ~register_7_q[2], ~register_7_q[3]);  // AND_Gate
  Pull_Resistor pull_resistor_7 (.node(clear_wait_counter));
  assign address = and_9_out ? 4'b0100 : 4'bz;  // Controlled_Buffer controlled_buffer_12
  and and_9 (and_9_out, register_8_q[0], ~register_8_q[1], register_8_q[2], register_8_q[3]);  // AND_Gate
  Pull_Resistor pull_resistor_8 (.node(and_9_out));
  Counter counter_1 (.Q(counter_1_q), .clk(inc_wait_counter), .clr(clear_wait_counter));  // open: load, D, count, carry
  Comparator comparator_3 (.a(counter_1_q), .b({8{1'b0}}), .eq(wait_counter));  // open: gt, lt
  rising_edge_detector_async rising_edge_detector_async_3 (
    .signal(load), .clear(buffer_11_out), .out(rising_edge_detector_async_3_out));
  Register #(.width(4), .trigger("low")) register_9 (.D(address), .Q(register_9_q), .clk(1'b0));  // open: en, clr
  Register #(.width(4), .trigger("low")) register_10 (.D(address), .Q(register_10_q), .clk(1'b0));  // open: en, clr
  not not_2 (not_2_out, rising_edge_detector_async_3_out);
  buf buffer_2 (buffer_2_out, buffer_4_out);
  buf buffer_3 (buffer_3_out, buffer_2_out);
  buf buffer_4 (buffer_4_out, buffer_7_out);
  buf buffer_5 (buffer_5_out, buffer_6_out);
  buf buffer_6 (buffer_6_out, buffer_15_out);
  buf buffer_7 (buffer_7_out, buffer_8_out);
  buf buffer_8 (buffer_8_out, buffer_5_out);
  buf buffer_9 (buffer_9_out, buffer_12_out);
  buf buffer_10 (buffer_10_out, buffer_9_out);
  buf buffer_11 (buffer_11_out, buffer_10_out);
  buf buffer_12 (buffer_12_out, buffer_17_out);
  not not_3 (not_3_out, rising_edge_detector_async_3_out);
  Pull_Resistor pull_resistor_9 (.node(pull_resistor_9_node));
  and and_10 (pull_resistor_9_node, ~register_9_q[0], ~register_9_q[1], register_9_q[2], ~register_9_q[3], wait_counter);  // AND_Gate
  assign address = pull_resistor_9_node ? 4'b0110 : 4'bz;  // Controlled_Buffer controlled_buffer_13
  assign address = inc_wait_counter ? 4'b1101 : 4'bz;  // Controlled_Buffer controlled_buffer_14
  and and_11 (inc_wait_counter, ~wait_counter, ~register_10_q[0], ~register_10_q[1], register_10_q[2], ~register_10_q[3]);  // AND_Gate
  Pull_Resistor pull_resistor_10 (.node(inc_wait_counter));
  buf buffer_13 (buffer_13_out, adder_6_out[0]);
  Subtractor #(.width(32)) subtractor_4 (.a(adder_6_out), .b({32{1'b0}}), .out(subtractor_4_out));  // open: bin, bout
  Adder #(.width(32)) adder_6 (.a({{31{1'b0}}, set_point}), .b({32{1'b0}}), .out(adder_6_out));  // open: cin, cout
  Adder #(.width(32)) adder_7 (.a(out_x_t), .b(32'h8000), .out(adder_7_out));  // open: cin, cout
  rising_edge_pulse rising_edge_pulse_1 (.signal(start), .out(rising_edge_pulse_1_out));
  Adder #(.width(32)) adder_8 (.a(out_y_t), .b(32'h8000), .out(adder_8_out));  // open: cin, cout
  Pull_Resistor #(.pull(1)) pull_resistor_11 (.node(not_2_out));
  and and_12 (and_12_out, ~not_2_out, ~buffer_3_out);  // AND_Gate
  buf buffer_14 (buffer_14_out, and_12_out);
  buf buffer_15 (buffer_15_out, buffer_14_out);
  buf buffer_16 (buffer_16_out, counter_2_carry);
  buf buffer_17 (buffer_17_out, buffer_16_out);
  Decoder #(.select(5), .enable("false")) decoder_1 (
    .out0(decoder_1_out31[31]), .out1(decoder_1_out31[30]), .out2(decoder_1_out31[29]),
    .out3(decoder_1_out31[28]), .out4(decoder_1_out31[27]), .out5(decoder_1_out31[26]),
    .out6(decoder_1_out31[25]), .out7(decoder_1_out31[24]), .out8(decoder_1_out31[23]),
    .out9(decoder_1_out31[22]), .out10(decoder_1_out31[21]), .out11(decoder_1_out31[20]),
    .out12(decoder_1_out31[19]), .out13(decoder_1_out31[18]), .out14(decoder_1_out31[17]),
    .out15(decoder_1_out31[16]), .out16(decoder_1_out31[15]), .out17(decoder_1_out31[14]),
    .out18(decoder_1_out31[13]), .out19(decoder_1_out31[12]), .out20(decoder_1_out31[11]),
    .out21(decoder_1_out31[10]), .out22(decoder_1_out31[9]), .out23(decoder_1_out31[8]),
    .out24(decoder_1_out31[7]), .out25(decoder_1_out31[6]), .out26(decoder_1_out31[5]),
    .out27(decoder_1_out31[4]), .out28(decoder_1_out31[3]), .out29(decoder_1_out31[2]),
    .out30(decoder_1_out31[1]), .out31(decoder_1_out31[0]), .sel(adder_7_out[20:16]));
  Pull_Resistor pull_resistor_12 (.node(buffer_13_out));
  assign controlled_buffer_15_out = not_4_out ? subtractor_4_out[0] : 1'bz;  // Controlled_Buffer controlled_buffer_15
  not not_4 (not_4_out, load);
  Counter #(.width(6), .max('h3f)) counter_2 (
    .Q(counter_2_q), .carry(counter_2_carry), .clk(and_12_out), .clr(not_3_out));  // open: load, D, count
  assign buffer_18_out = counter_2_q;  // Buffer buffer_18, 6 bits wide
  assign buffer_19_out = buffer_18_out;  // Buffer buffer_19, 6 bits wide
  assign buffer_20_out = buffer_19_out;  // Buffer buffer_20, 6 bits wide
  assign buffer_21_out = buffer_20_out;  // Buffer buffer_21, 6 bits wide
  assign buffer_22_out = buffer_21_out;  // Buffer buffer_22, 6 bits wide
  assign buffer_23_out = buffer_22_out;  // Buffer buffer_23, 6 bits wide
  assign buffer_24_out = buffer_23_out;  // Buffer buffer_24, 6 bits wide
  assign buffer_25_out = buffer_24_out;  // Buffer buffer_25, 6 bits wide
  assign buffer_26_out = buffer_25_out;  // Buffer buffer_26, 6 bits wide
  // Buffer buffer_27 has open pins: in=buffer_26_out, out=open
  Pull_Resistor pull_resistor_13 (.node(controlled_buffer_15_out));
  Multiplexer #(.width(6), .enable("false")) multiplexer_2 (
    .in0(adder_8_out[21:16]), .in1(counter_2_q), .out(multiplexer_2_out), .sel(load));
  Pull_Resistor pull_resistor_14 (.node(load));
  assign or_3_out = ram_1_data | decoder_1_out31;  // OR_Gate or_3, 32 bits wide
  buf buffer_28 (buffer_28_out, buffer_29_out);
  buf buffer_29 (buffer_29_out, subtractor_4_out[0]);
  Pull_Resistor pull_resistor_15 (.node(pull_resistor_15_node));
  not not_5 (pull_resistor_15_node, adder_7_out[21]);
  buf buffer_30 (pull_resistor_15_node, load);
  // Probe on stage
  RAM #(.addrWidth(6), .dataWidth(32), .bus("separate")) ram_1 (
    .addr(multiplexer_2_out), .din(or_3_out), .data(ram_1_data), .str(controlled_buffer_15_out),
    .sel(pull_resistor_15_node), .clk(buffer_28_out), .ld(buffer_13_out), .clr(rising_edge_pulse_1_out));
  buf buffer_31 (buffer_13_out, load);
  assign or_4_out = ram_2_data | decoder_1_out31;  // OR_Gate or_4, 32 bits wide
  Counter #(.width(2), .max('h3)) counter_3 (
    .Q(stage), .clk(inc_stage_counter), .clr(done_t));  // open: load, D, count, carry
  Pull_Resistor pull_resistor_16 (.node(inc_stage_counter));
  Register #(.width(4), .trigger("low")) register_11 (.D(address), .Q(register_11_q), .clk(1'b0));  // open: en, clr
  Register #(.width(4), .trigger("low")) register_12 (.D(address), .Q(register_12_q), .clk(1'b0));  // open: en, clr
  Register #(.width(4), .trigger("low")) register_13 (.D(address), .Q(register_13_q), .clk(1'b0));  // open: en, clr
  Register #(.width(4), .trigger("low")) register_14 (.D(address), .Q(register_14_q), .clk(1'b0));  // open: en, clr
  Register #(.width(4), .trigger("low")) register_15 (.D(address), .Q(register_15_q), .clk(1'b0));  // open: en, clr
  Register #(.width(4), .trigger("low")) register_16 (.D(address), .Q(register_16_q), .clk(1'b0));  // open: en, clr
  Register #(.width(4), .trigger("low")) register_17 (.D(address), .Q(register_17_q), .clk(1'b0));  // open: en, clr
  buf buffer_32 (buffer_32_out, buffer_33_out);
  buf buffer_33 (buffer_33_out, subtractor_4_out[0]);
  Pull_Resistor pull_resistor_17 (.node(pull_resistor_17_node));
  buf buffer_34 (pull_resistor_17_node, adder_7_out[21]);
  buf buffer_35 (pull_resistor_17_node, load);
  buf buffer_36 (buffer_13_out, load);
  Register #(.width(4), .trigger("low")) register_18 (.D(address), .Q(register_18_q), .clk(1'b0));  // open: en, clr
  RAM #(.addrWidth(6), .dataWidth(32), .bus("separate")) ram_2 (
    .addr(multiplexer_2_out), .din(or_4_out), .data(ram_2_data), .str(controlled_buffer_15_out),
    .sel(pull_resistor_17_node), .clk(buffer_32_out), .ld(buffer_13_out), .clr(rising_edge_pulse_1_out));
  and and_13 (reset, ~register_18_q[0], register_18_q[1], register_18_q[2], ~register_18_q[3]);  // AND_Gate
  assign address = and_14_out ? 4'b1111 : 4'bz;  // Controlled_Buffer controlled_buffer_16
  and and_14 (and_14_out, skip_loop, ~stage[0], stage[1], ~register_11_q[0], register_11_q[1], register_11_q[2], ~register_11_q[3]);  // AND_Gate
  Pull_Resistor pull_resistor_18 (.node(and_14_out));
  assign address = and_15_out ? 4'b0111 : 4'bz;  // Controlled_Buffer controlled_buffer_17
  and and_15 (and_15_out, skip_loop, stage[0], ~stage[1], ~register_12_q[0], register_12_q[1], register_12_q[2], ~register_12_q[3]);  // AND_Gate
  Pull_Resistor pull_resistor_19 (.node(and_15_out));
  assign address = and_16_out ? 4'b0111 : 4'bz;  // Controlled_Buffer controlled_buffer_18
  and and_16 (and_16_out, skip_loop, ~stage[0], ~stage[1], ~register_13_q[0], register_13_q[1], register_13_q[2], ~register_13_q[3]);  // AND_Gate
  Pull_Resistor pull_resistor_20 (.node(and_16_out));
  assign address = and_17_out ? 4'b1111 : 4'bz;  // Controlled_Buffer controlled_buffer_19
  and and_17 (and_17_out, ~skip_loop, stage[0], stage[1], ~register_14_q[0], register_14_q[1], register_14_q[2], ~register_14_q[3]);  // AND_Gate
  Pull_Resistor pull_resistor_21 (.node(and_17_out));
  assign address = and_18_out ? 4'b0111 : 4'bz;  // Controlled_Buffer controlled_buffer_20
  and and_18 (and_18_out, ~skip_loop, ~stage[0], stage[1], ~register_15_q[0], register_15_q[1], register_15_q[2], ~register_15_q[3]);  // AND_Gate
  Pull_Resistor pull_resistor_22 (.node(and_18_out));
  assign address = and_19_out ? 4'b1010 : 4'bz;  // Controlled_Buffer controlled_buffer_21
  and and_19 (and_19_out, ~skip_loop, stage[0], ~stage[1], ~register_16_q[0], register_16_q[1], register_16_q[2], ~register_16_q[3]);  // AND_Gate
  Pull_Resistor pull_resistor_23 (.node(and_19_out));
  assign address = and_20_out ? 4'b0111 : 4'bz;  // Controlled_Buffer controlled_buffer_22
  and and_20 (and_20_out, ~skip_loop, ~stage[0], ~stage[1], ~register_17_q[0], register_17_q[1], register_17_q[2], ~register_17_q[3]);  // AND_Gate
  Pull_Resistor pull_resistor_24 (.node(and_20_out));
  Register #(.width(4), .trigger("low")) register_19 (.D(address), .Q(register_19_q), .clk(1'b0));  // open: en, clr
  Register #(.width(4), .trigger("low")) register_20 (.D(address), .Q(register_20_q), .clk(1'b0));  // open: en, clr
  Register #(.width(4), .trigger("low")) register_21 (.D(address), .Q(register_21_q), .clk(1'b0));  // open: en, clr
  Register #(.width(4), .trigger("low")) register_22 (.D(address), .Q(register_22_q), .clk(1'b0));  // open: en, clr
  Register #(.width(4), .trigger("low")) register_23 (.D(address), .Q(register_23_q), .clk(1'b0));  // open: en, clr
  Register #(.width(4), .trigger("low")) register_24 (.D(address), .Q(register_24_q), .clk(1'b0));  // open: en, clr
  and and_21 (and_21_out, register_19_q[0], register_19_q[1], register_19_q[2], ~register_19_q[3]);  // AND_Gate
  Pull_Resistor pull_resistor_25 (.node(and_21_out));
  buf buffer_37 (inc_stage_counter, and_21_out);
  assign address = and_22_out ? 4'b1100 : 4'bz;  // Controlled_Buffer controlled_buffer_23
  and and_22 (and_22_out, skip_loop, stage[0], ~stage[1], register_20_q[0], register_20_q[1], register_20_q[2], ~register_20_q[3]);  // AND_Gate
  Pull_Resistor pull_resistor_26 (.node(and_22_out));
  assign address = and_23_out ? 4'b1011 : 4'bz;  // Controlled_Buffer controlled_buffer_24
  and and_23 (and_23_out, skip_loop, ~stage[0], ~stage[1], register_21_q[0], register_21_q[1], register_21_q[2], ~register_21_q[3]);  // AND_Gate
  Pull_Resistor pull_resistor_27 (.node(and_23_out));
  assign address = and_24_out ? 4'b1100 : 4'bz;  // Controlled_Buffer controlled_buffer_25
  and and_24 (and_24_out, ~skip_loop, ~stage[0], stage[1], register_22_q[0], register_22_q[1], register_22_q[2], ~register_22_q[3]);  // AND_Gate
  Pull_Resistor pull_resistor_28 (.node(and_24_out));
  assign address = and_25_out ? 4'b1011 : 4'bz;  // Controlled_Buffer controlled_buffer_26
  and and_25 (and_25_out, ~skip_loop, stage[0], ~stage[1], register_23_q[0], register_23_q[1], register_23_q[2], ~register_23_q[3]);  // AND_Gate
  Pull_Resistor pull_resistor_29 (.node(and_25_out));
  assign address = and_26_out ? 4'b1000 : 4'bz;  // Controlled_Buffer controlled_buffer_27
  and and_26 (and_26_out, ~skip_loop, ~stage[0], ~stage[1], register_24_q[0], register_24_q[1], register_24_q[2], ~register_24_q[3]);  // AND_Gate
  Pull_Resistor pull_resistor_30 (.node(and_26_out));
  Register #(.width(4), .trigger("low")) register_25 (.D(address), .Q(register_25_q), .clk(1'b0));  // open: en, clr
  assign address = inc_stored_values ? 4'b0010 : 4'bz;  // Controlled_Buffer controlled_buffer_28
  and and_27 (inc_stored_values, ~register_25_q[0], ~register_25_q[1], ~register_25_q[2], register_25_q[3]);  // AND_Gate
  Pull_Resistor pull_resistor_31 (.node(inc_stored_values));
  Counter counter_4 (.Q(counter_4_q), .clk(inc_loop_counter), .clr(clear));  // open: load, D, count, carry
  Counter counter_5 (.Q(counter_5_q), .clk(inc_loop_counter), .clr(or_5_out));  // open: load, D, count, carry
  or or_5 (or_5_out, and_28_out, clear);
  Comparator comparator_4 (.a(counter_4_q), .b(loop_count[23:16]), .lt(comparator_4_lt));  // open: gt, eq
  not not_6 (loop_counter, comparator_4_lt);
  Comparator comparator_5 (.a(counter_5_q), .b(8'ha), .lt(comparator_5_lt));  // open: gt, eq
  not not_7 (loop_stopper_counter, comparator_5_lt);
  and and_28 (and_28_out, loop_stopper_counter, sync);
  Register #(.width(4), .trigger("low")) register_26 (.D(address), .Q(register_26_q), .clk(1'b0));  // open: en, clr
  Register #(.width(4), .trigger("low")) register_27 (.D(address), .Q(register_27_q), .clk(1'b0));  // open: en, clr
  Register #(.width(4), .trigger("low")) register_28 (.D(address), .Q(register_28_q), .clk(1'b0));  // open: en, clr
  Register #(.width(4), .trigger("low")) register_29 (.D(address), .Q(register_29_q), .clk(1'b0));  // open: en, clr
  assign address = and_29_out ? 4'b1010 : 4'bz;  // Controlled_Buffer controlled_buffer_29
  and and_29 (and_29_out, loop_counter, loop_stopper_counter, ~register_26_q[0], register_26_q[1], ~register_26_q[2], register_26_q[3]);  // AND_Gate
  Pull_Resistor pull_resistor_32 (.node(and_29_out));
  assign address = and_30_out ? 4'b1010 : 4'bz;  // Controlled_Buffer controlled_buffer_30
  and and_30 (and_30_out, ~loop_counter, loop_stopper_counter, ~register_27_q[0], register_27_q[1], ~register_27_q[2], register_27_q[3]);  // AND_Gate
  Pull_Resistor pull_resistor_33 (.node(and_30_out));
  assign address = and_31_out ? 4'b0111 : 4'bz;  // Controlled_Buffer controlled_buffer_31
  and and_31 (and_31_out, loop_counter, ~loop_stopper_counter, ~register_28_q[0], register_28_q[1], ~register_28_q[2], register_28_q[3]);  // AND_Gate
  Pull_Resistor pull_resistor_34 (.node(and_31_out));
  assign address = inc_loop_counter ? 4'b1000 : 4'bz;  // Controlled_Buffer controlled_buffer_32
  and and_32 (inc_loop_counter, ~loop_counter, ~loop_stopper_counter, ~register_29_q[0], register_29_q[1], ~register_29_q[2], register_29_q[3]);  // AND_Gate
  Pull_Resistor pull_resistor_35 (.node(inc_loop_counter));
  Register #(.width(4), .trigger("low")) register_30 (.D(address), .Q(register_30_q), .clk(1'b0));  // open: en, clr
  and and_33 (load_x2y2, register_30_q[0], register_30_q[1], ~register_30_q[2], register_30_q[3]);  // AND_Gate
  Pull_Resistor pull_resistor_36 (.node(load_x2y2));
  assign address = load_x2y2 ? 4'b0010 : 4'bz;  // Controlled_Buffer controlled_buffer_33
  Register #(.width(4), .trigger("low")) register_31 (.D(address), .Q(register_31_q), .clk(1'b0));  // open: en, clr
  assign address = clear ? 4'b0011 : 4'bz;  // Controlled_Buffer controlled_buffer_34
  and and_34 (clear, ~register_31_q[0], ~register_31_q[1], register_31_q[2], register_31_q[3]);  // AND_Gate
  Pull_Resistor pull_resistor_37 (.node(clear));
  Register #(.width(4), .trigger("low")) register_32 (.D(address), .Q(register_32_q), .clk(1'b0));  // open: en, clr
  and and_35 (done_t, register_32_q[0], register_32_q[1], register_32_q[2], register_32_q[3]);
  assign address = done_t ? 4'b0000 : 4'bz;  // Controlled_Buffer controlled_buffer_35
  Pull_Resistor pull_resistor_38 (.node(done_t));

  // Other names for the same wires on the sheet: clk = sync

  // Notes on the sheet:
  //   done: pull=up
  //   set_point: pull=up
  //   Config
  //   In
  //   halt
  //   Mission decoder
  //   load x1y1
  //   Math
  //   Out
  //   Out reg
  //   set
  //   buffer_1 drives only 1 and floats otherwise
  //   clear wait counter
  //   (wait buff)
  //   wait
  //   not_2 drives only 0 and floats otherwise
  //   buffer_13 drives only 1 and floats otherwise
  //   Main logic 
  //   not_5 drives only 1 and floats otherwise
  //   buffer_30 drives only 1 and floats otherwise
  //   buffer_31 drives only 1 and floats otherwise
  //   buffer_34 drives only 1 and floats otherwise
  //   buffer_35 drives only 1 and floats otherwise
  //   buffer_36 drives only 1 and floats otherwise
  //   reset
  //   stage
  //   buffer_37 drives only 1 and floats otherwise
  //   inc
  //   loop
  //   load x2y2
  //   clear
  //   done
  //   kek
endmodule

module _64x64_display_controller_new (
  output [31:0] out_1,
  output [31:0] out_2,
  output [31:0] out_3,
  output [31:0] out_4,
  output [31:0] out_5,
  output [31:0] out_6,
  output [31:0] out_7,
  output [31:0] out_8,
  output [31:0] out_9,
  output [31:0] out_10,
  output [31:0] out_11,
  output [31:0] out_12,
  output [31:0] out_13,
  output [31:0] out_14,
  output [31:0] out_15,
  output [31:0] out_16,
  output [31:0] out_17,
  output [31:0] out_18,
  output [31:0] out_19,
  output [31:0] out_20,
  output [31:0] out_21,
  output [31:0] out_22,
  output [31:0] out_23,
  output [31:0] out_24,
  output [31:0] out_25,
  output [31:0] out_26,
  output [31:0] out_27,
  output [31:0] out_28,
  output [31:0] out_29,
  output [31:0] out_30,
  output [31:0] out_31,
  output [31:0] out_32,
  output [31:0] out_33,
  output [31:0] out_34,
  output [31:0] out_35,
  output [31:0] out_36,
  output [31:0] out_37,
  output [31:0] out_38,
  output [31:0] out_39,
  output [31:0] out_40,
  output [31:0] out_41,
  output [31:0] out_42,
  output [31:0] out_43,
  output [31:0] out_44,
  output [31:0] out_45,
  output [31:0] out_46,
  output [31:0] out_47,
  output [31:0] out_48,
  output [31:0] out_49,
  output [31:0] out_50,
  output [31:0] out_51,
  output [31:0] out_52,
  output [31:0] out_53,
  output [31:0] out_54,
  output [31:0] out_55,
  output [31:0] out_56,
  output [31:0] out_57,
  output [31:0] out_58,
  output [31:0] out_59,
  output [31:0] out_60,
  output [31:0] out_61,
  output [31:0] out_62,
  output [31:0] out_63,
  output [31:0] out_64,
  output [31:0] out_65,
  output [31:0] out_66,
  output [31:0] out_67,
  output [31:0] out_68,
  output [31:0] out_69,
  output [31:0] out_70,
  output [31:0] out_71,
  output [31:0] out_72,
  output [31:0] out_73,
  output [31:0] out_74,
  output [31:0] out_75,
  output [31:0] out_76,
  output [31:0] out_77,
  output [31:0] out_78,
  output [31:0] out_79,
  output [31:0] out_80,
  output [31:0] out_81,
  output [31:0] out_82,
  output [31:0] out_83,
  output [31:0] out_84,
  output [31:0] out_85,
  output [31:0] out_86,
  output [31:0] out_87,
  output [31:0] out_88,
  output [31:0] out_89,
  output [31:0] out_90,
  output [31:0] out_91,
  output [31:0] out_92,
  output [31:0] out_93,
  output [31:0] out_94,
  output [31:0] out_95,
  output [31:0] out_96,
  output [31:0] out_97,
  output [31:0] out_98,
  output [31:0] out_99,
  output [31:0] out_100,
  output [31:0] out_101,
  output [31:0] out_102,
  output [31:0] out_103,
  output [31:0] out_104,
  output [31:0] out_105,
  output [31:0] out_106,
  output [31:0] out_107,
  output [31:0] out_108,
  output [31:0] out_109,
  output [31:0] out_110,
  output [31:0] out_111,
  output [31:0] out_112,
  output [31:0] out_113,
  output [31:0] out_114,
  output [31:0] out_115,
  output [31:0] out_116,
  output [31:0] out_117,
  output [31:0] out_118,
  output [31:0] out_119,
  output [31:0] out_120,
  output [31:0] out_121,
  output [31:0] out_122,
  output [31:0] out_123,
  output [31:0] out_124,
  output [31:0] out_125,
  output [31:0] out_126,
  output [31:0] out_127,
  output [31:0] out_128
);

  wire and_1_out, and_2_out, and_3_out, and_4_out, undriven_4;
  wire [5:0] undriven_3;
  wire [31:0] demultiplexer_1_out0, demultiplexer_1_out1, demultiplexer_1_out2, demultiplexer_1_out3,
       demultiplexer_1_out4, demultiplexer_1_out5, demultiplexer_1_out6, demultiplexer_1_out7,
       demultiplexer_1_out8, demultiplexer_1_out9, demultiplexer_1_out10, demultiplexer_1_out11,
       demultiplexer_1_out12, demultiplexer_1_out13, demultiplexer_1_out14, demultiplexer_1_out15,
       demultiplexer_1_out16, demultiplexer_1_out17, demultiplexer_1_out18, demultiplexer_1_out19,
       demultiplexer_1_out20, demultiplexer_1_out21, demultiplexer_1_out22, demultiplexer_1_out23,
       demultiplexer_1_out24, demultiplexer_1_out25, demultiplexer_1_out26, demultiplexer_1_out27,
       demultiplexer_1_out28, demultiplexer_1_out29, demultiplexer_1_out30, demultiplexer_1_out31,
       demultiplexer_2_out0, demultiplexer_2_out1, demultiplexer_2_out2, demultiplexer_2_out3,
       demultiplexer_2_out4, demultiplexer_2_out5, demultiplexer_2_out6, demultiplexer_2_out7,
       demultiplexer_2_out8, demultiplexer_2_out9, demultiplexer_2_out10, demultiplexer_2_out11,
       demultiplexer_2_out12, demultiplexer_2_out13, demultiplexer_2_out14, demultiplexer_2_out15,
       demultiplexer_2_out16, demultiplexer_2_out17, demultiplexer_2_out18, demultiplexer_2_out19,
       demultiplexer_2_out20, demultiplexer_2_out21, demultiplexer_2_out22, demultiplexer_2_out23,
       demultiplexer_2_out24, demultiplexer_2_out25, demultiplexer_2_out26, demultiplexer_2_out27,
       demultiplexer_2_out28, demultiplexer_2_out29, demultiplexer_2_out30, demultiplexer_2_out31,
       demultiplexer_3_out0, demultiplexer_3_out1, demultiplexer_3_out2, demultiplexer_3_out3,
       demultiplexer_3_out4, demultiplexer_3_out5, demultiplexer_3_out6, demultiplexer_3_out7,
       demultiplexer_3_out8, demultiplexer_3_out9, demultiplexer_3_out10, demultiplexer_3_out11,
       demultiplexer_3_out12, demultiplexer_3_out13, demultiplexer_3_out14, demultiplexer_3_out15,
       demultiplexer_3_out16, demultiplexer_3_out17, demultiplexer_3_out18, demultiplexer_3_out19,
       demultiplexer_3_out20, demultiplexer_3_out21, demultiplexer_3_out22, demultiplexer_3_out23,
       demultiplexer_3_out24, demultiplexer_3_out25, demultiplexer_3_out26, demultiplexer_3_out27,
       demultiplexer_3_out28, demultiplexer_3_out29, demultiplexer_3_out30, demultiplexer_3_out31,
       demultiplexer_4_out0, demultiplexer_4_out1, demultiplexer_4_out2, demultiplexer_4_out3,
       demultiplexer_4_out4, demultiplexer_4_out5, demultiplexer_4_out6, demultiplexer_4_out7,
       demultiplexer_4_out8, demultiplexer_4_out9, demultiplexer_4_out10, demultiplexer_4_out11,
       demultiplexer_4_out12, demultiplexer_4_out13, demultiplexer_4_out14, demultiplexer_4_out15,
       demultiplexer_4_out16, demultiplexer_4_out17, demultiplexer_4_out18, demultiplexer_4_out19,
       demultiplexer_4_out20, demultiplexer_4_out21, demultiplexer_4_out22, demultiplexer_4_out23,
       demultiplexer_4_out24, demultiplexer_4_out25, demultiplexer_4_out26, demultiplexer_4_out27,
       demultiplexer_4_out28, demultiplexer_4_out29, demultiplexer_4_out30, demultiplexer_4_out31, undriven,
       undriven_2;

  Demultiplexer #(.select(5), .width(32), .tristate("true")) demultiplexer_1 (
    .out0(demultiplexer_1_out0), .out1(demultiplexer_1_out1), .out2(demultiplexer_1_out2),
    .out3(demultiplexer_1_out3), .out4(demultiplexer_1_out4), .out5(demultiplexer_1_out5),
    .out6(demultiplexer_1_out6), .out7(demultiplexer_1_out7), .out8(demultiplexer_1_out8),
    .out9(demultiplexer_1_out9), .out10(demultiplexer_1_out10), .out11(demultiplexer_1_out11),
    .out12(demultiplexer_1_out12), .out13(demultiplexer_1_out13), .out14(demultiplexer_1_out14),
    .out15(demultiplexer_1_out15), .out16(demultiplexer_1_out16), .out17(demultiplexer_1_out17),
    .out18(demultiplexer_1_out18), .out19(demultiplexer_1_out19), .out20(demultiplexer_1_out20),
    .out21(demultiplexer_1_out21), .out22(demultiplexer_1_out22), .out23(demultiplexer_1_out23),
    .out24(demultiplexer_1_out24), .out25(demultiplexer_1_out25), .out26(demultiplexer_1_out26),
    .out27(demultiplexer_1_out27), .out28(demultiplexer_1_out28), .out29(demultiplexer_1_out29),
    .out30(demultiplexer_1_out30), .out31(demultiplexer_1_out31), .in(undriven), .sel(undriven_3[4:0]),
    .en(and_1_out));
  and and_1 (and_1_out, undriven_4, undriven_3[5]);
  Demultiplexer #(.select(5), .width(32), .tristate("true")) demultiplexer_2 (
    .out0(demultiplexer_2_out0), .out1(demultiplexer_2_out1), .out2(demultiplexer_2_out2),
    .out3(demultiplexer_2_out3), .out4(demultiplexer_2_out4), .out5(demultiplexer_2_out5),
    .out6(demultiplexer_2_out6), .out7(demultiplexer_2_out7), .out8(demultiplexer_2_out8),
    .out9(demultiplexer_2_out9), .out10(demultiplexer_2_out10), .out11(demultiplexer_2_out11),
    .out12(demultiplexer_2_out12), .out13(demultiplexer_2_out13), .out14(demultiplexer_2_out14),
    .out15(demultiplexer_2_out15), .out16(demultiplexer_2_out16), .out17(demultiplexer_2_out17),
    .out18(demultiplexer_2_out18), .out19(demultiplexer_2_out19), .out20(demultiplexer_2_out20),
    .out21(demultiplexer_2_out21), .out22(demultiplexer_2_out22), .out23(demultiplexer_2_out23),
    .out24(demultiplexer_2_out24), .out25(demultiplexer_2_out25), .out26(demultiplexer_2_out26),
    .out27(demultiplexer_2_out27), .out28(demultiplexer_2_out28), .out29(demultiplexer_2_out29),
    .out30(demultiplexer_2_out30), .out31(demultiplexer_2_out31), .in(undriven_2), .sel(undriven_3[4:0]),
    .en(and_2_out));
  and and_2 (and_2_out, undriven_4, undriven_3[5]);
  Demultiplexer #(.select(5), .width(32), .tristate("true")) demultiplexer_3 (
    .out0(demultiplexer_3_out0), .out1(demultiplexer_3_out1), .out2(demultiplexer_3_out2),
    .out3(demultiplexer_3_out3), .out4(demultiplexer_3_out4), .out5(demultiplexer_3_out5),
    .out6(demultiplexer_3_out6), .out7(demultiplexer_3_out7), .out8(demultiplexer_3_out8),
    .out9(demultiplexer_3_out9), .out10(demultiplexer_3_out10), .out11(demultiplexer_3_out11),
    .out12(demultiplexer_3_out12), .out13(demultiplexer_3_out13), .out14(demultiplexer_3_out14),
    .out15(demultiplexer_3_out15), .out16(demultiplexer_3_out16), .out17(demultiplexer_3_out17),
    .out18(demultiplexer_3_out18), .out19(demultiplexer_3_out19), .out20(demultiplexer_3_out20),
    .out21(demultiplexer_3_out21), .out22(demultiplexer_3_out22), .out23(demultiplexer_3_out23),
    .out24(demultiplexer_3_out24), .out25(demultiplexer_3_out25), .out26(demultiplexer_3_out26),
    .out27(demultiplexer_3_out27), .out28(demultiplexer_3_out28), .out29(demultiplexer_3_out29),
    .out30(demultiplexer_3_out30), .out31(demultiplexer_3_out31), .in(undriven_2), .sel(undriven_3[4:0]),
    .en(and_3_out));
  and and_3 (and_3_out, undriven_4, ~undriven_3[5]);  // AND_Gate
  Demultiplexer #(.select(5), .width(32), .tristate("true")) demultiplexer_4 (
    .out0(demultiplexer_4_out0), .out1(demultiplexer_4_out1), .out2(demultiplexer_4_out2),
    .out3(demultiplexer_4_out3), .out4(demultiplexer_4_out4), .out5(demultiplexer_4_out5),
    .out6(demultiplexer_4_out6), .out7(demultiplexer_4_out7), .out8(demultiplexer_4_out8),
    .out9(demultiplexer_4_out9), .out10(demultiplexer_4_out10), .out11(demultiplexer_4_out11),
    .out12(demultiplexer_4_out12), .out13(demultiplexer_4_out13), .out14(demultiplexer_4_out14),
    .out15(demultiplexer_4_out15), .out16(demultiplexer_4_out16), .out17(demultiplexer_4_out17),
    .out18(demultiplexer_4_out18), .out19(demultiplexer_4_out19), .out20(demultiplexer_4_out20),
    .out21(demultiplexer_4_out21), .out22(demultiplexer_4_out22), .out23(demultiplexer_4_out23),
    .out24(demultiplexer_4_out24), .out25(demultiplexer_4_out25), .out26(demultiplexer_4_out26),
    .out27(demultiplexer_4_out27), .out28(demultiplexer_4_out28), .out29(demultiplexer_4_out29),
    .out30(demultiplexer_4_out30), .out31(demultiplexer_4_out31), .in(undriven), .sel(undriven_3[4:0]),
    .en(and_4_out));
  and and_4 (and_4_out, undriven_4, ~undriven_3[5]);  // AND_Gate
  Register #(.width(32), .trigger("high")) register_1 (
    .D(demultiplexer_1_out0), .Q(out_1), .clk(and_1_out));  // open: en, clr
  Register #(.width(32), .trigger("high")) register_2 (
    .D(demultiplexer_2_out0), .Q(out_33), .clk(and_2_out));  // open: en, clr
  Register #(.width(32), .trigger("high")) register_3 (
    .D(demultiplexer_3_out0), .Q(out_65), .clk(and_3_out));  // open: en, clr
  Register #(.width(32), .trigger("high")) register_4 (
    .D(demultiplexer_4_out0), .Q(out_97), .clk(and_4_out));  // open: en, clr
  Register #(.width(32), .trigger("high")) register_5 (
    .D(demultiplexer_1_out1), .Q(out_2), .clk(and_1_out));  // open: en, clr
  Register #(.width(32), .trigger("high")) register_6 (
    .D(demultiplexer_2_out1), .Q(out_34), .clk(and_2_out));  // open: en, clr
  Register #(.width(32), .trigger("high")) register_7 (
    .D(demultiplexer_3_out1), .Q(out_66), .clk(and_3_out));  // open: en, clr
  Register #(.width(32), .trigger("high")) register_8 (
    .D(demultiplexer_4_out1), .Q(out_98), .clk(and_4_out));  // open: en, clr
  Register #(.width(32), .trigger("high")) register_9 (
    .D(demultiplexer_1_out2), .Q(out_3), .clk(and_1_out));  // open: en, clr
  Register #(.width(32), .trigger("high")) register_10 (
    .D(demultiplexer_2_out2), .Q(out_35), .clk(and_2_out));  // open: en, clr
  Register #(.width(32), .trigger("high")) register_11 (
    .D(demultiplexer_3_out2), .Q(out_67), .clk(and_3_out));  // open: en, clr
  Register #(.width(32), .trigger("high")) register_12 (
    .D(demultiplexer_4_out2), .Q(out_99), .clk(and_4_out));  // open: en, clr
  Register #(.width(32), .trigger("high")) register_13 (
    .D(demultiplexer_1_out3), .Q(out_4), .clk(and_1_out));  // open: en, clr
  Register #(.width(32), .trigger("high")) register_14 (
    .D(demultiplexer_2_out3), .Q(out_36), .clk(and_2_out));  // open: en, clr
  Register #(.width(32), .trigger("high")) register_15 (
    .D(demultiplexer_3_out3), .Q(out_68), .clk(and_3_out));  // open: en, clr
  Register #(.width(32), .trigger("high")) register_16 (
    .D(demultiplexer_4_out3), .Q(out_100), .clk(and_4_out));  // open: en, clr
  Register #(.width(32), .trigger("high")) register_17 (
    .D(demultiplexer_1_out4), .Q(out_5), .clk(and_1_out));  // open: en, clr
  Register #(.width(32), .trigger("high")) register_18 (
    .D(demultiplexer_2_out4), .Q(out_37), .clk(and_2_out));  // open: en, clr
  Register #(.width(32), .trigger("high")) register_19 (
    .D(demultiplexer_3_out4), .Q(out_69), .clk(and_3_out));  // open: en, clr
  Register #(.width(32), .trigger("high")) register_20 (
    .D(demultiplexer_4_out4), .Q(out_101), .clk(and_4_out));  // open: en, clr
  Register #(.width(32), .trigger("high")) register_21 (
    .D(demultiplexer_1_out5), .Q(out_6), .clk(and_1_out));  // open: en, clr
  Register #(.width(32), .trigger("high")) register_22 (
    .D(demultiplexer_2_out5), .Q(out_38), .clk(and_2_out));  // open: en, clr
  Register #(.width(32), .trigger("high")) register_23 (
    .D(demultiplexer_3_out5), .Q(out_70), .clk(and_3_out));  // open: en, clr
  Register #(.width(32), .trigger("high")) register_24 (
    .D(demultiplexer_4_out5), .Q(out_102), .clk(and_4_out));  // open: en, clr
  Register #(.width(32), .trigger("high")) register_25 (
    .D(demultiplexer_1_out6), .Q(out_7), .clk(and_1_out));  // open: en, clr
  Register #(.width(32), .trigger("high")) register_26 (
    .D(demultiplexer_2_out6), .Q(out_39), .clk(and_2_out));  // open: en, clr
  Register #(.width(32), .trigger("high")) register_27 (
    .D(demultiplexer_3_out6), .Q(out_71), .clk(and_3_out));  // open: en, clr
  Register #(.width(32), .trigger("high")) register_28 (
    .D(demultiplexer_4_out6), .Q(out_103), .clk(and_4_out));  // open: en, clr
  Register #(.width(32), .trigger("high")) register_29 (
    .D(demultiplexer_1_out7), .Q(out_8), .clk(and_1_out));  // open: en, clr
  Register #(.width(32), .trigger("high")) register_30 (
    .D(demultiplexer_2_out7), .Q(out_40), .clk(and_2_out));  // open: en, clr
  Register #(.width(32), .trigger("high")) register_31 (
    .D(demultiplexer_3_out7), .Q(out_72), .clk(and_3_out));  // open: en, clr
  Register #(.width(32), .trigger("high")) register_32 (
    .D(demultiplexer_4_out7), .Q(out_104), .clk(and_4_out));  // open: en, clr
  Register #(.width(32), .trigger("high")) register_33 (
    .D(demultiplexer_1_out8), .Q(out_9), .clk(and_1_out));  // open: en, clr
  Register #(.width(32), .trigger("high")) register_34 (
    .D(demultiplexer_2_out8), .Q(out_41), .clk(and_2_out));  // open: en, clr
  Register #(.width(32), .trigger("high")) register_35 (
    .D(demultiplexer_3_out8), .Q(out_73), .clk(and_3_out));  // open: en, clr
  Register #(.width(32), .trigger("high")) register_36 (
    .D(demultiplexer_4_out8), .Q(out_105), .clk(and_4_out));  // open: en, clr
  Register #(.width(32), .trigger("high")) register_37 (
    .D(demultiplexer_1_out9), .Q(out_10), .clk(and_1_out));  // open: en, clr
  Register #(.width(32), .trigger("high")) register_38 (
    .D(demultiplexer_2_out9), .Q(out_42), .clk(and_2_out));  // open: en, clr
  Register #(.width(32), .trigger("high")) register_39 (
    .D(demultiplexer_3_out9), .Q(out_74), .clk(and_3_out));  // open: en, clr
  Register #(.width(32), .trigger("high")) register_40 (
    .D(demultiplexer_4_out9), .Q(out_106), .clk(and_4_out));  // open: en, clr
  Register #(.width(32), .trigger("high")) register_41 (
    .D(demultiplexer_1_out10), .Q(out_11), .clk(and_1_out));  // open: en, clr
  Register #(.width(32), .trigger("high")) register_42 (
    .D(demultiplexer_2_out10), .Q(out_43), .clk(and_2_out));  // open: en, clr
  Register #(.width(32), .trigger("high")) register_43 (
    .D(demultiplexer_3_out10), .Q(out_75), .clk(and_3_out));  // open: en, clr
  Register #(.width(32), .trigger("high")) register_44 (
    .D(demultiplexer_4_out10), .Q(out_107), .clk(and_4_out));  // open: en, clr
  Register #(.width(32), .trigger("high")) register_45 (
    .D(demultiplexer_1_out11), .Q(out_12), .clk(and_1_out));  // open: en, clr
  Register #(.width(32), .trigger("high")) register_46 (
    .D(demultiplexer_2_out11), .Q(out_44), .clk(and_2_out));  // open: en, clr
  Register #(.width(32), .trigger("high")) register_47 (
    .D(demultiplexer_3_out11), .Q(out_76), .clk(and_3_out));  // open: en, clr
  Register #(.width(32), .trigger("high")) register_48 (
    .D(demultiplexer_4_out11), .Q(out_108), .clk(and_4_out));  // open: en, clr
  Register #(.width(32), .trigger("high")) register_49 (
    .D(demultiplexer_1_out12), .Q(out_13), .clk(and_1_out));  // open: en, clr
  Register #(.width(32), .trigger("high")) register_50 (
    .D(demultiplexer_2_out12), .Q(out_45), .clk(and_2_out));  // open: en, clr
  Register #(.width(32), .trigger("high")) register_51 (
    .D(demultiplexer_3_out12), .Q(out_77), .clk(and_3_out));  // open: en, clr
  Register #(.width(32), .trigger("high")) register_52 (
    .D(demultiplexer_4_out12), .Q(out_109), .clk(and_4_out));  // open: en, clr
  Register #(.width(32), .trigger("high")) register_53 (
    .D(demultiplexer_1_out13), .Q(out_14), .clk(and_1_out));  // open: en, clr
  Register #(.width(32), .trigger("high")) register_54 (
    .D(demultiplexer_2_out13), .Q(out_46), .clk(and_2_out));  // open: en, clr
  Register #(.width(32), .trigger("high")) register_55 (
    .D(demultiplexer_3_out13), .Q(out_78), .clk(and_3_out));  // open: en, clr
  Register #(.width(32), .trigger("high")) register_56 (
    .D(demultiplexer_4_out13), .Q(out_110), .clk(and_4_out));  // open: en, clr
  Register #(.width(32), .trigger("high")) register_57 (
    .D(demultiplexer_1_out14), .Q(out_15), .clk(and_1_out));  // open: en, clr
  Register #(.width(32), .trigger("high")) register_58 (
    .D(demultiplexer_2_out14), .Q(out_47), .clk(and_2_out));  // open: en, clr
  Register #(.width(32), .trigger("high")) register_59 (
    .D(demultiplexer_3_out14), .Q(out_79), .clk(and_3_out));  // open: en, clr
  Register #(.width(32), .trigger("high")) register_60 (
    .D(demultiplexer_4_out14), .Q(out_111), .clk(and_4_out));  // open: en, clr
  Register #(.width(32), .trigger("high")) register_61 (
    .D(demultiplexer_1_out15), .Q(out_16), .clk(and_1_out));  // open: en, clr
  Register #(.width(32), .trigger("high")) register_62 (
    .D(demultiplexer_2_out15), .Q(out_48), .clk(and_2_out));  // open: en, clr
  Register #(.width(32), .trigger("high")) register_63 (
    .D(demultiplexer_3_out15), .Q(out_80), .clk(and_3_out));  // open: en, clr
  Register #(.width(32), .trigger("high")) register_64 (
    .D(demultiplexer_4_out15), .Q(out_112), .clk(and_4_out));  // open: en, clr
  Register #(.width(32), .trigger("high")) register_65 (
    .D(demultiplexer_1_out16), .Q(out_17), .clk(and_1_out));  // open: en, clr
  Register #(.width(32), .trigger("high")) register_66 (
    .D(demultiplexer_2_out16), .Q(out_49), .clk(and_2_out));  // open: en, clr
  Register #(.width(32), .trigger("high")) register_67 (
    .D(demultiplexer_3_out16), .Q(out_81), .clk(and_3_out));  // open: en, clr
  Register #(.width(32), .trigger("high")) register_68 (
    .D(demultiplexer_4_out16), .Q(out_113), .clk(and_4_out));  // open: en, clr
  Register #(.width(32), .trigger("high")) register_69 (
    .D(demultiplexer_1_out17), .Q(out_18), .clk(and_1_out));  // open: en, clr
  Register #(.width(32), .trigger("high")) register_70 (
    .D(demultiplexer_2_out17), .Q(out_50), .clk(and_2_out));  // open: en, clr
  Register #(.width(32), .trigger("high")) register_71 (
    .D(demultiplexer_3_out17), .Q(out_82), .clk(and_3_out));  // open: en, clr
  Register #(.width(32), .trigger("high")) register_72 (
    .D(demultiplexer_4_out17), .Q(out_114), .clk(and_4_out));  // open: en, clr
  Register #(.width(32), .trigger("high")) register_73 (
    .D(demultiplexer_1_out18), .Q(out_19), .clk(and_1_out));  // open: en, clr
  Register #(.width(32), .trigger("high")) register_74 (
    .D(demultiplexer_2_out18), .Q(out_51), .clk(and_2_out));  // open: en, clr
  Register #(.width(32), .trigger("high")) register_75 (
    .D(demultiplexer_3_out18), .Q(out_83), .clk(and_3_out));  // open: en, clr
  Register #(.width(32), .trigger("high")) register_76 (
    .D(demultiplexer_4_out18), .Q(out_115), .clk(and_4_out));  // open: en, clr
  Register #(.width(32), .trigger("high")) register_77 (
    .D(demultiplexer_1_out19), .Q(out_20), .clk(and_1_out));  // open: en, clr
  Register #(.width(32), .trigger("high")) register_78 (
    .D(demultiplexer_2_out19), .Q(out_52), .clk(and_2_out));  // open: en, clr
  Register #(.width(32), .trigger("high")) register_79 (
    .D(demultiplexer_3_out19), .Q(out_84), .clk(and_3_out));  // open: en, clr
  Register #(.width(32), .trigger("high")) register_80 (
    .D(demultiplexer_4_out19), .Q(out_116), .clk(and_4_out));  // open: en, clr
  Register #(.width(32), .trigger("high")) register_81 (
    .D(demultiplexer_1_out20), .Q(out_21), .clk(and_1_out));  // open: en, clr
  Register #(.width(32), .trigger("high")) register_82 (
    .D(demultiplexer_2_out20), .Q(out_53), .clk(and_2_out));  // open: en, clr
  Register #(.width(32), .trigger("high")) register_83 (
    .D(demultiplexer_3_out20), .Q(out_85), .clk(and_3_out));  // open: en, clr
  Register #(.width(32), .trigger("high")) register_84 (
    .D(demultiplexer_4_out20), .Q(out_117), .clk(and_4_out));  // open: en, clr
  Register #(.width(32), .trigger("high")) register_85 (
    .D(demultiplexer_1_out21), .Q(out_22), .clk(and_1_out));  // open: en, clr
  Register #(.width(32), .trigger("high")) register_86 (
    .D(demultiplexer_2_out21), .Q(out_54), .clk(and_2_out));  // open: en, clr
  Register #(.width(32), .trigger("high")) register_87 (
    .D(demultiplexer_3_out21), .Q(out_86), .clk(and_3_out));  // open: en, clr
  Register #(.width(32), .trigger("high")) register_88 (
    .D(demultiplexer_4_out21), .Q(out_118), .clk(and_4_out));  // open: en, clr
  Register #(.width(32), .trigger("high")) register_89 (
    .D(demultiplexer_1_out22), .Q(out_23), .clk(and_1_out));  // open: en, clr
  Register #(.width(32), .trigger("high")) register_90 (
    .D(demultiplexer_2_out22), .Q(out_55), .clk(and_2_out));  // open: en, clr
  Register #(.width(32), .trigger("high")) register_91 (
    .D(demultiplexer_3_out22), .Q(out_87), .clk(and_3_out));  // open: en, clr
  Register #(.width(32), .trigger("high")) register_92 (
    .D(demultiplexer_4_out22), .Q(out_119), .clk(and_4_out));  // open: en, clr
  Register #(.width(32), .trigger("high")) register_93 (
    .D(demultiplexer_1_out23), .Q(out_24), .clk(and_1_out));  // open: en, clr
  Register #(.width(32), .trigger("high")) register_94 (
    .D(demultiplexer_2_out23), .Q(out_56), .clk(and_2_out));  // open: en, clr
  Register #(.width(32), .trigger("high")) register_95 (
    .D(demultiplexer_3_out23), .Q(out_88), .clk(and_3_out));  // open: en, clr
  Register #(.width(32), .trigger("high")) register_96 (
    .D(demultiplexer_4_out23), .Q(out_120), .clk(and_4_out));  // open: en, clr
  Register #(.width(32), .trigger("high")) register_97 (
    .D(demultiplexer_1_out24), .Q(out_25), .clk(and_1_out));  // open: en, clr
  Register #(.width(32), .trigger("high")) register_98 (
    .D(demultiplexer_2_out24), .Q(out_57), .clk(and_2_out));  // open: en, clr
  Register #(.width(32), .trigger("high")) register_99 (
    .D(demultiplexer_3_out24), .Q(out_89), .clk(and_3_out));  // open: en, clr
  Register #(.width(32), .trigger("high")) register_100 (
    .D(demultiplexer_4_out24), .Q(out_121), .clk(and_4_out));  // open: en, clr
  Register #(.width(32), .trigger("high")) register_101 (
    .D(demultiplexer_1_out25), .Q(out_26), .clk(and_1_out));  // open: en, clr
  Register #(.width(32), .trigger("high")) register_102 (
    .D(demultiplexer_2_out25), .Q(out_58), .clk(and_2_out));  // open: en, clr
  Register #(.width(32), .trigger("high")) register_103 (
    .D(demultiplexer_3_out25), .Q(out_90), .clk(and_3_out));  // open: en, clr
  Register #(.width(32), .trigger("high")) register_104 (
    .D(demultiplexer_4_out25), .Q(out_122), .clk(and_4_out));  // open: en, clr
  Register #(.width(32), .trigger("high")) register_105 (
    .D(demultiplexer_1_out26), .Q(out_27), .clk(and_1_out));  // open: en, clr
  Register #(.width(32), .trigger("high")) register_106 (
    .D(demultiplexer_2_out26), .Q(out_59), .clk(and_2_out));  // open: en, clr
  Register #(.width(32), .trigger("high")) register_107 (
    .D(demultiplexer_3_out26), .Q(out_91), .clk(and_3_out));  // open: en, clr
  Register #(.width(32), .trigger("high")) register_108 (
    .D(demultiplexer_4_out26), .Q(out_123), .clk(and_4_out));  // open: en, clr
  Register #(.width(32), .trigger("high")) register_109 (
    .D(demultiplexer_1_out27), .Q(out_28), .clk(and_1_out));  // open: en, clr
  Register #(.width(32), .trigger("high")) register_110 (
    .D(demultiplexer_2_out27), .Q(out_60), .clk(and_2_out));  // open: en, clr
  Register #(.width(32), .trigger("high")) register_111 (
    .D(demultiplexer_3_out27), .Q(out_92), .clk(and_3_out));  // open: en, clr
  Register #(.width(32), .trigger("high")) register_112 (
    .D(demultiplexer_4_out27), .Q(out_124), .clk(and_4_out));  // open: en, clr
  Register #(.width(32), .trigger("high")) register_113 (
    .D(demultiplexer_1_out28), .Q(out_29), .clk(and_1_out));  // open: en, clr
  Register #(.width(32), .trigger("high")) register_114 (
    .D(demultiplexer_2_out28), .Q(out_61), .clk(and_2_out));  // open: en, clr
  Register #(.width(32), .trigger("high")) register_115 (
    .D(demultiplexer_3_out28), .Q(out_93), .clk(and_3_out));  // open: en, clr
  Register #(.width(32), .trigger("high")) register_116 (
    .D(demultiplexer_4_out28), .Q(out_125), .clk(and_4_out));  // open: en, clr
  Register #(.width(32), .trigger("high")) register_117 (
    .D(demultiplexer_1_out29), .Q(out_30), .clk(and_1_out));  // open: en, clr
  Register #(.width(32), .trigger("high")) register_118 (
    .D(demultiplexer_2_out29), .Q(out_62), .clk(and_2_out));  // open: en, clr
  Register #(.width(32), .trigger("high")) register_119 (
    .D(demultiplexer_3_out29), .Q(out_94), .clk(and_3_out));  // open: en, clr
  Register #(.width(32), .trigger("high")) register_120 (
    .D(demultiplexer_4_out29), .Q(out_126), .clk(and_4_out));  // open: en, clr
  Register #(.width(32), .trigger("high")) register_121 (
    .D(demultiplexer_1_out30), .Q(out_31), .clk(and_1_out));  // open: en, clr
  Register #(.width(32), .trigger("high")) register_122 (
    .D(demultiplexer_2_out30), .Q(out_63), .clk(and_2_out));  // open: en, clr
  Register #(.width(32), .trigger("high")) register_123 (
    .D(demultiplexer_3_out30), .Q(out_95), .clk(and_3_out));  // open: en, clr
  Register #(.width(32), .trigger("high")) register_124 (
    .D(demultiplexer_4_out30), .Q(out_127), .clk(and_4_out));  // open: en, clr
  Register #(.width(32), .trigger("high")) register_125 (
    .D(demultiplexer_1_out31), .Q(out_32), .clk(and_1_out));  // open: en, clr
  Register #(.width(32), .trigger("high")) register_126 (
    .D(demultiplexer_2_out31), .Q(out_64), .clk(and_2_out));  // open: en, clr
  Register #(.width(32), .trigger("high")) register_127 (
    .D(demultiplexer_3_out31), .Q(out_96), .clk(and_3_out));  // open: en, clr
  Register #(.width(32), .trigger("high")) register_128 (
    .D(demultiplexer_4_out31), .Q(out_128), .clk(and_4_out));  // open: en, clr

  // Notes on the sheet:
  //   kek
  //   kek
endmodule
