// Logisim project other_logic.circ as structural Verilog: 14 circuits, main circuit rising_edge_detector
module rising_edge_detector (
  input  signal,
  input  clear,
  input  sync,
  output out
);

  wire rising_edge_pulse_1_out, s_r_ff_1_q;

  S_R_Flip_Flop s_r_ff_1 (.Q(s_r_ff_1_q), .preset(rising_edge_pulse_1_out), .reset(clear));  // open: S, clk, R, Qn, en
  rising_edge_pulse rising_edge_pulse_1 (.signal(signal), .out(rising_edge_pulse_1_out));
  S_R_Flip_Flop s_r_ff_2 (.S(s_r_ff_1_q), .clk(sync), .R(1'b0), .Q(out), .reset(clear));  // open: Qn, preset, en

  // Notes on the sheet:
  //   clear: pull=down
  //   sync: pull=down
  //   signal: pull=down
  //   out: pull=down
endmodule

module falling_edge_detector (
  input  signal,
  input  clear,
  input  sync,
  output out
);

  wire falling_edge_pulse_1_out, s_r_ff_1_q;

  falling_edge_pulse falling_edge_pulse_1 (.signal(signal), .out(falling_edge_pulse_1_out));
  S_R_Flip_Flop s_r_ff_1 (.Q(s_r_ff_1_q), .preset(falling_edge_pulse_1_out), .reset(clear));  // open: S, clk, R, Qn, en
  S_R_Flip_Flop s_r_ff_2 (.S(s_r_ff_1_q), .clk(sync), .R(1'b0), .Q(out), .reset(clear));  // open: Qn, preset, en

  // Notes on the sheet:
  //   signal: pull=down
  //   clear: pull=down
  //   out: pull=down
  //   sync: pull=down
endmodule

module rising_edge_pulse (
  input  signal,
  output out
);

  wire not_1_out;

  not not_1 (not_1_out, signal);
  and and_1 (out, signal, not_1_out);

  // Notes on the sheet:
  //   signal: pull=down
  //   out: pull=down
endmodule

module falling_edge_pulse (
  input  signal,
  output out
);

  wire not_1_out, not_2_out, not_3_out;

  not not_1 (not_1_out, signal);
  not not_2 (not_2_out, signal);
  and and_1 (out, not_2_out, not_3_out);
  not not_3 (not_3_out, not_1_out);

  // Notes on the sheet:
  //   signal: pull=down
  //   out: pull=down
endmodule

module clock_x2 (
  input  clk,
  output clk_x2
);

  wire falling_edge_pulse_1_out, rising_edge_pulse_1_out;

  rising_edge_pulse rising_edge_pulse_1 (.signal(clk), .out(rising_edge_pulse_1_out));
  falling_edge_pulse falling_edge_pulse_1 (.signal(clk), .out(falling_edge_pulse_1_out));
  or or_1 (clk_x2, rising_edge_pulse_1_out, falling_edge_pulse_1_out);
endmodule

module clock_x4 (
  input  clk,
  output clk_x4
);

  wire clock_x2_1_clk_x2;

  clock_x2 clock_x2_1 (.clk(clk), .clk_x2(clock_x2_1_clk_x2));
  clock_x2 clock_x2_2 (.clk(clock_x2_1_clk_x2), .clk_x2(clk_x4));
endmodule

module clock_x8 (
  input  clk,
  output clk_x8
);

  wire clock_x4_1_clk_x4;

  clock_x4 clock_x4_1 (.clk(clk), .clk_x4(clock_x4_1_clk_x4));
  clock_x4 clock_x4_2 (.clk(clock_x4_1_clk_x4), .clk_x4(clk_x8));
endmodule

module clock_x16 (
  input  clk,
  output clk_x16
);

  wire clock_x8_1_clk_x8;

  clock_x8 clock_x8_1 (.clk(clk), .clk_x8(clock_x8_1_clk_x8));
  clock_x8 clock_x8_2 (.clk(clock_x8_1_clk_x8), .clk_x8(clk_x16));
endmodule

module clock_x32 (
  input  clk,
  output clk_x32
);

  wire clock_x16_1_clk_x16;

  clock_x16 clock_x16_1 (.clk(clk), .clk_x16(clock_x16_1_clk_x16));
  clock_x16 clock_x16_2 (.clk(clock_x16_1_clk_x16), .clk_x16(clk_x32));
endmodule

module clock_x64 (
  input  clk,
  output clk_x64
);

  wire clock_x32_1_clk_x32;

  clock_x32 clock_x32_1 (.clk(clk), .clk_x32(clock_x32_1_clk_x32));
  clock_x32 clock_x32_2 (.clk(clock_x32_1_clk_x32), .clk_x32(clk_x64));
endmodule

module clock_x128 (
  input  clk,
  output clk_x128
);

  wire clock_x64_1_clk_x64;

  clock_x64 clock_x64_1 (.clk(clk), .clk_x64(clock_x64_1_clk_x64));
  clock_x64 clock_x64_2 (.clk(clock_x64_1_clk_x64), .clk_x64(clk_x128));
endmodule

module clock__2 (
  input  clk,
  output clk__2
);

  wire d_ff_1_qn;

  D_Flip_Flop d_ff_1 (.clk(clk), .D(d_ff_1_qn), .Q(clk__2), .Qn(d_ff_1_qn));  // open: preset, en, reset
endmodule

module rising_edge_detector_async (
  input  signal,
  input  clear,
  output out
);

  wire rising_edge_pulse_1_out;

  S_R_Flip_Flop s_r_ff_1 (.Q(out), .preset(rising_edge_pulse_1_out), .reset(clear));  // open: S, clk, R, Qn, en
  rising_edge_pulse rising_edge_pulse_1 (.signal(signal), .out(rising_edge_pulse_1_out));

  // Notes on the sheet:
  //   clear: pull=down
  //   signal: pull=down
  //   out: pull=down
endmodule

module delay_1 (
  input  in_1,
  input  in_2,
  output out_3
);

  wire rising_edge_detector_async_1_out;

  rising_edge_detector_async rising_edge_detector_async_1 (
    .signal(in_1), .clear(out_3), .out(rising_edge_detector_async_1_out));
  D_Flip_Flop d_ff_1 (.clk(in_2), .D(rising_edge_detector_async_1_out), .Q(out_3));  // open: Qn, preset, en, reset
endmodule
