// Logisim project sin_cos.circ as structural Verilog: 3 circuits, main circuit sin
module sin (
  input  [31:0] in_fp,
  output [31:0] sin
);

  wire and_1_out, and_2_out, comparator_1_gt, comparator_2_gt, comparator_3_gt, not_1_out;
  wire [8:0] subtractor_1_out, subtractor_2_out, subtractor_3_out;
  wire [31:0] fp_abs_1_abs, negator_1_out, negator_2_out, rom_1_data, rom_3_data;

  fp_abs fp_abs_1 (.in(in_fp), .abs(fp_abs_1_abs));
  Comparator #(.width(9), .mode("unsigned")) comparator_1 (
    .a(fp_abs_1_abs[24:16]), .b(9'h5a), .gt(comparator_1_gt));  // open: eq, lt
  Comparator #(.width(9), .mode("unsigned")) comparator_2 (
    .a(fp_abs_1_abs[24:16]), .b(9'hb4), .gt(comparator_2_gt));  // open: eq, lt
  Comparator #(.width(9), .mode("unsigned")) comparator_3 (
    .a(fp_abs_1_abs[24:16]), .b(9'h10e), .gt(comparator_3_gt));  // open: eq, lt
  and and_1 (and_1_out, comparator_1_gt, ~comparator_2_gt);  // AND_Gate
  and and_2 (and_2_out, comparator_2_gt, ~comparator_3_gt);  // AND_Gate
  Subtractor #(.width(9)) subtractor_1 (.a(fp_abs_1_abs[24:16]), .b(9'h5a), .out(subtractor_1_out));  // open: bin, bout
  Subtractor #(.width(9)) subtractor_2 (.a(fp_abs_1_abs[24:16]), .b(9'hb4), .out(subtractor_2_out));  // open: bin, bout
  Subtractor #(.width(9)) subtractor_3 (
    .a(fp_abs_1_abs[24:16]), .b(9'h10e), .out(subtractor_3_out));  // open: bin, bout
  not not_1 (not_1_out, comparator_1_gt);
  ROM #(.addrWidth(7), .dataWidth(32)) rom_1 (.addr(fp_abs_1_abs[22:16]), .data(rom_1_data), .sel(not_1_out));
  ROM #(.addrWidth(7), .dataWidth(32)) rom_2 (.addr(subtractor_1_out[6:0]), .data(rom_1_data), .sel(and_1_out));
  ROM #(.addrWidth(7), .dataWidth(32)) rom_3 (.addr(subtractor_2_out[6:0]), .data(rom_3_data), .sel(and_2_out));
  Negator #(.width(32)) negator_1 (.in(rom_3_data), .out(negator_1_out));
  ROM #(.addrWidth(7), .dataWidth(32)) rom_4 (.addr(subtractor_3_out[6:0]), .data(rom_1_data), .sel(comparator_3_gt));
  assign rom_1_data = and_2_out ? negator_1_out : 32'bz;  // Controlled_Buffer controlled_buffer_1
  Multiplexer #(.width(32), .enable("false")) multiplexer_1 (
    .in0(rom_1_data), .in1(negator_2_out), .out(sin), .sel(in_fp[31]));
  Negator #(.width(32)) negator_2 (.in(rom_1_data), .out(negator_2_out));

  // Notes on the sheet:
  //   in_fp: pull=down
  //   contents of rom_1 (hex, n*v repeats v):
  //   0 47a 8ef d63 11de 1652 1ac0 1f34 23a2 2809 2c71 30d8 3538 3999 3ded 4240 468d 4ada 4f1a 535a 578d
  //   5bc0 5fe5 6404 681d 6c2f 703a 7439 7831 7c1b 8000 83d7 87a7 8b6a 8f27 92d7 967a 9a0f 9d9e a119 a48e
  //   a7f6 ab4a ae97 b1d7 b504 b824 bb3d be3b c134 c418 c6f0 c9ba cc71 cf1a d1b7 d439 d6b5 d916 db71 ddb2
  //   dfe5 e205 e418 e617 e803 e9db eba5 ed5c ef00 f090 f20c f37b f4d0 f617 f745 f865 f972 fa64 fb4a fc1b
  //   fcd9 fd84 fe14 fe97 ff06 ff62 ffa4 ffd8 fff2 10000
  //   contents of rom_2 (hex, n*v repeats v):
  //   10000 fff2 ffd8 ffa4 ff62 ff06 fe97 fe14 fd84 fcd9 fc1b fb4a fa64 f972 f865 f745 f617 f4d0 f37b f20c
  //   f090 ef00 ed5c eba5 e9db e803 e617 e418 e205 dfe5 ddb2 db71 d916 d6b5 d439 d1b7 cf1a cc71 c9ba c6f0
  //   c418 c134 be3b bb3d b824 b504 b1d7 ae97 ab4a a7f6 a48e a119 9d9e 9a0f 967a 92d7 8f27 8b6a 87a7 83d7
  //   8000 7c1b 7831 7439 703a 6c2f 681d 6404 5fe5 5bc0 578d 535a 4f1a 4ada 468d 4240 3ded 3999 3538 30d8
  //   2c71 2809 23a2 1f34 1ac0 1652 11de d63 8ef 47a
  //   contents of rom_3 (hex, n*v repeats v):
  //   0 47a 8ef d63 11de 1652 1ac0 1f34 23a2 2809 2c71 30d8 3538 3999 3ded 4240 468d 4ada 4f1a 535a 578d
  //   5bc0 5fe5 6404 681d 6c2f 703a 7439 7831 7c1b 8000 83d7 87a7 8b6a 8f27 92d7 967a 9a0f 9d9e a119 a48e
  //   a7f6 ab4a ae97 b1d7 b504 b824 bb3d be3b c134 c418 c6f0 c9ba cc71 cf1a d1b7 d439 d6b5 d916 db71 ddb2
  //   dfe5 e205 e418 e617 e803 e9db eba5 ed5c ef00 f090 f20c f37b f4d0 f617 f745 f865 f972 fa64 fb4a fc1b
  //   fcd9 fd84 fe14 fe97 ff06 ff62 ffa4 ffd8 fff2 10000
  //   contents of rom_4 (hex, n*v repeats v):
  //   0 47a 8ef d63 11de 1652 1ac0 1f34 23a2 2809 2c71 30d8 3538 3999 3ded 4240 468d 4ada 4f1a 535a 578d
  //   5bc0 5fe5 6404 681d 6c2f 703a 7439 7831 7c1b 8000 83d7 87a7 8b6a 8f27 92d7 967a 9a0f 9d9e a119 a48e
  //   a7f6 ab4a ae97 b1d7 b504 b824 bb3d be3b c134 c418 c6f0 c9ba cc71 cf1a d1b7 d439 d6b5 d916 db71 ddb2
  //   dfe5 e205 e418 e617 e803 e9db eba5 ed5c ef00 f090 f20c f37b f4d0 f617 f745 f865 f972 fa64 fb4a fc1b
  //   fcd9 fd84 fe14 fe97 ff06 ff62 ffa4 ffd8 fff2 10000
endmodule

module cos (
  input  [31:0] in_fp,
  output [31:0] cos
);

  wire and_1_out, and_2_out, comparator_1_gt, comparator_2_gt, comparator_3_gt, not_1_out;
  wire [8:0] subtractor_1_out, subtractor_2_out, subtractor_3_out;
  wire [31:0] fp_abs_1_abs, negator_1_out, negator_2_out, negator_3_out, negator_4_out, rom_1_data,
       rom_2_data, rom_3_data, rom_4_data;

  fp_abs fp_abs_1 (.in(in_fp), .abs(fp_abs_1_abs));
  Comparator #(.width(9), .mode("unsigned")) comparator_1 (
    .a(fp_abs_1_abs[24:16]), .b(9'h5a), .gt(comparator_1_gt));  // open: eq, lt
  Comparator #(.width(9), .mode("unsigned")) comparator_2 (
    .a(fp_abs_1_abs[24:16]), .b(9'hb4), .gt(comparator_2_gt));  // open: eq, lt
  Comparator #(.width(9), .mode("unsigned")) comparator_3 (
    .a(fp_abs_1_abs[24:16]), .b(9'h10e), .gt(comparator_3_gt));  // open: eq, lt
  and and_1 (and_1_out, comparator_1_gt, ~comparator_2_gt);  // AND_Gate
  and and_2 (and_2_out, comparator_2_gt, ~comparator_3_gt);  // AND_Gate
  Subtractor #(.width(9)) subtractor_1 (.a(fp_abs_1_abs[24:16]), .b(9'h5a), .out(subtractor_1_out));  // open: bin, bout
  Subtractor #(.width(9)) subtractor_2 (.a(fp_abs_1_abs[24:16]), .b(9'hb4), .out(subtractor_2_out));  // open: bin, bout
  Subtractor #(.width(9)) subtractor_3 (
    .a(fp_abs_1_abs[24:16]), .b(9'h10e), .out(subtractor_3_out));  // open: bin, bout
  not not_1 (not_1_out, comparator_1_gt);
  ROM #(.addrWidth(7), .dataWidth(32)) rom_1 (.addr(fp_abs_1_abs[22:16]), .data(rom_1_data), .sel(not_1_out));
  Negator #(.width(32)) negator_1 (.in(rom_2_data), .out(negator_1_out));
  ROM #(.addrWidth(7), .dataWidth(32)) rom_2 (.addr(subtractor_1_out[6:0]), .data(rom_2_data), .sel(and_1_out));
  ROM #(.addrWidth(7), .dataWidth(32)) rom_3 (.addr(subtractor_2_out[6:0]), .data(rom_3_data), .sel(and_2_out));
  Negator #(.width(32)) negator_2 (.in(rom_3_data), .out(negator_2_out));
  Negator #(.width(32)) negator_3 (.in(rom_4_data), .out(negator_3_out));
  ROM #(.addrWidth(7), .dataWidth(32)) rom_4 (.addr(subtractor_3_out[6:0]), .data(rom_4_data), .sel(comparator_3_gt));
  Negator #(.width(32)) negator_4 (.in(rom_1_data), .out(negator_4_out));
  assign rom_1_data = and_1_out ? negator_1_out : 32'bz;  // Controlled_Buffer controlled_buffer_1
  assign rom_1_data = and_2_out ? negator_2_out : 32'bz;  // Controlled_Buffer controlled_buffer_2
  assign rom_1_data = comparator_3_gt ? negator_3_out : 32'bz;  // Controlled_Buffer controlled_buffer_3
  Multiplexer #(.width(32), .enable("false")) multiplexer_1 (
    .in0(rom_1_data), .in1(negator_4_out), .out(cos), .sel(in_fp[31]));

  // Notes on the sheet:
  //   in_fp: pull=down
  //   contents of rom_1 (hex, n*v repeats v):
  //   10000 fff2 ffd8 ffa4 ff62 ff06 fe97 fe14 fd84 fcd9 fc1b fb4a fa64 f972 f865 f745 f617 f4d0 f37b f20c
  //   f090 ef00 ed5c eba5 e9db e803 e617 e418 e205 dfe5 ddb2 db71 d916 d6b5 d439 d1b7 cf1a cc71 c9ba c6f0
  //   c418 c134 be3b bb3d b824 b504 b1d7 ae97 ab4a a7f6 a48e a119 9d9e 9a0f 967a 92d7 8f27 8b6a 87a7 83d7
  //   8000 7c1b 7831 7439 703a 6c2f 681d 6404 5fe5 5bc0 578d 535a 4f1a 4ada 468d 4240 3ded 3999 3538 30d8
  //   2c71 2809 23a2 1f34 1ac0 1652 11de d63 8ef 47a
  //   contents of rom_2 (hex, n*v repeats v):
  //   0 47a 8ef d63 11de 1652 1ac0 1f34 23a2 2809 2c71 30d8 3538 3999 3ded 4240 468d 4ada 4f1a 535a 578d
  //   5bc0 5fe5 6404 681d 6c2f 703a 7439 7831 7c1b 8000 83d7 87a7 8b6a 8f27 92d7 967a 9a0f 9d9e a119 a48e
  //   a7f6 ab4a ae97 b1d7 b504 b824 bb3d be3b c134 c418 c6f0 c9ba cc71 cf1a d1b7 d439 d6b5 d916 db71 ddb2
  //   dfe5 e205 e418 e617 e803 e9db eba5 ed5c ef00 f090 f20c f37b f4d0 f617 f745 f865 f972 fa64 fb4a fc1b
  //   fcd9 fd84 fe14 fe97 ff06 ff62 ffa4 ffd8 fff2 10000
  //   contents of rom_3 (hex, n*v repeats v):
  //   10000 fff2 ffd8 ffa4 ff62 ff06 fe97 fe14 fd84 fcd9 fc1b fb4a fa64 f972 f865 f745 f617 f4d0 f37b f20c
  //   f090 ef00 ed5c eba5 e9db e803 e617 e418 e205 dfe5 ddb2 db71 d916 d6b5 d439 d1b7 cf1a cc71 c9ba c6f0
  //   c418 c134 be3b bb3d b824 b504 b1d7 ae97 ab4a a7f6 a48e a119 9d9e 9a0f 967a 92d7 8f27 8b6a 87a7 83d7
  //   8000 7c1b 7831 7439 703a 6c2f 681d 6404 5fe5 5bc0 578d 535a 4f1a 4ada 468d 4240 3ded 3999 3538 30d8
  //   2c71 2809 23a2 1f34 1ac0 1652 11de d63 8ef 47a
  //   contents of rom_4 (hex, n*v repeats v):
  //   10000 fff2 ffd8 ffa4 ff62 ff06 fe97 fe14 fd84 fcd9 fc1b fb4a fa64 f972 f865 f745 f617 f4d0 f37b f20c
  //   f090 ef00 ed5c eba5 e9db e803 e617 e418 e205 dfe5 ddb2 db71 d916 d6b5 d439 d1b7 cf1a cc71 c9ba c6f0
  //   c418 c134 be3b bb3d b824 b504 b1d7 ae97 ab4a a7f6 a48e a119 9d9e 9a0f 967a 92d7 8f27 8b6a 87a7 83d7
  //   8000 7c1b 7831 7439 703a 6c2f 681d 6404 5fe5 5bc0 578d 535a 4f1a 4ada 468d 4240 3ded 3999 3538 30d8
  //   2c71 2809 23a2 1f34 1ac0 1652 11de d63 8ef 47a
endmodule

module tg (
  input  [31:0] in_fp,
  output [31:0] tg
);

  wire [31:0] cos_1_cos, sin_1_sin;

  sin sin_1 (.in_fp(in_fp), .sin(sin_1_sin));
  cos cos_1 (.cos(cos_1_cos), .in_fp(in_fp));
  fp_div fp_div_1 (.in1(sin_1_sin), .in2(cos_1_cos), .out(tg));

  // Notes on the sheet:
  //   in_fp: pull=down
endmodule
