// Logisim project tablica_sin_i_cos.circ as structural Verilog: 1 circuit, main circuit sin&co
module sin_co (
  input  [6:0] in_1
);

  wire n32bit_decoder_short_1_dot, n32bit_decoder_short_1_sign, n32bit_decoder_short_2_dot,
       n32bit_decoder_short_2_sign;
  wire [3:0] n32bit_decoder_short_1__0, n32bit_decoder_short_1__1, n32bit_decoder_short_1__1_2,
       n32bit_decoder_short_1__2, n32bit_decoder_short_1__2_2, n32bit_decoder_short_1__3,
       n32bit_decoder_short_1__3_2, n32bit_decoder_short_1__4, n32bit_decoder_short_1__4_2,
       n32bit_decoder_short_1__5, n32bit_decoder_short_2__0, n32bit_decoder_short_2__1,
       n32bit_decoder_short_2__1_2, n32bit_decoder_short_2__2, n32bit_decoder_short_2__2_2,
       n32bit_decoder_short_2__3, n32bit_decoder_short_2__3_2, n32bit_decoder_short_2__4,
       n32bit_decoder_short_2__4_2, n32bit_decoder_short_2__5;
  wire [15:0] bit_extender_1_out;
  wire [31:0] rom_1_data, rom_2_data;

  assign bit_extender_1_out = {{9{1'b0}}, in_1};  // Bit_Extender bit_extender_1
  ROM #(.addrWidth(16), .dataWidth(32)) rom_1 (.addr(bit_extender_1_out), .data(rom_1_data));  // open: sel
  ROM #(.addrWidth(16), .dataWidth(32)) rom_2 (.addr(bit_extender_1_out), .data(rom_2_data));  // open: sel
  _7_Segment_Display u_7_segment_display_1 (.g(n32bit_decoder_short_1_sign));  // open: f, a, b, e, d, c, dp
  Hex_Digit_Display hex_digit_display_1 (.value(n32bit_decoder_short_1__4));  // open: dp
  _7_Segment_Display u_7_segment_display_2 (.g(n32bit_decoder_short_2_sign));  // open: f, a, b, e, d, c, dp
  Hex_Digit_Display hex_digit_display_2 (.value(n32bit_decoder_short_1__3));  // open: dp
  Hex_Digit_Display hex_digit_display_3 (.value(n32bit_decoder_short_1__2_2));  // open: dp
  Hex_Digit_Display hex_digit_display_4 (.value(n32bit_decoder_short_2__4));  // open: dp
  Hex_Digit_Display hex_digit_display_5 (.value(n32bit_decoder_short_2__3));  // open: dp
  Hex_Digit_Display hex_digit_display_6 (.value(n32bit_decoder_short_1__1_2));  // open: dp
  Hex_Digit_Display hex_digit_display_7 (.value(n32bit_decoder_short_1__0), .dp(n32bit_decoder_short_1_dot));
  Hex_Digit_Display hex_digit_display_8 (.value(n32bit_decoder_short_2__1_2));  // open: dp
  Hex_Digit_Display hex_digit_display_9 (.value(n32bit_decoder_short_2__2_2));  // open: dp
  Hex_Digit_Display hex_digit_display_10 (.value(n32bit_decoder_short_1__2));  // open: dp
  Hex_Digit_Display hex_digit_display_11 (.value(n32bit_decoder_short_1__1));  // open: dp
  Hex_Digit_Display hex_digit_display_12 (.value(n32bit_decoder_short_2__0), .dp(n32bit_decoder_short_2_dot));
  Hex_Digit_Display hex_digit_display_13 (.value(n32bit_decoder_short_2__1));  // open: dp
  Hex_Digit_Display hex_digit_display_14 (.value(n32bit_decoder_short_1__4_2));  // open: dp
  Hex_Digit_Display hex_digit_display_15 (.value(n32bit_decoder_short_1__3_2));  // open: dp
  Hex_Digit_Display hex_digit_display_16 (.value(n32bit_decoder_short_2__2));  // open: dp
  Hex_Digit_Display hex_digit_display_17 (.value(n32bit_decoder_short_2__3_2));  // open: dp
  Hex_Digit_Display hex_digit_display_18 (.value(n32bit_decoder_short_1__5));  // open: dp
  _32bit_decoder_short u_32bit_decoder_short_1 (
    .sign(n32bit_decoder_short_1_sign), ._4(n32bit_decoder_short_1__4), ._3(n32bit_decoder_short_1__3),
    ._2_2(n32bit_decoder_short_1__2_2), ._1_2(n32bit_decoder_short_1__1_2), ._0(n32bit_decoder_short_1__0),
    .dot(n32bit_decoder_short_1_dot), .in(rom_2_data), ._1(n32bit_decoder_short_1__1),
    ._2(n32bit_decoder_short_1__2), ._3_2(n32bit_decoder_short_1__3_2), ._4_2(n32bit_decoder_short_1__4_2),
    ._5(n32bit_decoder_short_1__5));
  Hex_Digit_Display hex_digit_display_19 (.value(n32bit_decoder_short_2__4_2));  // open: dp
  Hex_Digit_Display hex_digit_display_20 (.value(n32bit_decoder_short_2__5));  // open: dp
  _32bit_decoder_short u_32bit_decoder_short_2 (
    .sign(n32bit_decoder_short_2_sign), ._4(n32bit_decoder_short_2__4), ._3(n32bit_decoder_short_2__3),
    ._2_2(n32bit_decoder_short_2__2_2), ._1_2(n32bit_decoder_short_2__1_2), ._0(n32bit_decoder_short_2__0),
    .dot(n32bit_decoder_short_2_dot), .in(rom_1_data), ._1(n32bit_decoder_short_2__1),
    ._2(n32bit_decoder_short_2__2), ._3_2(n32bit_decoder_short_2__3_2), ._4_2(n32bit_decoder_short_2__4_2),
    ._5(n32bit_decoder_short_2__5));

  // Notes on the sheet:
  //   COSINUS
  //   SINUS
  //   contents of rom_1 (hex, n*v repeats v):
  //   10000 fff2 ffd8 ffa4 ff62 ff06 fe97 fe14 fd84 fcd9 fc1b fb4a fa64 f972 f865 f745 f617 f4d0 f37b f20c
  //   f090 ef00 ed5c eba5 e9db e803 e617 e418 e205 dfe5 ddb2 db71 d916 d6b5 d439 d1b7 cf1a cc71 c9ba c6f0
  //   c418 c134 be3b bb3d b824 b504 b1d7 ae97 ab4a a7f6 a48e a119 9d9e 9a0f 967a 92d7 8f27 8b6a 87a7 83d7
  //   8000 7c1b 7831 7439 703a 6c2f 681d 6404 5fe5 5bc0 578d 535a 4f1a 4ada 468d 4240 3ded 3999 3538 30d8
  //   2c71 2809 23a2 1f34 1ac0 1652 11de d63 8ef 47a
  //   contents of rom_2 (hex, n*v repeats v):
  //   0 47a 8ef d63 11de 1652 1ac0 1f34 23a2 2809 2c71 30d8 3538 3999 3ded 4240 468d 4ada 4f1a 535a 578d
  //   5bc0 5fe5 6404 681d 6c2f 703a 7439 7831 7c1b 8000 83d7 87a7 8b6a 8f27 92d7 967a 9a0f 9d9e a119 a48e
  //   a7f6 ab4a ae97 b1d7 b504 b824 bb3d be3b c134 c418 c6f0 c9ba cc71 cf1a d1b7 d439 d6b5 d916 db71 ddb2
  //   dfe5 e205 e418 e617 e803 e9db eba5 ed5c ef00 f090 f20c f37b f4d0 f617 f745 f865 f972 fa64 fb4a fc1b
  //   fcd9 fd84 fe14 fe97 ff06 ff62 ffa4 ffd8 fff2 10000
endmodule
