// Logisim project video - kopia.circ as structural Verilog: 4 circuits, main circuit 64 display 
module _64_display (
  input  [31:0] x_right_in,
  input  [31:0] x_left_in,
  input  [5:0] y_in,
  input  mode,
  input  clk,
  output [31:0] out_6,
  output [31:0] out_7,
  output [31:0] out_8,
  output [31:0] out_9,
  output [31:0] out_10,
  output [31:0] out_11,
  output [31:0] out_12,
  output [31:0] out_13,
  output [31:0] out_14,
  output [31:0] out_15,
  output [31:0] out_16,
  output [31:0] out_17,
  output [31:0] out_18,
  output [31:0] out_19,
  output [31:0] out_20,
  output [31:0] out_21,
  output [31:0] out_22,
  output [31:0] out_23,
  output [31:0] out_24,
  output [31:0] out_25,
  output [31:0] out_26,
  output [31:0] out_27,
  output [31:0] out_28,
  output [31:0] out_29,
  output [31:0] out_30,
  output [31:0] out_31,
  output [31:0] out_32,
  output [31:0] out_33,
  output [31:0] out_34,
  output [31:0] out_35,
  output [31:0] out_36,
  output [31:0] out_37,
  output [31:0] out_38,
  output [31:0] out_39,
  output [31:0] out_40,
  output [31:0] out_41,
  output [31:0] out_42,
  output [31:0] out_43,
  output [31:0] out_44,
  output [31:0] out_45,
  output [31:0] out_46,
  output [31:0] out_47,
  output [31:0] out_48,
  output [31:0] out_49,
  output [31:0] out_50,
  output [31:0] out_51,
  output [31:0] out_52,
  output [31:0] out_53,
  output [31:0] out_54,
  output [31:0] out_55,
  output [31:0] out_56,
  output [31:0] out_57,
  output [31:0] out_58,
  output [31:0] out_59,
  output [31:0] out_60,
  output [31:0] out_61,
  output [31:0] out_62,
  output [31:0] out_63,
  output [31:0] out_64,
  output [31:0] out_65,
  output [31:0] out_66,
  output [31:0] out_67,
  output [31:0] out_68,
  output [31:0] out_69,
  output [31:0] out_70,
  output [31:0] out_71,
  output [31:0] out_72,
  output [31:0] out_73,
  output [31:0] out_74,
  output [31:0] out_75,
  output [31:0] out_76,
  output [31:0] out_77,
  output [31:0] out_78,
  output [31:0] out_79,
  output [31:0] out_80,
  output [31:0] out_81,
  output [31:0] out_82,
  output [31:0] out_83,
  output [31:0] out_84,
  output [31:0] out_85,
  output [31:0] out_86,
  output [31:0] out_87,
  output [31:0] out_88,
  output [31:0] out_89,
  output [31:0] out_90,
  output [31:0] out_91,
  output [31:0] out_92,
  output [31:0] out_93,
  output [31:0] out_94,
  output [31:0] out_95,
  output [31:0] out_96,
  output [31:0] out_97,
  output [31:0] out_98,
  output [31:0] out_99,
  output [31:0] out_100,
  output [31:0] out_101,
  output [31:0] out_102,
  output [31:0] out_103,
  output [31:0] out_104,
  output [31:0] out_105,
  output [31:0] out_106,
  output [31:0] out_107,
  output [31:0] out_108,
  output [31:0] out_109,
  output [31:0] out_110,
  output [31:0] out_111,
  output [31:0] out_112,
  output [31:0] out_113,
  output [31:0] out_114,
  output [31:0] out_115,
  output [31:0] out_116,
  output [31:0] out_117,
  output [31:0] out_118,
  output [31:0] out_119,
  output [31:0] out_120,
  output [31:0] out_121,
  output [31:0] out_122,
  output [31:0] out_123,
  output [31:0] out_124,
  output [31:0] out_125,
  output [31:0] out_126,
  output [31:0] out_127,
  output [31:0] out_128,
  output [31:0] out_129,
  output [31:0] out_130,
  output [31:0] out_131,
  output [31:0] out_132,
  output [31:0] out_133
);

  wire and_1_out, and_2_out, and_3_out, and_4_out;
  wire [0:0] undriven;
  wire [31:0] adder_1_out, adder_2_out, demultiplexer_1_out0, demultiplexer_1_out1, demultiplexer_1_out2,
       demultiplexer_1_out3, demultiplexer_1_out4, demultiplexer_1_out5, demultiplexer_1_out6,
       demultiplexer_1_out7, demultiplexer_1_out8, demultiplexer_1_out9, demultiplexer_1_out10,
       demultiplexer_1_out11, demultiplexer_1_out12, demultiplexer_1_out13, demultiplexer_1_out14,
       demultiplexer_1_out15, demultiplexer_1_out16, demultiplexer_1_out17, demultiplexer_1_out18,
       demultiplexer_1_out19, demultiplexer_1_out20, demultiplexer_1_out21, demultiplexer_1_out22,
       demultiplexer_1_out23, demultiplexer_1_out24, demultiplexer_1_out25, demultiplexer_1_out26,
       demultiplexer_1_out27, demultiplexer_1_out28, demultiplexer_1_out29, demultiplexer_1_out30,
       demultiplexer_1_out31, demultiplexer_2_out0, demultiplexer_2_out1, demultiplexer_2_out2,
       demultiplexer_2_out3, demultiplexer_2_out4, demultiplexer_2_out5, demultiplexer_2_out6,
       demultiplexer_2_out7, demultiplexer_2_out8, demultiplexer_2_out9, demultiplexer_2_out10,
       demultiplexer_2_out11, demultiplexer_2_out12, demultiplexer_2_out13, demultiplexer_2_out14,
       demultiplexer_2_out15, demultiplexer_2_out16, demultiplexer_2_out17, demultiplexer_2_out18,
       demultiplexer_2_out19, demultiplexer_2_out20, demultiplexer_2_out21, demultiplexer_2_out22,
       demultiplexer_2_out23, demultiplexer_2_out24, demultiplexer_2_out25, demultiplexer_2_out26,
       demultiplexer_2_out27, demultiplexer_2_out28, demultiplexer_2_out29, demultiplexer_2_out30,
       demultiplexer_2_out31, demultiplexer_3_out0, demultiplexer_3_out1, demultiplexer_3_out2,
       demultiplexer_3_out3, demultiplexer_3_out4, demultiplexer_3_out5, demultiplexer_3_out6,
       demultiplexer_3_out7, demultiplexer_3_out8, demultiplexer_3_out9, demultiplexer_3_out10,
       demultiplexer_3_out11, demultiplexer_3_out12, demultiplexer_3_out13, demultiplexer_3_out14,
       demultiplexer_3_out15, demultiplexer_3_out16, demultiplexer_3_out17, demultiplexer_3_out18,
       demultiplexer_3_out19, demultiplexer_3_out20, demultiplexer_3_out21, demultiplexer_3_out22,
       demultiplexer_3_out23, demultiplexer_3_out24, demultiplexer_3_out25, demultiplexer_3_out26,
       demultiplexer_3_out27, demultiplexer_3_out28, demultiplexer_3_out29, demultiplexer_3_out30,
       demultiplexer_3_out31, demultiplexer_4_out0, demultiplexer_4_out1, demultiplexer_4_out2,
       demultiplexer_4_out3, demultiplexer_4_out4, demultiplexer_4_out5, demultiplexer_4_out6,
       demultiplexer_4_out7, demultiplexer_4_out8, demultiplexer_4_out9, demultiplexer_4_out10,
       demultiplexer_4_out11, demultiplexer_4_out12, demultiplexer_4_out13, demultiplexer_4_out14,
       demultiplexer_4_out15, demultiplexer_4_out16, demultiplexer_4_out17, demultiplexer_4_out18,
       demultiplexer_4_out19, demultiplexer_4_out20, demultiplexer_4_out21, demultiplexer_4_out22,
       demultiplexer_4_out23, demultiplexer_4_out24, demultiplexer_4_out25, demultiplexer_4_out26,
       demultiplexer_4_out27, demultiplexer_4_out28, demultiplexer_4_out29, demultiplexer_4_out30,
       demultiplexer_4_out31;

  Adder #(.width(32)) adder_1 (.a({{31{1'b0}}, undriven[0]}), .b({32{1'b0}}), .out(adder_1_out));  // open: cin, cout
  Adder #(.width(32)) adder_2 (.a(adder_1_out), .b({32{1'b0}}), .out(adder_2_out));  // open: cin, cout
  Demultiplexer #(.select(5), .width(32), .tristate("true")) demultiplexer_1 (
    .out0(demultiplexer_1_out0), .out1(demultiplexer_1_out1), .out2(demultiplexer_1_out2),
    .out3(demultiplexer_1_out3), .out4(demultiplexer_1_out4), .out5(demultiplexer_1_out5),
    .out6(demultiplexer_1_out6), .out7(demultiplexer_1_out7), .out8(demultiplexer_1_out8),
    .out9(demultiplexer_1_out9), .out10(demultiplexer_1_out10), .out11(demultiplexer_1_out11),
    .out12(demultiplexer_1_out12), .out13(demultiplexer_1_out13), .out14(demultiplexer_1_out14),
    .out15(demultiplexer_1_out15), .out16(demultiplexer_1_out16), .out17(demultiplexer_1_out17),
    .out18(demultiplexer_1_out18), .out19(demultiplexer_1_out19), .out20(demultiplexer_1_out20),
    .out21(demultiplexer_1_out21), .out22(demultiplexer_1_out22), .out23(demultiplexer_1_out23),
    .out24(demultiplexer_1_out24), .out25(demultiplexer_1_out25), .out26(demultiplexer_1_out26),
    .out27(demultiplexer_1_out27), .out28(demultiplexer_1_out28), .out29(demultiplexer_1_out29),
    .out30(demultiplexer_1_out30), .out31(demultiplexer_1_out31), .in(x_right_in), .sel(y_in[4:0]),
    .en(and_1_out));
  and and_1 (and_1_out, mode, y_in[5]);
  Demultiplexer #(.select(5), .width(32), .tristate("true")) demultiplexer_2 (
    .out0(demultiplexer_2_out0), .out1(demultiplexer_2_out1), .out2(demultiplexer_2_out2),
    .out3(demultiplexer_2_out3), .out4(demultiplexer_2_out4), .out5(demultiplexer_2_out5),
    .out6(demultiplexer_2_out6), .out7(demultiplexer_2_out7), .out8(demultiplexer_2_out8),
    .out9(demultiplexer_2_out9), .out10(demultiplexer_2_out10), .out11(demultiplexer_2_out11),
    .out12(demultiplexer_2_out12), .out13(demultiplexer_2_out13), .out14(demultiplexer_2_out14),
    .out15(demultiplexer_2_out15), .out16(demultiplexer_2_out16), .out17(demultiplexer_2_out17),
    .out18(demultiplexer_2_out18), .out19(demultiplexer_2_out19), .out20(demultiplexer_2_out20),
    .out21(demultiplexer_2_out21), .out22(demultiplexer_2_out22), .out23(demultiplexer_2_out23),
    .out24(demultiplexer_2_out24), .out25(demultiplexer_2_out25), .out26(demultiplexer_2_out26),
    .out27(demultiplexer_2_out27), .out28(demultiplexer_2_out28), .out29(demultiplexer_2_out29),
    .out30(demultiplexer_2_out30), .out31(demultiplexer_2_out31), .in(x_left_in), .sel(y_in[4:0]),
    .en(and_2_out));
  and and_2 (and_2_out, mode, y_in[5]);
  Demultiplexer #(.select(5), .width(32), .tristate("true")) demultiplexer_3 (
    .out0(demultiplexer_3_out0), .out1(demultiplexer_3_out1), .out2(demultiplexer_3_out2),
    .out3(demultiplexer_3_out3), .out4(demultiplexer_3_out4), .out5(demultiplexer_3_out5),
    .out6(demultiplexer_3_out6), .out7(demultiplexer_3_out7), .out8(demultiplexer_3_out8),
    .out9(demultiplexer_3_out9), .out10(demultiplexer_3_out10), .out11(demultiplexer_3_out11),
    .out12(demultiplexer_3_out12), .out13(demultiplexer_3_out13), .out14(demultiplexer_3_out14),
    .out15(demultiplexer_3_out15), .out16(demultiplexer_3_out16), .out17(demultiplexer_3_out17),
    .out18(demultiplexer_3_out18), .out19(demultiplexer_3_out19), .out20(demultiplexer_3_out20),
    .out21(demultiplexer_3_out21), .out22(demultiplexer_3_out22), .out23(demultiplexer_3_out23),
    .out24(demultiplexer_3_out24), .out25(demultiplexer_3_out25), .out26(demultiplexer_3_out26),
    .out27(demultiplexer_3_out27), .out28(demultiplexer_3_out28), .out29(demultiplexer_3_out29),
    .out30(demultiplexer_3_out30), .out31(demultiplexer_3_out31), .in(x_left_in), .sel(y_in[4:0]),
    .en(and_3_out));
  and and_3 (and_3_out, mode, ~y_in[5]);  // AND_Gate
  Demultiplexer #(.select(5), .width(32), .tristate("true")) demultiplexer_4 (
    .out0(demultiplexer_4_out0), .out1(demultiplexer_4_out1), .out2(demultiplexer_4_out2),
    .out3(demultiplexer_4_out3), .out4(demultiplexer_4_out4), .out5(demultiplexer_4_out5),
    .out6(demultiplexer_4_out6), .out7(demultiplexer_4_out7), .out8(demultiplexer_4_out8),
    .out9(demultiplexer_4_out9), .out10(demultiplexer_4_out10), .out11(demultiplexer_4_out11),
    .out12(demultiplexer_4_out12), .out13(demultiplexer_4_out13), .out14(demultiplexer_4_out14),
    .out15(demultiplexer_4_out15), .out16(demultiplexer_4_out16), .out17(demultiplexer_4_out17),
    .out18(demultiplexer_4_out18), .out19(demultiplexer_4_out19), .out20(demultiplexer_4_out20),
    .out21(demultiplexer_4_out21), .out22(demultiplexer_4_out22), .out23(demultiplexer_4_out23),
    .out24(demultiplexer_4_out24), .out25(demultiplexer_4_out25), .out26(demultiplexer_4_out26),
    .out27(demultiplexer_4_out27), .out28(demultiplexer_4_out28), .out29(demultiplexer_4_out29),
    .out30(demultiplexer_4_out30), .out31(demultiplexer_4_out31), .in(x_right_in), .sel(y_in[4:0]),
    .en(and_4_out));
  and and_4 (and_4_out, mode, ~y_in[5]);  // AND_Gate
  Register #(.width(32)) register_1 (.D(demultiplexer_1_out0), .Q(out_6), .clk(clk));  // open: en, clr
  Register #(.width(32)) register_2 (.D(demultiplexer_2_out0), .Q(out_38), .clk(clk));  // open: en, clr
  Register #(.width(32)) register_3 (.D(demultiplexer_3_out0), .Q(out_70), .clk(clk));  // open: en, clr
  Register #(.width(32)) register_4 (.D(demultiplexer_4_out0), .Q(out_102), .clk(clk));  // open: en, clr
  Register #(.width(32)) register_5 (.D(demultiplexer_1_out1), .Q(out_7), .clk(clk));  // open: en, clr
  Register #(.width(32)) register_6 (.D(demultiplexer_2_out1), .Q(out_39), .clk(clk));  // open: en, clr
  Register #(.width(32)) register_7 (.D(demultiplexer_3_out1), .Q(out_71), .clk(clk));  // open: en, clr
  Register #(.width(32)) register_8 (.D(demultiplexer_4_out1), .Q(out_103), .clk(clk));  // open: en, clr
  Register #(.width(32)) register_9 (.D(demultiplexer_1_out2), .Q(out_8), .clk(clk));  // open: en, clr
  Register #(.width(32)) register_10 (.D(demultiplexer_2_out2), .Q(out_40), .clk(clk));  // open: en, clr
  Register #(.width(32)) register_11 (.D(demultiplexer_3_out2), .Q(out_72), .clk(clk));  // open: en, clr
  Register #(.width(32)) register_12 (.D(demultiplexer_4_out2), .Q(out_104), .clk(clk));  // open: en, clr
  Register #(.width(32)) register_13 (.D(demultiplexer_1_out3), .Q(out_9), .clk(clk));  // open: en, clr
  Register #(.width(32)) register_14 (.D(demultiplexer_2_out3), .Q(out_41), .clk(clk));  // open: en, clr
  Register #(.width(32)) register_15 (.D(demultiplexer_3_out3), .Q(out_73), .clk(clk));  // open: en, clr
  Register #(.width(32)) register_16 (.D(demultiplexer_4_out3), .Q(out_105), .clk(clk));  // open: en, clr
  Register #(.width(32)) register_17 (.D(demultiplexer_1_out4), .Q(out_10), .clk(clk));  // open: en, clr
  Register #(.width(32)) register_18 (.D(demultiplexer_2_out4), .Q(out_42), .clk(clk));  // open: en, clr
  Register #(.width(32)) register_19 (.D(demultiplexer_3_out4), .Q(out_74), .clk(clk));  // open: en, clr
  Register #(.width(32)) register_20 (.D(demultiplexer_4_out4), .Q(out_106), .clk(clk));  // open: en, clr
  Register #(.width(32)) register_21 (.D(demultiplexer_1_out5), .Q(out_11), .clk(clk));  // open: en, clr
  Register #(.width(32)) register_22 (.D(demultiplexer_2_out5), .Q(out_43), .clk(clk));  // open: en, clr
  Register #(.width(32)) register_23 (.D(demultiplexer_3_out5), .Q(out_75), .clk(clk));  // open: en, clr
  Register #(.width(32)) register_24 (.D(demultiplexer_4_out5), .Q(out_107), .clk(clk));  // open: en, clr
  Register #(.width(32)) register_25 (.D(demultiplexer_1_out6), .Q(out_12), .clk(clk));  // open: en, clr
  Register #(.width(32)) register_26 (.D(demultiplexer_2_out6), .Q(out_44), .clk(clk));  // open: en, clr
  Register #(.width(32)) register_27 (.D(demultiplexer_3_out6), .Q(out_76), .clk(clk));  // open: en, clr
  Register #(.width(32)) register_28 (.D(demultiplexer_4_out6), .Q(out_108), .clk(clk));  // open: en, clr
  Register #(.width(32)) register_29 (.D(demultiplexer_1_out7), .Q(out_13), .clk(clk));  // open: en, clr
  Register #(.width(32)) register_30 (.D(demultiplexer_2_out7), .Q(out_45), .clk(clk));  // open: en, clr
  Register #(.width(32)) register_31 (.D(demultiplexer_3_out7), .Q(out_77), .clk(clk));  // open: en, clr
  Register #(.width(32)) register_32 (.D(demultiplexer_4_out7), .Q(out_109), .clk(clk));  // open: en, clr
  Register #(.width(32)) register_33 (.D(demultiplexer_1_out8), .Q(out_14), .clk(clk));  // open: en, clr
  Register #(.width(32)) register_34 (.D(demultiplexer_2_out8), .Q(out_46), .clk(clk));  // open: en, clr
  Register #(.width(32)) register_35 (.D(demultiplexer_3_out8), .Q(out_78), .clk(clk));  // open: en, clr
  Register #(.width(32)) register_36 (.D(demultiplexer_4_out8), .Q(out_110), .clk(clk));  // open: en, clr
  Register #(.width(32)) register_37 (.D(demultiplexer_1_out9), .Q(out_15), .clk(clk));  // open: en, clr
  Register #(.width(32)) register_38 (.D(demultiplexer_2_out9), .Q(out_47), .clk(clk));  // open: en, clr
  Register #(.width(32)) register_39 (.D(demultiplexer_3_out9), .Q(out_79), .clk(clk));  // open: en, clr
  Register #(.width(32)) register_40 (.D(demultiplexer_4_out9), .Q(out_111), .clk(clk));  // open: en, clr
  Register #(.width(32)) register_41 (.D(demultiplexer_1_out10), .Q(out_16), .clk(clk));  // open: en, clr
  Register #(.width(32)) register_42 (.D(demultiplexer_2_out10), .Q(out_48), .clk(clk));  // open: en, clr
  Register #(.width(32)) register_43 (.D(demultiplexer_3_out10), .Q(out_80), .clk(clk));  // open: en, clr
  Register #(.width(32)) register_44 (.D(demultiplexer_4_out10), .Q(out_112), .clk(clk));  // open: en, clr
  Register #(.width(32)) register_45 (.D(demultiplexer_1_out11), .Q(out_17), .clk(clk));  // open: en, clr
  Register #(.width(32)) register_46 (.D(demultiplexer_2_out11), .Q(out_49), .clk(clk));  // open: en, clr
  Register #(.width(32)) register_47 (.D(demultiplexer_3_out11), .Q(out_81), .clk(clk));  // open: en, clr
  Register #(.width(32)) register_48 (.D(demultiplexer_4_out11), .Q(out_113), .clk(clk));  // open: en, clr
  Register #(.width(32)) register_49 (.D(demultiplexer_1_out12), .Q(out_18), .clk(clk));  // open: en, clr
  Register #(.width(32)) register_50 (.D(demultiplexer_2_out12), .Q(out_50), .clk(clk));  // open: en, clr
  Register #(.width(32)) register_51 (.D(demultiplexer_3_out12), .Q(out_82), .clk(clk));  // open: en, clr
  Register #(.width(32)) register_52 (.D(demultiplexer_4_out12), .Q(out_114), .clk(clk));  // open: en, clr
  Register #(.width(32)) register_53 (.D(demultiplexer_1_out13), .Q(out_19), .clk(clk));  // open: en, clr
  Register #(.width(32)) register_54 (.D(demultiplexer_2_out13), .Q(out_51), .clk(clk));  // open: en, clr
  Register #(.width(32)) register_55 (.D(demultiplexer_3_out13), .Q(out_83), .clk(clk));  // open: en, clr
  Register #(.width(32)) register_56 (.D(demultiplexer_4_out13), .Q(out_115), .clk(clk));  // open: en, clr
  Register #(.width(32)) register_57 (.D(demultiplexer_1_out14), .Q(out_20), .clk(clk));  // open: en, clr
  Register #(.width(32)) register_58 (.D(demultiplexer_2_out14), .Q(out_52), .clk(clk));  // open: en, clr
  Register #(.width(32)) register_59 (.D(demultiplexer_3_out14), .Q(out_84), .clk(clk));  // open: en, clr
  Register #(.width(32)) register_60 (.D(demultiplexer_4_out14), .Q(out_116), .clk(clk));  // open: en, clr
  Register #(.width(32)) register_61 (.D(demultiplexer_1_out15), .Q(out_21), .clk(clk));  // open: en, clr
  Register #(.width(32)) register_62 (.D(demultiplexer_2_out15), .Q(out_53), .clk(clk));  // open: en, clr
  Register #(.width(32)) register_63 (.D(demultiplexer_3_out15), .Q(out_85), .clk(clk));  // open: en, clr
  Register #(.width(32)) register_64 (.D(demultiplexer_4_out15), .Q(out_117), .clk(clk));  // open: en, clr
  Register #(.width(32)) register_65 (.D(demultiplexer_1_out16), .Q(out_22), .clk(clk));  // open: en, clr
  Register #(.width(32)) register_66 (.D(demultiplexer_2_out16), .Q(out_54), .clk(clk));  // open: en, clr
  Register #(.width(32)) register_67 (.D(demultiplexer_3_out16), .Q(out_86), .clk(clk));  // open: en, clr
  Register #(.width(32)) register_68 (.D(demultiplexer_4_out16), .Q(out_118), .clk(clk));  // open: en, clr
  Register #(.width(32)) register_69 (.D(demultiplexer_1_out17), .Q(out_23), .clk(clk));  // open: en, clr
  Register #(.width(32)) register_70 (.D(demultiplexer_2_out17), .Q(out_55), .clk(clk));  // open: en, clr
  Register #(.width(32)) register_71 (.D(demultiplexer_3_out17), .Q(out_87), .clk(clk));  // open: en, clr
  Register #(.width(32)) register_72 (.D(demultiplexer_4_out17), .Q(out_119), .clk(clk));  // open: en, clr
  Register #(.width(32)) register_73 (.D(demultiplexer_1_out18), .Q(out_24), .clk(clk));  // open: en, clr
  Register #(.width(32)) register_74 (.D(demultiplexer_2_out18), .Q(out_56), .clk(clk));  // open: en, clr
  Register #(.width(32)) register_75 (.D(demultiplexer_3_out18), .Q(out_88), .clk(clk));  // open: en, clr
  Register #(.width(32)) register_76 (.D(demultiplexer_4_out18), .Q(out_120), .clk(clk));  // open: en, clr
  Register #(.width(32)) register_77 (.D(demultiplexer_1_out19), .Q(out_25), .clk(clk));  // open: en, clr
  Register #(.width(32)) register_78 (.D(demultiplexer_2_out19), .Q(out_57), .clk(clk));  // open: en, clr
  Register #(.width(32)) register_79 (.D(demultiplexer_3_out19), .Q(out_89), .clk(clk));  // open: en, clr
  Register #(.width(32)) register_80 (.D(demultiplexer_4_out19), .Q(out_121), .clk(clk));  // open: en, clr
  Register #(.width(32)) register_81 (.D(demultiplexer_1_out20), .Q(out_26), .clk(clk));  // open: en, clr
  Register #(.width(32)) register_82 (.D(demultiplexer_2_out20), .Q(out_58), .clk(clk));  // open: en, clr
  Register #(.width(32)) register_83 (.D(demultiplexer_3_out20), .Q(out_90), .clk(clk));  // open: en, clr
  Register #(.width(32)) register_84 (.D(demultiplexer_4_out20), .Q(out_122), .clk(clk));  // open: en, clr
  Register #(.width(32)) register_85 (.D(demultiplexer_1_out21), .Q(out_27), .clk(clk));  // open: en, clr
  Register #(.width(32)) register_86 (.D(demultiplexer_2_out21), .Q(out_59), .clk(clk));  // open: en, clr
  Register #(.width(32)) register_87 (.D(demultiplexer_3_out21), .Q(out_91), .clk(clk));  // open: en, clr
  Register #(.width(32)) register_88 (.D(demultiplexer_4_out21), .Q(out_123), .clk(clk));  // open: en, clr
  Register #(.width(32)) register_89 (.D(demultiplexer_1_out22), .Q(out_28), .clk(clk));  // open: en, clr
  Register #(.width(32)) register_90 (.D(demultiplexer_2_out22), .Q(out_60), .clk(clk));  // open: en, clr
  Register #(.width(32)) register_91 (.D(demultiplexer_3_out22), .Q(out_92), .clk(clk));  // open: en, clr
  Register #(.width(32)) register_92 (.D(demultiplexer_4_out22), .Q(out_124), .clk(clk));  // open: en, clr
  Register #(.width(32)) register_93 (.D(demultiplexer_1_out23), .Q(out_29), .clk(clk));  // open: en, clr
  Register #(.width(32)) register_94 (.D(demultiplexer_2_out23), .Q(out_61), .clk(clk));  // open: en, clr
  Register #(.width(32)) register_95 (.D(demultiplexer_3_out23), .Q(out_93), .clk(clk));  // open: en, clr
  Register #(.width(32)) register_96 (.D(demultiplexer_4_out23), .Q(out_125), .clk(clk));  // open: en, clr
  Register #(.width(32)) register_97 (.D(demultiplexer_1_out24), .Q(out_30), .clk(clk));  // open: en, clr
  Register #(.width(32)) register_98 (.D(demultiplexer_2_out24), .Q(out_62), .clk(clk));  // open: en, clr
  Register #(.width(32)) register_99 (.D(demultiplexer_3_out24), .Q(out_94), .clk(clk));  // open: en, clr
  Register #(.width(32)) register_100 (.D(demultiplexer_4_out24), .Q(out_126), .clk(clk));  // open: en, clr
  Register #(.width(32)) register_101 (.D(demultiplexer_1_out25), .Q(out_31), .clk(clk));  // open: en, clr
  Register #(.width(32)) register_102 (.D(demultiplexer_2_out25), .Q(out_63), .clk(clk));  // open: en, clr
  Register #(.width(32)) register_103 (.D(demultiplexer_3_out25), .Q(out_95), .clk(clk));  // open: en, clr
  Register #(.width(32)) register_104 (.D(demultiplexer_4_out25), .Q(out_127), .clk(clk));  // open: en, clr
  Register #(.width(32)) register_105 (.D(demultiplexer_1_out26), .Q(out_32), .clk(clk));  // open: en, clr
  Register #(.width(32)) register_106 (.D(demultiplexer_2_out26), .Q(out_64), .clk(clk));  // open: en, clr
  Register #(.width(32)) register_107 (.D(demultiplexer_3_out26), .Q(out_96), .clk(clk));  // open: en, clr
  Register #(.width(32)) register_108 (.D(demultiplexer_4_out26), .Q(out_128), .clk(clk));  // open: en, clr
  Register #(.width(32)) register_109 (.D(demultiplexer_1_out27), .Q(out_33), .clk(clk));  // open: en, clr
  Register #(.width(32)) register_110 (.D(demultiplexer_2_out27), .Q(out_65), .clk(clk));  // open: en, clr
  Register #(.width(32)) register_111 (.D(demultiplexer_3_out27), .Q(out_97), .clk(clk));  // open: en, clr
  Register #(.width(32)) register_112 (.D(demultiplexer_4_out27), .Q(out_129), .clk(clk));  // open: en, clr
  Register #(.width(32)) register_113 (.D(demultiplexer_1_out28), .Q(out_34), .clk(clk));  // open: en, clr
  Register #(.width(32)) register_114 (.D(demultiplexer_2_out28), .Q(out_66), .clk(clk));  // open: en, clr
  Register #(.width(32)) register_115 (.D(demultiplexer_3_out28), .Q(out_98), .clk(clk));  // open: en, clr
  Register #(.width(32)) register_116 (.D(demultiplexer_4_out28), .Q(out_130), .clk(clk));  // open: en, clr
  Register #(.width(32)) register_117 (.D(demultiplexer_1_out29), .Q(out_35), .clk(clk));  // open: en, clr
  Register #(.width(32)) register_118 (.D(demultiplexer_2_out29), .Q(out_67), .clk(clk));  // open: en, clr
  Register #(.width(32)) register_119 (.D(demultiplexer_3_out29), .Q(out_99), .clk(clk));  // open: en, clr
  Register #(.width(32)) register_120 (.D(demultiplexer_4_out29), .Q(out_131), .clk(clk));  // open: en, clr
  Register #(.width(32)) register_121 (.D(demultiplexer_1_out30), .Q(out_36), .clk(clk));  // open: en, clr
  Register #(.width(32)) register_122 (.D(demultiplexer_2_out30), .Q(out_68), .clk(clk));  // open: en, clr
  Register #(.width(32)) register_123 (.D(demultiplexer_3_out30), .Q(out_100), .clk(clk));  // open: en, clr
  Register #(.width(32)) register_124 (.D(demultiplexer_4_out30), .Q(out_132), .clk(clk));  // open: en, clr
  Register #(.width(32)) register_125 (.D(demultiplexer_1_out31), .Q(out_37), .clk(clk));  // open: en, clr
  Register #(.width(32)) register_126 (.D(demultiplexer_2_out31), .Q(out_69), .clk(clk));  // open: en, clr
  Register #(.width(32)) register_127 (.D(demultiplexer_3_out31), .Q(out_101), .clk(clk));  // open: en, clr
  Register #(.width(32)) register_128 (.D(demultiplexer_4_out31), .Q(out_133), .clk(clk));  // open: en, clr

  // Notes on the sheet:
  //   kek
  //   kek
endmodule

module VRAM_aa (
  input  set,
  input  [31:0] x1,
  input  clear,
  input  [31:0] y1,
  input  load_to_screen,
  output [31:0] x_right_out,
  output [31:0] x_left_out,
  output [5:0] y_out,
  output mode
);

  wire buffer_1_out, buffer_2_out, buffer_3_out, buffer_4_out, buffer_5_out, buffer_6_out, buffer_7_out,
       buffer_8_out, buffer_9_out, buffer_10_out, buffer_11_out, buffer_12_out, buffer_13_out, buffer_14_out,
       buffer_15_out, buffer_17_out, buffer_18_out, buffer_28_out, buffer_29_out, controlled_buffer_4_out,
       counter_1_carry, not_1_out, not_3_out, not_4_out, pull_resistor_2_node, pull_resistor_3_node,
       pull_resistor_5_node, pull_resistor_6_node, rising_edge_detector_async_1_out, rising_edge_pulse_1_out;
  wire [0:0] controlled_buffer_1_out;
  wire [5:0] buffer_21_out, buffer_22_out, buffer_24_out, buffer_25_out, buffer_26_out, buffer_27_out,
       buffer_32_out, buffer_33_out, buffer_34_out, buffer_35_out, counter_1_q, multiplexer_1_out;
  wire [31:0] adder_1_out, adder_2_out, adder_3_out, adder_4_out, adder_5_out, controlled_buffer_2_out,
       controlled_buffer_3_out, decoder_1_out31, or_1_out, or_2_out, ram_1_data, ram_2_data;

  assign controlled_buffer_1_out[0] = not_1_out ? set : 1'bz;  // Controlled_Buffer controlled_buffer_1
  assign controlled_buffer_2_out = not_1_out ? x1 : 32'bz;  // Controlled_Buffer controlled_buffer_2
  assign controlled_buffer_3_out = not_1_out ? y1 : 32'bz;  // Controlled_Buffer controlled_buffer_3
  not not_1 (not_1_out, load_to_screen);
  Pull_Resistor pull_resistor_1 (.node(load_to_screen));
  Adder #(.width(32)) adder_1 (
    .a({{31{1'b0}}, controlled_buffer_1_out[0]}), .b({32{1'b0}}), .out(adder_1_out));  // open: cin, cout
  rising_edge_detector_async rising_edge_detector_async_1 (
    .signal(load_to_screen), .clear(buffer_5_out), .out(rising_edge_detector_async_1_out));
  buf buffer_1 (buffer_1_out, buffer_3_out);
  buf buffer_2 (buffer_2_out, buffer_8_out);
  buf buffer_3 (buffer_3_out, buffer_2_out);
  buf buffer_4 (buffer_4_out, buffer_14_out);
  buf buffer_5 (buffer_5_out, buffer_4_out);
  Adder #(.width(32)) adder_2 (.a(adder_1_out), .b({32{1'b0}}), .out(adder_2_out));  // open: cin, cout
  Pull_Resistor #(.pull(1)) pull_resistor_2 (.node(pull_resistor_2_node));
  not not_2 (pull_resistor_2_node, rising_edge_detector_async_1_out);
  buf buffer_6 (buffer_6_out, buffer_1_out);
  buf buffer_7 (buffer_7_out, buffer_6_out);
  buf buffer_8 (buffer_8_out, buffer_11_out);
  buf buffer_9 (buffer_9_out, buffer_10_out);
  buf buffer_10 (buffer_10_out, mode);
  buf buffer_11 (buffer_11_out, buffer_9_out);
  buf buffer_12 (buffer_12_out, buffer_15_out);
  buf buffer_13 (buffer_13_out, counter_1_carry);
  buf buffer_14 (buffer_14_out, buffer_12_out);
  buf buffer_15 (buffer_15_out, buffer_13_out);
  not not_3 (not_3_out, rising_edge_detector_async_1_out);
  Pull_Resistor pull_resistor_3 (.node(pull_resistor_3_node));
  buf buffer_16 (pull_resistor_3_node, adder_2_out[0]);
  Adder #(.width(32)) adder_3 (.a(adder_2_out), .b({32{1'b0}}), .out(adder_3_out));  // open: cin, cout
  Adder #(.width(32)) adder_4 (.a(controlled_buffer_2_out), .b(32'h8000), .out(adder_4_out));  // open: cin, cout
  rising_edge_pulse rising_edge_pulse_1 (.signal(clear), .out(rising_edge_pulse_1_out));
  Adder #(.width(32)) adder_5 (.a(controlled_buffer_3_out), .b(32'h8000), .out(adder_5_out));  // open: cin, cout
  Counter #(.width(6), .max('h3f)) counter_1 (
    .Q(counter_1_q), .carry(counter_1_carry), .clk(mode), .clr(not_3_out));  // open: load, D, count
  and and_1 (mode, ~pull_resistor_2_node, ~buffer_7_out);  // AND_Gate
  Decoder #(.select(5), .enable("false")) decoder_1 (
    .out0(decoder_1_out31[31]), .out1(decoder_1_out31[30]), .out2(decoder_1_out31[29]),
    .out3(decoder_1_out31[28]), .out4(decoder_1_out31[27]), .out5(decoder_1_out31[26]),
    .out6(decoder_1_out31[25]), .out7(decoder_1_out31[24]), .out8(decoder_1_out31[23]),
    .out9(decoder_1_out31[22]), .out10(decoder_1_out31[21]), .out11(decoder_1_out31[20]),
    .out12(decoder_1_out31[19]), .out13(decoder_1_out31[18]), .out14(decoder_1_out31[17]),
    .out15(decoder_1_out31[16]), .out16(decoder_1_out31[15]), .out17(decoder_1_out31[14]),
    .out18(decoder_1_out31[13]), .out19(decoder_1_out31[12]), .out20(decoder_1_out31[11]),
    .out21(decoder_1_out31[10]), .out22(decoder_1_out31[9]), .out23(decoder_1_out31[8]),
    .out24(decoder_1_out31[7]), .out25(decoder_1_out31[6]), .out26(decoder_1_out31[5]),
    .out27(decoder_1_out31[4]), .out28(decoder_1_out31[3]), .out29(decoder_1_out31[2]),
    .out30(decoder_1_out31[1]), .out31(decoder_1_out31[0]), .sel(adder_4_out[20:16]));
  assign controlled_buffer_4_out = not_4_out ? adder_3_out[0] : 1'bz;  // Controlled_Buffer controlled_buffer_4
  not not_4 (not_4_out, rising_edge_detector_async_1_out);
  Pull_Resistor pull_resistor_4 (.node(controlled_buffer_4_out));
  Multiplexer #(.width(6), .enable("false")) multiplexer_1 (
    .in0(adder_5_out[21:16]), .in1(counter_1_q), .out(multiplexer_1_out),
    .sel(rising_edge_detector_async_1_out));
  assign or_1_out = ram_1_data | decoder_1_out31;  // OR_Gate or_1, 32 bits wide
  Pull_Resistor pull_resistor_5 (.node(pull_resistor_5_node));
  buf buffer_17 (buffer_17_out, buffer_18_out);
  buf buffer_18 (buffer_18_out, adder_3_out[0]);
  not not_5 (pull_resistor_5_node, adder_4_out[21]);
  buf buffer_19 (pull_resistor_3_node, rising_edge_detector_async_1_out);
  buf buffer_20 (pull_resistor_5_node, rising_edge_detector_async_1_out);
  RAM #(.addrWidth(6), .dataWidth(32), .bus("separate")) ram_1 (
    .addr(multiplexer_1_out), .din(or_1_out), .data(ram_1_data), .str(controlled_buffer_4_out),
    .sel(pull_resistor_5_node), .clk(buffer_17_out), .ld(pull_resistor_3_node), .clr(rising_edge_pulse_1_out));
  assign or_2_out = ram_2_data | decoder_1_out31;  // OR_Gate or_2, 32 bits wide
  assign buffer_21_out = buffer_22_out;  // Buffer buffer_21, 6 bits wide
  assign buffer_22_out = counter_1_q;  // Buffer buffer_22, 6 bits wide
  Pull_Resistor pull_resistor_6 (.node(pull_resistor_6_node));
  buf buffer_23 (pull_resistor_6_node, adder_4_out[21]);
  assign buffer_24_out = buffer_27_out;  // Buffer buffer_24, 6 bits wide
  assign buffer_25_out = buffer_26_out;  // Buffer buffer_25, 6 bits wide
  assign buffer_26_out = buffer_24_out;  // Buffer buffer_26, 6 bits wide
  assign buffer_27_out = buffer_21_out;  // Buffer buffer_27, 6 bits wide
  RAM #(.addrWidth(6), .dataWidth(32), .bus("separate")) ram_2 (
    .addr(multiplexer_1_out), .din(or_2_out), .data(ram_2_data), .str(controlled_buffer_4_out),
    .sel(pull_resistor_6_node), .clk(buffer_28_out), .ld(pull_resistor_3_node), .clr(rising_edge_pulse_1_out));
  buf buffer_28 (buffer_28_out, buffer_29_out);
  buf buffer_29 (buffer_29_out, adder_3_out[0]);
  buf buffer_30 (pull_resistor_6_node, rising_edge_detector_async_1_out);
  buf buffer_31 (pull_resistor_3_node, rising_edge_detector_async_1_out);
  assign buffer_32_out = buffer_34_out;  // Buffer buffer_32, 6 bits wide
  assign buffer_33_out = buffer_25_out;  // Buffer buffer_33, 6 bits wide
  assign buffer_34_out = buffer_33_out;  // Buffer buffer_34, 6 bits wide
  assign buffer_35_out = buffer_32_out;  // Buffer buffer_35, 6 bits wide
  assign x_right_out = rising_edge_detector_async_1_out ? ram_2_data : 32'bz;  // Controlled_Buffer controlled_buffer_5
  assign x_left_out = rising_edge_detector_async_1_out ? ram_1_data : 32'bz;  // Controlled_Buffer controlled_buffer_6
  assign y_out = rising_edge_detector_async_1_out ? buffer_35_out : 6'bz;  // Controlled_Buffer controlled_buffer_7

  // Notes on the sheet:
  //   not_2 drives only 0 and floats otherwise
  //   buffer_16 drives only 1 and floats otherwise
  //   not_5 drives only 1 and floats otherwise
  //   buffer_19 drives only 1 and floats otherwise
  //   buffer_20 drives only 1 and floats otherwise
  //   buffer_23 drives only 1 and floats otherwise
  //   buffer_30 drives only 1 and floats otherwise
  //   buffer_31 drives only 1 and floats otherwise
endmodule

module VRAM_as (
  input  set,
  input  [31:0] x1,
  input  clear,
  input  [31:0] y1,
  input  load_to_screen,
  input  clk,
  output [31:0] x_right_out,
  output [31:0] x_left_out,
  output [5:0] y_out,
  output mode
);

  wire and_1_out, buffer_2_out, buffer_3_out, buffer_7_out, buffer_8_out, controlled_buffer_4_out,
       counter_1_carry, not_1_out, not_2_out, not_3_out, pull_resistor_2_node, pull_resistor_4_node,
       pull_resistor_5_node, rising_edge_detector_async_1_out, rising_edge_pulse_1_out;
  wire [0:0] controlled_buffer_1_out;
  wire [5:0] counter_1_q, multiplexer_1_out;
  wire [31:0] adder_1_out, adder_2_out, adder_3_out, adder_4_out, adder_5_out, controlled_buffer_2_out,
       controlled_buffer_3_out, decoder_1_out31, or_1_out, or_2_out, ram_1_data, ram_2_data;

  assign controlled_buffer_1_out[0] = not_1_out ? set : 1'bz;  // Controlled_Buffer controlled_buffer_1
  assign controlled_buffer_2_out = not_1_out ? x1 : 32'bz;  // Controlled_Buffer controlled_buffer_2
  assign controlled_buffer_3_out = not_1_out ? y1 : 32'bz;  // Controlled_Buffer controlled_buffer_3
  not not_1 (not_1_out, load_to_screen);
  Pull_Resistor pull_resistor_1 (.node(load_to_screen));
  Adder #(.width(32)) adder_1 (
    .a({{31{1'b0}}, controlled_buffer_1_out[0]}), .b({32{1'b0}}), .out(adder_1_out));  // open: cin, cout
  rising_edge_detector_async rising_edge_detector_async_1 (
    .signal(load_to_screen), .clear(counter_1_carry), .out(rising_edge_detector_async_1_out));
  Adder #(.width(32)) adder_2 (.a(adder_1_out), .b({32{1'b0}}), .out(adder_2_out));  // open: cin, cout
  rising_edge_detector rising_edge_detector_1 (
    .signal(rising_edge_detector_async_1_out), .clear(counter_1_carry), .sync(clk), .out(mode));
  not not_2 (not_2_out, rising_edge_detector_async_1_out);
  Pull_Resistor pull_resistor_2 (.node(pull_resistor_2_node));
  buf buffer_1 (pull_resistor_2_node, adder_2_out[0]);
  Adder #(.width(32)) adder_3 (.a(adder_2_out), .b({32{1'b0}}), .out(adder_3_out));  // open: cin, cout
  Adder #(.width(32)) adder_4 (.a(controlled_buffer_2_out), .b(32'h8000), .out(adder_4_out));  // open: cin, cout
  rising_edge_pulse rising_edge_pulse_1 (.signal(clear), .out(rising_edge_pulse_1_out));
  Adder #(.width(32)) adder_5 (.a(controlled_buffer_3_out), .b(32'h8000), .out(adder_5_out));  // open: cin, cout
  Counter #(.width(6), .max('h3f)) counter_1 (
    .Q(counter_1_q), .carry(counter_1_carry), .clk(and_1_out), .clr(not_2_out));  // open: load, D, count
  and and_1 (and_1_out, mode, clk);
  Decoder #(.select(5), .enable("false")) decoder_1 (
    .out0(decoder_1_out31[31]), .out1(decoder_1_out31[30]), .out2(decoder_1_out31[29]),
    .out3(decoder_1_out31[28]), .out4(decoder_1_out31[27]), .out5(decoder_1_out31[26]),
    .out6(decoder_1_out31[25]), .out7(decoder_1_out31[24]), .out8(decoder_1_out31[23]),
    .out9(decoder_1_out31[22]), .out10(decoder_1_out31[21]), .out11(decoder_1_out31[20]),
    .out12(decoder_1_out31[19]), .out13(decoder_1_out31[18]), .out14(decoder_1_out31[17]),
    .out15(decoder_1_out31[16]), .out16(decoder_1_out31[15]), .out17(decoder_1_out31[14]),
    .out18(decoder_1_out31[13]), .out19(decoder_1_out31[12]), .out20(decoder_1_out31[11]),
    .out21(decoder_1_out31[10]), .out22(decoder_1_out31[9]), .out23(decoder_1_out31[8]),
    .out24(decoder_1_out31[7]), .out25(decoder_1_out31[6]), .out26(decoder_1_out31[5]),
    .out27(decoder_1_out31[4]), .out28(decoder_1_out31[3]), .out29(decoder_1_out31[2]),
    .out30(decoder_1_out31[1]), .out31(decoder_1_out31[0]), .sel(adder_4_out[20:16]));
  assign controlled_buffer_4_out = not_3_out ? adder_3_out[0] : 1'bz;  // Controlled_Buffer controlled_buffer_4
  not not_3 (not_3_out, rising_edge_detector_async_1_out);
  Pull_Resistor pull_resistor_3 (.node(controlled_buffer_4_out));
  Multiplexer #(.width(6), .enable("false")) multiplexer_1 (
    .in0(adder_5_out[21:16]), .in1(counter_1_q), .out(multiplexer_1_out),
    .sel(rising_edge_detector_async_1_out));
  assign or_1_out = ram_1_data | decoder_1_out31;  // OR_Gate or_1, 32 bits wide
  Pull_Resistor pull_resistor_4 (.node(pull_resistor_4_node));
  buf buffer_2 (buffer_2_out, buffer_3_out);
  buf buffer_3 (buffer_3_out, adder_3_out[0]);
  not not_4 (pull_resistor_4_node, adder_4_out[21]);
  buf buffer_4 (pull_resistor_2_node, rising_edge_detector_async_1_out);
  buf buffer_5 (pull_resistor_4_node, rising_edge_detector_async_1_out);
  RAM #(.addrWidth(6), .dataWidth(32), .bus("separate")) ram_1 (
    .addr(multiplexer_1_out), .din(or_1_out), .data(ram_1_data), .str(controlled_buffer_4_out),
    .sel(pull_resistor_4_node), .clk(buffer_2_out), .ld(pull_resistor_2_node), .clr(rising_edge_pulse_1_out));
  assign or_2_out = ram_2_data | decoder_1_out31;  // OR_Gate or_2, 32 bits wide
  Pull_Resistor pull_resistor_5 (.node(pull_resistor_5_node));
  buf buffer_6 (pull_resistor_5_node, adder_4_out[21]);
  RAM #(.addrWidth(6), .dataWidth(32), .bus("separate")) ram_2 (
    .addr(multiplexer_1_out), .din(or_2_out), .data(ram_2_data), .str(controlled_buffer_4_out),
    .sel(pull_resistor_5_node), .clk(buffer_7_out), .ld(pull_resistor_2_node), .clr(rising_edge_pulse_1_out));
  buf buffer_7 (buffer_7_out, buffer_8_out);
  buf buffer_8 (buffer_8_out, adder_3_out[0]);
  buf buffer_9 (pull_resistor_5_node, rising_edge_detector_async_1_out);
  buf buffer_10 (pull_resistor_2_node, rising_edge_detector_async_1_out);
  assign x_right_out = rising_edge_detector_async_1_out ? ram_2_data : 32'bz;  // Controlled_Buffer controlled_buffer_5
  assign x_left_out = rising_edge_detector_async_1_out ? ram_1_data : 32'bz;  // Controlled_Buffer controlled_buffer_6
  assign y_out = rising_edge_detector_async_1_out ? counter_1_q : 6'bz;  // Controlled_Buffer controlled_buffer_7

  // Notes on the sheet:
  //   buffer_1 drives only 1 and floats otherwise
  //   not_4 drives only 1 and floats otherwise
  //   buffer_4 drives only 1 and floats otherwise
  //   buffer_5 drives only 1 and floats otherwise
  //   buffer_6 drives only 1 and floats otherwise
  //   buffer_9 drives only 1 and floats otherwise
  //   buffer_10 drives only 1 and floats otherwise
endmodule

module _64_display_v2 (
  input  clk,
  input  [5:0] y,
  input  [5:0] x,
  input  update_pt,
  input  update,
  input  clear,
  output [31:0] out_7,
  output [31:0] out_8,
  output [31:0] out_9,
  output [31:0] out_10,
  output [31:0] out_11,
  output [31:0] out_12,
  output [31:0] out_13,
  output [31:0] out_14
);

  wire clk_t, cnt_loop, d_ff_1_q, d_ff_2_q, not_1_out, not_2_out, not_3_out, not_4_out, not_5_out,
       update_pt_t, update_t;
  wire [5:0] counter, y_t;
  wire [31:0] or_1_out, or_2_out, pull_resistor_2_node, pull_resistor_3_node, ram_1_data, ram_3_data,
       rom_2_data, rom_3_data, x_t;

  D_Flip_Flop d_ff_1 (.clk(clk_t), .D(update_pt_t), .Q(d_ff_1_q));  // open: Qn, preset, en, reset
  D_Flip_Flop d_ff_2 (.clk(cnt_loop), .D(update_t), .Q(d_ff_2_q));  // open: Qn, preset, en, reset
  Counter #(.width(6), .max('h3f)) counter_1 (.Q(counter), .carry(cnt_loop), .clk(clk_t));  // open: load, D, count, clr
  Clock clock_1 (.out(clk_t));
  rising_edge_detector rising_edge_detector_1 (.signal(update_pt), .clear(d_ff_1_q), .sync(clk_t), .out(update_pt_t));
  rising_edge_detector rising_edge_detector_2 (.signal(update), .clear(d_ff_2_q), .sync(cnt_loop), .out(update_t));
  ROM #(.addrWidth(5), .dataWidth(32)) rom_1 (.addr(x[4:0]), .data(x_t));  // open: sel
  Multiplexer #(.width(6), .enable("false")) multiplexer_1 (.in0(y), .in1(counter), .out(y_t), .sel(update_t));
  Pull_Resistor pull_resistor_1 (.node(update_t));
  Pull_Resistor pull_resistor_2 (.node(pull_resistor_2_node));
  assign or_1_out = pull_resistor_2_node | x_t;  // OR_Gate or_1, 32 bits wide
  not not_1 (not_1_out, x[5]);
  RAM #(.addrWidth(6), .dataWidth(32)) ram_1 (
    .addr(counter), .data(ram_1_data), .clk(clk_t), .ld(not_2_out), .clr(clear));  // open: sel
  not not_2 (not_2_out, update_t);
  ROM #(.addrWidth(5), .dataWidth(32)) rom_2 (.addr(counter[4:0]), .data(rom_2_data));  // open: sel
  RAM #(.addrWidth(6), .dataWidth(32), .bus("separate")) ram_2 (
    .addr(y_t), .din(or_1_out), .data(pull_resistor_2_node), .str(update_pt_t), .sel(not_1_out), .clk(clk_t),
    .clr(clear));  // open: ld
  assign ram_1_data = update_t ? pull_resistor_2_node : 32'bz;  // Controlled_Buffer controlled_buffer_1
  not not_3 (not_3_out, counter[5]);
  Register #(.width(32), .trigger("falling")) register_1 (
    .D(ram_1_data), .en(counter[5]), .Q(out_7), .clk(clk_t));  // open: clr
  Register #(.width(32), .trigger("falling")) register_2 (
    .D(rom_2_data), .en(counter[5]), .Q(out_9), .clk(clk_t));  // open: clr
  Register #(.width(32), .trigger("falling")) register_3 (
    .D(ram_1_data), .en(not_3_out), .Q(out_11), .clk(clk_t));  // open: clr
  Register #(.width(32), .trigger("falling")) register_4 (
    .D(rom_2_data), .en(not_3_out), .Q(out_13), .clk(clk_t));  // open: clr
  Pull_Resistor pull_resistor_3 (.node(pull_resistor_3_node));
  assign or_2_out = pull_resistor_3_node | x_t;  // OR_Gate or_2, 32 bits wide
  not not_4 (not_4_out, update_t);
  RAM #(.addrWidth(6), .dataWidth(32)) ram_3 (
    .addr(counter), .data(ram_3_data), .clk(clk_t), .ld(not_4_out), .clr(clear));  // open: sel
  ROM #(.addrWidth(5), .dataWidth(32)) rom_3 (.addr(counter[4:0]), .data(rom_3_data));  // open: sel
  not not_5 (not_5_out, counter[5]);
  RAM #(.addrWidth(6), .dataWidth(32), .bus("separate")) ram_4 (
    .addr(y_t), .din(or_2_out), .data(pull_resistor_3_node), .str(update_pt_t), .sel(x[5]), .clk(clk_t),
    .clr(clear));  // open: ld
  assign ram_3_data = update_t ? pull_resistor_3_node : 32'bz;  // Controlled_Buffer controlled_buffer_2
  Register #(.width(32), .trigger("falling")) register_5 (
    .D(ram_3_data), .en(counter[5]), .Q(out_8), .clk(clk_t));  // open: clr
  Register #(.width(32), .trigger("falling")) register_6 (
    .D(rom_3_data), .en(counter[5]), .Q(out_10), .clk(clk_t));  // open: clr
  Register #(.width(32), .trigger("falling")) register_7 (
    .D(ram_3_data), .en(not_5_out), .Q(out_12), .clk(clk_t));  // open: clr
  Register #(.width(32), .trigger("falling")) register_8 (
    .D(rom_3_data), .en(not_5_out), .Q(out_14), .clk(clk_t));  // open: clr

  // Notes on the sheet:
  //   out_9: pull=down
  //   out_14: pull=down
  //   out_10: pull=down
  //   out_7: pull=down
  //   out_11: pull=down
  //   out_12: pull=down
  //   out_8: pull=down
  //   out_13: pull=down
  //   contents of rom_1 (hex, n*v repeats v):
  //   1 2 4 8 10 20 40 80 100 200 400 800 1000 2000 4000 8000 10000 20000 40000 80000 100000 200000 400000
  //   800000 1000000 2000000 4000000 8000000 10000000 20000000 40000000 80000000
  //   contents of rom_2 (hex, n*v repeats v):
  //   1 2 4 8 10 20 40 80 100 200 400 800 1000 2000 4000 8000 10000 20000 40000 80000 100000 200000 400000
  //   800000 1000000 2000000 4000000 8000000 10000000 20000000 40000000 80000000
  //   contents of rom_3 (hex, n*v repeats v):
  //   1 2 4 8 10 20 40 80 100 200 400 800 1000 2000 4000 8000 10000 20000 40000 80000 100000 200000 400000
  //   800000 1000000 2000000 4000000 8000000 10000000 20000000 40000000 80000000
endmodule
